// Logisim project CPU完整设计.circ as structural Verilog: 25 circuits, main circuit ◇单周期RISC-V
module \单周期RISC_V  (
  input  IR1,
  input  IR2,
  input  IR3,
  output RegWrite,
  output MemWrite,
  output [31:0] PC,
  output [31:0] IR,
  output [31:0] RDin,
  output [31:0] MDin,
  output [31:0] LedData
);

  wire and_1_out, and_2_out, and_3_out, and_4_out, Beq, Bne, CLK, clock_1_out, comparator_1_eq,
       comparator_2_eq, comparator_2_lt, d_ff_1_q, dasb, ecall, equ, ge, Go, halt, IR1_t, IR2_t, IR3_t, IRA,
       IRB, IRC, jal, jalr, MemToReg, nand_1_out, not_1_out, not_2_out, not_3_out, not_4_out, or_1_out,
       or_2_out, riscv_probe_1_p2, S_type, W1, W2, W3, \单周期硬布线控制器_1_alu_src , \单周期硬布线控制器_1_bgeu ;
  wire [1:0] priority_encoder_1_out;
  wire [1:1] or_6_out;
  wire [3:0] \单周期硬布线控制器_1_alu_op ;
  wire [4:0] multiplexer_2_out, multiplexer_3_out;
  wire [11:0] multiplexer_4_out;
  wire [12:0] CNT_num;
  wire [15:0] \总周期数 ;
  wire [31:0] adder_2_out, adder_3_out, \ALU计算结果 , bit_extender_1_out, bit_extender_2_out,
       bit_extender_3_out, multiplexer_1_out, multiplexer_5_out, PC_4, ram_1_data, regifile_1_r1,
       regifile_1_r2, shifter_1_out, shifter_2_out;

  Button \u_继续运行  (.out(Go));
  Button _1 (.out(IRA));
  Button _2 (.out(IRB));
  Button _3 (.out(IRC));
  LED #(.active("true")) led_1 (.in(W1));
  LED #(.active("true")) led_2 (.in(W2));
  LED #(.active("true")) led_3 (.in(W3));
  Priority_Encoder #(.select(2), .disabled("Z")) priority_encoder_1 (
    .in0(1'b1), .in1(jalr), .in2(jal), .in3(or_1_out), .out(priority_encoder_1_out), .en_in(1'b1));  // open: gs, en_out
  Hex_Digit_Display hex_digit_display_1 (.value(LedData[31:28]));  // open: dp
  not not_1 (not_1_out, equ);
  and and_1 (and_1_out, not_1_out, Bne);
  and and_2 (and_2_out, Beq, equ);
  or or_1 (or_1_out, and_2_out, and_1_out, and_3_out);
  Register #(.width(32), .trigger("rising"), .Select("low")) u_PC (
    .D(multiplexer_1_out), .en(or_2_out), .Q(PC), .clk(CLK), .clr(1'b0), .cs(1'b0), .preset(1'b0));
  Multiplexer #(.select(2), .width(32), .disabled("Z"), .enable("false")) multiplexer_1 (
    .in0(PC_4), .in1(\ALU计算结果 ), .in2(adder_3_out), .in3(adder_2_out), .out(multiplexer_1_out),
    .sel(priority_encoder_1_out));
  or or_2 (or_2_out, not_2_out, Go);
  not not_2 (not_2_out, halt);
  Hex_Digit_Display hex_digit_display_2 (.value(LedData[23:20]));  // open: dp
  Hex_Digit_Display hex_digit_display_3 (.value(LedData[27:24]));  // open: dp
  and and_3 (and_3_out, ge, \单周期硬布线控制器_1_bgeu );
  Hex_Digit_Display hex_digit_display_4 (.value(LedData[15:12]));  // open: dp
  Hex_Digit_Display hex_digit_display_5 (.value(LedData[19:16]));  // open: dp
  // RiscV_Probe riscv_probe_1: pin names not known; wires that end beside it: IR, riscv_probe_1_p2
  Adder #(.width(32)) adder_1 (.a(PC), .b(32'h4), .out(PC_4), .cin(1'b0));  // open: cout
  Hex_Digit_Display hex_digit_display_6 (.value(LedData[11:8]));  // open: dp
  Hex_Digit_Display hex_digit_display_7 (.value(LedData[7:4]));  // open: dp
  // Probe on \总周期数 
  ROM #(.addrWidth(10), .dataWidth(32), .Select("high")) rom_1 (.addr(PC[11:2]), .data(IR), .sel(1'b1));
  Hex_Digit_Display hex_digit_display_8 (.value(LedData[3:0]));  // open: dp
  Multiplexer #(.select(1), .width(5), .disabled("Z"), .enable("false")) multiplexer_2 (
    .in0(IR[19:15]), .in1(5'b10001), .out(multiplexer_2_out), .sel(ecall));
  Multiplexer #(.select(1), .width(5), .disabled("Z"), .enable("false")) multiplexer_3 (
    .in0(IR[24:20]), .in1(5'b01010), .out(multiplexer_3_out), .sel(ecall));
  // Probe on IR[11:7]
  Multiplexer #(.select(1), .width(12), .disabled("Z"), .enable("false")) multiplexer_4 (
    .in0(IR[31:20]), .in1({IR[31:25], IR[11:7]}), .out(multiplexer_4_out), .sel(S_type));
  or or_3 (IR1_t, IR1, IRA);
  \单周期硬布线控制器  \u_单周期硬布线控制器_1  (
    .Funct({IR[30], IR[25], IR[14:12]}), .OP(IR[6:2]), .ALU_OP(\单周期硬布线控制器_1_alu_op ), .MemToReg(MemToReg),
    .MemWrite(MemWrite), .ALU_SRC(\单周期硬布线控制器_1_alu_src ), .RegWrite(RegWrite), .ecall(ecall),
    .S_type(S_type), .Jalr(jalr), .Beq(Beq), .JAL(jal), .Bne(Bne), .in_3(IR[21]), .uret(riscv_probe_1_p2),
    .bgeu(\单周期硬布线控制器_1_bgeu ), .dasb(dasb));  // open: csr, user1, user2
  assign bit_extender_1_out = {{20{multiplexer_4_out[11]}}, multiplexer_4_out};  // Bit_Extender bit_extender_1
  assign bit_extender_2_out = {{20{IR[31]}}, {IR[31], IR[7], IR[30:25], IR[11:8]}};  // Bit_Extender bit_extender_2
  assign bit_extender_3_out = {{12{IR[31]}}, {IR[31], IR[19:12], IR[20], IR[30:21]}};  // Bit_Extender bit_extender_3
  or or_4 (IR2_t, IR2, IRB);
  Shifter #(.width(32), .shift("ll")) shifter_1 (.in(bit_extender_2_out), .\dist (5'b00001), .out(shifter_1_out));
  Shifter #(.width(32), .shift("ll")) shifter_2 (.in(bit_extender_3_out), .\dist (5'b00001), .out(shifter_2_out));
  Regifile regifile_1 (
    .Din(RDin), .Clk(CLK), .R1(regifile_1_r1), .R2(regifile_1_r2), .WE(RegWrite), .W_num(IR[11:7]),
    .R1_num(multiplexer_2_out), .R2_num(multiplexer_3_out));
  Adder #(.width(32)) adder_2 (.a(shifter_1_out), .b(PC), .out(adder_2_out), .cin(1'b0));  // open: cout
  Adder #(.width(32)) adder_3 (.a(shifter_2_out), .b(PC), .out(adder_3_out), .cin(1'b0));  // open: cout
  or or_5 (IR3_t, IR3, IRC);
  // Probe on regifile_1_r1
  // Probe on regifile_1_r2
  Multiplexer #(.select(1), .width(32), .disabled("Z"), .enable("false")) multiplexer_5 (
    .in0(regifile_1_r2), .in1(bit_extender_1_out), .out(multiplexer_5_out), .sel(\单周期硬布线控制器_1_alu_src ));
  ALU alu_1 (
    .X(regifile_1_r1), .Y(multiplexer_5_out), .AluOP(\单周期硬布线控制器_1_alu_op ), .Equal(equ), .Result(\ALU计算结果 ),
    .out_4(ge));  // open: Result_2, out_6
  Comparator #(.width(32), .mode("twosComplement")) comparator_1 (
    .a(regifile_1_r1), .b(32'h22), .eq(comparator_1_eq));  // open: gt, lt
  Register #(.width(32), .trigger("rising"), .Select("low")) register_1 (
    .D(regifile_1_r2), .en(and_4_out), .Q(LedData), .clk(CLK), .clr(1'b0), .cs(1'b0), .preset(1'b0));
  not not_3 (not_3_out, comparator_1_eq);
  and and_4 (and_4_out, ecall, comparator_1_eq);
  not not_4 (not_4_out, halt);
  Counter #(.width(16), .max('hffff), .ongoal("wrap"), .trigger("rising"), .behavior("new")) counter_1 (
    .load(1'b0), .D({16{1'b0}}), .count(not_4_out), .Q(\总周期数 ), .clk(CLK), .clr(1'b0), .down(1'b0));  // open: carry, preset
  \专门给SB画的电路  \u_专门给sb画的电路_1  (.r2(regifile_1_r2), .addr(\ALU计算结果 ), .pre_data(ram_1_data), .MDin(MDin), .dasb(dasb));
  and and_5 (halt, ecall, not_3_out);
  D_Flip_Flop #(.trigger("high"), .Pre_Clr_Positions("LEGACY"), .NegatePresetClear("false"), .enable("true"), .NewFFLayout("false")) d_ff_1 (.Q(d_ff_1_q));  // open: clk, D, Qn, preset, en, reset
  // Probe on 13'h600
  RAM #(.addrWidth(10), .dataWidth(32), .bus("separate"), .Select("high")) ram_1 (
    .addr(\ALU计算结果 [11:2]), .din(MDin), .data(ram_1_data), .str(MemWrite), .sel(1'b1), .clk(CLK), .ld(1'b1),
    .clr(1'b0));
  Comparator #(.width(13), .mode("twosComplement")) comparator_2 (
    .a(CNT_num), .b(13'h600), .eq(comparator_2_eq), .lt(comparator_2_lt));  // open: gt
  Clock #(.highDuration(1), .lowDuration(1)) clock_1 (.out(clock_1_out));
  Multiplexer #(.select(2), .width(32), .disabled("Z"), .enable("false")) multiplexer_6 (
    .in0(\ALU计算结果 ), .in1(ram_1_data), .in2(PC_4), .out(RDin), .sel({or_6_out[1], MemToReg}));  // open: in3
  or or_6 (or_6_out[1], jal, jalr);
  Counter #(.width(13), .max('h1fff), .ongoal("stay"), .trigger("rising"), .behavior("old")) counter_2 (
    .count(comparator_2_lt), .Q(CNT_num), .clk(clock_1_out));  // open: load, D, carry, clr, preset
  nand nand_1 (nand_1_out, d_ff_1_q, comparator_2_eq);
  assign CLK = nand_1_out ? clock_1_out : 1'bz;  // Controlled_Buffer controlled_buffer_1
  Pull_Resistor #(.pull(1)) pull_resistor_1 (.node(CLK));

  // Notes on the sheet:
  //   中断源
  //   中断等待指示
  //   选择PC
  //   数码管输出应该用寄存器锁存，否则显示数据只能一闪而过
  //   数码管输出
  //   指令探针
  //   指令存储器
  //   指令字
  //   contents of rom_1 (hex, n*v repeats v):
  //   100493 100006f 100493 200913 300993 100006f 100493 200913 300993 100006f 100493 200913 300993
  //   100006f 100493 200913 300993 3a4000ef 100413 100493 1f49493 900533 2200893 73 24d493 48463 fedff06f
  //   900533 2200893 73 100493 249493 900533 2200893 73 48463 fedff06f 100493 1f49493 900533 2200893 73
  //   4034d493 900533 2200893 73 4044d493 900533 2200893 73 4044d493 900533 2200893 73 4044d493 900533
  //   2200893 73 4044d493 900533 2200893 73 4044d493 900533 2200893 73 4044d493 900533 2200893 73 4044d493
  //   900533 2200893 73 100413 1f41993 41f9d993 433 c00913 300b13 140413 f47413 800293 100313 499993
  //   89e9b3 1300533 2200893 73 406282b3 fe0294e3 140413 f00f93 1f47433 1c41413 800293 100313 49d993
  //   89e9b3 1300533 2200893 73 406282b3 fe0294e3 1c45413 406b0b33 b0463 f95ff06f 2b3 fff2c293 829293
  //   ff2e293 500533 2200893 73 fff00413 493 84a023 140413 448493 84a023 140413 448493 84a023 140413
  //   448493 84a023 140413 448493 84a023 140413 448493 84a023 140413 448493 84a023 140413 448493 84a023
  //   140413 448493 84a023 140413 448493 84a023 140413 448493 84a023 140413 448493 84a023 140413 448493
  //   84a023 140413 448493 84a023 140413 448493 84a023 140413 448493 84a023 140413 448493 140413 433
  //   3c00493 42983 4aa03 149a2b3 28663 134a023 1442023 ffc48493 fe9412e3 800533 2200893 73 440413 3c00493
  //   fc9416e3 3200893 73 313 2000e13 493 100913 930023 900533 2200893 73 12484b3 130313 fffe0e13 fe0e12e3
  //   800e13 313 32483 900533 2200893 73 430313 fffe0e13 fe0e14e3 a00893 73 100293 300313 800493 849493
  //   7648493 900533 2200893 73 800e13 5494b3 6494b3 900533 2200893 73 fffe0e13 fe0e14e3 a00893 73
  //   fff00293 313 1900413 841413 9700493 940533 2200893 73 5484b3 494b313 fe0306e3 a00893 73 f00493
  //   100913 409909b3 900533 2200893 73 fff48493 ff29f6e3 a00893 73 a00893 73 413 140413 800533 2200893 73
  //   240413 800533 2200893 73 340413 800533 2200893 73 440413 800533 2200893 73 540413 800533 2200893 73
  //   640413 800533 2200893 73 740413 800533 2200893 73 840413 800533 2200893 2200893 73 8067
  //   JAL
  //   JALR
  //   URET
  //   rs1
  //   rs2
  //   rd
  //   I指令
  //   S指令
  //   B指令
  //   J指令
  //   bgeu
  //   跳转地址生成
  //   Beq
  //   Bne
  //   MemToReg
  //   MemWrite
  //   AluOP
  //   AluSrcB
  //   RegWrite
  //   ecall的LED显示
  //   为方便自动评测，需要输出PC，IR，寄存器堆写如数据RDin
  //   RAM写使能MemWrite、RAM写入数据MDin等信号
  //   实现sb
  //   数据存储器
  //   控制位
  //   暂停节拍，不能为0
  //   戳工具置1进入计数暂停模式，ctrl+k时钟自动运行到对应节拍暂停
  //   ctrl+k关闭时钟连续运行，将控制位置零，进入单步调试模式调试
  //   用这个时钟源需要去掉电路中的其他时钟源
  //   选择RDin
  //   可计数暂停的时钟源
endmodule

// 单周期硬布线控制器
module \单周期硬布线控制器  (
  input  [4:0] OP,
  input  [4:0] Funct,
  input  in_3,
  output [3:0] ALU_OP,
  output uret,
  output MemToReg,
  output ecall,
  output csr,
  output bgeu,
  output MemWrite,
  output ALU_SRC,
  output RegWrite,
  output S_type,
  output Beq,
  output Bne,
  output user1,
  output Jalr,
  output JAL,
  output user2,
  output dasb
);

  wire \控制信号自动生成_1_ecall ;

  \运算控制器自动生成  \u_运算控制器自动生成_1  (
    .OP2(OP[0]), .OP3(OP[1]), .OP4(OP[2]), .OP5(OP[3]), .OP6(OP[4]), .F12(Funct[0]), .F13(Funct[1]),
    .F14(Funct[2]), .F25(Funct[3]), .F30(Funct[4]), .S0(ALU_OP[0]), .S1(ALU_OP[1]), .S2(ALU_OP[2]),
    .S3(ALU_OP[3]));
  \控制信号自动生成  \u_控制信号自动生成_1  (
    .OP2(OP[0]), .OP3(OP[1]), .MemToReg(MemToReg), .OP4(OP[2]), .OP5(OP[3]), .OP6(OP[4]), .F12(Funct[0]),
    .csr(csr), .F13(Funct[1]), .F14(Funct[2]), .F25(Funct[3]), .F30(Funct[4]), .user1(user1), .bgeu(bgeu),
    .user2(user2), .MemWrite(MemWrite), .dasb(dasb), .ALU_SRC(ALU_SRC), .RegWrite(RegWrite),
    .ecall(\控制信号自动生成_1_ecall ), .S_Type(S_type), .BEQ(Beq), .BNE(Bne), .JALR(Jalr), .JAL(JAL));
  and and_1 (uret, in_3, \控制信号自动生成_1_ecall );
  and and_2 (ecall, ~in_3, \控制信号自动生成_1_ecall );  // AND_Gate

  // Other names for the same wires on the sheet: IR21 = in_3; OP_CODE[4:0] = OP

  // Notes on the sheet:
  //   运算器控制器，根据指令生成运算器功能选择信号
  //   控制信号生成，产生数据通路需要的其他控制信号
endmodule

// 运算器控制器
module \运算控制器自动生成  (
  input  OP2,
  input  OP3,
  input  OP4,
  input  OP5,
  input  OP6,
  input  F12,
  input  F13,
  input  F14,
  input  F25,
  input  F30,
  output S0,
  output S1,
  output S2,
  output S3
);

  wire and_1_out, and_2_out, and_3_out, and_4_out, and_5_out, and_6_out, and_7_out, and_8_out, and_9_out,
       and_10_out, and_11_out, and_12_out, and_13_out, and_14_out, and_15_out, and_16_out, and_17_out,
       and_18_out, and_19_out, and_20_out, and_21_out, and_22_out, and_23_out, and_24_out, and_25_out,
       and_26_out, and_27_out, and_28_out, and_29_out, and_30_out, and_31_out, and_32_out, and_33_out,
       and_34_out, and_35_out, and_36_out, and_37_out, and_38_out, and_39_out, and_40_out, and_41_out,
       and_42_out, and_43_out, and_44_out, and_45_out, and_46_out, not_1_out, not_2_out, not_3_out,
       not_4_out, not_5_out, not_6_out, not_7_out, not_8_out, not_9_out, not_10_out, not_11_out, not_12_out,
       not_13_out, not_14_out, not_15_out, not_16_out, not_17_out, not_18_out, not_19_out, not_20_out,
       not_21_out, not_22_out, not_23_out, not_24_out, not_25_out, not_26_out, not_27_out, not_28_out,
       not_29_out, not_30_out, not_31_out, not_32_out, not_33_out, not_34_out, not_35_out, not_36_out,
       not_37_out, not_38_out, not_39_out, not_40_out, not_41_out, not_42_out, not_43_out, not_44_out,
       not_45_out, not_46_out, not_47_out, not_48_out, not_49_out, not_50_out, not_51_out, not_52_out,
       not_53_out, not_54_out, not_55_out, not_56_out, not_57_out, not_58_out, not_59_out, not_60_out,
       not_61_out, not_62_out, not_63_out, not_64_out, not_65_out, not_66_out, not_67_out, not_68_out,
       not_69_out, not_70_out, not_71_out, not_72_out, not_73_out, not_74_out, not_75_out, not_76_out,
       not_77_out, not_78_out, not_79_out, not_80_out, not_81_out, not_82_out, not_83_out, not_84_out,
       not_85_out, not_86_out, not_87_out, not_88_out, not_89_out, not_90_out, not_91_out, not_92_out,
       not_93_out, not_94_out, not_95_out, not_96_out, not_97_out, not_98_out, not_99_out, not_100_out,
       not_101_out, not_102_out, not_103_out, not_104_out, not_105_out, not_106_out, not_107_out,
       not_108_out, not_109_out, not_110_out, not_111_out, not_112_out, not_113_out, not_114_out,
       not_115_out, not_116_out, not_117_out, not_118_out, not_119_out, not_120_out, not_121_out,
       not_122_out, not_123_out, not_124_out, not_125_out, not_126_out, not_127_out, not_128_out,
       not_129_out, not_130_out, not_131_out, not_132_out, not_133_out, not_134_out, not_135_out,
       not_136_out, not_137_out, not_138_out, not_139_out, not_140_out, not_141_out, not_142_out,
       not_143_out, not_144_out, not_145_out, not_146_out, not_147_out, not_148_out, not_149_out,
       not_150_out, not_151_out, not_152_out, not_153_out, not_154_out, not_155_out, not_156_out,
       not_157_out, not_158_out, not_159_out, not_160_out, not_161_out, not_162_out, not_163_out,
       not_164_out, not_165_out, not_166_out, not_167_out, not_168_out, not_169_out, not_170_out,
       not_171_out, not_172_out, not_173_out, not_174_out, not_175_out, not_176_out, not_177_out,
       not_178_out, not_179_out, not_180_out, not_181_out, not_182_out, not_183_out, not_184_out,
       not_185_out, not_186_out, not_187_out, not_188_out, not_189_out, not_190_out, not_191_out,
       not_192_out, not_193_out, not_194_out, not_195_out, not_196_out, not_197_out, not_198_out,
       not_199_out, not_200_out, not_201_out, not_202_out, not_203_out, not_204_out, not_205_out,
       not_206_out, not_207_out, not_208_out, not_209_out, not_210_out, not_211_out, not_212_out,
       not_213_out, not_214_out, not_215_out, not_216_out, not_217_out, not_218_out, not_219_out,
       not_220_out, not_221_out, not_222_out, not_223_out, not_224_out, not_225_out, not_226_out,
       not_227_out, not_228_out, not_229_out, not_230_out, not_231_out, not_232_out, not_233_out,
       not_234_out, not_235_out, not_236_out, not_237_out, not_238_out, not_239_out, not_240_out,
       not_241_out, not_242_out, not_243_out, not_244_out, not_245_out, not_246_out, not_247_out,
       not_248_out, not_249_out, not_250_out, not_251_out, not_252_out, not_253_out, not_254_out, not_255_out;

  not not_1 (not_1_out, F30);
  not not_2 (not_2_out, F25);
  not not_3 (not_3_out, F14);
  not not_4 (not_4_out, F13);
  not not_5 (not_5_out, F12);
  not not_6 (not_6_out, OP6);
  not not_7 (not_7_out, OP3);
  not not_8 (not_8_out, OP2);
  not not_9 (not_9_out, F30);
  not not_10 (not_10_out, F25);
  not not_11 (not_11_out, OP6);
  not not_12 (not_12_out, OP3);
  not not_13 (not_13_out, OP2);
  not not_14 (not_14_out, F30);
  not not_15 (not_15_out, F25);
  not not_16 (not_16_out, F14);
  not not_17 (not_17_out, F12);
  not not_18 (not_18_out, OP6);
  not not_19 (not_19_out, OP3);
  not not_20 (not_20_out, OP2);
  not not_21 (not_21_out, F14);
  not not_22 (not_22_out, F13);
  not not_23 (not_23_out, F12);
  not not_24 (not_24_out, OP6);
  not not_25 (not_25_out, OP5);
  not not_26 (not_26_out, OP3);
  not not_27 (not_27_out, OP2);
  not not_28 (not_28_out, OP6);
  not not_29 (not_29_out, OP5);
  not not_30 (not_30_out, OP3);
  not not_31 (not_31_out, OP2);
  not not_32 (not_32_out, F13);
  not not_33 (not_33_out, F12);
  not not_34 (not_34_out, OP6);
  not not_35 (not_35_out, OP5);
  not not_36 (not_36_out, OP3);
  not not_37 (not_37_out, OP2);
  not not_38 (not_38_out, F14);
  not not_39 (not_39_out, F12);
  not not_40 (not_40_out, OP6);
  not not_41 (not_41_out, OP5);
  not not_42 (not_42_out, OP3);
  not not_43 (not_43_out, OP2);
  not not_44 (not_44_out, F25);
  not not_45 (not_45_out, F13);
  not not_46 (not_46_out, OP6);
  not not_47 (not_47_out, OP5);
  not not_48 (not_48_out, OP3);
  not not_49 (not_49_out, OP2);
  not not_50 (not_50_out, F14);
  not not_51 (not_51_out, F12);
  not not_52 (not_52_out, OP6);
  not not_53 (not_53_out, OP5);
  not not_54 (not_54_out, OP4);
  not not_55 (not_55_out, OP3);
  not not_56 (not_56_out, OP2);
  not not_57 (not_57_out, F14);
  not not_58 (not_58_out, F12);
  not not_59 (not_59_out, OP6);
  not not_60 (not_60_out, OP4);
  not not_61 (not_61_out, OP3);
  not not_62 (not_62_out, OP2);
  not not_63 (not_63_out, OP3);
  not not_64 (not_64_out, OP2);
  not not_65 (not_65_out, F14);
  not not_66 (not_66_out, F13);
  not not_67 (not_67_out, F12);
  not not_68 (not_68_out, OP6);
  not not_69 (not_69_out, OP4);
  not not_70 (not_70_out, OP3);
  not not_71 (not_71_out, OP2);
  not not_72 (not_72_out, F25);
  not not_73 (not_73_out, F14);
  not not_74 (not_74_out, F13);
  not not_75 (not_75_out, F12);
  not not_76 (not_76_out, OP6);
  not not_77 (not_77_out, OP3);
  not not_78 (not_78_out, OP2);
  not not_79 (not_79_out, F30);
  not not_80 (not_80_out, F25);
  not not_81 (not_81_out, OP6);
  not not_82 (not_82_out, OP3);
  not not_83 (not_83_out, OP2);
  not not_84 (not_84_out, F30);
  not not_85 (not_85_out, F25);
  not not_86 (not_86_out, F14);
  not not_87 (not_87_out, F12);
  not not_88 (not_88_out, OP6);
  not not_89 (not_89_out, OP3);
  not not_90 (not_90_out, OP2);
  not not_91 (not_91_out, OP6);
  not not_92 (not_92_out, OP5);
  not not_93 (not_93_out, OP3);
  not not_94 (not_94_out, OP2);
  not not_95 (not_95_out, F14);
  not not_96 (not_96_out, F12);
  not not_97 (not_97_out, OP6);
  not not_98 (not_98_out, OP5);
  not not_99 (not_99_out, OP3);
  not not_100 (not_100_out, OP2);
  not not_101 (not_101_out, F30);
  not not_102 (not_102_out, F25);
  not not_103 (not_103_out, F13);
  not not_104 (not_104_out, OP6);
  not not_105 (not_105_out, OP5);
  not not_106 (not_106_out, OP3);
  not not_107 (not_107_out, OP2);
  not not_108 (not_108_out, F14);
  not not_109 (not_109_out, F13);
  not not_110 (not_110_out, F12);
  not not_111 (not_111_out, OP4);
  not not_112 (not_112_out, OP3);
  not not_113 (not_113_out, OP2);
  not not_114 (not_114_out, F14);
  not not_115 (not_115_out, F13);
  not not_116 (not_116_out, OP4);
  not not_117 (not_117_out, OP3);
  not not_118 (not_118_out, OP2);
  not not_119 (not_119_out, F14);
  not not_120 (not_120_out, F13);
  not not_121 (not_121_out, F12);
  not not_122 (not_122_out, OP4);
  not not_123 (not_123_out, OP3);
  not not_124 (not_124_out, OP3);
  not not_125 (not_125_out, OP2);
  not not_126 (not_126_out, F30);
  not not_127 (not_127_out, F25);
  not not_128 (not_128_out, F14);
  not not_129 (not_129_out, F13);
  not not_130 (not_130_out, F12);
  not not_131 (not_131_out, OP6);
  not not_132 (not_132_out, OP3);
  not not_133 (not_133_out, OP2);
  not not_134 (not_134_out, F25);
  not not_135 (not_135_out, F14);
  not not_136 (not_136_out, F13);
  not not_137 (not_137_out, F12);
  not not_138 (not_138_out, OP6);
  not not_139 (not_139_out, OP3);
  not not_140 (not_140_out, OP2);
  not not_141 (not_141_out, F30);
  not not_142 (not_142_out, F25);
  not not_143 (not_143_out, OP6);
  not not_144 (not_144_out, OP3);
  not not_145 (not_145_out, OP2);
  not not_146 (not_146_out, F30);
  not not_147 (not_147_out, F25);
  not not_148 (not_148_out, F14);
  not not_149 (not_149_out, OP6);
  not not_150 (not_150_out, OP3);
  not not_151 (not_151_out, OP2);
  not not_152 (not_152_out, F14);
  not not_153 (not_153_out, F13);
  not not_154 (not_154_out, F12);
  not not_155 (not_155_out, OP6);
  not not_156 (not_156_out, OP5);
  not not_157 (not_157_out, OP3);
  not not_158 (not_158_out, OP2);
  not not_159 (not_159_out, OP6);
  not not_160 (not_160_out, OP5);
  not not_161 (not_161_out, OP3);
  not not_162 (not_162_out, OP2);
  not not_163 (not_163_out, F14);
  not not_164 (not_164_out, F12);
  not not_165 (not_165_out, OP6);
  not not_166 (not_166_out, OP5);
  not not_167 (not_167_out, OP4);
  not not_168 (not_168_out, OP3);
  not not_169 (not_169_out, OP2);
  not not_170 (not_170_out, F14);
  not not_171 (not_171_out, F12);
  not not_172 (not_172_out, OP6);
  not not_173 (not_173_out, OP4);
  not not_174 (not_174_out, OP3);
  not not_175 (not_175_out, OP2);
  not not_176 (not_176_out, F14);
  not not_177 (not_177_out, F13);
  not not_178 (not_178_out, F12);
  not not_179 (not_179_out, OP4);
  not not_180 (not_180_out, OP3);
  not not_181 (not_181_out, OP2);
  not not_182 (not_182_out, F14);
  not not_183 (not_183_out, F13);
  not not_184 (not_184_out, OP4);
  not not_185 (not_185_out, OP3);
  not not_186 (not_186_out, OP2);
  not not_187 (not_187_out, F14);
  not not_188 (not_188_out, F13);
  not not_189 (not_189_out, F12);
  not not_190 (not_190_out, OP4);
  not not_191 (not_191_out, OP3);
  not not_192 (not_192_out, OP3);
  not not_193 (not_193_out, OP2);
  not not_194 (not_194_out, F14);
  not not_195 (not_195_out, OP6);
  not not_196 (not_196_out, OP5);
  not not_197 (not_197_out, OP3);
  not not_198 (not_198_out, OP2);
  not not_199 (not_199_out, F14);
  not not_200 (not_200_out, F13);
  not not_201 (not_201_out, F12);
  not not_202 (not_202_out, OP6);
  not not_203 (not_203_out, OP4);
  not not_204 (not_204_out, OP3);
  not not_205 (not_205_out, OP2);
  not not_206 (not_206_out, OP4);
  not not_207 (not_207_out, OP3);
  not not_208 (not_208_out, OP2);
  not not_209 (not_209_out, F30);
  not not_210 (not_210_out, F25);
  not not_211 (not_211_out, F12);
  not not_212 (not_212_out, OP6);
  not not_213 (not_213_out, OP3);
  not not_214 (not_214_out, OP2);
  not not_215 (not_215_out, F30);
  not not_216 (not_216_out, F25);
  not not_217 (not_217_out, F14);
  not not_218 (not_218_out, F12);
  not not_219 (not_219_out, OP6);
  not not_220 (not_220_out, OP3);
  not not_221 (not_221_out, OP2);
  not not_222 (not_222_out, F30);
  not not_223 (not_223_out, F25);
  not not_224 (not_224_out, F14);
  not not_225 (not_225_out, OP6);
  not not_226 (not_226_out, OP3);
  not not_227 (not_227_out, OP2);
  not not_228 (not_228_out, F12);
  not not_229 (not_229_out, OP6);
  not not_230 (not_230_out, OP5);
  not not_231 (not_231_out, OP3);
  not not_232 (not_232_out, OP2);
  not not_233 (not_233_out, F13);
  not not_234 (not_234_out, F12);
  not not_235 (not_235_out, OP6);
  not not_236 (not_236_out, OP5);
  not not_237 (not_237_out, OP3);
  not not_238 (not_238_out, OP2);
  not not_239 (not_239_out, F14);
  not not_240 (not_240_out, F12);
  not not_241 (not_241_out, OP6);
  not not_242 (not_242_out, OP5);
  not not_243 (not_243_out, OP3);
  not not_244 (not_244_out, OP2);
  not not_245 (not_245_out, F12);
  not not_246 (not_246_out, OP3);
  not not_247 (not_247_out, OP2);
  not not_248 (not_248_out, F14);
  not not_249 (not_249_out, OP6);
  not not_250 (not_250_out, OP5);
  not not_251 (not_251_out, OP3);
  not not_252 (not_252_out, OP2);
  not not_253 (not_253_out, OP4);
  not not_254 (not_254_out, OP3);
  not not_255 (not_255_out, OP2);
  and and_1 (and_1_out, not_1_out, not_2_out, not_3_out, not_4_out, not_5_out, not_6_out, OP5, OP4, not_7_out, not_8_out);
  and and_2 (and_2_out, not_9_out, not_10_out, F14, F13, F12, not_11_out, OP5, OP4, not_12_out, not_13_out);
  and and_3 (and_3_out, not_14_out, not_15_out, not_16_out, F13, not_17_out, not_18_out, OP5, OP4, not_19_out, not_20_out);
  and and_4 (and_4_out, not_21_out, not_22_out, not_23_out, not_24_out, not_25_out, OP4, not_26_out, not_27_out);
  and and_5 (and_5_out, F14, F13, F12, not_28_out, not_29_out, OP4, not_30_out, not_31_out);
  and and_6 (and_6_out, F14, not_32_out, not_33_out, not_34_out, not_35_out, OP4, not_36_out, not_37_out);
  and and_7 (and_7_out, not_38_out, F13, not_39_out, not_40_out, not_41_out, OP4, not_42_out, not_43_out);
  and and_8 (and_8_out, F30, not_44_out, F14, not_45_out, F12, not_46_out, not_47_out, OP4, not_48_out, not_49_out);
  and and_9 (and_9_out, not_50_out, F13, not_51_out, not_52_out, not_53_out, not_54_out, not_55_out, not_56_out);
  and and_10 (and_10_out, not_57_out, F13, not_58_out, not_59_out, OP5, not_60_out, not_61_out, not_62_out);
  and and_11 (and_11_out, F14, F13, F12, OP6, OP5, OP4, not_63_out, not_64_out);
  and and_12 (and_12_out, not_65_out, not_66_out, not_67_out, not_68_out, OP5, not_69_out, not_70_out, not_71_out);
  and and_13 (and_13_out, F30, not_72_out, not_73_out, not_74_out, not_75_out, not_76_out, OP5, OP4, not_77_out, not_78_out);
  and and_14 (and_14_out, not_79_out, not_80_out, F14, F13, F12, not_81_out, OP5, OP4, not_82_out, not_83_out);
  and and_15 (and_15_out, not_84_out, not_85_out, not_86_out, F13, not_87_out, not_88_out, OP5, OP4, not_89_out, not_90_out);
  and and_16 (and_16_out, F14, F13, F12, not_91_out, not_92_out, OP4, not_93_out, not_94_out);
  and and_17 (and_17_out, not_95_out, F13, not_96_out, not_97_out, not_98_out, OP4, not_99_out, not_100_out);
  and and_18 (and_18_out, not_101_out, not_102_out, F14, not_103_out, F12, not_104_out, not_105_out, OP4, not_106_out, not_107_out);
  and and_19 (and_19_out, not_108_out, not_109_out, not_110_out, OP6, OP5, not_111_out, not_112_out, not_113_out);
  and and_20 (and_20_out, not_114_out, not_115_out, F12, OP6, OP5, not_116_out, not_117_out, not_118_out);
  and and_21 (and_21_out, not_119_out, not_120_out, not_121_out, OP6, OP5, not_122_out, not_123_out, OP2);
  and and_22 (and_22_out, F14, F13, F12, OP6, OP5, OP4, not_124_out, not_125_out);
  and and_23 (and_23_out, not_126_out, not_127_out, not_128_out, not_129_out, not_130_out, not_131_out, OP5, OP4, not_132_out, not_133_out);
  and and_24 (and_24_out, F30, not_134_out, not_135_out, not_136_out, not_137_out, not_138_out, OP5, OP4, not_139_out, not_140_out);
  and and_25 (and_25_out, not_141_out, not_142_out, F14, F13, F12, not_143_out, OP5, OP4, not_144_out, not_145_out);
  and and_26 (and_26_out, not_146_out, not_147_out, not_148_out, F13, F12, not_149_out, OP5, OP4, not_150_out, not_151_out);
  and and_27 (and_27_out, not_152_out, not_153_out, not_154_out, not_155_out, not_156_out, OP4, not_157_out, not_158_out);
  and and_28 (and_28_out, F14, F13, F12, not_159_out, not_160_out, OP4, not_161_out, not_162_out);
  and and_29 (and_29_out, not_163_out, F13, not_164_out, not_165_out, not_166_out, not_167_out, not_168_out, not_169_out);
  and and_30 (and_30_out, not_170_out, F13, not_171_out, not_172_out, OP5, not_173_out, not_174_out, not_175_out);
  and and_31 (and_31_out, not_176_out, not_177_out, not_178_out, OP6, OP5, not_179_out, not_180_out, not_181_out);
  and and_32 (and_32_out, not_182_out, not_183_out, F12, OP6, OP5, not_184_out, not_185_out, not_186_out);
  and and_33 (and_33_out, not_187_out, not_188_out, not_189_out, OP6, OP5, not_190_out, not_191_out, OP2);
  and and_34 (and_34_out, F14, F13, F12, OP6, OP5, OP4, not_192_out, not_193_out);
  and and_35 (and_35_out, not_194_out, F13, F12, not_195_out, not_196_out, OP4, not_197_out, not_198_out);
  and and_36 (and_36_out, not_199_out, not_200_out, not_201_out, not_202_out, OP5, not_203_out, not_204_out, not_205_out);
  and and_37 (and_37_out, F14, F13, F12, OP6, OP5, not_206_out, not_207_out, not_208_out);
  and and_38 (and_38_out, not_209_out, not_210_out, F14, F13, not_211_out, not_212_out, OP5, OP4, not_213_out, not_214_out);
  and and_39 (and_39_out, not_215_out, not_216_out, not_217_out, F13, not_218_out, not_219_out, OP5, OP4, not_220_out, not_221_out);
  and and_40 (and_40_out, not_222_out, not_223_out, not_224_out, F13, F12, not_225_out, OP5, OP4, not_226_out, not_227_out);
  and and_41 (and_41_out, F14, F13, not_228_out, not_229_out, not_230_out, OP4, not_231_out, not_232_out);
  and and_42 (and_42_out, F14, not_233_out, not_234_out, not_235_out, not_236_out, OP4, not_237_out, not_238_out);
  and and_43 (and_43_out, not_239_out, F13, not_240_out, not_241_out, not_242_out, OP4, not_243_out, not_244_out);
  and and_44 (and_44_out, F14, F13, not_245_out, OP6, OP5, OP4, not_246_out, not_247_out);
  and and_45 (and_45_out, not_248_out, F13, F12, not_249_out, not_250_out, OP4, not_251_out, not_252_out);
  and and_46 (and_46_out, F14, F13, F12, OP6, OP5, not_253_out, not_254_out, not_255_out);
  or or_1 (S0, and_1_out, and_2_out, and_3_out, and_4_out, and_5_out, and_6_out, and_7_out, and_8_out, and_9_out, and_10_out, and_11_out, and_12_out);
  or or_2 (S1, and_13_out, and_14_out, and_15_out, and_16_out, and_17_out, and_18_out, and_19_out, and_20_out, and_21_out, and_22_out);
  or or_3 (S2, and_23_out, and_24_out, and_25_out, and_26_out, and_27_out, and_28_out, and_29_out, and_30_out, and_31_out, and_32_out, and_33_out, and_34_out, and_35_out, and_36_out, and_37_out);
  or or_4 (S3, and_38_out, and_39_out, and_40_out, and_41_out, and_42_out, and_43_out, and_44_out, and_45_out, and_46_out);
endmodule

// 控制信号生成
module \控制信号自动生成  (
  input  OP2,
  input  OP3,
  input  OP4,
  input  OP5,
  input  OP6,
  input  F12,
  input  F13,
  input  F14,
  input  F25,
  input  F30,
  output MemToReg,
  output csr,
  output user1,
  output bgeu,
  output user2,
  output MemWrite,
  output dasb,
  output ALU_SRC,
  output RegWrite,
  output ecall,
  output S_Type,
  output BEQ,
  output BNE,
  output JALR,
  output JAL
);

  wire and_3_out, and_4_out, and_5_out, and_6_out, and_7_out, and_8_out, and_9_out, and_10_out, and_11_out,
       and_12_out, and_13_out, and_14_out, and_15_out, and_16_out, and_17_out, and_18_out, and_19_out,
       and_20_out, and_21_out, and_22_out, and_23_out, and_24_out, and_25_out, and_27_out, and_28_out,
       and_29_out, and_30_out, and_31_out, and_32_out, and_33_out, and_34_out, and_35_out, and_36_out,
       and_37_out, and_38_out, and_41_out, and_42_out, and_43_out, and_44_out, and_45_out, and_46_out,
       and_47_out, and_48_out, and_49_out, and_50_out, and_51_out, and_52_out, and_53_out, and_54_out,
       and_55_out, and_56_out, and_57_out, not_1_out, not_2_out, not_3_out, not_4_out, not_5_out, not_6_out,
       not_7_out, not_8_out, not_9_out, not_10_out, not_11_out, not_12_out, not_13_out, not_14_out,
       not_15_out, not_16_out, not_17_out, not_18_out, not_19_out, not_20_out, not_21_out, not_22_out,
       not_23_out, not_24_out, not_25_out, not_26_out, not_27_out, not_28_out, not_29_out, not_30_out,
       not_31_out, not_32_out, not_33_out, not_34_out, not_35_out, not_36_out, not_37_out, not_38_out,
       not_39_out, not_40_out, not_41_out, not_42_out, not_43_out, not_44_out, not_45_out, not_46_out,
       not_47_out, not_48_out, not_49_out, not_50_out, not_51_out, not_52_out, not_53_out, not_54_out,
       not_55_out, not_56_out, not_57_out, not_58_out, not_59_out, not_60_out, not_61_out, not_62_out,
       not_63_out, not_64_out, not_65_out, not_66_out, not_67_out, not_68_out, not_69_out, not_70_out,
       not_71_out, not_72_out, not_73_out, not_74_out, not_75_out, not_76_out, not_77_out, not_78_out,
       not_79_out, not_80_out, not_81_out, not_82_out, not_83_out, not_84_out, not_85_out, not_86_out,
       not_87_out, not_88_out, not_89_out, not_90_out, not_91_out, not_92_out, not_93_out, not_94_out,
       not_95_out, not_96_out, not_97_out, not_98_out, not_99_out, not_100_out, not_101_out, not_102_out,
       not_103_out, not_104_out, not_105_out, not_106_out, not_107_out, not_108_out, not_109_out,
       not_110_out, not_111_out, not_112_out, not_113_out, not_114_out, not_115_out, not_116_out,
       not_117_out, not_118_out, not_119_out, not_120_out, not_121_out, not_122_out, not_123_out,
       not_124_out, not_125_out, not_126_out, not_127_out, not_128_out, not_129_out, not_130_out,
       not_131_out, not_132_out, not_133_out, not_134_out, not_135_out, not_136_out, not_137_out,
       not_138_out, not_139_out, not_140_out, not_141_out, not_142_out, not_143_out, not_144_out,
       not_145_out, not_146_out, not_147_out, not_148_out, not_149_out, not_150_out, not_151_out,
       not_152_out, not_153_out, not_154_out, not_155_out, not_156_out, not_157_out, not_158_out,
       not_159_out, not_160_out, not_161_out, not_162_out, not_163_out, not_164_out, not_165_out,
       not_166_out, not_167_out, not_168_out, not_169_out, not_170_out, not_171_out, not_172_out,
       not_173_out, not_174_out, not_175_out, not_176_out, not_177_out, not_178_out, not_179_out,
       not_180_out, not_181_out, not_182_out, not_183_out, not_184_out, not_185_out, not_186_out,
       not_187_out, not_188_out, not_189_out, not_190_out, not_191_out, not_192_out, not_193_out,
       not_194_out, not_195_out, not_196_out, not_197_out, not_198_out, not_199_out, not_200_out,
       not_201_out, not_202_out, not_203_out, not_204_out, not_205_out, not_206_out, not_207_out,
       not_208_out, not_209_out, not_210_out, not_211_out, not_212_out, not_213_out, not_214_out,
       not_215_out, not_216_out, not_217_out, not_218_out, not_219_out, not_220_out, not_221_out,
       not_222_out, not_223_out, not_224_out, not_225_out, not_226_out, not_227_out, not_228_out,
       not_229_out, not_230_out, not_231_out, not_232_out, not_233_out, not_234_out, not_235_out,
       not_236_out, not_237_out, not_238_out, not_239_out, not_240_out, not_241_out, not_242_out,
       not_243_out, not_244_out, not_245_out, not_246_out, not_247_out, not_248_out, not_249_out,
       not_250_out, not_251_out, not_252_out, not_253_out, not_254_out, not_255_out, not_256_out,
       not_257_out, not_258_out, not_259_out, not_260_out, not_261_out, not_262_out, not_263_out,
       not_264_out, not_265_out, not_266_out, not_267_out, not_268_out, not_269_out, not_270_out,
       not_271_out, not_272_out, not_273_out, not_274_out, not_275_out, not_276_out, not_277_out,
       not_278_out, not_279_out, not_280_out, not_281_out, not_282_out, not_283_out, not_284_out,
       not_285_out, not_286_out, not_287_out, not_288_out, not_289_out, not_290_out, not_291_out,
       not_292_out, not_293_out, not_294_out, not_295_out, not_296_out, not_297_out, not_298_out,
       not_299_out, not_300_out, not_301_out, not_302_out, not_303_out, not_304_out, not_305_out,
       not_306_out, not_307_out, not_308_out, not_309_out, not_310_out, not_311_out, not_312_out,
       not_313_out, not_314_out, not_315_out, not_316_out, not_317_out, not_318_out, not_319_out,
       not_320_out, not_321_out, not_322_out, not_323_out, not_324_out, not_325_out, not_326_out,
       not_327_out, not_328_out, not_329_out, not_330_out, not_331_out, not_332_out, not_333_out,
       not_334_out, not_335_out, not_336_out, not_337_out, not_338_out, not_339_out, not_340_out,
       not_341_out, not_342_out, not_343_out, not_344_out, not_345_out, not_346_out, not_347_out,
       not_348_out, not_349_out;

  not not_1 (not_1_out, OP2);
  not not_2 (not_2_out, OP3);
  not not_3 (not_3_out, OP4);
  not not_4 (not_4_out, OP5);
  not not_5 (not_5_out, OP6);
  not not_6 (not_6_out, F12);
  not not_7 (not_7_out, F14);
  not not_8 (not_8_out, OP2);
  not not_9 (not_9_out, OP3);
  not not_10 (not_10_out, F30);
  not not_11 (not_11_out, F25);
  not not_12 (not_12_out, F14);
  not not_13 (not_13_out, F13);
  not not_14 (not_14_out, F12);
  not not_15 (not_15_out, OP6);
  not not_16 (not_16_out, OP3);
  not not_17 (not_17_out, OP2);
  not not_18 (not_18_out, F25);
  not not_19 (not_19_out, F14);
  not not_20 (not_20_out, F13);
  not not_21 (not_21_out, F12);
  not not_22 (not_22_out, OP6);
  not not_23 (not_23_out, OP3);
  not not_24 (not_24_out, OP2);
  not not_25 (not_25_out, F30);
  not not_26 (not_26_out, F25);
  not not_27 (not_27_out, OP6);
  not not_28 (not_28_out, OP3);
  not not_29 (not_29_out, OP2);
  not not_30 (not_30_out, F30);
  not not_31 (not_31_out, F25);
  not not_32 (not_32_out, F12);
  not not_33 (not_33_out, OP6);
  not not_34 (not_34_out, OP3);
  not not_35 (not_35_out, OP2);
  not not_36 (not_36_out, F30);
  not not_37 (not_37_out, F25);
  not not_38 (not_38_out, F14);
  not not_39 (not_39_out, F12);
  not not_40 (not_40_out, OP6);
  not not_41 (not_41_out, OP3);
  not not_42 (not_42_out, OP2);
  not not_43 (not_43_out, F30);
  not not_44 (not_44_out, F25);
  not not_45 (not_45_out, F14);
  not not_46 (not_46_out, OP6);
  not not_47 (not_47_out, OP3);
  not not_48 (not_48_out, OP2);
  not not_49 (not_49_out, F14);
  not not_50 (not_50_out, F13);
  not not_51 (not_51_out, F12);
  not not_52 (not_52_out, OP6);
  not not_53 (not_53_out, OP5);
  not not_54 (not_54_out, OP3);
  not not_55 (not_55_out, OP2);
  not not_56 (not_56_out, OP6);
  not not_57 (not_57_out, OP5);
  not not_58 (not_58_out, OP3);
  not not_59 (not_59_out, OP2);
  not not_60 (not_60_out, F12);
  not not_61 (not_61_out, OP6);
  not not_62 (not_62_out, OP5);
  not not_63 (not_63_out, OP3);
  not not_64 (not_64_out, OP2);
  not not_65 (not_65_out, F13);
  not not_66 (not_66_out, F12);
  not not_67 (not_67_out, OP6);
  not not_68 (not_68_out, OP5);
  not not_69 (not_69_out, OP3);
  not not_70 (not_70_out, OP2);
  not not_71 (not_71_out, F14);
  not not_72 (not_72_out, F12);
  not not_73 (not_73_out, OP6);
  not not_74 (not_74_out, OP5);
  not not_75 (not_75_out, OP3);
  not not_76 (not_76_out, OP2);
  not not_77 (not_77_out, F30);
  not not_78 (not_78_out, F25);
  not not_79 (not_79_out, F14);
  not not_80 (not_80_out, F13);
  not not_81 (not_81_out, OP6);
  not not_82 (not_82_out, OP5);
  not not_83 (not_83_out, OP3);
  not not_84 (not_84_out, OP2);
  not not_85 (not_85_out, F30);
  not not_86 (not_86_out, F25);
  not not_87 (not_87_out, F13);
  not not_88 (not_88_out, OP6);
  not not_89 (not_89_out, OP5);
  not not_90 (not_90_out, OP3);
  not not_91 (not_91_out, OP2);
  not not_92 (not_92_out, F25);
  not not_93 (not_93_out, F13);
  not not_94 (not_94_out, OP6);
  not not_95 (not_95_out, OP5);
  not not_96 (not_96_out, OP3);
  not not_97 (not_97_out, OP2);
  not not_98 (not_98_out, F14);
  not not_99 (not_99_out, F12);
  not not_100 (not_100_out, OP6);
  not not_101 (not_101_out, OP5);
  not not_102 (not_102_out, OP4);
  not not_103 (not_103_out, OP3);
  not not_104 (not_104_out, OP2);
  not not_105 (not_105_out, F14);
  not not_106 (not_106_out, F12);
  not not_107 (not_107_out, OP6);
  not not_108 (not_108_out, OP4);
  not not_109 (not_109_out, OP3);
  not not_110 (not_110_out, OP2);
  not not_111 (not_111_out, F14);
  not not_112 (not_112_out, F13);
  not not_113 (not_113_out, F12);
  not not_114 (not_114_out, OP4);
  not not_115 (not_115_out, OP3);
  not not_116 (not_116_out, OP2);
  not not_117 (not_117_out, F14);
  not not_118 (not_118_out, F13);
  not not_119 (not_119_out, OP4);
  not not_120 (not_120_out, OP3);
  not not_121 (not_121_out, OP2);
  not not_122 (not_122_out, F14);
  not not_123 (not_123_out, F13);
  not not_124 (not_124_out, F12);
  not not_125 (not_125_out, OP4);
  not not_126 (not_126_out, OP3);
  not not_127 (not_127_out, F30);
  not not_128 (not_128_out, F25);
  not not_129 (not_129_out, F14);
  not not_130 (not_130_out, F13);
  not not_131 (not_131_out, OP6);
  not not_132 (not_132_out, OP3);
  not not_133 (not_133_out, OP2);
  not not_134 (not_134_out, F14);
  not not_135 (not_135_out, OP6);
  not not_136 (not_136_out, OP5);
  not not_137 (not_137_out, OP3);
  not not_138 (not_138_out, OP2);
  not not_139 (not_139_out, F14);
  not not_140 (not_140_out, F13);
  not not_141 (not_141_out, F12);
  not not_142 (not_142_out, OP6);
  not not_143 (not_143_out, OP4);
  not not_144 (not_144_out, OP3);
  not not_145 (not_145_out, OP2);
  not not_146 (not_146_out, OP4);
  not not_147 (not_147_out, OP3);
  not not_148 (not_148_out, OP2);
  not not_149 (not_149_out, OP2);
  not not_150 (not_150_out, OP3);
  not not_151 (not_151_out, OP4);
  not not_152 (not_152_out, F30);
  not not_153 (not_153_out, F25);
  not not_154 (not_154_out, F14);
  not not_155 (not_155_out, F13);
  not not_156 (not_156_out, F12);
  not not_157 (not_157_out, OP6);
  not not_158 (not_158_out, OP3);
  not not_159 (not_159_out, OP2);
  not not_160 (not_160_out, F25);
  not not_161 (not_161_out, F14);
  not not_162 (not_162_out, F13);
  not not_163 (not_163_out, F12);
  not not_164 (not_164_out, OP6);
  not not_165 (not_165_out, OP3);
  not not_166 (not_166_out, OP2);
  not not_167 (not_167_out, F30);
  not not_168 (not_168_out, F25);
  not not_169 (not_169_out, OP6);
  not not_170 (not_170_out, OP3);
  not not_171 (not_171_out, OP2);
  not not_172 (not_172_out, F30);
  not not_173 (not_173_out, F25);
  not not_174 (not_174_out, F12);
  not not_175 (not_175_out, OP6);
  not not_176 (not_176_out, OP3);
  not not_177 (not_177_out, OP2);
  not not_178 (not_178_out, F30);
  not not_179 (not_179_out, F25);
  not not_180 (not_180_out, F14);
  not not_181 (not_181_out, F12);
  not not_182 (not_182_out, OP6);
  not not_183 (not_183_out, OP3);
  not not_184 (not_184_out, OP2);
  not not_185 (not_185_out, F30);
  not not_186 (not_186_out, F25);
  not not_187 (not_187_out, F14);
  not not_188 (not_188_out, OP6);
  not not_189 (not_189_out, OP3);
  not not_190 (not_190_out, OP2);
  not not_191 (not_191_out, F14);
  not not_192 (not_192_out, F12);
  not not_193 (not_193_out, OP6);
  not not_194 (not_194_out, OP4);
  not not_195 (not_195_out, OP3);
  not not_196 (not_196_out, OP2);
  not not_197 (not_197_out, F14);
  not not_198 (not_198_out, F13);
  not not_199 (not_199_out, F12);
  not not_200 (not_200_out, OP4);
  not not_201 (not_201_out, OP3);
  not not_202 (not_202_out, OP2);
  not not_203 (not_203_out, F14);
  not not_204 (not_204_out, F13);
  not not_205 (not_205_out, OP4);
  not not_206 (not_206_out, OP3);
  not not_207 (not_207_out, OP2);
  not not_208 (not_208_out, F30);
  not not_209 (not_209_out, F25);
  not not_210 (not_210_out, F14);
  not not_211 (not_211_out, F13);
  not not_212 (not_212_out, OP6);
  not not_213 (not_213_out, OP3);
  not not_214 (not_214_out, OP2);
  not not_215 (not_215_out, F14);
  not not_216 (not_216_out, F13);
  not not_217 (not_217_out, F12);
  not not_218 (not_218_out, OP6);
  not not_219 (not_219_out, OP4);
  not not_220 (not_220_out, OP3);
  not not_221 (not_221_out, OP2);
  not not_222 (not_222_out, OP4);
  not not_223 (not_223_out, OP3);
  not not_224 (not_224_out, OP2);
  not not_225 (not_225_out, OP2);
  not not_226 (not_226_out, OP3);
  not not_227 (not_227_out, OP4);
  not not_228 (not_228_out, OP6);
  not not_229 (not_229_out, F12);
  not not_230 (not_230_out, F14);
  not not_231 (not_231_out, OP2);
  not not_232 (not_232_out, OP3);
  not not_233 (not_233_out, OP4);
  not not_234 (not_234_out, OP6);
  not not_235 (not_235_out, F12);
  not not_236 (not_236_out, F13);
  not not_237 (not_237_out, F14);
  not not_238 (not_238_out, OP2);
  not not_239 (not_239_out, OP3);
  not not_240 (not_240_out, OP5);
  not not_241 (not_241_out, OP6);
  not not_242 (not_242_out, F12);
  not not_243 (not_243_out, F14);
  not not_244 (not_244_out, OP2);
  not not_245 (not_245_out, OP3);
  not not_246 (not_246_out, OP4);
  not not_247 (not_247_out, OP6);
  not not_248 (not_248_out, F12);
  not not_249 (not_249_out, F14);
  not not_250 (not_250_out, OP2);
  not not_251 (not_251_out, OP3);
  not not_252 (not_252_out, OP5);
  not not_253 (not_253_out, OP6);
  not not_254 (not_254_out, F12);
  not not_255 (not_255_out, OP2);
  not not_256 (not_256_out, OP3);
  not not_257 (not_257_out, OP5);
  not not_258 (not_258_out, OP6);
  not not_259 (not_259_out, F25);
  not not_260 (not_260_out, F30);
  not not_261 (not_261_out, OP2);
  not not_262 (not_262_out, OP3);
  not not_263 (not_263_out, OP5);
  not not_264 (not_264_out, OP6);
  not not_265 (not_265_out, F25);
  not not_266 (not_266_out, OP2);
  not not_267 (not_267_out, OP3);
  not not_268 (not_268_out, OP5);
  not not_269 (not_269_out, OP6);
  not not_270 (not_270_out, OP2);
  not not_271 (not_271_out, OP3);
  not not_272 (not_272_out, OP3);
  not not_273 (not_273_out, OP4);
  not not_274 (not_274_out, F12);
  not not_275 (not_275_out, F13);
  not not_276 (not_276_out, F14);
  not not_277 (not_277_out, OP2);
  not not_278 (not_278_out, OP3);
  not not_279 (not_279_out, OP5);
  not not_280 (not_280_out, OP6);
  not not_281 (not_281_out, F12);
  not not_282 (not_282_out, F14);
  not not_283 (not_283_out, OP2);
  not not_284 (not_284_out, OP3);
  not not_285 (not_285_out, OP5);
  not not_286 (not_286_out, OP6);
  not not_287 (not_287_out, F12);
  not not_288 (not_288_out, OP2);
  not not_289 (not_289_out, OP3);
  not not_290 (not_290_out, OP6);
  not not_291 (not_291_out, F12);
  not not_292 (not_292_out, F13);
  not not_293 (not_293_out, F14);
  not not_294 (not_294_out, F25);
  not not_295 (not_295_out, OP2);
  not not_296 (not_296_out, OP3);
  not not_297 (not_297_out, OP6);
  not not_298 (not_298_out, F14);
  not not_299 (not_299_out, F25);
  not not_300 (not_300_out, F30);
  not not_301 (not_301_out, OP2);
  not not_302 (not_302_out, OP3);
  not not_303 (not_303_out, OP5);
  not not_304 (not_304_out, OP6);
  not not_305 (not_305_out, F25);
  not not_306 (not_306_out, OP2);
  not not_307 (not_307_out, OP3);
  not not_308 (not_308_out, OP5);
  not not_309 (not_309_out, OP6);
  not not_310 (not_310_out, OP2);
  not not_311 (not_311_out, OP3);
  not not_312 (not_312_out, OP6);
  not not_313 (not_313_out, F25);
  not not_314 (not_314_out, F30);
  not not_315 (not_315_out, OP4);
  not not_316 (not_316_out, F12);
  not not_317 (not_317_out, F13);
  not not_318 (not_318_out, F14);
  not not_319 (not_319_out, OP4);
  not not_320 (not_320_out, OP2);
  not not_321 (not_321_out, OP3);
  not not_322 (not_322_out, F12);
  not not_323 (not_323_out, F13);
  not not_324 (not_324_out, F14);
  not not_325 (not_325_out, F25);
  not not_326 (not_326_out, F30);
  not not_327 (not_327_out, OP2);
  not not_328 (not_328_out, OP3);
  not not_329 (not_329_out, OP4);
  not not_330 (not_330_out, OP6);
  not not_331 (not_331_out, F12);
  not not_332 (not_332_out, F14);
  not not_333 (not_333_out, OP2);
  not not_334 (not_334_out, OP3);
  not not_335 (not_335_out, OP4);
  not not_336 (not_336_out, F12);
  not not_337 (not_337_out, F13);
  not not_338 (not_338_out, F14);
  not not_339 (not_339_out, OP2);
  not not_340 (not_340_out, OP3);
  not not_341 (not_341_out, OP4);
  not not_342 (not_342_out, F13);
  not not_343 (not_343_out, F14);
  not not_344 (not_344_out, OP3);
  not not_345 (not_345_out, OP4);
  not not_346 (not_346_out, F12);
  not not_347 (not_347_out, F13);
  not not_348 (not_348_out, F14);
  not not_349 (not_349_out, OP4);
  and and_1 (MemToReg, not_1_out, not_2_out, not_3_out, not_4_out, not_5_out, not_6_out, F13, not_7_out);
  and and_2 (csr, not_8_out, not_9_out, OP4, OP5, OP6, F13, F14);
  and and_3 (and_3_out, not_10_out, not_11_out, not_12_out, not_13_out, not_14_out, not_15_out, OP5, OP4, not_16_out, not_17_out);
  and and_4 (and_4_out, F30, not_18_out, not_19_out, not_20_out, not_21_out, not_22_out, OP5, OP4, not_23_out, not_24_out);
  and and_5 (and_5_out, not_25_out, not_26_out, F14, F13, F12, not_27_out, OP5, OP4, not_28_out, not_29_out);
  and and_6 (and_6_out, not_30_out, not_31_out, F14, F13, not_32_out, not_33_out, OP5, OP4, not_34_out, not_35_out);
  and and_7 (and_7_out, not_36_out, not_37_out, not_38_out, F13, not_39_out, not_40_out, OP5, OP4, not_41_out, not_42_out);
  and and_8 (and_8_out, not_43_out, not_44_out, not_45_out, F13, F12, not_46_out, OP5, OP4, not_47_out, not_48_out);
  and and_9 (and_9_out, not_49_out, not_50_out, not_51_out, not_52_out, not_53_out, OP4, not_54_out, not_55_out);
  and and_10 (and_10_out, F14, F13, F12, not_56_out, not_57_out, OP4, not_58_out, not_59_out);
  and and_11 (and_11_out, F14, F13, not_60_out, not_61_out, not_62_out, OP4, not_63_out, not_64_out);
  and and_12 (and_12_out, F14, not_65_out, not_66_out, not_67_out, not_68_out, OP4, not_69_out, not_70_out);
  and and_13 (and_13_out, not_71_out, F13, not_72_out, not_73_out, not_74_out, OP4, not_75_out, not_76_out);
  and and_14 (and_14_out, not_77_out, not_78_out, not_79_out, not_80_out, F12, not_81_out, not_82_out, OP4, not_83_out, not_84_out);
  and and_15 (and_15_out, not_85_out, not_86_out, F14, not_87_out, F12, not_88_out, not_89_out, OP4, not_90_out, not_91_out);
  and and_16 (and_16_out, F30, not_92_out, F14, not_93_out, F12, not_94_out, not_95_out, OP4, not_96_out, not_97_out);
  and and_17 (and_17_out, not_98_out, F13, not_99_out, not_100_out, not_101_out, not_102_out, not_103_out, not_104_out);
  and and_18 (and_18_out, not_105_out, F13, not_106_out, not_107_out, OP5, not_108_out, not_109_out, not_110_out);
  and and_19 (and_19_out, not_111_out, not_112_out, not_113_out, OP6, OP5, not_114_out, not_115_out, not_116_out);
  and and_20 (and_20_out, not_117_out, not_118_out, F12, OP6, OP5, not_119_out, not_120_out, not_121_out);
  and and_21 (and_21_out, not_122_out, not_123_out, not_124_out, OP6, OP5, not_125_out, not_126_out, OP2);
  and and_22 (and_22_out, not_127_out, not_128_out, not_129_out, not_130_out, F12, not_131_out, OP5, OP4, not_132_out, not_133_out);
  and and_23 (and_23_out, not_134_out, F13, F12, not_135_out, not_136_out, OP4, not_137_out, not_138_out);
  and and_24 (and_24_out, not_139_out, not_140_out, not_141_out, not_142_out, OP5, not_143_out, not_144_out, not_145_out);
  and and_25 (and_25_out, F14, F13, F12, OP6, OP5, not_146_out, not_147_out, not_148_out);
  and and_26 (bgeu, not_149_out, not_150_out, not_151_out, OP5, OP6, F12, F13, F14);
  and and_27 (and_27_out, not_152_out, not_153_out, not_154_out, not_155_out, not_156_out, not_157_out, OP5, OP4, not_158_out, not_159_out);
  and and_28 (and_28_out, F30, not_160_out, not_161_out, not_162_out, not_163_out, not_164_out, OP5, OP4, not_165_out, not_166_out);
  and and_29 (and_29_out, not_167_out, not_168_out, F14, F13, F12, not_169_out, OP5, OP4, not_170_out, not_171_out);
  and and_30 (and_30_out, not_172_out, not_173_out, F14, F13, not_174_out, not_175_out, OP5, OP4, not_176_out, not_177_out);
  and and_31 (and_31_out, not_178_out, not_179_out, not_180_out, F13, not_181_out, not_182_out, OP5, OP4, not_183_out, not_184_out);
  and and_32 (and_32_out, not_185_out, not_186_out, not_187_out, F13, F12, not_188_out, OP5, OP4, not_189_out, not_190_out);
  and and_33 (and_33_out, not_191_out, F13, not_192_out, not_193_out, OP5, not_194_out, not_195_out, not_196_out);
  and and_34 (and_34_out, not_197_out, not_198_out, not_199_out, OP6, OP5, not_200_out, not_201_out, not_202_out);
  and and_35 (and_35_out, not_203_out, not_204_out, F12, OP6, OP5, not_205_out, not_206_out, not_207_out);
  and and_36 (and_36_out, not_208_out, not_209_out, not_210_out, not_211_out, F12, not_212_out, OP5, OP4, not_213_out, not_214_out);
  and and_37 (and_37_out, not_215_out, not_216_out, not_217_out, not_218_out, OP5, not_219_out, not_220_out, not_221_out);
  and and_38 (and_38_out, F14, F13, F12, OP6, OP5, not_222_out, not_223_out, not_224_out);
  and and_39 (MemWrite, not_225_out, not_226_out, not_227_out, OP5, not_228_out, not_229_out, not_230_out);
  and and_40 (dasb, not_231_out, not_232_out, not_233_out, OP5, not_234_out, not_235_out, not_236_out, not_237_out);
  and and_41 (and_41_out, not_238_out, not_239_out, not_240_out, not_241_out, not_242_out, F13, not_243_out);
  and and_42 (and_42_out, not_244_out, not_245_out, not_246_out, OP5, not_247_out, not_248_out, not_249_out);
  and and_43 (and_43_out, not_250_out, not_251_out, OP4, not_252_out, not_253_out, not_254_out);
  and and_44 (and_44_out, not_255_out, not_256_out, OP4, not_257_out, not_258_out, not_259_out, not_260_out);
  and and_45 (and_45_out, not_261_out, not_262_out, OP4, not_263_out, not_264_out, F14, not_265_out);
  and and_46 (and_46_out, not_266_out, not_267_out, OP4, not_268_out, not_269_out, F13);
  and and_47 (and_47_out, not_270_out, not_271_out, OP4, OP5, OP6, F13, F14);
  and and_48 (and_48_out, OP2, not_272_out, not_273_out, OP5, OP6, not_274_out, not_275_out, not_276_out);
  and and_49 (and_49_out, not_277_out, not_278_out, not_279_out, not_280_out, not_281_out, F13, not_282_out);
  and and_50 (and_50_out, not_283_out, not_284_out, OP4, not_285_out, not_286_out, not_287_out);
  and and_51 (and_51_out, not_288_out, not_289_out, OP4, not_290_out, not_291_out, not_292_out, not_293_out, not_294_out);
  and and_52 (and_52_out, not_295_out, not_296_out, OP4, not_297_out, not_298_out, not_299_out, not_300_out);
  and and_53 (and_53_out, not_301_out, not_302_out, OP4, not_303_out, not_304_out, F14, not_305_out);
  and and_54 (and_54_out, not_306_out, not_307_out, OP4, not_308_out, not_309_out, F13);
  and and_55 (and_55_out, not_310_out, not_311_out, OP4, not_312_out, F13, not_313_out, not_314_out);
  and and_56 (and_56_out, OP2, not_315_out, OP5, OP6, not_316_out, not_317_out, not_318_out);
  and and_57 (and_57_out, OP2, OP3, not_319_out, OP5, OP6);
  and and_58 (ecall, not_320_out, not_321_out, OP4, OP5, OP6, not_322_out, not_323_out, not_324_out, not_325_out, not_326_out);
  and and_59 (S_Type, not_327_out, not_328_out, not_329_out, OP5, not_330_out, not_331_out, not_332_out);
  and and_60 (BEQ, not_333_out, not_334_out, not_335_out, OP5, OP6, not_336_out, not_337_out, not_338_out);
  and and_61 (BNE, not_339_out, not_340_out, not_341_out, OP5, OP6, F12, not_342_out, not_343_out);
  and and_62 (JALR, OP2, not_344_out, not_345_out, OP5, OP6, not_346_out, not_347_out, not_348_out);
  and and_63 (JAL, OP2, OP3, not_349_out, OP5, OP6);
  or or_1 (user2, and_27_out, and_28_out, and_29_out, and_30_out, and_31_out, and_32_out, and_33_out, and_34_out, and_35_out, and_36_out, and_37_out, and_38_out);
  or or_2 (ALU_SRC, and_41_out, and_42_out, and_43_out, and_44_out, and_45_out, and_46_out, and_47_out, and_48_out);
  or or_3 (RegWrite, and_49_out, and_50_out, and_51_out, and_52_out, and_53_out, and_54_out, and_55_out, and_56_out, and_57_out);
  or or_4 (user1, and_3_out, and_4_out, and_5_out, and_6_out, and_7_out, and_8_out, and_9_out, and_10_out, and_11_out, and_12_out, and_13_out, and_14_out, and_15_out, and_16_out, and_17_out, and_18_out, and_19_out, and_20_out, and_21_out, and_22_out, and_23_out, and_24_out, and_25_out);
endmodule

// ALU
module ALU (
  input  [31:0] X,
  input  [31:0] Y,
  input  [3:0] AluOP,
  output out_4,
  output Equal,
  output out_6,
  output [31:0] Result,
  output [31:0] Result_2
);

  wire [0:0] comparator_1_lt, comparator_2_lt;
  wire [31:0] adder_1_out, AND_out, divider_1_out, divider_1_rem, multiplier_1_cout, multiplier_1_out,
       NOR_out, OR_out, shifter_1_out, shifter_2_out, shifter_3_out, subtractor_1_out, XOR_out;

  assign AND_out = X & Y;  // AND_Gate AND, 32 bits wide
  assign OR_out = X | Y;  // OR_Gate OR, 32 bits wide
  Shifter #(.width(32), .shift("ll")) shifter_1 (.in(X), .\dist (Y[4:0]), .out(shifter_1_out));
  Shifter #(.width(32), .shift("ar")) shifter_2 (.in(X), .\dist (Y[4:0]), .out(shifter_2_out));
  Shifter #(.width(32), .shift("lr")) shifter_3 (.in(X), .\dist (Y[4:0]), .out(shifter_3_out));
  Multiplier #(.width(32)) multiplier_1 (.a(X), .b(Y), .out(multiplier_1_out), .cout(multiplier_1_cout));  // open: cin
  Divider #(.width(32)) divider_1 (.a(X), .b(Y), .out(divider_1_out), .rem(divider_1_rem));  // open: upper
  Adder #(.width(32)) adder_1 (.a(X), .b(Y), .out(adder_1_out));  // open: cin, cout
  Subtractor #(.width(32)) subtractor_1 (.a(X), .b(Y), .out(subtractor_1_out));  // open: bin, bout
  assign XOR_out = X ^ Y;  // XOR_Gate XOR, 32 bits wide
  assign NOR_out = ~(X | Y);  // NOR_Gate NOR, 32 bits wide
  Comparator #(.width(32), .mode("twosComplement")) comparator_1 (
    .a(X), .b(Y), .eq(Equal), .lt(comparator_1_lt[0]));  // open: gt
  Comparator #(.width(32), .mode("unsigned")) comparator_2 (.a(X), .b(Y), .lt(comparator_2_lt[0]));  // open: gt, eq
  Multiplexer #(.select(4), .width(32), .disabled("Z"), .enable("false")) multiplexer_1 (
    .in0(shifter_1_out), .in1(shifter_2_out), .in2(shifter_3_out), .in3(multiplier_1_out),
    .in4(divider_1_out), .in5(adder_1_out), .in6(subtractor_1_out), .in7(AND_out), .in8(OR_out),
    .in9(XOR_out), .in10(NOR_out), .in11({{31{1'b0}}, comparator_1_lt[0]}),
    .in12({{31{1'b0}}, comparator_2_lt[0]}), .in13({32{1'b0}}), .in14({32{1'b0}}), .in15({32{1'b0}}),
    .out(Result), .sel(AluOP));
  Multiplexer #(.select(4), .width(32), .disabled("Z"), .enable("false")) multiplexer_2 (
    .in0({32{1'b0}}), .in1({32{1'b0}}), .in2({32{1'b0}}), .in3(multiplier_1_cout), .in4(divider_1_rem),
    .in5({32{1'b0}}), .in6({32{1'b0}}), .in7({32{1'b0}}), .in8({32{1'b0}}), .in9({32{1'b0}}),
    .in10({32{1'b0}}), .in11({32{1'b0}}), .in12({32{1'b0}}), .in13({32{1'b0}}), .in14({32{1'b0}}),
    .in15({32{1'b0}}), .out(Result_2), .sel(AluOP));
  Multiplexer #(.select(4), .width(1), .disabled("Z"), .enable("false")) multiplexer_3 (
    .in0(1'b0), .in1(1'b0), .in2(1'b0), .in3(1'b0), .in4(1'b0), .in5(1'b0), .in6(1'b0), .in7(1'b0),
    .in8(1'b0), .in9(1'b0), .in10(1'b0), .in11(comparator_1_lt[0]), .in12(comparator_2_lt[0]), .in13(1'b0),
    .in14(1'b0), .in15(1'b0), .out(out_6), .sel(AluOP));
  not not_1 (out_4, out_6);

  // Other names for the same wires on the sheet: Result2[31:0] = Result_2; S[3:0] = AluOP; tunnel = out_6;
  //   tunnel_t = out_4

  // Notes on the sheet:
  //   不要改变此引脚区域内容，也不要改变ALU封装形式
  //   输入引脚
  //   输出引脚
endmodule

module Regifile (
  input  [31:0] Din,
  input  Clk,
  input  WE,
  input  [4:0] R1_num,
  input  [4:0] W_num,
  input  [4:0] R2_num,
  output [31:0] R1,
  output [31:0] R2
);

  // RegisterFile registerfile_1: pin names not known; wires that end beside it: Din, Clk, WE, W_num, R1_num, R2_num, R1, R2
endmodule

module \理想流水线  (
  output RegWrite,
  output MemWrite,
  output [31:0] IF_PC,
  output [31:0] ID_PC,
  output [31:0] EX_PC,
  output [31:0] M_PC,
  output [31:0] WB_PC,
  output [31:0] RDin,
  output [31:0] MDin,
  output [31:0] LedData
);

  wire and_1_out, and_2_out, and_3_out, and_4_out, CLK, clock_1_out, comparator_1_eq, comparator_1_lt,
       comparator_2_eq, d_ff_1_q, equ, ex_mem_1_dasb_2, ex_mem_1_halt_2, ex_mem_1_jal_2, ex_mem_1_jalr_2,
       ex_mem_1_memtoreg_2, ex_mem_1_regwrite_2, ex_mem_1_uret_2, exdasb, execall, exhalt, ge, Go, halt,
       id_ex_1_alusrcb_2, id_ex_1_beq_2, id_ex_1_bgeu_2, id_ex_1_bne_2, id_ex_1_jal_2, id_ex_1_memtoreg_2,
       id_ex_1_memwrite_2, id_ex_1_regwrite_2, id_ex_1_uret_2, idecall, IR1, IR2, IR3, jal, mem_wb_1_halt_2,
       mem_wb_1_jal_2, mem_wb_1_jalr_2, nand_1_out, not_1_out, not_2_out, not_3_out, not_4_out, or_1_out,
       or_2_out, RST, S_type, W1, W2, W3, \单周期硬布线控制器_1_alu_src , \单周期硬布线控制器_1_beq , \单周期硬布线控制器_1_bgeu ,
       \单周期硬布线控制器_1_bne , \单周期硬布线控制器_1_csr , \单周期硬布线控制器_1_dasb , \单周期硬布线控制器_1_jalr , \单周期硬布线控制器_1_memtoreg ,
       \单周期硬布线控制器_1_memwrite , \单周期硬布线控制器_1_regwrite , \单周期硬布线控制器_1_uret ;
  wire [1:0] id_ex_1_jalr_2, mem_wb_1_memtoreg_2;
  wire [3:0] id_ex_1_aluop_2, \单周期硬布线控制器_1_alu_op ;
  wire [4:0] ex_mem_1_rd_a_2, id_ex_1_rd_a_2, multiplexer_2_out, multiplexer_3_out, \写回地址 ;
  wire [11:0] multiplexer_4_out;
  wire [12:0] CNT_num;
  wire [15:0] \LoadUse次数 , \总周期数 , \插入气泡数 , \无条件分支数 , \条件分支成功数 ;
  wire [31:0] \ALU计算结果 , bit_extender_1_out, bit_extender_2_out, bit_extender_3_out, EX_IR, ex_mem_1_pc_4_2,
       ex_mem_1_r2_2, ex_mem_1_res_2, id_ex_1_imm1_2, id_ex_1_imm2_2, id_ex_1_pc_4_2, id_ex_1_r1_2,
       id_ex_1_r2_2, ID_IR, if_id_1_pc_4_2, IF_IR, \jal指令地址 , MEM_IR, mem_wb_1_memdata_2, mem_wb_1_pc_4_2,
       mem_wb_1_res_2, multiplexer_1_out, multiplexer_5_out, multiplexer_6_out, PC_4, ram_1_data,
       regifile_1_r1, regifile_1_r2, shifter_1_out, WB_IR;

  Button \u_总复位  (.out(RST));
  Button _1 (.out(IR1));
  Button _2 (.out(IR2));
  Button _3 (.out(IR3));
  // Probe on \总周期数 
  // Probe on \总周期数 
  Button \u_继续运行  (.out(Go));
  LED #(.active("true")) led_1 (.in(W1));
  LED #(.active("true")) led_2 (.in(W2));
  LED #(.active("true")) led_3 (.in(W3));
  Multiplexer #(.select(2), .width(32), .disabled("Z"), .enable("false")) multiplexer_1 (
    .in0(PC_4), .in1(\ALU计算结果 ), .in2(\jal指令地址 ), .out(multiplexer_1_out), .sel(id_ex_1_jalr_2));  // open: in3
  Hex_Digit_Display hex_digit_display_1 (.value(LedData[31:28]));  // open: dp
  // Probe on IF_PC[19:0]
  // RiscV_Probe riscv_probe_1: pin names not known; wires that end beside it: IF_IR
  Register #(.width(32), .trigger("rising"), .Select("low")) PC (
    .D(multiplexer_1_out), .en(or_1_out), .Q(IF_PC), .clk(CLK), .clr(1'b0), .cs(1'b0), .preset(1'b0));
  or or_1 (or_1_out, not_1_out, Go);
  not not_1 (not_1_out, halt);
  Hex_Digit_Display hex_digit_display_2 (.value(LedData[27:24]));  // open: dp
  Hex_Digit_Display hex_digit_display_3 (.value(LedData[23:20]));  // open: dp
  // Probe on ID_PC[19:0]
  // RiscV_Probe riscv_probe_2: pin names not known; wires that end beside it: ID_IR
  // Probe on IF_PC[11:2]
  Adder #(.width(32)) adder_1 (.a(IF_PC), .b(32'h4), .out(PC_4), .cin(1'b0));  // open: cout
  Hex_Digit_Display hex_digit_display_4 (.value(LedData[15:12]));  // open: dp
  Hex_Digit_Display hex_digit_display_5 (.value(LedData[19:16]));  // open: dp
  // RiscV_Probe riscv_probe_3: pin names not known; wires that end beside it: IF_IR
  Hex_Digit_Display hex_digit_display_6 (.value(LedData[11:8]));  // open: dp
  Hex_Digit_Display hex_digit_display_7 (.value(LedData[7:4]));  // open: dp
  // Probe on EX_PC[19:0]
  // RiscV_Probe riscv_probe_4: pin names not known; wires that end beside it: EX_IR
  ROM #(.addrWidth(10), .dataWidth(32), .Select("high")) rom_1 (.addr(IF_PC[11:2]), .data(IF_IR), .sel(1'b1));
  Hex_Digit_Display hex_digit_display_8 (.value(LedData[3:0]));  // open: dp
  or or_2 (or_2_out, id_ex_1_jalr_2[0], id_ex_1_jalr_2[1]);
  IF_ID if_id_1 (
    .PC(IF_PC), .PC_4(PC_4), .IR(IF_IR), .PC_2(ID_PC), .PC_4_2(if_id_1_pc_4_2), .IR_2(ID_IR), .reset(1'b0),
    .refresh(or_2_out), .en(1'b1), .CLK(CLK));  // open: 预测跳转, 预测跳转_2
  // Probe on \总周期数 
  // Probe on M_PC[19:0]
  // RiscV_Probe riscv_probe_5: pin names not known; wires that end beside it: MEM_IR
  // Probe on \总周期数 
  // Probe on \无条件分支数 
  // Probe on \条件分支成功数 
  // Probe on \插入气泡数 
  // Probe on \LoadUse次数 
  Multiplexer #(.select(1), .width(5), .disabled("Z"), .enable("false")) multiplexer_2 (
    .in0(ID_IR[19:15]), .in1(5'b10001), .out(multiplexer_2_out), .sel(idecall));
  Multiplexer #(.select(1), .width(5), .disabled("Z"), .enable("false")) multiplexer_3 (
    .in0(ID_IR[24:20]), .in1(5'b01010), .out(multiplexer_3_out), .sel(idecall));
  Multiplexer #(.select(1), .width(12), .disabled("Z"), .enable("false")) multiplexer_4 (
    .in0(ID_IR[31:20]), .in1({ID_IR[31:25], ID_IR[11:7]}), .out(multiplexer_4_out), .sel(S_type));
  // Probe on IF_PC[11:0]
  // Probe on WB_PC[19:0]
  // RiscV_Probe riscv_probe_6: pin names not known; wires that end beside it: WB_IR
  \单周期硬布线控制器  \u_单周期硬布线控制器_1  (
    .Funct({ID_IR[30], ID_IR[25], ID_IR[14:12]}), .OP(ID_IR[6:2]), .ALU_OP(\单周期硬布线控制器_1_alu_op ),
    .MemToReg(\单周期硬布线控制器_1_memtoreg ), .MemWrite(\单周期硬布线控制器_1_memwrite ), .ALU_SRC(\单周期硬布线控制器_1_alu_src ),
    .RegWrite(\单周期硬布线控制器_1_regwrite ), .ecall(idecall), .S_type(S_type), .Jalr(\单周期硬布线控制器_1_jalr ),
    .Beq(\单周期硬布线控制器_1_beq ), .JAL(jal), .Bne(\单周期硬布线控制器_1_bne ), .in_3(ID_IR[21]), .uret(\单周期硬布线控制器_1_uret ),
    .bgeu(\单周期硬布线控制器_1_bgeu ), .csr(\单周期硬布线控制器_1_csr ), .dasb(\单周期硬布线控制器_1_dasb ));  // open: user1, user2
  assign bit_extender_1_out = {{20{multiplexer_4_out[11]}}, multiplexer_4_out};  // Bit_Extender bit_extender_1
  assign bit_extender_2_out = {{20{ID_IR[31]}}, {ID_IR[31], ID_IR[7], ID_IR[30:25], ID_IR[11:8]}};  // Bit_Extender bit_extender_2
  assign bit_extender_3_out = {{12{ID_IR[31]}}, {ID_IR[31], ID_IR[19:12], ID_IR[20], ID_IR[30:21]}};  // Bit_Extender bit_extender_3
  // Probe on EX_PC[11:0]
  // Probe on ID_PC[11:0]
  Multiplexer #(.select(1), .width(32), .disabled("Z"), .enable("false")) multiplexer_5 (
    .in0(bit_extender_2_out), .in1(bit_extender_3_out), .out(multiplexer_5_out), .sel(jal));
  // Probe on M_PC[11:0]
  D_Flip_Flop #(.trigger("high"), .Pre_Clr_Positions("LEGACY"), .NegatePresetClear("false"), .enable("true"), .NewFFLayout("false")) d_ff_1 (.Q(d_ff_1_q));  // open: clk, D, Qn, preset, en, reset
  // Probe on 13'hc
  // Probe on WB_PC[11:0]
  Comparator #(.width(13), .mode("twosComplement")) comparator_1 (
    .a(CNT_num), .b(13'hc), .eq(comparator_1_eq), .lt(comparator_1_lt));  // open: gt
  Clock #(.highDuration(1), .lowDuration(1)) clock_1 (.out(clock_1_out));
  Regifile regifile_1 (
    .Din(RDin), .Clk(CLK), .R1(regifile_1_r1), .R2(regifile_1_r2), .WE(RegWrite), .W_num(\写回地址 ),
    .R1_num(multiplexer_2_out), .R2_num(multiplexer_3_out));
  nand nand_1 (nand_1_out, d_ff_1_q, comparator_1_eq);
  Counter #(.width(13), .max('h1fff), .ongoal("stay"), .trigger("rising"), .behavior("old")) counter_1 (
    .count(comparator_1_lt), .Q(CNT_num), .clk(clock_1_out));  // open: load, D, carry, clr, preset
  ID_EX id_ex_1 (
    .Beq(\单周期硬布线控制器_1_beq ), .Bne(\单周期硬布线控制器_1_bne ), .MemToReg(\单周期硬布线控制器_1_memtoreg ),
    .MemWrite(\单周期硬布线控制器_1_memwrite ), .AluSrcB(\单周期硬布线控制器_1_alu_src ), .RegWrite(\单周期硬布线控制器_1_regwrite ),
    .JAL(jal), .JALR(\单周期硬布线控制器_1_jalr ), .URET(\单周期硬布线控制器_1_uret ), .csr(\单周期硬布线控制器_1_csr ),
    .bgeu(\单周期硬布线控制器_1_bgeu ), .S_type(S_type), .dasb(\单周期硬布线控制器_1_dasb ), .AluOP(\单周期硬布线控制器_1_alu_op ),
    .r1(regifile_1_r1), .r2(regifile_1_r2), .rd_a(ID_IR[11:7]), .imm1(bit_extender_1_out),
    .imm2(multiplexer_5_out), .PC(ID_PC), .PC_4(if_id_1_pc_4_2), .IR(ID_IR), .Beq_2(id_ex_1_beq_2),
    .Bne_2(id_ex_1_bne_2), .MemToReg_2(id_ex_1_memtoreg_2), .MemWrite_2(id_ex_1_memwrite_2),
    .AluSrcB_2(id_ex_1_alusrcb_2), .RegWrite_2(id_ex_1_regwrite_2), .JAL_2(id_ex_1_jal_2),
    .JALR_2(id_ex_1_jalr_2[0]), .URET_2(id_ex_1_uret_2), .bgeu_2(id_ex_1_bgeu_2), .dasb_2(exdasb),
    .AluOP_2(id_ex_1_aluop_2), .r1_2(id_ex_1_r1_2), .r2_2(id_ex_1_r2_2), .rd_a_2(id_ex_1_rd_a_2),
    .imm1_2(id_ex_1_imm1_2), .imm2_2(id_ex_1_imm2_2), .PC_2(EX_PC), .PC_4_2(id_ex_1_pc_4_2), .IR_2(EX_IR),
    .reset(1'b0), .refresh(1'b0), .en(1'b1), .CLK(CLK), .ecall(idecall), .ecall_2(execall));  // open: csr_2, S_type_2, r1_forward, r1_forward_2, r2_forward, r2_forward_2, 预测跳转, 预测跳转_2
  assign CLK = nand_1_out ? clock_1_out : 1'bz;  // Controlled_Buffer controlled_buffer_1
  or or_3 (id_ex_1_jalr_2[1], and_2_out, and_3_out, and_1_out, id_ex_1_jal_2);
  Shifter #(.width(32), .shift("ll")) shifter_1 (.in(id_ex_1_imm2_2), .\dist (5'b00001), .out(shifter_1_out));
  Adder #(.width(32)) adder_2 (.a(shifter_1_out), .b(EX_PC), .out(\jal指令地址 ), .cin(1'b0));  // open: cout
  Pull_Resistor #(.pull(1)) pull_resistor_1 (.node(CLK));
  and and_1 (and_1_out, id_ex_1_beq_2, equ);
  Multiplexer #(.select(1), .width(32), .disabled("Z"), .enable("false")) multiplexer_6 (
    .in0(id_ex_1_r2_2), .in1(id_ex_1_imm1_2), .out(multiplexer_6_out), .sel(id_ex_1_alusrcb_2));
  Register #(.width(32), .trigger("rising"), .Select("low")) register_1 (
    .D(id_ex_1_r2_2), .en(and_4_out), .Q(LedData), .clk(CLK), .clr(1'b0), .cs(1'b0), .preset(1'b0));
  not not_2 (not_2_out, halt);
  Counter #(.width(16), .max('hffff), .ongoal("wrap"), .trigger("rising"), .behavior("new")) counter_2 (
    .count(not_2_out), .Q(\总周期数 ), .clk(CLK));  // open: load, D, carry, clr, preset, down
  and and_2 (and_2_out, id_ex_1_bgeu_2, ge);
  and and_3 (and_3_out, not_3_out, id_ex_1_bne_2);
  not not_3 (not_3_out, equ);
  ALU alu_1 (
    .X(id_ex_1_r1_2), .Y(multiplexer_6_out), .AluOP(id_ex_1_aluop_2), .Equal(equ), .Result(\ALU计算结果 ),
    .out_4(ge));  // open: Result_2, out_6
  not not_4 (not_4_out, comparator_2_eq);
  Comparator #(.width(32), .mode("twosComplement")) comparator_2 (
    .a(id_ex_1_r1_2), .b(32'h22), .eq(comparator_2_eq));  // open: gt, lt
  and and_4 (and_4_out, execall, comparator_2_eq);
  and and_5 (exhalt, execall, not_4_out);
  EX_MEM ex_mem_1 (
    .MemToReg(id_ex_1_memtoreg_2), .MemWrite(id_ex_1_memwrite_2), .RegWrite(id_ex_1_regwrite_2),
    .JAL(id_ex_1_jal_2), .JALR(id_ex_1_jalr_2[0]), .URET(id_ex_1_uret_2), .dasb(exdasb), .halt(exhalt),
    .res(\ALU计算结果 ), .rd_a(id_ex_1_rd_a_2), .r2(id_ex_1_r2_2), .PC(EX_PC), .PC_4(id_ex_1_pc_4_2), .IR(EX_IR),
    .MemToReg_2(ex_mem_1_memtoreg_2), .MemWrite_2(MemWrite), .RegWrite_2(ex_mem_1_regwrite_2),
    .JAL_2(ex_mem_1_jal_2), .JALR_2(ex_mem_1_jalr_2), .URET_2(ex_mem_1_uret_2), .dasb_2(ex_mem_1_dasb_2),
    .halt_2(ex_mem_1_halt_2), .res_2(ex_mem_1_res_2), .rd_a_2(ex_mem_1_rd_a_2), .r2_2(ex_mem_1_r2_2),
    .PC_2(M_PC), .PC_4_2(ex_mem_1_pc_4_2), .IR_2(MEM_IR), .reset(1'b0), .refresh(1'b0), .en(1'b1), .CLK(CLK));
  \专门给SB画的电路  \u_专门给sb画的电路_1  (
    .r2(ex_mem_1_r2_2), .addr(ex_mem_1_res_2), .pre_data(ram_1_data), .MDin(MDin), .dasb(ex_mem_1_dasb_2));
  RAM #(.addrWidth(10), .dataWidth(32), .bus("separate"), .Select("high")) ram_1 (
    .addr(ex_mem_1_res_2[11:2]), .din(MDin), .data(ram_1_data), .str(MemWrite), .sel(1'b1), .clk(CLK),
    .ld(1'b1), .clr(1'b0));
  MEM_WB mem_wb_1 (
    .MemToReg(ex_mem_1_memtoreg_2), .RegWrite(ex_mem_1_regwrite_2), .JAL(ex_mem_1_jal_2),
    .JALR(ex_mem_1_jalr_2), .URET(ex_mem_1_uret_2), .dasb(ex_mem_1_dasb_2), .halt(ex_mem_1_halt_2),
    .res(ex_mem_1_res_2), .rd_a(ex_mem_1_rd_a_2), .MemData(ram_1_data), .PC(M_PC), .PC_4(ex_mem_1_pc_4_2),
    .IR(MEM_IR), .MemToReg_2(mem_wb_1_memtoreg_2[0]), .RegWrite_2(RegWrite), .JAL_2(mem_wb_1_jal_2),
    .JALR_2(mem_wb_1_jalr_2), .halt_2(mem_wb_1_halt_2), .res_2(mem_wb_1_res_2), .rd_a_2(\写回地址 ),
    .MemData_2(mem_wb_1_memdata_2), .PC_2(WB_PC), .PC_4_2(mem_wb_1_pc_4_2), .IR_2(WB_IR), .reset(1'b0),
    .refresh(1'b0), .en(1'b1), .CLK(CLK));  // open: URET_2, dasb_2
  or or_4 (mem_wb_1_memtoreg_2[1], mem_wb_1_jal_2, mem_wb_1_jalr_2);
  Multiplexer #(.select(2), .width(32), .disabled("Z"), .enable("false")) multiplexer_7 (
    .in0(mem_wb_1_res_2), .in1(mem_wb_1_memdata_2), .in2(mem_wb_1_pc_4_2), .out(RDin),
    .sel(mem_wb_1_memtoreg_2));  // open: in3
  D_Flip_Flop #(.trigger("rising"), .Pre_Clr_Positions("ABOVE_BELOW"), .NegatePresetClear("false"), .enable("true"), .NewFFLayout("true")) d_ff_2 (
    .clk(mem_wb_1_halt_2), .D(1'b1), .Q(halt), .preset(1'b0), .en(1'b1), .reset(Go));  // open: Qn

  // Other names for the same wires on the sheet: MEM_PC[31:0] = M_PC

  // Notes on the sheet:
  //   中断源
  //   时空图监测，可删除
  //   中断等待指示
  //   选择PC
  //   数码管输出
  //   取指
  //   指令探针
  //   指令存储器
  //   contents of rom_1 (hex, n*v repeats v):
  //   413 493 913 993 46413 14e493 296913 39e993 842023 942223 1242423 1342623 a00893 493 913 993 73
  //   rs1
  //   rs2
  //   I指令
  //   S指令
  //   B指令
  //   J指令
  //   rd
  //   JAL
  //   JALR
  //   URET
  //   bgeu
  //   跳转地址生成
  //   译码
  //   Beq
  //   Bne
  //   MemToReg
  //   MemWrite
  //   AluOP
  //   AluSrcB
  //   RegWrite
  //   控制位
  //   流水调试日志用
  //   暂停节拍，不能为0
  //   用这个时钟源需要去掉电路中的其他时钟源
  //   戳工具置1进入计数暂停模式，ctrl+k时钟自动运行到对应节拍暂停
  //   ctrl+k关闭时钟连续运行，将控制位置零，进入单步调试模式调试
  //   可计数暂停的时钟源
  //   执行
  //   ecall的LED显示
  //   为方便自动评测，需要输出流水线各段保存的PC值，注意是PC不是PC+4，另外ID段寄存器写入信息，Mem段内存写入信息也要输出
  //   实现sb
  //   存储
  //   数据存储器
  //   写回
  //   选择RDin
endmodule

module \气泡流水线  (
  output RegWrite,
  output MemWrite,
  output [31:0] IF_PC,
  output [31:0] ID_PC,
  output [31:0] EX_PC,
  output [31:0] M_PC,
  output [31:0] WB_PC,
  output [31:0] RDin,
  output [31:0] MDin,
  output [31:0] LedData
);

  wire and_1_out, and_2_out, and_3_out, and_4_out, and_5_out, and_6_out, and_8_out, \B型指令分支跳转 , CLK,
       clock_1_out, comparator_1_eq, comparator_1_lt, comparator_2_eq, d_ff_1_q, equ, ex_mem_1_dasb_2,
       ex_mem_1_halt_2, ex_mem_1_jal_2, ex_mem_1_jalr_2, ex_mem_1_memtoreg_2, ex_mem_1_regwrite_2,
       ex_mem_1_uret_2, exdasb, execall, exhalt, ge, Go, halt, id_ex_1_alusrcb_2, id_ex_1_beq_2,
       id_ex_1_bgeu_2, id_ex_1_bne_2, id_ex_1_jal_2, id_ex_1_memtoreg_2, id_ex_1_memwrite_2,
       id_ex_1_regwrite_2, id_ex_1_uret_2, idecall, IR1, IR2, IR3, jal, \J型指令分支跳转 , mem_wb_1_halt_2,
       mem_wb_1_jal_2, mem_wb_1_jalr_2, nand_1_out, not_1_out, not_2_out, not_3_out, not_4_out, not_5_out,
       not_6_out, not_7_out, not_8_out, not_9_out, or_1_out, or_3_out, or_5_out, RST, S_type, W1, W2, W3,
       \单周期硬布线控制器_1_alu_src , \单周期硬布线控制器_1_beq , \单周期硬布线控制器_1_bgeu , \单周期硬布线控制器_1_bne , \单周期硬布线控制器_1_csr ,
       \单周期硬布线控制器_1_dasb , \单周期硬布线控制器_1_jalr , \单周期硬布线控制器_1_memtoreg , \单周期硬布线控制器_1_memwrite ,
       \单周期硬布线控制器_1_regwrite , \单周期硬布线控制器_1_uret , \单周期硬布线控制器_1_user1 , \单周期硬布线控制器_1_user2 , \存在分支 , \清空 ,
       \阻塞 ;
  wire [1:0] id_ex_1_jalr_2, mem_wb_1_memtoreg_2;
  wire [3:0] id_ex_1_aluop_2, \单周期硬布线控制器_1_alu_op ;
  wire [4:0] ex_mem_1_rd_a_2, id_ex_1_rd_a_2, multiplexer_2_out, multiplexer_3_out, \写回地址 ;
  wire [11:0] multiplexer_4_out;
  wire [12:0] CNT_num;
  wire [15:0] \LoadUse次数 , \总周期数 , \插入气泡数 , \无条件分支数 , \条件分支成功数 ;
  wire [31:0] \ALU计算结果 , bit_extender_1_out, bit_extender_2_out, bit_extender_3_out, EX_IR, ex_mem_1_pc_4_2,
       ex_mem_1_r2_2, ex_mem_1_res_2, id_ex_1_imm1_2, id_ex_1_imm2_2, id_ex_1_pc_4_2, id_ex_1_r1_2,
       id_ex_1_r2_2, ID_IR, if_id_1_pc_4_2, IF_IR, \jal指令地址 , MEM_IR, mem_wb_1_memdata_2, mem_wb_1_pc_4_2,
       mem_wb_1_res_2, multiplexer_1_out, multiplexer_5_out, multiplexer_6_out, PC_4, ram_1_data,
       regifile_1_r1, regifile_1_r2, shifter_1_out, WB_IR;

  Button \u_总复位  (.out(RST));
  Button _1 (.out(IR1));
  Button _2 (.out(IR2));
  Button _3 (.out(IR3));
  // Probe on \总周期数 
  // Probe on \总周期数 
  Button \u_继续运行  (.out(Go));
  LED #(.active("true")) led_1 (.in(W1));
  LED #(.active("true")) led_2 (.in(W2));
  LED #(.active("true")) led_3 (.in(W3));
  and and_1 (and_1_out, or_1_out, not_2_out);
  or or_1 (or_1_out, not_1_out, Go);
  not not_1 (not_1_out, halt);
  Hex_Digit_Display hex_digit_display_1 (.value(LedData[31:28]));  // open: dp
  // Probe on IF_PC[19:0]
  // RiscV_Probe riscv_probe_1: pin names not known; wires that end beside it: IF_IR
  Multiplexer #(.select(2), .width(32), .disabled("Z"), .enable("false")) multiplexer_1 (
    .in0(PC_4), .in1(\ALU计算结果 ), .in2(\jal指令地址 ), .out(multiplexer_1_out), .sel(id_ex_1_jalr_2));  // open: in3
  Register #(.width(32), .trigger("rising"), .Select("low")) PC (
    .D(multiplexer_1_out), .en(and_1_out), .Q(IF_PC), .clk(CLK), .clr(1'b0), .cs(1'b0), .preset(1'b0));
  not not_2 (not_2_out, \阻塞 );
  Hex_Digit_Display hex_digit_display_2 (.value(LedData[27:24]));  // open: dp
  Hex_Digit_Display hex_digit_display_3 (.value(LedData[23:20]));  // open: dp
  // Probe on ID_PC[19:0]
  // RiscV_Probe riscv_probe_2: pin names not known; wires that end beside it: ID_IR
  Hex_Digit_Display hex_digit_display_4 (.value(LedData[15:12]));  // open: dp
  Hex_Digit_Display hex_digit_display_5 (.value(LedData[19:16]));  // open: dp
  // RiscV_Probe riscv_probe_3: pin names not known; wires that end beside it: IF_IR
  Adder #(.width(32)) adder_1 (.a(IF_PC), .b(32'h4), .out(PC_4), .cin(1'b0));  // open: cout
  Hex_Digit_Display hex_digit_display_6 (.value(LedData[7:4]));  // open: dp
  Hex_Digit_Display hex_digit_display_7 (.value(LedData[11:8]));  // open: dp
  // Probe on EX_PC[19:0]
  // RiscV_Probe riscv_probe_4: pin names not known; wires that end beside it: EX_IR
  ROM #(.addrWidth(10), .dataWidth(32), .Select("high")) rom_1 (.addr(IF_PC[11:2]), .data(IF_IR), .sel(1'b1));
  Hex_Digit_Display hex_digit_display_8 (.value(LedData[3:0]));  // open: dp
  or or_2 (\存在分支 , id_ex_1_jalr_2[0], id_ex_1_jalr_2[1]);
  IF_ID if_id_1 (
    .PC(IF_PC), .PC_4(PC_4), .IR(IF_IR), .PC_2(ID_PC), .PC_4_2(if_id_1_pc_4_2), .IR_2(ID_IR), .reset(1'b0),
    .refresh(\存在分支 ), .en(and_2_out), .CLK(CLK));  // open: 预测跳转, 预测跳转_2
  and and_2 (and_2_out, or_3_out, not_3_out);
  or or_3 (or_3_out, not_4_out, Go);
  not not_3 (not_3_out, \阻塞 );
  not not_4 (not_4_out, halt);
  // Probe on \总周期数 
  // Probe on M_PC[19:0]
  // RiscV_Probe riscv_probe_5: pin names not known; wires that end beside it: MEM_IR
  // Probe on \总周期数 
  // Probe on \无条件分支数 
  // Probe on \条件分支成功数 
  // Probe on \插入气泡数 
  // Probe on \LoadUse次数 
  Multiplexer #(.select(1), .width(5), .disabled("Z"), .enable("false")) multiplexer_2 (
    .in0(ID_IR[19:15]), .in1(5'b10001), .out(multiplexer_2_out), .sel(idecall));
  Multiplexer #(.select(1), .width(5), .disabled("Z"), .enable("false")) multiplexer_3 (
    .in0(ID_IR[24:20]), .in1(5'b01010), .out(multiplexer_3_out), .sel(idecall));
  Multiplexer #(.select(1), .width(12), .disabled("Z"), .enable("false")) multiplexer_4 (
    .in0(ID_IR[31:20]), .in1({ID_IR[31:25], ID_IR[11:7]}), .out(multiplexer_4_out), .sel(S_type));
  // Probe on IF_PC[11:0]
  // Probe on WB_PC[19:0]
  // RiscV_Probe riscv_probe_6: pin names not known; wires that end beside it: WB_IR
  \单周期硬布线控制器  \u_单周期硬布线控制器_1  (
    .Funct({ID_IR[30], ID_IR[25], ID_IR[14:12]}), .OP(ID_IR[6:2]), .ALU_OP(\单周期硬布线控制器_1_alu_op ),
    .MemToReg(\单周期硬布线控制器_1_memtoreg ), .MemWrite(\单周期硬布线控制器_1_memwrite ), .ALU_SRC(\单周期硬布线控制器_1_alu_src ),
    .RegWrite(\单周期硬布线控制器_1_regwrite ), .ecall(idecall), .S_type(S_type), .Jalr(\单周期硬布线控制器_1_jalr ),
    .Beq(\单周期硬布线控制器_1_beq ), .JAL(jal), .Bne(\单周期硬布线控制器_1_bne ), .in_3(ID_IR[21]), .uret(\单周期硬布线控制器_1_uret ),
    .bgeu(\单周期硬布线控制器_1_bgeu ), .csr(\单周期硬布线控制器_1_csr ), .dasb(\单周期硬布线控制器_1_dasb ),
    .user1(\单周期硬布线控制器_1_user1 ), .user2(\单周期硬布线控制器_1_user2 ));
  assign bit_extender_1_out = {{20{multiplexer_4_out[11]}}, multiplexer_4_out};  // Bit_Extender bit_extender_1
  assign bit_extender_2_out = {{20{ID_IR[31]}}, {ID_IR[31], ID_IR[7], ID_IR[30:25], ID_IR[11:8]}};  // Bit_Extender bit_extender_2
  assign bit_extender_3_out = {{12{ID_IR[31]}}, {ID_IR[31], ID_IR[19:12], ID_IR[20], ID_IR[30:21]}};  // Bit_Extender bit_extender_3
  // Probe on ID_PC[11:0]
  // Probe on EX_PC[11:0]
  Multiplexer #(.select(1), .width(32), .disabled("Z"), .enable("false")) multiplexer_5 (
    .in0(bit_extender_2_out), .in1(bit_extender_3_out), .out(multiplexer_5_out), .sel(jal));
  // Probe on M_PC[11:0]
  D_Flip_Flop #(.trigger("high"), .Pre_Clr_Positions("LEGACY"), .NegatePresetClear("false"), .enable("true"), .NewFFLayout("false")) d_ff_1 (.Q(d_ff_1_q));  // open: clk, D, Qn, preset, en, reset
  // Probe on 13'hc
  not not_5 (not_5_out, CLK);
  // Probe on WB_PC[11:0]
  Comparator #(.width(13), .mode("twosComplement")) comparator_1 (
    .a(CNT_num), .b(13'hc), .eq(comparator_1_eq), .lt(comparator_1_lt));  // open: gt
  Clock #(.highDuration(1), .lowDuration(1)) clock_1 (.out(clock_1_out));
  Regifile regifile_1 (
    .Din(RDin), .Clk(not_5_out), .R1(regifile_1_r1), .R2(regifile_1_r2), .WE(RegWrite), .W_num(\写回地址 ),
    .R1_num(multiplexer_2_out), .R2_num(multiplexer_3_out));
  nand nand_1 (nand_1_out, d_ff_1_q, comparator_1_eq);
  Counter #(.width(13), .max('h1fff), .ongoal("stay"), .trigger("rising"), .behavior("old")) counter_1 (
    .count(comparator_1_lt), .Q(CNT_num), .clk(clock_1_out));  // open: load, D, carry, clr, preset
  or or_4 (id_ex_1_jalr_2[1], \B型指令分支跳转 , id_ex_1_jal_2);
  ID_EX id_ex_1 (
    .Beq(\单周期硬布线控制器_1_beq ), .Bne(\单周期硬布线控制器_1_bne ), .MemToReg(\单周期硬布线控制器_1_memtoreg ),
    .MemWrite(\单周期硬布线控制器_1_memwrite ), .AluSrcB(\单周期硬布线控制器_1_alu_src ), .RegWrite(\单周期硬布线控制器_1_regwrite ),
    .JAL(jal), .JALR(\单周期硬布线控制器_1_jalr ), .URET(\单周期硬布线控制器_1_uret ), .csr(\单周期硬布线控制器_1_csr ),
    .bgeu(\单周期硬布线控制器_1_bgeu ), .S_type(S_type), .dasb(\单周期硬布线控制器_1_dasb ), .AluOP(\单周期硬布线控制器_1_alu_op ),
    .r1(regifile_1_r1), .r2(regifile_1_r2), .rd_a(ID_IR[11:7]), .imm1(bit_extender_1_out),
    .imm2(multiplexer_5_out), .PC(ID_PC), .PC_4(if_id_1_pc_4_2), .IR(ID_IR), .Beq_2(id_ex_1_beq_2),
    .Bne_2(id_ex_1_bne_2), .MemToReg_2(id_ex_1_memtoreg_2), .MemWrite_2(id_ex_1_memwrite_2),
    .AluSrcB_2(id_ex_1_alusrcb_2), .RegWrite_2(id_ex_1_regwrite_2), .JAL_2(id_ex_1_jal_2),
    .JALR_2(id_ex_1_jalr_2[0]), .URET_2(id_ex_1_uret_2), .bgeu_2(id_ex_1_bgeu_2), .dasb_2(exdasb),
    .AluOP_2(id_ex_1_aluop_2), .r1_2(id_ex_1_r1_2), .r2_2(id_ex_1_r2_2), .rd_a_2(id_ex_1_rd_a_2),
    .imm1_2(id_ex_1_imm1_2), .imm2_2(id_ex_1_imm2_2), .PC_2(EX_PC), .PC_4_2(id_ex_1_pc_4_2), .IR_2(EX_IR),
    .reset(1'b0), .refresh(\清空 ), .en(or_5_out), .CLK(CLK), .ecall(idecall), .ecall_2(execall));  // open: csr_2, S_type_2, r1_forward, r1_forward_2, r2_forward, r2_forward_2, 预测跳转, 预测跳转_2
  or or_5 (or_5_out, not_6_out, Go);
  not not_6 (not_6_out, halt);
  assign CLK = nand_1_out ? clock_1_out : 1'bz;  // Controlled_Buffer controlled_buffer_1
  \冲突处理_bub  \u_冲突处理_bub_1  (
    .exrd(id_ex_1_rd_a_2), .memRegWrite(ex_mem_1_regwrite_2), .user1(\单周期硬布线控制器_1_user1 ), .IR(ID_IR),
    .memrd(ex_mem_1_rd_a_2), .user2(\单周期硬布线控制器_1_user2 ), .exRegWrite(id_ex_1_regwrite_2), .ecall(idecall),
    .branch(\存在分支 ), .\清空 (\清空 ), .\阻塞 (\阻塞 ));
  or or_6 (\B型指令分支跳转 , and_5_out, and_4_out, and_3_out);
  Shifter #(.width(32), .shift("ll")) shifter_1 (.in(id_ex_1_imm2_2), .\dist (5'b00001), .out(shifter_1_out));
  Pull_Resistor #(.pull(1)) pull_resistor_1 (.node(CLK));
  and and_3 (and_3_out, id_ex_1_beq_2, equ);
  Multiplexer #(.select(1), .width(32), .disabled("Z"), .enable("false")) multiplexer_6 (
    .in0(id_ex_1_r2_2), .in1(id_ex_1_imm1_2), .out(multiplexer_6_out), .sel(id_ex_1_alusrcb_2));
  Register #(.width(32), .trigger("rising"), .Select("low")) register_1 (
    .D(id_ex_1_r2_2), .en(and_6_out), .Q(LedData), .clk(CLK), .clr(1'b0), .cs(1'b0), .preset(1'b0));
  Adder #(.width(32)) adder_2 (.a(shifter_1_out), .b(EX_PC), .out(\jal指令地址 ), .cin(1'b0));  // open: cout
  Counter #(.width(16), .max('hffff), .ongoal("wrap"), .trigger("rising"), .behavior("new")) counter_2 (
    .count(CLK), .Q(\总周期数 ), .clk(and_8_out));  // open: load, D, carry, clr, preset, down
  and and_4 (and_4_out, not_7_out, id_ex_1_bne_2);
  and and_5 (and_5_out, id_ex_1_bgeu_2, ge);
  not not_7 (not_7_out, equ);
  ALU alu_1 (
    .X(id_ex_1_r1_2), .Y(multiplexer_6_out), .AluOP(id_ex_1_aluop_2), .Equal(equ), .Result(\ALU计算结果 ),
    .out_4(ge));  // open: Result_2, out_6
  Comparator #(.width(32), .mode("twosComplement")) comparator_2 (
    .a(id_ex_1_r1_2), .b(32'h22), .eq(comparator_2_eq));  // open: gt, lt
  not not_8 (not_8_out, comparator_2_eq);
  and and_6 (and_6_out, execall, comparator_2_eq);
  or or_7 (\J型指令分支跳转 , id_ex_1_jalr_2[0], id_ex_1_jal_2);
  and and_7 (exhalt, execall, not_8_out);
  Counter #(.width(16), .max('hffff), .ongoal("wrap"), .trigger("rising"), .behavior("new")) counter_3 (
    .count(\J型指令分支跳转 ), .Q(\无条件分支数 ), .clk(and_8_out));  // open: load, D, carry, clr, preset, down
  EX_MEM ex_mem_1 (
    .MemToReg(id_ex_1_memtoreg_2), .MemWrite(id_ex_1_memwrite_2), .RegWrite(id_ex_1_regwrite_2),
    .JAL(id_ex_1_jal_2), .JALR(id_ex_1_jalr_2[0]), .URET(id_ex_1_uret_2), .dasb(exdasb), .halt(exhalt),
    .res(\ALU计算结果 ), .rd_a(id_ex_1_rd_a_2), .r2(id_ex_1_r2_2), .PC(EX_PC), .PC_4(id_ex_1_pc_4_2), .IR(EX_IR),
    .MemToReg_2(ex_mem_1_memtoreg_2), .MemWrite_2(MemWrite), .RegWrite_2(ex_mem_1_regwrite_2),
    .JAL_2(ex_mem_1_jal_2), .JALR_2(ex_mem_1_jalr_2), .URET_2(ex_mem_1_uret_2), .dasb_2(ex_mem_1_dasb_2),
    .halt_2(ex_mem_1_halt_2), .res_2(ex_mem_1_res_2), .rd_a_2(ex_mem_1_rd_a_2), .r2_2(ex_mem_1_r2_2),
    .PC_2(M_PC), .PC_4_2(ex_mem_1_pc_4_2), .IR_2(MEM_IR), .reset(1'b0), .refresh(1'b0), .en(or_5_out),
    .CLK(CLK));
  Counter #(.width(16), .max('hffff), .ongoal("wrap"), .trigger("rising"), .behavior("new")) counter_4 (
    .count(\B型指令分支跳转 ), .Q(\条件分支成功数 ), .clk(and_8_out));  // open: load, D, carry, clr, preset, down
  \专门给SB画的电路  \u_专门给sb画的电路_1  (
    .r2(ex_mem_1_r2_2), .addr(ex_mem_1_res_2), .pre_data(ram_1_data), .MDin(MDin), .dasb(ex_mem_1_dasb_2));
  Counter #(.width(16), .max('hffff), .ongoal("wrap"), .trigger("rising"), .behavior("new")) counter_5 (
    .count(\清空 ), .Q(\插入气泡数 ), .clk(and_8_out));  // open: load, D, carry, clr, preset, down
  RAM #(.addrWidth(10), .dataWidth(32), .bus("separate"), .Select("high")) ram_1 (
    .addr(ex_mem_1_res_2[11:2]), .din(MDin), .data(ram_1_data), .str(MemWrite), .sel(1'b1), .clk(CLK),
    .ld(1'b1), .clr(1'b0));
  Counter #(.width(16), .max('hffff), .ongoal("wrap"), .trigger("rising"), .behavior("new")) counter_6 (
    .count(\阻塞 ), .Q(\LoadUse次数 ), .clk(and_8_out));  // open: load, D, carry, clr, preset, down
  or or_8 (mem_wb_1_memtoreg_2[1], mem_wb_1_jal_2, mem_wb_1_jalr_2);
  MEM_WB mem_wb_1 (
    .MemToReg(ex_mem_1_memtoreg_2), .RegWrite(ex_mem_1_regwrite_2), .JAL(ex_mem_1_jal_2),
    .JALR(ex_mem_1_jalr_2), .URET(ex_mem_1_uret_2), .dasb(ex_mem_1_dasb_2), .halt(ex_mem_1_halt_2),
    .res(ex_mem_1_res_2), .rd_a(ex_mem_1_rd_a_2), .MemData(ram_1_data), .PC(M_PC), .PC_4(ex_mem_1_pc_4_2),
    .IR(MEM_IR), .MemToReg_2(mem_wb_1_memtoreg_2[0]), .RegWrite_2(RegWrite), .JAL_2(mem_wb_1_jal_2),
    .JALR_2(mem_wb_1_jalr_2), .halt_2(mem_wb_1_halt_2), .res_2(mem_wb_1_res_2), .rd_a_2(\写回地址 ),
    .MemData_2(mem_wb_1_memdata_2), .PC_2(WB_PC), .PC_4_2(mem_wb_1_pc_4_2), .IR_2(WB_IR), .reset(1'b0),
    .refresh(1'b0), .en(or_5_out), .CLK(CLK));  // open: URET_2, dasb_2
  and and_8 (and_8_out, CLK, not_9_out);
  not not_9 (not_9_out, halt);
  Multiplexer #(.select(2), .width(32), .disabled("Z"), .enable("false")) multiplexer_7 (
    .in0(mem_wb_1_res_2), .in1(mem_wb_1_memdata_2), .in2(mem_wb_1_pc_4_2), .out(RDin),
    .sel(mem_wb_1_memtoreg_2));  // open: in3
  D_Flip_Flop #(.trigger("rising"), .Pre_Clr_Positions("ABOVE_BELOW"), .NegatePresetClear("false"), .enable("true"), .NewFFLayout("true")) d_ff_2 (
    .clk(mem_wb_1_halt_2), .D(1'b1), .Q(halt), .preset(1'b0), .en(1'b1), .reset(Go));  // open: Qn

  // Other names for the same wires on the sheet: MEM_PC[31:0] = M_PC

  // Notes on the sheet:
  //   中断源
  //   时空图监测，可删除
  //   中断等待指示
  //   选择PC
  //   数码管输出
  //   取指
  //   指令探针
  //   指令存储器
  //   contents of rom_1 (hex, n*v repeats v):
  //   100493 100006f 100493 200913 300993 100006f 100493 200913 300993 100006f 100493 200913 300993
  //   100006f 100493 200913 300993 3a4000ef 100413 100493 1f49493 900533 2200893 73 24d493 48463 fedff06f
  //   900533 2200893 73 100493 249493 900533 2200893 73 48463 fedff06f 100493 1f49493 900533 2200893 73
  //   4034d493 900533 2200893 73 4044d493 900533 2200893 73 4044d493 900533 2200893 73 4044d493 900533
  //   2200893 73 4044d493 900533 2200893 73 4044d493 900533 2200893 73 4044d493 900533 2200893 73 4044d493
  //   900533 2200893 73 100413 1f41993 41f9d993 433 c00913 300b13 140413 f47413 800293 100313 499993
  //   89e9b3 1300533 2200893 73 406282b3 fe0294e3 140413 f00f93 1f47433 1c41413 800293 100313 49d993
  //   89e9b3 1300533 2200893 73 406282b3 fe0294e3 1c45413 406b0b33 b0463 f95ff06f 2b3 fff2c293 829293
  //   ff2e293 500533 2200893 73 fff00413 493 84a023 140413 448493 84a023 140413 448493 84a023 140413
  //   448493 84a023 140413 448493 84a023 140413 448493 84a023 140413 448493 84a023 140413 448493 84a023
  //   140413 448493 84a023 140413 448493 84a023 140413 448493 84a023 140413 448493 84a023 140413 448493
  //   84a023 140413 448493 84a023 140413 448493 84a023 140413 448493 84a023 140413 448493 140413 433
  //   3c00493 42983 4aa03 149a2b3 28663 134a023 1442023 ffc48493 fe9412e3 800533 2200893 73 440413 3c00493
  //   fc9416e3 3200893 73 313 2000e13 493 100913 930023 900533 2200893 73 12484b3 130313 fffe0e13 fe0e12e3
  //   800e13 313 32483 900533 2200893 73 430313 fffe0e13 fe0e14e3 a00893 73 100293 300313 800493 849493
  //   7648493 900533 2200893 73 800e13 5494b3 6494b3 900533 2200893 73 fffe0e13 fe0e14e3 a00893 73
  //   fff00293 313 1900413 841413 9700493 940533 2200893 73 5484b3 494b313 fe0306e3 a00893 73 f00493
  //   100913 409909b3 900533 2200893 73 fff48493 ff29f6e3 a00893 73 a00893 73 413 140413 800533 2200893 73
  //   240413 800533 2200893 73 340413 800533 2200893 73 440413 800533 2200893 73 540413 800533 2200893 73
  //   640413 800533 2200893 73 740413 800533 2200893 73 840413 800533 2200893 2200893 73 8067
  //   rs1
  //   rs2
  //   I指令
  //   S指令
  //   B指令
  //   J指令
  //   rd
  //   JAL
  //   JALR
  //   URET
  //   bgeu
  //   跳转地址生成
  //   Beq
  //   Bne
  //   MemToReg
  //   MemWrite
  //   AluOP
  //   AluSrcB
  //   RegWrite
  //   控制位
  //   译码
  //   流水调试日志用
  //   暂停节拍，不能为0
  //   戳工具置1进入计数暂停模式，ctrl+k时钟自动运行到对应节拍暂停
  //   ctrl+k关闭时钟连续运行，将控制位置零，进入单步调试模式调试
  //   可计数暂停的时钟源
  //   执行
  //   ecall的LED显示
  //   为方便自动评测，需要输出流水线各段保存的PC值，注意是PC不是PC+4，另外ID段寄存器写入信息，Mem段内存写入信息也要输出
  //   实现sb
  //   存储
  //   数据存储器
  //   写回
  //   选择RDin
endmodule
module \重定向流水线  (
  output RegWrite,
  output MemWrite,
  output [31:0] IF_PC,
  output [31:0] ID_PC,
  output [31:0] EX_PC,
  output [31:0] M_PC,
  output [31:0] WB_PC,
  output [31:0] RDin,
  output [31:0] MDin,
  output [31:0] LedData
);

  wire and_1_out, and_2_out, and_3_out, and_4_out, and_5_out, and_6_out, and_8_out, \B型指令分支跳转 , CLK,
       clock_1_out, comparator_1_eq, comparator_1_lt, comparator_2_eq, d_ff_1_q, equ, ex_mem_1_dasb_2,
       ex_mem_1_halt_2, ex_mem_1_jal_2, ex_mem_1_jalr_2, ex_mem_1_memtoreg_2, ex_mem_1_regwrite_2,
       ex_mem_1_uret_2, exdasb, execall, exhalt, ge, Go, halt, id_ex_1_alusrcb_2, id_ex_1_beq_2,
       id_ex_1_bgeu_2, id_ex_1_bne_2, id_ex_1_jal_2, id_ex_1_memtoreg_2, id_ex_1_memwrite_2,
       id_ex_1_regwrite_2, id_ex_1_uret_2, idecall, IR1, IR2, IR3, jal, \J型指令分支跳转 , mem_wb_1_halt_2,
       mem_wb_1_jal_2, mem_wb_1_jalr_2, nand_1_out, not_1_out, not_2_out, not_3_out, not_4_out, not_5_out,
       not_6_out, not_7_out, not_8_out, not_9_out, or_1_out, or_3_out, or_5_out, RST, S_type, W1, W2, W3,
       \单周期硬布线控制器_1_alu_src , \单周期硬布线控制器_1_beq , \单周期硬布线控制器_1_bgeu , \单周期硬布线控制器_1_bne , \单周期硬布线控制器_1_csr ,
       \单周期硬布线控制器_1_dasb , \单周期硬布线控制器_1_jalr , \单周期硬布线控制器_1_memtoreg , \单周期硬布线控制器_1_memwrite ,
       \单周期硬布线控制器_1_regwrite , \单周期硬布线控制器_1_uret , \单周期硬布线控制器_1_user1 , \单周期硬布线控制器_1_user2 , \存在分支 , \清空 ,
       \清空_t , \阻塞 ;
  wire [1:0] id_ex_1_jalr_2, id_ex_1_r1_forward_2, id_ex_1_r2_forward_2, mem_wb_1_memtoreg_2, r1_forward,
       r2_forward;
  wire [3:0] id_ex_1_aluop_2, \单周期硬布线控制器_1_alu_op ;
  wire [4:0] ex_mem_1_rd_a_2, id_ex_1_rd_a_2, multiplexer_2_out, multiplexer_3_out, \写回地址 ;
  wire [11:0] multiplexer_4_out;
  wire [12:0] CNT_num;
  wire [15:0] \LoadUse次数 , \总周期数 , \插入气泡数 , \无条件分支数 , \条件分支成功数 ;
  wire [31:0] \ALU计算结果 , bit_extender_1_out, bit_extender_2_out, bit_extender_3_out, EX_IR, ex_mem_1_pc_4_2,
       ex_mem_1_r2_2, exr1, exr2, id_ex_1_imm1_2, id_ex_1_imm2_2, id_ex_1_pc_4_2, ID_IR, if_id_1_pc_4_2,
       IF_IR, \jal指令地址 , MEM_IR, mem_wb_1_memdata_2, mem_wb_1_pc_4_2, mem_wb_1_res_2, \memALU计算结果 ,
       multiplexer_1_out, multiplexer_5_out, multiplexer_8_out, PC_4, ram_1_data, regifile_1_r1,
       regifile_1_r2, rer1, rer2, shifter_1_out, WB_IR;

  Button \u_总复位  (.out(RST));
  Button _1 (.out(IR1));
  Button _2 (.out(IR2));
  Button _3 (.out(IR3));
  // Probe on \总周期数 
  // Probe on \总周期数 
  Button \u_继续运行  (.out(Go));
  LED #(.active("true")) led_1 (.in(W1));
  LED #(.active("true")) led_2 (.in(W2));
  LED #(.active("true")) led_3 (.in(W3));
  and and_1 (and_1_out, or_1_out, not_2_out);
  or or_1 (or_1_out, not_1_out, Go);
  not not_1 (not_1_out, halt);
  Hex_Digit_Display hex_digit_display_1 (.value(LedData[31:28]));  // open: dp
  // Probe on IF_PC[19:0]
  // RiscV_Probe riscv_probe_1: pin names not known; wires that end beside it: IF_IR
  Register #(.width(32), .trigger("rising"), .Select("low")) PC (
    .D(multiplexer_1_out), .en(and_1_out), .Q(IF_PC), .clk(CLK), .clr(1'b0), .cs(1'b0), .preset(1'b0));
  Multiplexer #(.select(2), .width(32), .disabled("Z"), .enable("false")) multiplexer_1 (
    .in0(PC_4), .in1(\ALU计算结果 ), .in2(\jal指令地址 ), .out(multiplexer_1_out), .sel(id_ex_1_jalr_2));  // open: in3
  not not_2 (not_2_out, \阻塞 );
  Hex_Digit_Display hex_digit_display_2 (.value(LedData[27:24]));  // open: dp
  Hex_Digit_Display hex_digit_display_3 (.value(LedData[23:20]));  // open: dp
  // Probe on ID_PC[19:0]
  // RiscV_Probe riscv_probe_2: pin names not known; wires that end beside it: ID_IR
  Hex_Digit_Display hex_digit_display_4 (.value(LedData[15:12]));  // open: dp
  Hex_Digit_Display hex_digit_display_5 (.value(LedData[19:16]));  // open: dp
  // RiscV_Probe riscv_probe_3: pin names not known; wires that end beside it: IF_IR
  Adder #(.width(32)) adder_1 (.a(IF_PC), .b(32'h4), .out(PC_4), .cin(1'b0));  // open: cout
  Hex_Digit_Display hex_digit_display_6 (.value(LedData[11:8]));  // open: dp
  Hex_Digit_Display hex_digit_display_7 (.value(LedData[7:4]));  // open: dp
  // Probe on EX_PC[19:0]
  // RiscV_Probe riscv_probe_4: pin names not known; wires that end beside it: EX_IR
  ROM #(.addrWidth(10), .dataWidth(32), .Select("high")) rom_1 (.addr(IF_PC[11:2]), .data(IF_IR), .sel(1'b1));
  Hex_Digit_Display hex_digit_display_8 (.value(LedData[3:0]));  // open: dp
  or or_2 (\存在分支 , id_ex_1_jalr_2[0], id_ex_1_jalr_2[1]);
  IF_ID if_id_1 (
    .PC(IF_PC), .PC_4(PC_4), .IR(IF_IR), .PC_2(ID_PC), .PC_4_2(if_id_1_pc_4_2), .IR_2(ID_IR), .reset(1'b0),
    .refresh(\存在分支 ), .en(and_2_out), .CLK(CLK));  // open: 预测跳转, 预测跳转_2
  and and_2 (and_2_out, or_3_out, not_3_out);
  not not_3 (not_3_out, \阻塞 );
  or or_3 (or_3_out, not_4_out, Go);
  not not_4 (not_4_out, halt);
  // Probe on \总周期数 
  // Probe on M_PC[19:0]
  // RiscV_Probe riscv_probe_5: pin names not known; wires that end beside it: MEM_IR
  // Probe on \总周期数 
  // Probe on \无条件分支数 
  // Probe on \条件分支成功数 
  // Probe on \插入气泡数 
  // Probe on \LoadUse次数 
  Multiplexer #(.select(1), .width(5), .disabled("Z"), .enable("false")) multiplexer_2 (
    .in0(ID_IR[19:15]), .in1(5'b10001), .out(multiplexer_2_out), .sel(idecall));
  Multiplexer #(.select(1), .width(5), .disabled("Z"), .enable("false")) multiplexer_3 (
    .in0(ID_IR[24:20]), .in1(5'b01010), .out(multiplexer_3_out), .sel(idecall));
  Multiplexer #(.select(1), .width(12), .disabled("Z"), .enable("false")) multiplexer_4 (
    .in0(ID_IR[31:20]), .in1({ID_IR[31:25], ID_IR[11:7]}), .out(multiplexer_4_out), .sel(S_type));
  // Probe on IF_PC[11:0]
  // Probe on WB_PC[19:0]
  // RiscV_Probe riscv_probe_6: pin names not known; wires that end beside it: WB_IR
  \单周期硬布线控制器  \u_单周期硬布线控制器_1  (
    .Funct({ID_IR[30], ID_IR[25], ID_IR[14:12]}), .OP(ID_IR[6:2]), .ALU_OP(\单周期硬布线控制器_1_alu_op ),
    .MemToReg(\单周期硬布线控制器_1_memtoreg ), .MemWrite(\单周期硬布线控制器_1_memwrite ), .ALU_SRC(\单周期硬布线控制器_1_alu_src ),
    .RegWrite(\单周期硬布线控制器_1_regwrite ), .ecall(idecall), .S_type(S_type), .Jalr(\单周期硬布线控制器_1_jalr ),
    .Beq(\单周期硬布线控制器_1_beq ), .JAL(jal), .Bne(\单周期硬布线控制器_1_bne ), .in_3(ID_IR[21]), .uret(\单周期硬布线控制器_1_uret ),
    .bgeu(\单周期硬布线控制器_1_bgeu ), .csr(\单周期硬布线控制器_1_csr ), .dasb(\单周期硬布线控制器_1_dasb ),
    .user1(\单周期硬布线控制器_1_user1 ), .user2(\单周期硬布线控制器_1_user2 ));
  assign bit_extender_1_out = {{20{multiplexer_4_out[11]}}, multiplexer_4_out};  // Bit_Extender bit_extender_1
  assign bit_extender_2_out = {{20{ID_IR[31]}}, {ID_IR[31], ID_IR[7], ID_IR[30:25], ID_IR[11:8]}};  // Bit_Extender bit_extender_2
  assign bit_extender_3_out = {{12{ID_IR[31]}}, {ID_IR[31], ID_IR[19:12], ID_IR[20], ID_IR[30:21]}};  // Bit_Extender bit_extender_3
  // Probe on ID_PC[11:0]
  // Probe on EX_PC[11:0]
  Multiplexer #(.select(1), .width(32), .disabled("Z"), .enable("false")) multiplexer_5 (
    .in0(bit_extender_2_out), .in1(bit_extender_3_out), .out(multiplexer_5_out), .sel(jal));
  // Probe on M_PC[11:0]
  D_Flip_Flop #(.trigger("high"), .Pre_Clr_Positions("LEGACY"), .NegatePresetClear("false"), .enable("true"), .NewFFLayout("false")) d_ff_1 (.Q(d_ff_1_q));  // open: clk, D, Qn, preset, en, reset
  // Probe on 13'h10e
  not not_5 (not_5_out, CLK);
  // Probe on WB_PC[11:0]
  Comparator #(.width(13), .mode("twosComplement")) comparator_1 (
    .a(CNT_num), .b(13'h10e), .eq(comparator_1_eq), .lt(comparator_1_lt));  // open: gt
  Clock #(.highDuration(1), .lowDuration(1)) clock_1 (.out(clock_1_out));
  Regifile regifile_1 (
    .Din(RDin), .Clk(not_5_out), .R1(regifile_1_r1), .R2(regifile_1_r2), .WE(RegWrite), .W_num(\写回地址 ),
    .R1_num(multiplexer_2_out), .R2_num(multiplexer_3_out));
  nand nand_1 (nand_1_out, d_ff_1_q, comparator_1_eq);
  Counter #(.width(13), .max('h1fff), .ongoal("stay"), .trigger("rising"), .behavior("old")) counter_1 (
    .count(comparator_1_lt), .Q(CNT_num), .clk(clock_1_out));  // open: load, D, carry, clr, preset
  \冲突处理_redirect  \u_冲突处理_redirect_1  (
    .exrd(id_ex_1_rd_a_2), .memRegWrite(ex_mem_1_regwrite_2), .ecall(idecall), .user1(\单周期硬布线控制器_1_user1 ),
    .IR(ID_IR), .memrd(ex_mem_1_rd_a_2), .user2(\单周期硬布线控制器_1_user2 ), .exRegWrite(id_ex_1_regwrite_2),
    .\存在分支 (\存在分支 ), .\阻塞 (\阻塞 ), .\清空 (\清空 ), .r1_forward(r1_forward), .r2_forward(r2_forward),
    .exMemToReg(id_ex_1_memtoreg_2));
  or or_4 (id_ex_1_jalr_2[1], \B型指令分支跳转 , id_ex_1_jal_2);
  ID_EX id_ex_1 (
    .Beq(\单周期硬布线控制器_1_beq ), .Bne(\单周期硬布线控制器_1_bne ), .MemToReg(\单周期硬布线控制器_1_memtoreg ),
    .MemWrite(\单周期硬布线控制器_1_memwrite ), .AluSrcB(\单周期硬布线控制器_1_alu_src ), .RegWrite(\单周期硬布线控制器_1_regwrite ),
    .JAL(jal), .JALR(\单周期硬布线控制器_1_jalr ), .URET(\单周期硬布线控制器_1_uret ), .csr(\单周期硬布线控制器_1_csr ),
    .bgeu(\单周期硬布线控制器_1_bgeu ), .S_type(S_type), .dasb(\单周期硬布线控制器_1_dasb ), .AluOP(\单周期硬布线控制器_1_alu_op ),
    .r1(regifile_1_r1), .r2(regifile_1_r2), .rd_a(ID_IR[11:7]), .imm1(bit_extender_1_out),
    .imm2(multiplexer_5_out), .PC(ID_PC), .PC_4(if_id_1_pc_4_2), .IR(ID_IR), .Beq_2(id_ex_1_beq_2),
    .Bne_2(id_ex_1_bne_2), .MemToReg_2(id_ex_1_memtoreg_2), .MemWrite_2(id_ex_1_memwrite_2),
    .AluSrcB_2(id_ex_1_alusrcb_2), .RegWrite_2(id_ex_1_regwrite_2), .JAL_2(id_ex_1_jal_2),
    .JALR_2(id_ex_1_jalr_2[0]), .URET_2(id_ex_1_uret_2), .bgeu_2(id_ex_1_bgeu_2), .dasb_2(exdasb),
    .AluOP_2(id_ex_1_aluop_2), .r1_2(exr1), .r2_2(exr2), .rd_a_2(id_ex_1_rd_a_2), .imm1_2(id_ex_1_imm1_2),
    .imm2_2(id_ex_1_imm2_2), .PC_2(EX_PC), .PC_4_2(id_ex_1_pc_4_2), .IR_2(EX_IR), .reset(1'b0),
    .refresh(\清空_t ), .en(or_5_out), .CLK(CLK), .ecall(idecall), .ecall_2(execall), .r1_forward(r1_forward),
    .r1_forward_2(id_ex_1_r1_forward_2), .r2_forward(r2_forward), .r2_forward_2(id_ex_1_r2_forward_2));  // open: csr_2, S_type_2, 预测跳转, 预测跳转_2
  or or_5 (or_5_out, not_6_out, Go);
  not not_6 (not_6_out, halt);
  Multiplexer #(.select(2), .width(32), .disabled("Z"), .enable("false")) multiplexer_6 (
    .in0(exr1), .in1(RDin), .in2(\memALU计算结果 ), .out(rer1), .sel(id_ex_1_r1_forward_2));  // open: in3
  assign CLK = nand_1_out ? clock_1_out : 1'bz;  // Controlled_Buffer controlled_buffer_1
  or or_6 (\B型指令分支跳转 , and_5_out, and_4_out, and_3_out);
  Shifter #(.width(32), .shift("ll")) shifter_1 (.in(id_ex_1_imm2_2), .\dist (5'b00001), .out(shifter_1_out));
  Multiplexer #(.select(2), .width(32), .disabled("Z"), .enable("false")) multiplexer_7 (
    .in0(exr2), .in1(RDin), .in2(\memALU计算结果 ), .out(rer2), .sel(id_ex_1_r2_forward_2));  // open: in3
  Pull_Resistor #(.pull(1)) pull_resistor_1 (.node(CLK));
  and and_3 (and_3_out, id_ex_1_beq_2, equ);
  Multiplexer #(.select(1), .width(32), .disabled("Z"), .enable("false")) multiplexer_8 (
    .in0(rer2), .in1(id_ex_1_imm1_2), .out(multiplexer_8_out), .sel(id_ex_1_alusrcb_2));
  Register #(.width(32), .trigger("rising"), .Select("low")) register_1 (
    .D(rer2), .en(and_6_out), .Q(LedData), .clk(CLK), .clr(1'b0), .cs(1'b0), .preset(1'b0));
  Adder #(.width(32)) adder_2 (.a(shifter_1_out), .b(EX_PC), .out(\jal指令地址 ), .cin(1'b0));  // open: cout
  Counter #(.width(16), .max('hffff), .ongoal("wrap"), .trigger("rising"), .behavior("new")) counter_2 (
    .count(CLK), .Q(\总周期数 ), .clk(and_8_out));  // open: load, D, carry, clr, preset, down
  and and_4 (and_4_out, not_7_out, id_ex_1_bne_2);
  and and_5 (and_5_out, id_ex_1_bgeu_2, ge);
  not not_7 (not_7_out, equ);
  ALU alu_1 (
    .X(rer1), .Y(multiplexer_8_out), .AluOP(id_ex_1_aluop_2), .Equal(equ), .Result(\ALU计算结果 ), .out_4(ge));  // open: Result_2, out_6
  not not_8 (not_8_out, comparator_2_eq);
  Comparator #(.width(32), .mode("twosComplement")) comparator_2 (
    .a(rer1), .b(32'h22), .eq(comparator_2_eq));  // open: gt, lt
  and and_6 (and_6_out, execall, comparator_2_eq);
  or or_7 (\J型指令分支跳转 , id_ex_1_jalr_2[0], id_ex_1_jal_2);
  and and_7 (exhalt, execall, not_8_out);
  Counter #(.width(16), .max('hffff), .ongoal("wrap"), .trigger("rising"), .behavior("new")) counter_3 (
    .count(\J型指令分支跳转 ), .Q(\无条件分支数 ), .clk(and_8_out));  // open: load, D, carry, clr, preset, down
  EX_MEM ex_mem_1 (
    .MemToReg(id_ex_1_memtoreg_2), .MemWrite(id_ex_1_memwrite_2), .RegWrite(id_ex_1_regwrite_2),
    .JAL(id_ex_1_jal_2), .JALR(id_ex_1_jalr_2[0]), .URET(id_ex_1_uret_2), .dasb(exdasb), .halt(exhalt),
    .res(\ALU计算结果 ), .rd_a(id_ex_1_rd_a_2), .r2(rer2), .PC(EX_PC), .PC_4(id_ex_1_pc_4_2), .IR(EX_IR),
    .MemToReg_2(ex_mem_1_memtoreg_2), .MemWrite_2(MemWrite), .RegWrite_2(ex_mem_1_regwrite_2),
    .JAL_2(ex_mem_1_jal_2), .JALR_2(ex_mem_1_jalr_2), .URET_2(ex_mem_1_uret_2), .dasb_2(ex_mem_1_dasb_2),
    .halt_2(ex_mem_1_halt_2), .res_2(\memALU计算结果 ), .rd_a_2(ex_mem_1_rd_a_2), .r2_2(ex_mem_1_r2_2),
    .PC_2(M_PC), .PC_4_2(ex_mem_1_pc_4_2), .IR_2(MEM_IR), .reset(1'b0), .refresh(1'b0), .en(or_5_out),
    .CLK(CLK));
  Counter #(.width(16), .max('hffff), .ongoal("wrap"), .trigger("rising"), .behavior("new")) counter_4 (
    .count(\B型指令分支跳转 ), .Q(\条件分支成功数 ), .clk(and_8_out));  // open: load, D, carry, clr, preset, down
  \专门给SB画的电路  \u_专门给sb画的电路_1  (
    .r2(ex_mem_1_r2_2), .addr(\memALU计算结果 ), .pre_data(ram_1_data), .MDin(MDin), .dasb(ex_mem_1_dasb_2));
  Counter #(.width(16), .max('hffff), .ongoal("wrap"), .trigger("rising"), .behavior("new")) counter_5 (
    .count(\清空 ), .Q(\插入气泡数 ), .clk(and_8_out));  // open: load, D, carry, clr, preset, down
  RAM #(.addrWidth(10), .dataWidth(32), .bus("separate"), .Select("high")) ram_1 (
    .addr(\memALU计算结果 [11:2]), .din(MDin), .data(ram_1_data), .str(MemWrite), .sel(1'b1), .clk(CLK),
    .ld(1'b1), .clr(1'b0));
  Counter #(.width(16), .max('hffff), .ongoal("wrap"), .trigger("rising"), .behavior("new")) counter_6 (
    .count(\阻塞 ), .Q(\LoadUse次数 ), .clk(and_8_out));  // open: load, D, carry, clr, preset, down
  or or_8 (mem_wb_1_memtoreg_2[1], mem_wb_1_jal_2, mem_wb_1_jalr_2);
  MEM_WB mem_wb_1 (
    .MemToReg(ex_mem_1_memtoreg_2), .RegWrite(ex_mem_1_regwrite_2), .JAL(ex_mem_1_jal_2),
    .JALR(ex_mem_1_jalr_2), .URET(ex_mem_1_uret_2), .dasb(ex_mem_1_dasb_2), .halt(ex_mem_1_halt_2),
    .res(\memALU计算结果 ), .rd_a(ex_mem_1_rd_a_2), .MemData(ram_1_data), .PC(M_PC), .PC_4(ex_mem_1_pc_4_2),
    .IR(MEM_IR), .MemToReg_2(mem_wb_1_memtoreg_2[0]), .RegWrite_2(RegWrite), .JAL_2(mem_wb_1_jal_2),
    .JALR_2(mem_wb_1_jalr_2), .halt_2(mem_wb_1_halt_2), .res_2(mem_wb_1_res_2), .rd_a_2(\写回地址 ),
    .MemData_2(mem_wb_1_memdata_2), .PC_2(WB_PC), .PC_4_2(mem_wb_1_pc_4_2), .IR_2(WB_IR), .reset(1'b0),
    .refresh(1'b0), .en(or_5_out), .CLK(CLK));  // open: URET_2, dasb_2
  and and_8 (and_8_out, CLK, not_9_out);
  not not_9 (not_9_out, halt);
  Multiplexer #(.select(2), .width(32), .disabled("Z"), .enable("false")) multiplexer_9 (
    .in0(mem_wb_1_res_2), .in1(mem_wb_1_memdata_2), .in2(mem_wb_1_pc_4_2), .out(RDin),
    .sel(mem_wb_1_memtoreg_2));  // open: in3
  D_Flip_Flop #(.trigger("rising"), .Pre_Clr_Positions("ABOVE_BELOW"), .NegatePresetClear("false"), .enable("true"), .NewFFLayout("true")) d_ff_2 (
    .clk(mem_wb_1_halt_2), .D(1'b1), .Q(halt), .preset(1'b0), .en(1'b1), .reset(Go));  // open: Qn

  // Other names for the same wires on the sheet: MEM_PC[31:0] = M_PC

  // Notes on the sheet:
  //   中断源
  //   时空图监测，可删除
  //   中断等待指示
  //   选择PC
  //   数码管输出
  //   取指
  //   指令探针
  //   指令存储器
  //   contents of rom_1 (hex, n*v repeats v):
  //   100493 100006f 100493 200913 300993 100006f 100493 200913 300993 100006f 100493 200913 300993
  //   100006f 100493 200913 300993 3a4000ef 100413 100493 1f49493 900533 2200893 73 24d493 48463 fedff06f
  //   900533 2200893 73 100493 249493 900533 2200893 73 48463 fedff06f 100493 1f49493 900533 2200893 73
  //   4034d493 900533 2200893 73 4044d493 900533 2200893 73 4044d493 900533 2200893 73 4044d493 900533
  //   2200893 73 4044d493 900533 2200893 73 4044d493 900533 2200893 73 4044d493 900533 2200893 73 4044d493
  //   900533 2200893 73 100413 1f41993 41f9d993 433 c00913 300b13 140413 f47413 800293 100313 499993
  //   89e9b3 1300533 2200893 73 406282b3 fe0294e3 140413 f00f93 1f47433 1c41413 800293 100313 49d993
  //   89e9b3 1300533 2200893 73 406282b3 fe0294e3 1c45413 406b0b33 b0463 f95ff06f 2b3 fff2c293 829293
  //   ff2e293 500533 2200893 73 fff00413 493 84a023 140413 448493 84a023 140413 448493 84a023 140413
  //   448493 84a023 140413 448493 84a023 140413 448493 84a023 140413 448493 84a023 140413 448493 84a023
  //   140413 448493 84a023 140413 448493 84a023 140413 448493 84a023 140413 448493 84a023 140413 448493
  //   84a023 140413 448493 84a023 140413 448493 84a023 140413 448493 84a023 140413 448493 140413 433
  //   3c00493 42983 4aa03 149a2b3 28663 134a023 1442023 ffc48493 fe9412e3 800533 2200893 73 440413 3c00493
  //   fc9416e3 3200893 73 313 2000e13 493 100913 930023 900533 2200893 73 12484b3 130313 fffe0e13 fe0e12e3
  //   800e13 313 32483 900533 2200893 73 430313 fffe0e13 fe0e14e3 a00893 73 100293 300313 800493 849493
  //   7648493 900533 2200893 73 800e13 5494b3 6494b3 900533 2200893 73 fffe0e13 fe0e14e3 a00893 73
  //   fff00293 313 1900413 841413 9700493 940533 2200893 73 5484b3 494b313 fe0306e3 a00893 73 f00493
  //   100913 409909b3 900533 2200893 73 fff48493 ff29f6e3 a00893 73 a00893 73 413 140413 800533 2200893 73
  //   240413 800533 2200893 73 340413 800533 2200893 73 440413 800533 2200893 73 540413 800533 2200893 73
  //   640413 800533 2200893 73 740413 800533 2200893 73 840413 800533 2200893 2200893 73 8067
  //   rs1
  //   rs2
  //   I指令
  //   S指令
  //   B指令
  //   J指令
  //   rd
  //   JAL
  //   JALR
  //   URET
  //   bgeu
  //   跳转地址生成
  //   Beq
  //   Bne
  //   MemToReg
  //   MemWrite
  //   AluOP
  //   AluSrcB
  //   RegWrite
  //   控制位
  //   译码
  //   流水调试日志用
  //   暂停节拍，不能为0
  //   戳工具置1进入计数暂停模式，ctrl+k时钟自动运行到对应节拍暂停
  //   ctrl+k关闭时钟连续运行，将控制位置零，进入单步调试模式调试
  //   可计数暂停的时钟源
  //   计算参数重定向
  //   执行
  //   ecall的LED显示
  //   为方便自动评测，需要输出流水线各段保存的PC值，注意是PC不是PC+4，另外ID段寄存器写入信息，Mem段内存写入信息也要输出
  //   实现sb
  //   存储
  //   数据存储器
  //   写回
  //   选择RDin
endmodule

module \中断按键参考电路  (
  input  \同步清零信号 ,
  output \与中断屏蔽位与 
);

  wire \_1号中断_out , and_1_out, clock_1_out, d_ff_1_q, or_1_out, or_2_out;

  Clock #(.highDuration(1), .lowDuration(1)) clock_1 (.out(clock_1_out));
  Button \_1号中断  (.out(\_1号中断_out ));
  or or_1 (or_1_out, \与中断屏蔽位与 , d_ff_1_q);
  LED #(.active("true")) \_1号中断等待指示灯  (.in(or_1_out));
  D_Flip_Flop #(.trigger("rising"), .Pre_Clr_Positions("LEGACY"), .NegatePresetClear("false"), .enable("true"), .NewFFLayout("false")) d_ff_1 (
    .clk(\_1号中断_out ), .D(1'b1), .Q(d_ff_1_q), .reset(\与中断屏蔽位与 ));  // open: Qn, preset, en
  or or_2 (or_2_out, d_ff_1_q, \与中断屏蔽位与 );
  and and_1 (and_1_out, or_2_out, ~\同步清零信号 );  // AND_Gate
  D_Flip_Flop #(.trigger("rising"), .Pre_Clr_Positions("LEGACY"), .NegatePresetClear("false"), .enable("true"), .NewFFLayout("false")) IR1 (
    .clk(clock_1_out), .D(and_1_out), .Q(\与中断屏蔽位与 ));  // open: Qn, preset, en, reset

  // Notes on the sheet:
  //   中断信号采样参考电路
  //   Reset 
endmodule

module \单周期_单级中断  (
  input  IR1,
  input  IR2,
  input  IR3,
  output RegWrite,
  output MemWrite,
  output [31:0] PC,
  output [31:0] IR,
  output [31:0] RDin,
  output [31:0] MDin,
  output [31:0] LedData
);

  wire CLK, clock_1_out, comparator_1_eq, comparator_2_eq, comparator_3_eq, comparator_4_eq, comparator_5_eq,
       comparator_5_lt, d_ff_1_q, Go, IR1_t, IR2_t, IR3_t, IRA, IRB, IRC, nand_1_out, or_1_out, W1, W2, W3;
  wire [12:0] CNT_num;
  wire [15:0] \总周期数 ;

  Button \u_继续运行  (.out(Go));
  Button _1 ();  // open: out
  Button _2 ();  // open: out
  Button _3 ();  // open: out
  LED #(.active("true")) led_1 (.in(W1));
  LED #(.active("true")) led_2 (.in(W2));
  LED #(.active("true")) led_3 (.in(W3));
  Hex_Digit_Display hex_digit_display_1 (.value(LedData[31:28]));  // open: dp
  Comparator #(.width(16), .mode("twosComplement")) comparator_1 (
    .a(16'h23b), .b(\总周期数 ), .eq(comparator_1_eq));  // open: gt, lt
  Comparator #(.width(16), .mode("twosComplement")) comparator_2 (
    .a(\总周期数 ), .b(16'h1), .eq(comparator_2_eq));  // open: gt, lt
  Comparator #(.width(16), .mode("twosComplement")) comparator_3 (
    .a(\总周期数 ), .b(16'h4), .eq(comparator_3_eq));  // open: gt, lt
  Comparator #(.width(16), .mode("twosComplement")) comparator_4 (
    .a(\总周期数 ), .b(16'h7), .eq(comparator_4_eq));  // open: gt, lt
  Hex_Digit_Display hex_digit_display_2 (.value(LedData[23:20]));  // open: dp
  Hex_Digit_Display hex_digit_display_3 (.value(LedData[27:24]));  // open: dp
  or or_1 (or_1_out, comparator_1_eq, comparator_2_eq);
  Pull_Resistor #(.pull(0)) pull_resistor_1 (.node(IRA));
  assign IRA = or_1_out ? ~CLK : 1'bz;  // Controlled_Inverter controlled_inverter_1
  Pull_Resistor #(.pull(0)) pull_resistor_2 (.node(IRB));
  assign IRB = comparator_3_eq ? ~CLK : 1'bz;  // Controlled_Inverter controlled_inverter_2
  Pull_Resistor #(.pull(0)) pull_resistor_3 (.node(IRC));
  assign IRC = comparator_4_eq ? ~CLK : 1'bz;  // Controlled_Inverter controlled_inverter_3
  Hex_Digit_Display hex_digit_display_4 (.value(LedData[15:12]));  // open: dp
  Hex_Digit_Display hex_digit_display_5 (.value(LedData[19:16]));  // open: dp
  Hex_Digit_Display hex_digit_display_6 (.value(LedData[11:8]));  // open: dp
  Hex_Digit_Display hex_digit_display_7 (.value(LedData[7:4]));  // open: dp
  // Probe on \总周期数 
  Hex_Digit_Display hex_digit_display_8 (.value(LedData[3:0]));  // open: dp
  or or_2 (IR1_t, IR1, IRA);
  or or_3 (IR2_t, IR2, IRB);
  or or_4 (IR3_t, IR3, IRC);
  D_Flip_Flop #(.trigger("high"), .Pre_Clr_Positions("LEGACY"), .NegatePresetClear("false"), .enable("true"), .NewFFLayout("false")) d_ff_1 (.Q(d_ff_1_q));  // open: clk, D, Qn, preset, en, reset
  // Probe on 13'hc
  Comparator #(.width(13), .mode("twosComplement")) comparator_5 (
    .a(CNT_num), .b(13'hc), .eq(comparator_5_eq), .lt(comparator_5_lt));  // open: gt
  Clock #(.highDuration(1), .lowDuration(1)) clock_1 (.out(clock_1_out));
  Counter #(.width(13), .max('h1fff), .ongoal("stay"), .trigger("rising"), .behavior("old")) counter_1 (
    .count(comparator_5_lt), .Q(CNT_num), .clk(clock_1_out));  // open: load, D, carry, clr, preset
  nand nand_1 (nand_1_out, d_ff_1_q, comparator_5_eq);
  assign CLK = nand_1_out ? clock_1_out : 1'bz;  // Controlled_Buffer controlled_buffer_1
  Pull_Resistor #(.pull(1)) pull_resistor_4 (.node(CLK));

  // Notes on the sheet:
  //   中断源
  //   中断等待指示
  //   总复位信号应将除ROM以外所有存储组件全部清零
  //   单级中断测试信号模拟器
  //   数码管输出
  //   数码管输出应该用寄存器锁存，否则显示数据只能一闪而过
  //   为方便自动评测，需要输出PC，IR，寄存器堆写如数据RDin
  //   RAM写使能MemWrite、RAM写入数据MDin等信号
  //   控制位
  //   暂停节拍，不能为0
  //   戳工具置1进入计数暂停模式，ctrl+k时钟自动运行到对应节拍暂停
  //   ctrl+k关闭时钟连续运行，将控制位置零，进入单步调试模式调试
  //   可计数暂停的时钟源
endmodule

module \单周期_多级中断  (
  input  IR1,
  input  IR2,
  input  IR3,
  output RegWrite,
  output MemWrite,
  output [31:0] PC,
  output [31:0] IR,
  output [31:0] RDin,
  output [31:0] MDin,
  output [31:0] LedData
);

  wire and_1_out, and_2_out, and_3_out, and_4_out, and_5_out, and_6_out, and_7_out, and_8_out, and_10_out,
       and_11_out, and_12_out, and_13_out, and_15_out, and_16_out, and_17_out, Beq, Bne, CLK, clock_1_out,
       comparator_1_eq, comparator_2_eq, comparator_3_eq, comparator_4_eq, comparator_6_eq, comparator_6_lt,
       comparator_7_eq, comparator_8_eq, comparator_9_eq, comparator_10_eq, comparator_11_eq, csr, d_ff_1_q,
       d_ff_2_q, d_ff_3_q, d_ff_4_q, dasb, decoder_1_out0, decoder_1_out1, decoder_1_out2, decoder_2_out2,
       decoder_2_out3, ecall, equ, ge, Go, halt, IR1_2_q, IR1_3_q, IR1_q, IR1_t, IR2_t, IR3_t, IRA, IRB, IRC,
       jal, jalr, MemToReg, nand_1_out, not_1_out, not_2_out, not_3_out, not_4_out, not_5_out, not_6_out,
       or_1_out, or_2_out, or_6_out, or_7_out, or_8_out, or_10_out, or_11_out, or_14_out, or_16_out,
       or_17_out, priority_encoder_2_gs, pull_resistor_4_node, S_type, uret, W1, W2, W3, \中断1返回 , \中断2返回 ,
       \中断3返回 , \中断产生 , \中断使能寄存器_q , \单周期硬布线控制器_1_alu_src , \单周期硬布线控制器_1_bgeu , \当前指令优先 ;
  wire [1:0] counter_1_q, IR_id_2_q, IR_id_3_q, IR_id_q, multiplexer_8_out, priority_encoder_1_out,
       priority_encoder_2_out;
  wire [1:1] or_15_out;
  wire [3:0] \单周期硬布线控制器_1_alu_op ;
  wire [4:0] multiplexer_2_out, multiplexer_3_out;
  wire [11:0] multiplexer_4_out;
  wire [12:0] CNT_num;
  wire [15:0] \总周期数 ;
  wire [31:0] adder_2_out, adder_3_out, \ALU计算结果 , bit_extender_1_out, bit_extender_2_out,
       bit_extender_3_out, EPC, EPC_2_q, EPC_3_q, EPC_q, multiplexer_5_out, multiplexer_6_out, PC_4,
       ram_1_data, regifile_1_r1, regifile_1_r2, shifter_1_out, shifter_2_out, \下条PC , \原始PC ;

  Button \u_继续运行  (.out(Go));
  Button _1 ();  // open: out
  Button _2 ();  // open: out
  Button _3 ();  // open: out
  LED #(.active("true")) led_1 (.in(W1));
  LED #(.active("true")) led_2 (.in(W2));
  LED #(.active("true")) led_3 (.in(W3));
  Priority_Encoder #(.select(2), .disabled("Z")) priority_encoder_1 (
    .in0(1'b1), .in1(jalr), .in2(jal), .in3(or_1_out), .out(priority_encoder_1_out), .en_in(1'b1));  // open: gs, en_out
  Hex_Digit_Display hex_digit_display_1 (.value(LedData[31:28]));  // open: dp
  not not_1 (not_1_out, equ);
  and and_1 (and_1_out, Beq, equ);
  and and_2 (and_2_out, not_1_out, Bne);
  or or_1 (or_1_out, and_1_out, and_2_out, and_3_out);
  Multiplexer #(.select(2), .width(32), .disabled("Z"), .enable("false")) multiplexer_1 (
    .in0(PC_4), .in1(\ALU计算结果 ), .in2(adder_3_out), .in3(adder_2_out), .out(\原始PC ),
    .sel(priority_encoder_1_out));
  Register #(.width(32), .trigger("rising"), .Select("low")) u_PC (
    .D(\下条PC ), .en(or_2_out), .Q(PC), .clk(CLK), .clr(1'b0), .cs(1'b0), .preset(1'b0));
  or or_2 (or_2_out, not_2_out, Go);
  not not_2 (not_2_out, halt);
  or or_3 (W1, IR1_q, d_ff_1_q);
  or or_4 (W2, IR1_2_q, d_ff_2_q);
  or or_5 (W3, IR1_3_q, d_ff_3_q);
  Hex_Digit_Display hex_digit_display_2 (.value(LedData[27:24]));  // open: dp
  Hex_Digit_Display hex_digit_display_3 (.value(LedData[23:20]));  // open: dp
  and and_3 (and_3_out, ge, \单周期硬布线控制器_1_bgeu );
  D_Flip_Flop #(.trigger("rising"), .Pre_Clr_Positions("LEGACY"), .NegatePresetClear("false"), .enable("true"), .NewFFLayout("false")) d_ff_1 (
    .clk(IR1_t), .D(1'b1), .Q(d_ff_1_q), .preset(1'b0), .en(1'b1), .reset(IR1_q));  // open: Qn
  D_Flip_Flop #(.trigger("rising"), .Pre_Clr_Positions("LEGACY"), .NegatePresetClear("false"), .enable("true"), .NewFFLayout("false")) d_ff_2 (
    .clk(IR2_t), .D(1'b1), .Q(d_ff_2_q), .preset(1'b0), .en(1'b1), .reset(IR1_2_q));  // open: Qn
  D_Flip_Flop #(.trigger("rising"), .Pre_Clr_Positions("LEGACY"), .NegatePresetClear("false"), .enable("true"), .NewFFLayout("false")) d_ff_3 (
    .clk(IR3_t), .D(1'b1), .Q(d_ff_3_q), .preset(1'b0), .en(1'b1), .reset(IR1_3_q));  // open: Qn
  Hex_Digit_Display hex_digit_display_4 (.value(LedData[15:12]));  // open: dp
  Hex_Digit_Display hex_digit_display_5 (.value(LedData[19:16]));  // open: dp
  // RiscV_Probe riscv_probe_1: pin names not known; wires that end beside it: IR
  Adder #(.width(32)) adder_1 (.a(PC), .b(32'h4), .out(PC_4), .cin(1'b0));  // open: cout
  or or_6 (or_6_out, d_ff_1_q, IR1_q);
  or or_7 (or_7_out, d_ff_2_q, IR1_2_q);
  or or_8 (or_8_out, d_ff_3_q, IR1_3_q);
  Hex_Digit_Display hex_digit_display_6 (.value(LedData[7:4]));  // open: dp
  Hex_Digit_Display hex_digit_display_7 (.value(LedData[11:8]));  // open: dp
  // Probe on \总周期数 
  ROM #(.addrWidth(10), .dataWidth(32), .Select("high")) rom_1 (.addr(PC[11:2]), .data(IR), .sel(1'b1));
  and and_4 (and_4_out, or_6_out, ~\中断1返回 );  // AND_Gate
  and and_5 (and_5_out, or_7_out, ~\中断2返回 );  // AND_Gate
  and and_6 (and_6_out, or_8_out, ~\中断3返回 );  // AND_Gate
  Hex_Digit_Display hex_digit_display_8 (.value(LedData[3:0]));  // open: dp
  D_Flip_Flop #(.trigger("rising"), .Pre_Clr_Positions("LEGACY"), .NegatePresetClear("false"), .enable("true"), .NewFFLayout("false")) u_IR1 (
    .clk(CLK), .D(and_4_out), .Q(IR1_q), .preset(1'b0), .en(1'b1), .reset(1'b0));  // open: Qn
  D_Flip_Flop #(.trigger("rising"), .Pre_Clr_Positions("LEGACY"), .NegatePresetClear("false"), .enable("true"), .NewFFLayout("false")) IR1_2 (
    .clk(CLK), .D(and_5_out), .Q(IR1_2_q), .preset(1'b0), .en(1'b1), .reset(1'b0));  // open: Qn
  D_Flip_Flop #(.trigger("rising"), .Pre_Clr_Positions("LEGACY"), .NegatePresetClear("false"), .enable("true"), .NewFFLayout("false")) IR1_3 (
    .clk(CLK), .D(and_6_out), .Q(IR1_3_q), .preset(1'b0), .en(1'b1), .reset(1'b0));  // open: Qn
  Comparator #(.width(3), .mode("twosComplement")) comparator_1 (
    .a(3'b110), .b(IR[14:12]), .eq(comparator_1_eq));  // open: gt, lt
  Comparator #(.width(3), .mode("twosComplement")) comparator_2 (
    .a(IR[14:12]), .b(3'b111), .eq(comparator_2_eq));  // open: gt, lt
  Multiplexer #(.select(1), .width(5), .disabled("Z"), .enable("false")) multiplexer_2 (
    .in0(IR[19:15]), .in1(5'b10001), .out(multiplexer_2_out), .sel(ecall));
  Multiplexer #(.select(1), .width(5), .disabled("Z"), .enable("false")) multiplexer_3 (
    .in0(IR[24:20]), .in1(5'b01010), .out(multiplexer_3_out), .sel(ecall));
  // Probe on IR[11:7]
  Multiplexer #(.select(1), .width(12), .disabled("Z"), .enable("false")) multiplexer_4 (
    .in0(IR[31:20]), .in1({IR[31:25], IR[11:7]}), .out(multiplexer_4_out), .sel(S_type));
  and and_7 (and_7_out, comparator_1_eq, csr);
  and and_8 (and_8_out, comparator_2_eq, csr);
  or or_9 (IR1_t, IR1, IRA);
  \单周期硬布线控制器  \u_单周期硬布线控制器_1  (
    .Funct({IR[30], IR[25], IR[14:12]}), .OP(IR[6:2]), .ALU_OP(\单周期硬布线控制器_1_alu_op ), .MemToReg(MemToReg),
    .MemWrite(MemWrite), .ALU_SRC(\单周期硬布线控制器_1_alu_src ), .RegWrite(RegWrite), .ecall(ecall),
    .S_type(S_type), .Jalr(jalr), .Beq(Beq), .JAL(jal), .Bne(Bne), .in_3(IR[21]), .uret(uret),
    .bgeu(\单周期硬布线控制器_1_bgeu ), .csr(csr), .dasb(dasb));  // open: user1, user2
  assign bit_extender_1_out = {{20{multiplexer_4_out[11]}}, multiplexer_4_out};  // Bit_Extender bit_extender_1
  assign bit_extender_2_out = {{20{IR[31]}}, {IR[31], IR[7], IR[30:25], IR[11:8]}};  // Bit_Extender bit_extender_2
  assign bit_extender_3_out = {{12{IR[31]}}, {IR[31], IR[19:12], IR[20], IR[30:21]}};  // Bit_Extender bit_extender_3
  not not_3 (not_3_out, \中断产生 );
  or or_10 (or_10_out, not_3_out, and_7_out);
  or or_11 (or_11_out, and_7_out, and_8_out, \中断产生 , uret, comparator_3_eq);
  Comparator #(.width(16), .mode("twosComplement")) comparator_3 (
    .a({16{1'b0}}), .b(\总周期数 ), .eq(comparator_3_eq));  // open: gt, lt
  or or_12 (IR2_t, IR2, IRB);
  Shifter #(.width(32), .shift("ll")) shifter_1 (.in(bit_extender_2_out), .\dist (5'b00001), .out(shifter_1_out));
  Shifter #(.width(32), .shift("ll")) shifter_2 (.in(bit_extender_3_out), .\dist (5'b00001), .out(shifter_2_out));
  Priority_Encoder #(.select(2), .disabled("Z")) priority_encoder_2 (
    .in0(1'b0), .in1(IR1_q), .in2(IR1_2_q), .in3(IR1_3_q), .out(priority_encoder_2_out),
    .gs(priority_encoder_2_gs), .en_in(1'b1));  // open: en_out
  Register #(.width(1), .trigger("rising"), .Select("low")) \u_中断使能寄存器  (
    .D(or_10_out), .en(or_11_out), .Q(\中断使能寄存器_q ), .clk(CLK), .clr(1'b0), .cs(1'b0), .preset(1'b0));
  Regifile regifile_1 (
    .Din(RDin), .Clk(CLK), .R1(regifile_1_r1), .R2(regifile_1_r2), .WE(RegWrite), .W_num(IR[11:7]),
    .R1_num(multiplexer_2_out), .R2_num(multiplexer_3_out));
  Adder #(.width(32)) adder_2 (.a(shifter_1_out), .b(PC), .out(adder_2_out), .cin(1'b0));  // open: cout
  Adder #(.width(32)) adder_3 (.a(shifter_2_out), .b(PC), .out(adder_3_out), .cin(1'b0));  // open: cout
  Multiplexer #(.select(2), .width(32), .disabled("Z"), .enable("false")) multiplexer_5 (
    .in0({32{1'b0}}), .in1(32'h30ac), .in2(32'h3158), .in3(32'h3204), .out(multiplexer_5_out),
    .sel(priority_encoder_2_out));
  and and_9 (\中断产生 , priority_encoder_2_gs, \中断使能寄存器_q , \当前指令优先 );
  Demultiplexer #(.select(2), .width(1), .tristate("false"), .disabled("Z"), .enable("false")) demultiplexer_1 (
    .out1(\中断1返回 ), .out2(\中断2返回 ), .out3(\中断3返回 ), .in(uret), .sel(priority_encoder_2_out));  // open: out0
  or or_13 (IR3_t, IR3, IRC);
  // Probe on regifile_1_r1
  // Probe on regifile_1_r2
  Multiplexer #(.select(1), .width(32), .disabled("Z"), .enable("false")) multiplexer_6 (
    .in0(regifile_1_r2), .in1(bit_extender_1_out), .out(multiplexer_6_out), .sel(\单周期硬布线控制器_1_alu_src ));
  Pull_Resistor #(.pull(0)) pull_resistor_1 (.node(\中断1返回 ));
  Pull_Resistor #(.pull(0)) pull_resistor_2 (.node(\中断3返回 ));
  or or_14 (or_14_out, \中断产生 , uret);
  not not_4 (not_4_out, \中断产生 );
  ALU alu_1 (
    .X(regifile_1_r1), .Y(multiplexer_6_out), .AluOP(\单周期硬布线控制器_1_alu_op ), .Equal(equ), .Result(\ALU计算结果 ),
    .out_4(ge));  // open: Result_2, out_6
  Comparator #(.width(32), .mode("twosComplement")) comparator_4 (
    .a(regifile_1_r1), .b(32'h22), .eq(comparator_4_eq));  // open: gt, lt
  Register #(.width(32), .trigger("rising"), .Select("low")) register_1 (
    .D(regifile_1_r2), .en(and_10_out), .Q(LedData), .clk(CLK), .clr(1'b0), .cs(1'b0), .preset(1'b0));
  Multiplexer #(.select(2), .width(32), .disabled("Z"), .enable("false")) multiplexer_7 (
    .in0(\原始PC ), .in1(EPC), .in2(multiplexer_5_out), .in3(EPC), .out(\下条PC ), .sel({\中断产生 , uret}));
  Pull_Resistor #(.pull(0)) pull_resistor_3 (.node(\中断2返回 ));
  Counter #(.width(2), .max('h3), .ongoal("wrap"), .trigger("rising"), .behavior("new")) counter_1 (
    .load(1'b0), .count(or_14_out), .Q(counter_1_q), .clk(CLK), .clr(1'b0), .preset(1'b0), .down(not_4_out));  // open: D, carry
  Decoder #(.select(2), .tristate("false"), .disabled("Z"), .enable("false")) decoder_1 (
    .out0(decoder_1_out0), .out1(decoder_1_out1), .out2(decoder_1_out2), .sel(counter_1_q));  // open: out3
  not not_5 (not_5_out, comparator_4_eq);
  and and_10 (and_10_out, ecall, comparator_4_eq);
  Pull_Resistor #(.pull(0)) pull_resistor_4 (.node(pull_resistor_4_node));
  Decoder #(.select(2), .tristate("false"), .disabled("Z"), .enable("false")) decoder_2 (
    .out1(pull_resistor_4_node), .out2(decoder_2_out2), .out3(decoder_2_out3), .sel(priority_encoder_2_out));  // open: out0
  Pull_Resistor #(.pull(0)) pull_resistor_5 (.node(decoder_2_out3));
  and and_11 (and_11_out, \中断产生 , decoder_1_out0);
  and and_12 (and_12_out, decoder_1_out1, \中断产生 );
  and and_13 (and_13_out, decoder_1_out2, \中断产生 );
  not not_6 (not_6_out, halt);
  Counter #(.width(16), .max('hffff), .ongoal("wrap"), .trigger("rising"), .behavior("new")) counter_2 (
    .load(1'b0), .D({16{1'b0}}), .count(not_6_out), .Q(\总周期数 ), .clk(CLK), .clr(1'b0), .down(1'b0));  // open: carry, preset
  \专门给SB画的电路  \u_专门给sb画的电路_1  (.r2(regifile_1_r2), .addr(\ALU计算结果 ), .pre_data(ram_1_data), .MDin(MDin), .dasb(dasb));
  and and_14 (halt, ecall, not_5_out);
  Pull_Resistor #(.pull(0)) pull_resistor_6 (.node(decoder_2_out2));
  and and_15 (and_15_out, pull_resistor_4_node, \中断产生 );
  and and_16 (and_16_out, decoder_2_out2, \中断产生 );
  and and_17 (and_17_out, decoder_2_out3, \中断产生 );
  Register #(.width(2), .trigger("rising"), .Select("low")) IR_id (
    .D(priority_encoder_2_out), .en(and_11_out), .Q(IR_id_q), .clk(CLK), .clr(1'b0), .cs(1'b0), .preset(1'b0));
  Register #(.width(2), .trigger("rising"), .Select("low")) IR_id_2 (
    .D(priority_encoder_2_out), .en(and_12_out), .Q(IR_id_2_q), .clk(CLK), .clr(1'b0), .cs(1'b0),
    .preset(1'b0));
  Register #(.width(2), .trigger("rising"), .Select("low")) IR_id_3 (
    .D(priority_encoder_2_out), .en(and_13_out), .Q(IR_id_3_q), .clk(CLK), .clr(1'b0), .cs(1'b0),
    .preset(1'b0));
  Register #(.width(32), .trigger("rising"), .Select("low")) u_EPC (
    .D(\原始PC ), .en(and_15_out), .Q(EPC_q), .clk(CLK), .clr(1'b0), .cs(1'b0), .preset(1'b0));
  Register #(.width(32), .trigger("rising"), .Select("low")) EPC_2 (
    .D(\原始PC ), .en(and_16_out), .Q(EPC_2_q), .clk(CLK), .clr(1'b0), .cs(1'b0), .preset(1'b0));
  Register #(.width(32), .trigger("rising"), .Select("low")) EPC_3 (
    .D(\原始PC ), .en(and_17_out), .Q(EPC_3_q), .clk(CLK), .clr(1'b0), .cs(1'b0), .preset(1'b0));
  Multiplexer #(.select(2), .width(2), .disabled("Z"), .enable("false")) multiplexer_8 (
    .in1(IR_id_q), .in2(IR_id_2_q), .in3(IR_id_3_q), .out(multiplexer_8_out), .sel(counter_1_q));  // open: in0
  Multiplexer #(.select(2), .width(32), .disabled("Z"), .enable("false")) multiplexer_9 (
    .in1(EPC_q), .in2(EPC_2_q), .in3(EPC_3_q), .out(EPC), .sel(multiplexer_8_out));  // open: in0
  D_Flip_Flop #(.trigger("high"), .Pre_Clr_Positions("LEGACY"), .NegatePresetClear("false"), .enable("true"), .NewFFLayout("false")) d_ff_4 (.Q(d_ff_4_q));  // open: clk, D, Qn, preset, en, reset
  // Probe on 13'hc
  RAM #(.addrWidth(10), .dataWidth(32), .bus("separate"), .Select("high")) ram_1 (
    .addr(\ALU计算结果 [11:2]), .din(MDin), .data(ram_1_data), .str(MemWrite), .sel(1'b1), .clk(CLK), .ld(1'b1),
    .clr(1'b0));
  Comparator #(.width(2), .mode("unsigned")) comparator_5 (
    .a(multiplexer_8_out), .b(priority_encoder_2_out), .lt(\当前指令优先 ));  // open: gt, eq
  Pull_Resistor #(.pull(1)) pull_resistor_7 (.node(\当前指令优先 ));
  Comparator #(.width(13), .mode("twosComplement")) comparator_6 (
    .a(CNT_num), .b(13'hc), .eq(comparator_6_eq), .lt(comparator_6_lt));  // open: gt
  Clock #(.highDuration(1), .lowDuration(1)) clock_1 (.out(clock_1_out));
  Comparator #(.width(16), .mode("twosComplement")) comparator_7 (
    .a(16'h258), .b(\总周期数 ), .eq(comparator_7_eq));  // open: gt, lt
  Comparator #(.width(16), .mode("twosComplement")) comparator_8 (
    .a(\总周期数 ), .b(16'h1), .eq(comparator_8_eq));  // open: gt, lt
  Comparator #(.width(16), .mode("twosComplement")) comparator_9 (
    .a(\总周期数 ), .b(16'h4), .eq(comparator_9_eq));  // open: gt, lt
  Comparator #(.width(16), .mode("twosComplement")) comparator_10 (
    .a(\总周期数 ), .b(16'h7), .eq(comparator_10_eq));  // open: gt, lt
  Comparator #(.width(16), .mode("twosComplement")) comparator_11 (
    .a(\总周期数 ), .b(16'h241), .eq(comparator_11_eq));  // open: gt, lt
  Multiplexer #(.select(2), .width(32), .disabled("Z"), .enable("false")) multiplexer_10 (
    .in0(\ALU计算结果 ), .in1(ram_1_data), .in2(PC_4), .out(RDin), .sel({or_15_out[1], MemToReg}));  // open: in3
  or or_15 (or_15_out[1], jal, jalr);
  Counter #(.width(13), .max('h1fff), .ongoal("stay"), .trigger("rising"), .behavior("old")) counter_3 (
    .count(comparator_6_lt), .Q(CNT_num), .clk(clock_1_out));  // open: load, D, carry, clr, preset
  or or_16 (or_16_out, comparator_7_eq, comparator_8_eq);
  assign IRA = or_16_out ? ~CLK : 1'bz;  // Controlled_Inverter controlled_inverter_1
  assign IRB = comparator_9_eq ? ~CLK : 1'bz;  // Controlled_Inverter controlled_inverter_2
  or or_17 (or_17_out, comparator_10_eq, comparator_11_eq);
  assign IRC = or_17_out ? ~CLK : 1'bz;  // Controlled_Inverter controlled_inverter_3
  nand nand_1 (nand_1_out, d_ff_4_q, comparator_6_eq);
  Pull_Resistor #(.pull(0)) pull_resistor_8 (.node(IRA));
  Pull_Resistor #(.pull(0)) pull_resistor_9 (.node(IRB));
  Pull_Resistor #(.pull(0)) pull_resistor_10 (.node(IRC));
  assign CLK = nand_1_out ? clock_1_out : 1'bz;  // Controlled_Buffer controlled_buffer_1
  Pull_Resistor #(.pull(1)) pull_resistor_11 (.node(CLK));

  // Notes on the sheet:
  //   中断源
  //   中断等待指示
  //   总复位信号应将除ROM以外所有存储组件全部清零
  //   选择PC
  //   数码管输出
  //   指令探针
  //   指令存储器
  //   数码管输出应该用寄存器锁存，否则显示数据只能一闪而过
  //   指令字
  //   contents of rom_1 (hex, n*v repeats v):
  //   7d000113 100413 1f41993 41f9d993 433 c00913 800b13 140413 f47413 800293 100313 499993 89e9b3 1300533
  //   2200893 73 406282b3 fe0294e3 140413 f00f93 1f47433 1c41413 800293 100313 49d993 89e9b3 1300533
  //   2200893 73 406282b3 fe0294e3 1c45413 406b0b33 b0463 f95ff06f 2b3 fff2c293 1029293 fff2e293 500533
  //   2200893 73 f5dff06f 1112023 410113 a12023 410113 812023 410113 1312023 410113 1412023 410113 1512023
  //   410113 1612023 410113 40e073 100b13 300a13 100a93 1600433 441413 14469b3 1300533 2200893 73 fe0416e3
  //   415a0a33 fe0a10e3 40f073 ffc10113 12b03 ffc10113 12a83 ffc10113 12a03 ffc10113 12983 ffc10113 12403
  //   ffc10113 12503 ffc10113 12883 200073 1112023 410113 a12023 410113 812023 410113 1312023 410113
  //   1412023 410113 1512023 410113 1612023 410113 40e073 200b13 300a13 100a93 1600433 441413 14469b3
  //   1300533 2200893 73 fe0416e3 415a0a33 fe0a10e3 40f073 ffc10113 12b03 ffc10113 12a83 ffc10113 12a03
  //   ffc10113 12983 ffc10113 12403 ffc10113 12503 ffc10113 12883 200073 1112023 410113 a12023 410113
  //   812023 410113 1312023 410113 1412023 410113 1512023 410113 1612023 410113 40e073 300b13 300a13
  //   100a93 1600433 441413 14469b3 1300533 2200893 73 fe0416e3 415a0a33 fe0a10e3 40f073 ffc10113 12b03
  //   ffc10113 12a83 ffc10113 12a03 ffc10113 12983 ffc10113 12403 ffc10113 12503 ffc10113 12883 200073
  //   Reset 
  //   Reset 
  //   Reset 
  //   JAL
  //   JALR
  //   URET
  //   rs1
  //   rs2
  //   rd
  //   I指令
  //   S指令
  //   B指令
  //   J指令
  //   bgeu
  //   跳转地址生成
  //   Beq
  //   Bne
  //   MemToReg
  //   MemWrite
  //   AluOP
  //   AluSrcB
  //   RegWrite
  //   中断PC计算
  //   中断使能维护
  //   中断返回信号
  //   ecall的LED显示
  //   中断数量计数
  //   为方便自动评测，需要输出PC，IR，寄存器堆写如数据RDin
  //   EPC寄存器堆维护
  //   RAM写使能MemWrite、RAM写入数据MDin等信号
  //   实现sb
  //   中断优先级确定
  //   数据存储器
  //   控制位
  //   暂停节拍，不能为0
  //   戳工具置1进入计数暂停模式，ctrl+k时钟自动运行到对应节拍暂停
  //   ctrl+k关闭时钟连续运行，将控制位置零，进入单步调试模式调试
  //   多级中断测试信号模拟器
  //   选择RDin
  //   可计数暂停的时钟源
endmodule

module \流水线_中断  (
  input  IR1,
  input  IR2,
  input  IR3,
  output RegWrite,
  output MemWrite,
  output [31:0] PC,
  output [31:0] IR,
  output [31:0] RDin,
  output [31:0] MDin,
  output [31:0] LedData
);

  wire and_1_out, and_2_out, and_3_out, and_4_out, and_5_out, and_6_out, and_8_out, and_9_out, and_10_out,
       and_11_out, and_12_out, and_13_out, and_15_out, and_16_out, and_17_out, and_18_out, and_19_out,
       and_20_out, BranchNum, BranchOK, \B型指令分支跳转 , CLK, clock_1_out, comparator_1_eq, comparator_1_lt,
       comparator_2_eq, comparator_3_eq, comparator_4_eq, comparator_5_eq, comparator_6_eq, comparator_7_eq,
       comparator_8_eq, comparator_9_eq, comparator_10_eq, d_ff_1_q, d_ff_3_q, d_ff_4_q, d_ff_5_q,
       decoder_1_out1, decoder_1_out2, decoder_1_out3, decoder_2_out0, decoder_2_out1, decoder_2_out2, equ,
       ex_mem_1_dasb_2, ex_mem_1_halt_2, ex_mem_1_jal_2, ex_mem_1_jalr_2, ex_mem_1_memtoreg_2,
       ex_mem_1_regwrite_2, ex_mem_1_uret_2, excsr, exdasb, execall, exhalt, ge, Go, halt, id_ex_1_alusrcb_2,
       id_ex_1_beq_2, id_ex_1_bgeu_2, id_ex_1_bne_2, id_ex_1_jal_2, id_ex_1_memtoreg_2, id_ex_1_memwrite_2,
       id_ex_1_regwrite_2, idecall, IR1_2_q, IR1_3_q, IR1_q, IR1_t, IR2_t, IR3_t, IRA, IRB, IRC, jal,
       \J型指令分支跳转 , mem_wb_1_halt_2, mem_wb_1_jal_2, mem_wb_1_jalr_2, nand_1_out, not_1_out, not_2_out,
       not_3_out, not_4_out, not_5_out, not_6_out, not_7_out, not_8_out, not_9_out, not_10_out, not_11_out,
       or_1_out, or_3_out, or_8_out, or_12_out, or_13_out, or_17_out, or_18_out, or_19_out, or_20_out,
       or_21_out, or_22_out, priority_encoder_1_gs, refresh, S_type, stall, uret, W1, W2, W3, \中断1返回 ,
       \中断2返回 , \中断3返回 , \中断产生 , \中断使能寄存器_q , \单周期硬布线控制器_1_alu_src , \单周期硬布线控制器_1_beq , \单周期硬布线控制器_1_bgeu ,
       \单周期硬布线控制器_1_bne , \单周期硬布线控制器_1_csr , \单周期硬布线控制器_1_dasb , \单周期硬布线控制器_1_jalr , \单周期硬布线控制器_1_memtoreg ,
       \单周期硬布线控制器_1_memwrite , \单周期硬布线控制器_1_regwrite , \单周期硬布线控制器_1_uret , \单周期硬布线控制器_1_user1 ,
       \单周期硬布线控制器_1_user2 , \存在分支 , \当前指令优先 , \清空 , \清空_t , \阻塞 ;
  wire [1:0] counter_7_q, d_ff_6_q, id_ex_1_jalr_2, id_ex_1_r1_forward_2, id_ex_1_r2_forward_2, IR_id_2_q,
       IR_id_3_q, IR_id_q, mem_wb_1_memtoreg_2, multiplexer_13_out, priority_encoder_1_out, r1_forward,
       r2_forward;
  wire [3:0] id_ex_1_aluop_2, \单周期硬布线控制器_1_alu_op ;
  wire [4:0] ex_mem_1_rd_a_2, id_ex_1_rd_a_2, multiplexer_2_out, multiplexer_3_out, \写回地址 ;
  wire [11:0] multiplexer_4_out;
  wire [12:0] CNT_num;
  wire [15:0] \LoadUse次数 , \总周期数 , \插入气泡数 , \无条件分支数 , \条件分支成功数 ;
  wire [31:0] \ALU计算结果 , bit_extender_1_out, bit_extender_2_out, bit_extender_3_out, EPC, EPC_2_q, EPC_3_q,
       EPC_q, EX_IR, ex_mem_1_pc_4_2, ex_mem_1_r2_2, EX_PC, exr1, exr2, id_ex_1_imm1_2, id_ex_1_imm2_2,
       id_ex_1_pc_4_2, ID_IR, ID_PC, if_id_1_pc_4_2, IF_IR, IF_PC, \jal指令地址 , MEM_IR, MEM_PC,
       mem_wb_1_memdata_2, mem_wb_1_pc_4_2, mem_wb_1_res_2, \memALU计算结果 , multiplexer_5_out,
       multiplexer_8_out, multiplexer_10_out, multiplexer_12_out, PC_4, ram_1_data, regifile_1_r1,
       regifile_1_r2, rer1, rer2, shifter_1_out, WB_IR, WB_PC, \下条PC , \原始PC ;

  Button \u_继续运行  (.out(Go));
  Button _1 ();  // open: out
  Button _2 ();  // open: out
  Button _3 ();  // open: out
  // Probe on \总周期数 
  // Probe on \总周期数 
  LED #(.active("true")) led_1 (.in(W1));
  LED #(.active("true")) led_2 (.in(W2));
  LED #(.active("true")) led_3 (.in(W3));
  Multiplexer #(.select(2), .width(32), .disabled("Z"), .enable("false")) multiplexer_1 (
    .in0(PC_4), .in1(\ALU计算结果 ), .in2(\jal指令地址 ), .out(\原始PC ), .sel(id_ex_1_jalr_2));  // open: in3
  and and_1 (and_1_out, or_1_out, not_1_out);
  or or_1 (or_1_out, not_2_out, Go);
  not not_1 (not_1_out, \阻塞 );
  not not_2 (not_2_out, halt);
  Hex_Digit_Display hex_digit_display_1 (.value(LedData[31:28]));  // open: dp
  // Probe on IF_PC[19:0]
  // RiscV_Probe riscv_probe_1: pin names not known; wires that end beside it: IRA, IRB, IRC, IF_IR
  Register #(.width(32), .trigger("rising"), .Select("low")) u_PC (
    .D(\下条PC ), .en(and_1_out), .Q(IF_PC), .clk(CLK), .clr(1'b0), .cs(1'b0), .preset(1'b0));
  Hex_Digit_Display hex_digit_display_2 (.value(LedData[23:20]));  // open: dp
  Hex_Digit_Display hex_digit_display_3 (.value(LedData[27:24]));  // open: dp
  // Probe on ID_PC[19:0]
  // RiscV_Probe riscv_probe_2: pin names not known; wires that end beside it: ID_IR
  Adder #(.width(32)) adder_1 (.a(IF_PC), .b(32'h4), .out(PC_4), .cin(1'b0));  // open: cout
  Hex_Digit_Display hex_digit_display_4 (.value(LedData[19:16]));  // open: dp
  Hex_Digit_Display hex_digit_display_5 (.value(LedData[15:12]));  // open: dp
  // RiscV_Probe riscv_probe_3: pin names not known; wires that end beside it: IF_IR
  Hex_Digit_Display hex_digit_display_6 (.value(LedData[11:8]));  // open: dp
  Hex_Digit_Display hex_digit_display_7 (.value(LedData[7:4]));  // open: dp
  // Probe on \总周期数 
  // Probe on EX_PC[19:0]
  // RiscV_Probe riscv_probe_4: pin names not known; wires that end beside it: EX_IR
  ROM #(.addrWidth(10), .dataWidth(32), .Select("high")) rom_1 (.addr(IF_PC[11:2]), .data(IF_IR), .sel(1'b1));
  Hex_Digit_Display hex_digit_display_8 (.value(LedData[3:0]));  // open: dp
  or or_2 (\存在分支 , id_ex_1_jalr_2[0], id_ex_1_jalr_2[1]);
  IF_ID if_id_1 (
    .PC(IF_PC), .PC_4(PC_4), .IR(IF_IR), .PC_2(ID_PC), .PC_4_2(if_id_1_pc_4_2), .IR_2(ID_IR), .reset(1'b0),
    .refresh(\存在分支 ), .en(and_2_out), .CLK(CLK));  // open: 预测跳转, 预测跳转_2
  and and_2 (and_2_out, or_3_out, not_3_out);
  or or_3 (or_3_out, not_4_out, Go);
  not not_3 (not_3_out, \阻塞 );
  not not_4 (not_4_out, halt);
  // Probe on MEM_PC[19:0]
  // RiscV_Probe riscv_probe_5: pin names not known; wires that end beside it: MEM_IR
  or or_4 (IR1_t, IR1, IRA);
  Multiplexer #(.select(1), .width(5), .disabled("Z"), .enable("false")) multiplexer_2 (
    .in0(ID_IR[19:15]), .in1(5'b10001), .out(multiplexer_2_out), .sel(idecall));
  Multiplexer #(.select(1), .width(5), .disabled("Z"), .enable("false")) multiplexer_3 (
    .in0(ID_IR[24:20]), .in1(5'b01010), .out(multiplexer_3_out), .sel(idecall));
  Multiplexer #(.select(1), .width(12), .disabled("Z"), .enable("false")) multiplexer_4 (
    .in0(ID_IR[31:20]), .in1({ID_IR[31:25], ID_IR[11:7]}), .out(multiplexer_4_out), .sel(S_type));
  or or_5 (IR2_t, IR2, IRB);
  // Probe on WB_PC[19:0]
  // RiscV_Probe riscv_probe_6: pin names not known; wires that end beside it: WB_IR
  \单周期硬布线控制器  \u_单周期硬布线控制器_1  (
    .Funct({ID_IR[30], ID_IR[25], ID_IR[14:12]}), .OP(ID_IR[6:2]), .ALU_OP(\单周期硬布线控制器_1_alu_op ),
    .MemToReg(\单周期硬布线控制器_1_memtoreg ), .MemWrite(\单周期硬布线控制器_1_memwrite ), .ALU_SRC(\单周期硬布线控制器_1_alu_src ),
    .RegWrite(\单周期硬布线控制器_1_regwrite ), .ecall(idecall), .S_type(S_type), .Jalr(\单周期硬布线控制器_1_jalr ),
    .Beq(\单周期硬布线控制器_1_beq ), .JAL(jal), .Bne(\单周期硬布线控制器_1_bne ), .in_3(ID_IR[21]), .uret(\单周期硬布线控制器_1_uret ),
    .bgeu(\单周期硬布线控制器_1_bgeu ), .csr(\单周期硬布线控制器_1_csr ), .dasb(\单周期硬布线控制器_1_dasb ),
    .user1(\单周期硬布线控制器_1_user1 ), .user2(\单周期硬布线控制器_1_user2 ));
  assign bit_extender_1_out = {{20{multiplexer_4_out[11]}}, multiplexer_4_out};  // Bit_Extender bit_extender_1
  assign bit_extender_2_out = {{20{ID_IR[31]}}, {ID_IR[31], ID_IR[7], ID_IR[30:25], ID_IR[11:8]}};  // Bit_Extender bit_extender_2
  assign bit_extender_3_out = {{12{ID_IR[31]}}, {ID_IR[31], ID_IR[19:12], ID_IR[20], ID_IR[30:21]}};  // Bit_Extender bit_extender_3
  not not_5 (not_5_out, CLK);
  Multiplexer #(.select(1), .width(32), .disabled("Z"), .enable("false")) multiplexer_5 (
    .in0(bit_extender_2_out), .in1(bit_extender_3_out), .out(multiplexer_5_out), .sel(jal));
  or or_6 (IR3_t, IR3, IRC);
  D_Flip_Flop #(.trigger("high"), .Pre_Clr_Positions("LEGACY"), .NegatePresetClear("false"), .enable("true"), .NewFFLayout("false")) d_ff_1 (.Q(d_ff_1_q));  // open: clk, D, Qn, preset, en, reset
  // Probe on 13'h241
  Comparator #(.width(13), .mode("twosComplement")) comparator_1 (
    .a(CNT_num), .b(13'h241), .eq(comparator_1_eq), .lt(comparator_1_lt));  // open: gt
  Clock #(.highDuration(1), .lowDuration(1)) clock_1 (.out(clock_1_out));
  Regifile regifile_1 (
    .Din(RDin), .Clk(not_5_out), .R1(regifile_1_r1), .R2(regifile_1_r2), .WE(RegWrite), .W_num(\写回地址 ),
    .R1_num(multiplexer_2_out), .R2_num(multiplexer_3_out));
  not not_6 (not_6_out, halt);
  nand nand_1 (nand_1_out, d_ff_1_q, comparator_1_eq);
  Counter #(.width(13), .max('h1fff), .ongoal("stay"), .trigger("rising"), .behavior("old")) counter_1 (
    .count(comparator_1_lt), .Q(CNT_num), .clk(clock_1_out));  // open: load, D, carry, clr, preset
  \冲突处理_redirect  \u_冲突处理_redirect_1  (
    .exrd(id_ex_1_rd_a_2), .memRegWrite(ex_mem_1_regwrite_2), .ecall(idecall), .user1(\单周期硬布线控制器_1_user1 ),
    .IR(ID_IR), .memrd(ex_mem_1_rd_a_2), .user2(\单周期硬布线控制器_1_user2 ), .exRegWrite(id_ex_1_regwrite_2),
    .\存在分支 (\存在分支 ), .\阻塞 (\阻塞 ), .\清空 (\清空 ), .r1_forward(r1_forward), .r2_forward(r2_forward),
    .exMemToReg(id_ex_1_memtoreg_2));
  or or_7 (id_ex_1_jalr_2[1], \B型指令分支跳转 , id_ex_1_jal_2);
  ID_EX id_ex_1 (
    .Beq(\单周期硬布线控制器_1_beq ), .Bne(\单周期硬布线控制器_1_bne ), .MemToReg(\单周期硬布线控制器_1_memtoreg ),
    .MemWrite(\单周期硬布线控制器_1_memwrite ), .AluSrcB(\单周期硬布线控制器_1_alu_src ), .RegWrite(\单周期硬布线控制器_1_regwrite ),
    .JAL(jal), .JALR(\单周期硬布线控制器_1_jalr ), .URET(\单周期硬布线控制器_1_uret ), .csr(\单周期硬布线控制器_1_csr ),
    .bgeu(\单周期硬布线控制器_1_bgeu ), .S_type(S_type), .dasb(\单周期硬布线控制器_1_dasb ), .AluOP(\单周期硬布线控制器_1_alu_op ),
    .r1(regifile_1_r1), .r2(regifile_1_r2), .rd_a(ID_IR[11:7]), .imm1(bit_extender_1_out),
    .imm2(multiplexer_5_out), .PC(ID_PC), .PC_4(if_id_1_pc_4_2), .IR(ID_IR), .Beq_2(id_ex_1_beq_2),
    .Bne_2(id_ex_1_bne_2), .MemToReg_2(id_ex_1_memtoreg_2), .MemWrite_2(id_ex_1_memwrite_2),
    .AluSrcB_2(id_ex_1_alusrcb_2), .RegWrite_2(id_ex_1_regwrite_2), .JAL_2(id_ex_1_jal_2),
    .JALR_2(id_ex_1_jalr_2[0]), .URET_2(uret), .csr_2(excsr), .bgeu_2(id_ex_1_bgeu_2), .dasb_2(exdasb),
    .AluOP_2(id_ex_1_aluop_2), .r1_2(exr1), .r2_2(exr2), .rd_a_2(id_ex_1_rd_a_2), .imm1_2(id_ex_1_imm1_2),
    .imm2_2(id_ex_1_imm2_2), .PC_2(EX_PC), .PC_4_2(id_ex_1_pc_4_2), .IR_2(EX_IR), .reset(1'b0),
    .refresh(\清空_t ), .en(or_8_out), .CLK(CLK), .ecall(idecall), .ecall_2(execall), .r1_forward(r1_forward),
    .r1_forward_2(id_ex_1_r1_forward_2), .r2_forward(r2_forward), .r2_forward_2(id_ex_1_r2_forward_2));  // open: S_type_2, 预测跳转, 预测跳转_2
  or or_8 (or_8_out, not_6_out, Go);
  Multiplexer #(.select(2), .width(32), .disabled("Z"), .enable("false")) multiplexer_6 (
    .in0(exr1), .in1(RDin), .in2(\memALU计算结果 ), .out(rer1), .sel(id_ex_1_r1_forward_2));  // open: in3
  assign CLK = nand_1_out ? clock_1_out : 1'bz;  // Controlled_Buffer controlled_buffer_1
  or or_9 (\B型指令分支跳转 , and_4_out, and_5_out, and_3_out);
  Shifter #(.width(32), .shift("ll")) shifter_1 (.in(id_ex_1_imm2_2), .\dist (5'b00001), .out(shifter_1_out));
  Adder #(.width(32)) adder_2 (.a(shifter_1_out), .b(EX_PC), .out(\jal指令地址 ), .cin(1'b0));  // open: cout
  Multiplexer #(.select(2), .width(32), .disabled("Z"), .enable("false")) multiplexer_7 (
    .in0(exr2), .in1(RDin), .in2(\memALU计算结果 ), .out(rer2), .sel(id_ex_1_r2_forward_2));  // open: in3
  Pull_Resistor #(.pull(1)) pull_resistor_1 (.node(CLK));
  and and_3 (and_3_out, id_ex_1_beq_2, equ);
  not not_7 (not_7_out, equ);
  Multiplexer #(.select(1), .width(32), .disabled("Z"), .enable("false")) multiplexer_8 (
    .in0(rer2), .in1(id_ex_1_imm1_2), .out(multiplexer_8_out), .sel(id_ex_1_alusrcb_2));
  Comparator #(.width(32), .mode("twosComplement")) comparator_2 (
    .a(rer1), .b(32'h22), .eq(comparator_2_eq));  // open: gt, lt
  Register #(.width(32), .trigger("rising"), .Select("low")) register_1 (
    .D(rer2), .en(and_6_out), .Q(LedData), .clk(CLK), .clr(1'b0), .cs(1'b0), .preset(1'b0));
  Counter #(.width(16), .max('hffff), .ongoal("wrap"), .trigger("rising"), .behavior("new")) counter_2 (
    .count(CLK), .Q(\总周期数 ), .clk(and_8_out));  // open: load, D, carry, clr, preset, down
  and and_4 (and_4_out, id_ex_1_bgeu_2, ge);
  and and_5 (and_5_out, not_7_out, id_ex_1_bne_2);
  ALU alu_1 (
    .X(rer1), .Y(multiplexer_8_out), .AluOP(id_ex_1_aluop_2), .Equal(equ), .Result(\ALU计算结果 ), .out_4(ge));  // open: Result_2, out_6
  not not_8 (not_8_out, comparator_2_eq);
  and and_6 (and_6_out, execall, comparator_2_eq);
  or or_10 (\J型指令分支跳转 , id_ex_1_jalr_2[0], id_ex_1_jal_2);
  and and_7 (exhalt, execall, not_8_out);
  Counter #(.width(16), .max('hffff), .ongoal("wrap"), .trigger("rising"), .behavior("new")) counter_3 (
    .count(BranchNum), .Q(\无条件分支数 ), .clk(and_8_out));  // open: load, D, carry, clr, preset, down
  EX_MEM ex_mem_1 (
    .MemToReg(id_ex_1_memtoreg_2), .MemWrite(id_ex_1_memwrite_2), .RegWrite(id_ex_1_regwrite_2),
    .JAL(id_ex_1_jal_2), .JALR(id_ex_1_jalr_2[0]), .URET(uret), .dasb(exdasb), .halt(exhalt),
    .res(\ALU计算结果 ), .rd_a(id_ex_1_rd_a_2), .r2(rer2), .PC(EX_PC), .PC_4(id_ex_1_pc_4_2), .IR(EX_IR),
    .MemToReg_2(ex_mem_1_memtoreg_2), .MemWrite_2(MemWrite), .RegWrite_2(ex_mem_1_regwrite_2),
    .JAL_2(ex_mem_1_jal_2), .JALR_2(ex_mem_1_jalr_2), .URET_2(ex_mem_1_uret_2), .dasb_2(ex_mem_1_dasb_2),
    .halt_2(ex_mem_1_halt_2), .res_2(\memALU计算结果 ), .rd_a_2(ex_mem_1_rd_a_2), .r2_2(ex_mem_1_r2_2),
    .PC_2(MEM_PC), .PC_4_2(ex_mem_1_pc_4_2), .IR_2(MEM_IR), .reset(1'b0), .refresh(1'b0), .en(or_8_out),
    .CLK(CLK));
  Counter #(.width(16), .max('hffff), .ongoal("wrap"), .trigger("rising"), .behavior("new")) counter_4 (
    .count(BranchOK), .Q(\条件分支成功数 ), .clk(and_8_out));  // open: load, D, carry, clr, preset, down
  \专门给SB画的电路  \u_专门给sb画的电路_1  (
    .r2(ex_mem_1_r2_2), .addr(\memALU计算结果 ), .pre_data(ram_1_data), .MDin(MDin), .dasb(ex_mem_1_dasb_2));
  Counter #(.width(16), .max('hffff), .ongoal("wrap"), .trigger("rising"), .behavior("new")) counter_5 (
    .count(refresh), .Q(\插入气泡数 ), .clk(and_8_out));  // open: load, D, carry, clr, preset, down
  RAM #(.addrWidth(10), .dataWidth(32), .bus("separate"), .Select("high")) ram_1 (
    .addr(\memALU计算结果 [11:2]), .din(MDin), .data(ram_1_data), .str(MemWrite), .sel(1'b1), .clk(CLK),
    .ld(1'b1), .clr(1'b0));
  MEM_WB mem_wb_1 (
    .MemToReg(ex_mem_1_memtoreg_2), .RegWrite(ex_mem_1_regwrite_2), .JAL(ex_mem_1_jal_2),
    .JALR(ex_mem_1_jalr_2), .URET(ex_mem_1_uret_2), .dasb(ex_mem_1_dasb_2), .halt(ex_mem_1_halt_2),
    .res(\memALU计算结果 ), .rd_a(ex_mem_1_rd_a_2), .MemData(ram_1_data), .PC(MEM_PC), .PC_4(ex_mem_1_pc_4_2),
    .IR(MEM_IR), .MemToReg_2(mem_wb_1_memtoreg_2[0]), .RegWrite_2(RegWrite), .JAL_2(mem_wb_1_jal_2),
    .JALR_2(mem_wb_1_jalr_2), .halt_2(mem_wb_1_halt_2), .res_2(mem_wb_1_res_2), .rd_a_2(\写回地址 ),
    .MemData_2(mem_wb_1_memdata_2), .PC_2(WB_PC), .PC_4_2(mem_wb_1_pc_4_2), .IR_2(WB_IR), .reset(1'b0),
    .refresh(1'b0), .en(or_8_out), .CLK(CLK));  // open: URET_2, dasb_2
  Counter #(.width(16), .max('hffff), .ongoal("wrap"), .trigger("rising"), .behavior("new")) counter_6 (
    .count(stall), .Q(\LoadUse次数 ), .clk(and_8_out));  // open: load, D, carry, clr, preset, down
  or or_11 (mem_wb_1_memtoreg_2[1], mem_wb_1_jal_2, mem_wb_1_jalr_2);
  and and_8 (and_8_out, CLK, not_9_out);
  not not_9 (not_9_out, halt);
  Multiplexer #(.select(2), .width(32), .disabled("Z"), .enable("false")) multiplexer_9 (
    .in0(mem_wb_1_res_2), .in1(mem_wb_1_memdata_2), .in2(mem_wb_1_pc_4_2), .out(RDin),
    .sel(mem_wb_1_memtoreg_2));  // open: in3
  D_Flip_Flop #(.trigger("rising"), .Pre_Clr_Positions("ABOVE_BELOW"), .NegatePresetClear("false"), .enable("true"), .NewFFLayout("true")) d_ff_2 (
    .clk(mem_wb_1_halt_2), .D(1'b1), .Q(halt), .preset(1'b0), .en(1'b1), .reset(Go));  // open: Qn
  Comparator #(.width(16), .mode("twosComplement")) comparator_3 (
    .a(16'h258), .b(\总周期数 ), .eq(comparator_3_eq));  // open: gt, lt
  Comparator #(.width(16), .mode("twosComplement")) comparator_4 (
    .a(\总周期数 ), .b(16'h1), .eq(comparator_4_eq));  // open: gt, lt
  Comparator #(.width(16), .mode("twosComplement")) comparator_5 (
    .a(\总周期数 ), .b(16'h4), .eq(comparator_5_eq));  // open: gt, lt
  Comparator #(.width(16), .mode("twosComplement")) comparator_6 (
    .a(\总周期数 ), .b(16'h7), .eq(comparator_6_eq));  // open: gt, lt
  Comparator #(.width(16), .mode("twosComplement")) comparator_7 (
    .a(\总周期数 ), .b(16'h241), .eq(comparator_7_eq));  // open: gt, lt
  or or_12 (or_12_out, comparator_3_eq, comparator_4_eq);
  assign IRA = or_12_out ? ~CLK : 1'bz;  // Controlled_Inverter controlled_inverter_1
  assign IRB = comparator_5_eq ? ~CLK : 1'bz;  // Controlled_Inverter controlled_inverter_2
  or or_13 (or_13_out, comparator_6_eq, comparator_7_eq);
  assign IRC = or_13_out ? ~CLK : 1'bz;  // Controlled_Inverter controlled_inverter_3
  Pull_Resistor #(.pull(0)) pull_resistor_2 (.node(IRA));
  Pull_Resistor #(.pull(0)) pull_resistor_3 (.node(IRB));
  Pull_Resistor #(.pull(0)) pull_resistor_4 (.node(IRC));
  or or_14 (W1, IR1_3_q, d_ff_3_q);
  or or_15 (W2, IR1_q, d_ff_4_q);
  or or_16 (W3, IR1_2_q, d_ff_5_q);
  D_Flip_Flop #(.trigger("rising"), .Pre_Clr_Positions("LEGACY"), .NegatePresetClear("false"), .enable("true"), .NewFFLayout("false")) d_ff_3 (
    .clk(IR1_t), .D(1'b1), .Q(d_ff_3_q), .preset(1'b0), .en(1'b1), .reset(IR1_3_q));  // open: Qn
  D_Flip_Flop #(.trigger("rising"), .Pre_Clr_Positions("LEGACY"), .NegatePresetClear("false"), .enable("true"), .NewFFLayout("false")) d_ff_4 (
    .clk(IR2_t), .D(1'b1), .Q(d_ff_4_q), .preset(1'b0), .en(1'b1), .reset(IR1_q));  // open: Qn
  D_Flip_Flop #(.trigger("rising"), .Pre_Clr_Positions("LEGACY"), .NegatePresetClear("false"), .enable("true"), .NewFFLayout("false")) d_ff_5 (
    .clk(IR3_t), .D(1'b1), .Q(d_ff_5_q), .preset(1'b0), .en(1'b1), .reset(IR1_2_q));  // open: Qn
  or or_17 (or_17_out, d_ff_3_q, IR1_3_q);
  or or_18 (or_18_out, d_ff_4_q, IR1_q);
  and and_9 (and_9_out, or_18_out, ~\中断2返回 );  // AND_Gate
  or or_19 (or_19_out, d_ff_5_q, IR1_2_q);
  and and_10 (and_10_out, or_19_out, ~\中断3返回 );  // AND_Gate
  and and_11 (and_11_out, or_17_out, ~\中断1返回 );  // AND_Gate
  D_Flip_Flop #(.trigger("rising"), .Pre_Clr_Positions("LEGACY"), .NegatePresetClear("false"), .enable("true"), .NewFFLayout("false")) u_IR1 (
    .clk(CLK), .D(and_9_out), .Q(IR1_q), .preset(1'b0), .en(1'b1), .reset(1'b0));  // open: Qn
  D_Flip_Flop #(.trigger("rising"), .Pre_Clr_Positions("LEGACY"), .NegatePresetClear("false"), .enable("true"), .NewFFLayout("false")) IR1_2 (
    .clk(CLK), .D(and_10_out), .Q(IR1_2_q), .preset(1'b0), .en(1'b1), .reset(1'b0));  // open: Qn
  Comparator #(.width(3), .mode("twosComplement")) comparator_8 (
    .a(3'b110), .b(EX_IR[14:12]), .eq(comparator_8_eq));  // open: gt, lt
  Comparator #(.width(3), .mode("twosComplement")) comparator_9 (
    .a(EX_IR[14:12]), .b(3'b111), .eq(comparator_9_eq));  // open: gt, lt
  D_Flip_Flop #(.trigger("rising"), .Pre_Clr_Positions("LEGACY"), .NegatePresetClear("false"), .enable("true"), .NewFFLayout("false")) IR1_3 (
    .clk(CLK), .D(and_11_out), .Q(IR1_3_q), .preset(1'b0), .en(1'b1), .reset(1'b0));  // open: Qn
  and and_12 (and_12_out, comparator_8_eq, excsr);
  and and_13 (and_13_out, comparator_9_eq, excsr);
  not not_10 (not_10_out, \中断产生 );
  Comparator #(.width(16), .mode("twosComplement")) comparator_10 (
    .a({16{1'b0}}), .b(\总周期数 ), .eq(comparator_10_eq));  // open: gt, lt
  Priority_Encoder #(.select(2), .disabled("Z")) priority_encoder_1 (
    .in0(1'b0), .in1(IR1_3_q), .in2(IR1_q), .in3(IR1_2_q), .out(priority_encoder_1_out),
    .gs(priority_encoder_1_gs), .en_in(1'b1));  // open: en_out
  or or_20 (or_20_out, not_10_out, and_12_out);
  or or_21 (or_21_out, and_12_out, and_13_out, \中断产生 , uret, comparator_10_eq);
  Multiplexer #(.select(2), .width(32), .disabled("Z"), .enable("false")) multiplexer_10 (
    .in0({32{1'b0}}), .in1(32'h30ac), .in2(32'h3158), .in3(32'h3204), .out(multiplexer_10_out),
    .sel(priority_encoder_1_out));
  Register #(.width(1), .trigger("rising"), .Select("low")) \u_中断使能寄存器  (
    .D(or_20_out), .en(or_21_out), .Q(\中断使能寄存器_q ), .clk(CLK), .clr(1'b0), .cs(1'b0), .preset(1'b0));
  and and_14 (\中断产生 , priority_encoder_1_gs, \中断使能寄存器_q , \当前指令优先 );
  Demultiplexer #(.select(2), .width(1), .tristate("false"), .disabled("Z"), .enable("false")) demultiplexer_1 (
    .out1(\中断1返回 ), .out2(\中断2返回 ), .out3(\中断3返回 ), .in(uret), .sel(priority_encoder_1_out));  // open: out0
  Multiplexer #(.select(2), .width(32), .disabled("Z"), .enable("false")) multiplexer_11 (
    .in0(\原始PC ), .in1(EPC), .in2(multiplexer_10_out), .in3(EPC), .out(\下条PC ), .sel({\中断产生 , uret}));
  Pull_Resistor #(.pull(0)) pull_resistor_5 (.node(\中断1返回 ));
  Pull_Resistor #(.pull(0)) pull_resistor_6 (.node(\中断3返回 ));
  or or_22 (or_22_out, \中断产生 , uret);
  not not_11 (not_11_out, \中断产生 );
  Counter #(.width(2), .max('h3), .ongoal("wrap"), .trigger("rising"), .behavior("new")) counter_7 (
    .load(1'b0), .count(or_22_out), .Q(counter_7_q), .clk(CLK), .clr(1'b0), .preset(1'b0), .down(not_11_out));  // open: D, carry
  Decoder #(.select(2), .tristate("false"), .disabled("Z"), .enable("false")) decoder_1 (
    .out1(decoder_1_out1), .out2(decoder_1_out2), .out3(decoder_1_out3), .sel(priority_encoder_1_out));  // open: out0
  Pull_Resistor #(.pull(0)) pull_resistor_7 (.node(\中断2返回 ));
  Decoder #(.select(2), .tristate("false"), .disabled("Z"), .enable("false")) decoder_2 (
    .out0(decoder_2_out0), .out1(decoder_2_out1), .out2(decoder_2_out2), .sel(counter_7_q));  // open: out3
  D_Flip_Flop #(.trigger("rising"), .Pre_Clr_Positions("ABOVE_BELOW"), .NegatePresetClear("false"), .enable("false"), .NewFFLayout("true")) d_ff_6 (
    .clk(CLK), .D(\存在分支 ), .Q(d_ff_6_q[0]), .preset(1'b0), .reset(1'b0));  // open: Qn
  D_Flip_Flop #(.trigger("rising"), .Pre_Clr_Positions("ABOVE_BELOW"), .NegatePresetClear("false"), .enable("false"), .NewFFLayout("true")) d_ff_7 (
    .clk(CLK), .D(uret), .Q(d_ff_6_q[1]), .preset(1'b0), .reset(1'b0));  // open: Qn
  Pull_Resistor #(.pull(0)) pull_resistor_8 (.node(decoder_1_out2));
  Pull_Resistor #(.pull(0)) pull_resistor_9 (.node(decoder_1_out1));
  Pull_Resistor #(.pull(0)) pull_resistor_10 (.node(decoder_1_out3));
  and and_15 (and_15_out, \中断产生 , decoder_2_out0);
  and and_16 (and_16_out, decoder_2_out1, \中断产生 );
  and and_17 (and_17_out, decoder_2_out2, \中断产生 );
  Multiplexer #(.select(2), .width(32), .disabled("Z"), .enable("false")) multiplexer_12 (
    .in0(ID_PC), .in1(\原始PC ), .in2(IF_PC), .in3(\原始PC ), .out(multiplexer_12_out), .sel(d_ff_6_q));
  and and_18 (and_18_out, decoder_1_out1, \中断产生 );
  and and_19 (and_19_out, decoder_1_out2, \中断产生 );
  and and_20 (and_20_out, decoder_1_out3, \中断产生 );
  Register #(.width(2), .trigger("rising"), .Select("low")) IR_id (
    .D(priority_encoder_1_out), .en(and_15_out), .Q(IR_id_q), .clk(CLK), .clr(1'b0), .cs(1'b0), .preset(1'b0));
  Register #(.width(2), .trigger("rising"), .Select("low")) IR_id_2 (
    .D(priority_encoder_1_out), .en(and_16_out), .Q(IR_id_2_q), .clk(CLK), .clr(1'b0), .cs(1'b0),
    .preset(1'b0));
  Register #(.width(2), .trigger("rising"), .Select("low")) IR_id_3 (
    .D(priority_encoder_1_out), .en(and_17_out), .Q(IR_id_3_q), .clk(CLK), .clr(1'b0), .cs(1'b0),
    .preset(1'b0));
  Register #(.width(32), .trigger("rising"), .Select("low")) u_EPC (
    .D(multiplexer_12_out), .en(and_18_out), .Q(EPC_q), .clk(CLK), .clr(1'b0), .cs(1'b0), .preset(1'b0));
  Register #(.width(32), .trigger("rising"), .Select("low")) EPC_2 (
    .D(multiplexer_12_out), .en(and_19_out), .Q(EPC_2_q), .clk(CLK), .clr(1'b0), .cs(1'b0), .preset(1'b0));
  Register #(.width(32), .trigger("rising"), .Select("low")) EPC_3 (
    .D(multiplexer_12_out), .en(and_20_out), .Q(EPC_3_q), .clk(CLK), .clr(1'b0), .cs(1'b0), .preset(1'b0));
  Multiplexer #(.select(2), .width(2), .disabled("Z"), .enable("false")) multiplexer_13 (
    .in1(IR_id_q), .in2(IR_id_2_q), .in3(IR_id_3_q), .out(multiplexer_13_out), .sel(counter_7_q));  // open: in0
  Multiplexer #(.select(2), .width(32), .disabled("Z"), .enable("false")) multiplexer_14 (
    .in1(EPC_q), .in2(EPC_2_q), .in3(EPC_3_q), .out(EPC), .sel(multiplexer_13_out));  // open: in0
  Comparator #(.width(2), .mode("unsigned")) comparator_11 (
    .a(multiplexer_13_out), .b(priority_encoder_1_out), .lt(\当前指令优先 ));  // open: gt, eq
  Pull_Resistor #(.pull(1)) pull_resistor_11 (.node(\当前指令优先 ));

  // Notes on the sheet:
  //   中断源
  //   时空图监测，可删除
  //   中断等待指示
  //   选择PC
  //   取指
  //   数码管输出
  //   指令探针
  //   指令存储器
  //   contents of rom_1 (hex, n*v repeats v):
  //   7d000113 100413 1f41993 41f9d993 433 c00913 800b13 140413 f47413 800293 100313 499993 89e9b3 1300533
  //   2200893 73 406282b3 fe0294e3 140413 f00f93 1f47433 1c41413 800293 100313 49d993 89e9b3 1300533
  //   2200893 73 406282b3 fe0294e3 1c45413 406b0b33 b0463 f95ff06f 2b3 fff2c293 1029293 fff2e293 500533
  //   2200893 73 f5dff06f 1112023 410113 a12023 410113 812023 410113 1312023 410113 1412023 410113 1512023
  //   410113 1612023 410113 40e073 100b13 300a13 100a93 1600433 441413 14469b3 1300533 2200893 73 fe0416e3
  //   415a0a33 fe0a10e3 40f073 ffc10113 12b03 ffc10113 12a83 ffc10113 12a03 ffc10113 12983 ffc10113 12403
  //   ffc10113 12503 ffc10113 12883 200073 1112023 410113 a12023 410113 812023 410113 1312023 410113
  //   1412023 410113 1512023 410113 1612023 410113 40e073 200b13 300a13 100a93 1600433 441413 14469b3
  //   1300533 2200893 73 fe0416e3 415a0a33 fe0a10e3 40f073 ffc10113 12b03 ffc10113 12a83 ffc10113 12a03
  //   ffc10113 12983 ffc10113 12403 ffc10113 12503 ffc10113 12883 200073 1112023 410113 a12023 410113
  //   812023 410113 1312023 410113 1412023 410113 1512023 410113 1612023 410113 40e073 300b13 300a13
  //   100a93 1600433 441413 14469b3 1300533 2200893 73 fe0416e3 415a0a33 fe0a10e3 40f073 ffc10113 12b03
  //   ffc10113 12a83 ffc10113 12a03 ffc10113 12983 ffc10113 12403 ffc10113 12503 ffc10113 12883 200073
  //   rs1
  //   rs2
  //   I指令
  //   S指令
  //   B指令
  //   J指令
  //   rd
  //   JAL
  //   JALR
  //   URET
  //   bgeu
  //   跳转地址生成
  //   译码
  //   Beq
  //   Bne
  //   MemToReg
  //   MemWrite
  //   AluOP
  //   AluSrcB
  //   RegWrite
  //   控制位
  //   暂停节拍，不能为0
  //   戳工具置1进入计数暂停模式，ctrl+k时钟自动运行到对应节拍暂停
  //   ctrl+k关闭时钟连续运行，将控制位置零，进入单步调试模式调试
  //   为方便自动评测，需要输出PC，IR，寄存器堆写如数据RDin
  //   可计数暂停的时钟源
  //   RAM写使能MemWrite、RAM写入数据MDin等信号
  //   执行
  //   计算参数重定向
  //   ecall的LED显示
  //   实现sb
  //   存储
  //   数据存储器
  //   写回
  //   选择RDin
  //   多级中断测试信号模拟器
  //   Reset 
  //   Reset 
  //   Reset 
  //   中断PC计算
  //   中断使能维护
  //   中断使能维护
  //   中断返回信号
  //   中断数量计数
  //   中断优先级确定
  //   EPC寄存器堆维护
endmodule

module \动态分支预测  (
  output RegWrite,
  output MemWrite,
  output [31:0] IF_PC,
  output [31:0] ID_PC,
  output [31:0] EX_PC,
  output [31:0] M_PC,
  output [31:0] WB_PC,
  output [31:0] RDin,
  output [31:0] MDin,
  output [31:0] LedData
);

  wire and_1_out, and_2_out, and_3_out, and_4_out, and_5_out, and_6_out, and_8_out, and_9_out, and_10_out,
       and_11_out, and_12_out, and_13_out, and_15_out, and_16_out, and_17_out, and_18_out, and_19_out,
       and_20_out, branch, BranchNum, BranchOK, Bs, CLK, clock_1_out, comparator_1_eq, comparator_1_lt,
       comparator_2_eq, comparator_3_eq, comparator_4_eq, comparator_5_eq, d_ff_1_q, d_ff_3_q, d_ff_4_q,
       d_ff_5_q, decoder_1_out0, decoder_1_out1, decoder_1_out2, decoder_2_out3, equ, ex_mem_1_dasb_2,
       ex_mem_1_halt_2, ex_mem_1_jal_2, ex_mem_1_jalr_2, ex_mem_1_memtoreg_2, ex_mem_1_regwrite_2,
       ex_mem_1_uret_2, excsr, exdasb, execall, exhalt, exjal, exjalr, ge, Go, halt, id_ex_1_alusrcb_2,
       id_ex_1_beq_2, id_ex_1_bgeu_2, id_ex_1_bne_2, id_ex_1_memtoreg_2, id_ex_1_memwrite_2,
       id_ex_1_regwrite_2, \id_ex_1_预测跳转_2 , idecall, iduret, \if_id_1_预测跳转_2 , IR1, IR1_2_q, IR1_3_q, IR1_q,
       IR2, IR3, jal, mem_wb_1_halt_2, mem_wb_1_jal_2, mem_wb_1_jalr_2, nand_1_out, not_1_out, not_2_out,
       not_3_out, not_4_out, not_5_out, not_6_out, not_7_out, not_8_out, not_9_out, not_10_out, not_11_out,
       or_1_out, or_2_out, or_4_out, or_5_out, or_6_out, or_8_out, or_16_out, or_17_out, or_18_out,
       or_19_out, or_20_out, or_21_out, priority_encoder_1_gs, pull_resistor_5_node, pull_resistor_6_node,
       refresh, riscv_probe_1_p1, RST, S_type, stall, uret, W1, W2, W3, \中断1返回 , \中断2返回 , \中断3返回 , \中断产生 ,
       \中断使能寄存器_q , \分支历史表_1_预测跳转 , \分支预测出错 , \单周期硬布线控制器_1_alu_src , \单周期硬布线控制器_1_beq , \单周期硬布线控制器_1_bgeu ,
       \单周期硬布线控制器_1_bne , \单周期硬布线控制器_1_csr , \单周期硬布线控制器_1_dasb , \单周期硬布线控制器_1_jalr , \单周期硬布线控制器_1_memtoreg ,
       \单周期硬布线控制器_1_memwrite , \单周期硬布线控制器_1_regwrite , \单周期硬布线控制器_1_user1 , \单周期硬布线控制器_1_user2 , \当前指令优先 ;
  wire [1:0] counter_7_q, d_ff_6_q, id_ex_1_r1_forward_2, id_ex_1_r2_forward_2, IR_id_2_q, IR_id_3_q,
       IR_id_q, mem_wb_1_memtoreg_2, multiplexer_16_out, priority_encoder_1_out, r1_forward, r2_forward;
  wire [1:1] or_7_out;
  wire [3:0] id_ex_1_aluop_2, \单周期硬布线控制器_1_alu_op ;
  wire [4:0] ex_mem_1_rd_a_2, id_ex_1_rd_a_2, multiplexer_5_out, multiplexer_6_out, wbrd_a;
  wire [11:0] multiplexer_7_out;
  wire [12:0] CNT_num;
  wire [15:0] \LoadUse次数 , \总周期数 , \插入气泡数 , \无条件分支数 , \条件分支成功数 ;
  wire [31:0] adder_1_out, ALUres, bit_extender_1_out, bit_extender_2_out, bit_extender_3_out, EPC, EPC_2_q,
       EPC_3_q, EPC_q, EX_IR, ex_mem_1_pc_4_2, ex_mem_1_r2_2, exr1, exr2, id_ex_1_imm1_2, id_ex_1_imm2_2,
       id_ex_1_pc_4_2, ID_IR, if_id_1_pc_4_2, IF_IR, ja, MEM_IR, mem_wb_1_memdata_2, mem_wb_1_pc_4_2,
       mem_wb_1_res_2, memALUres, multiplexer_1_out, multiplexer_3_out, multiplexer_8_out,
       multiplexer_11_out, multiplexer_13_out, multiplexer_15_out, PC_4, ram_1_data, regifile_1_r1,
       regifile_1_r2, rer1, rer2, shifter_1_out, WB_IR, \下条PC , \分支历史表_1_预测结果 , \原始PC , \预测地址 ;

  Button \u_总复位  (.out(RST));
  Button _1 (.out(IR1));
  Button _2 (.out(IR2));
  Button _3 (.out(IR3));
  // Probe on \总周期数 
  // Probe on \总周期数 
  or or_1 (or_1_out, Bs, exjal, exjalr);
  Button \u_继续运行  (.out(Go));
  LED #(.active("true")) led_1 (.in(W1));
  LED #(.active("true")) led_2 (.in(W2));
  LED #(.active("true")) led_3 (.in(W3));
  Adder #(.width(32)) adder_1 (.a(EX_PC), .b(32'h4), .out(adder_1_out), .cin(1'b0));  // open: cout
  or or_2 (or_2_out, not_1_out, Go);
  not not_1 (not_1_out, halt);
  Multiplexer #(.select(3), .width(32), .disabled("Z"), .enable("false")) multiplexer_1 (
    .in0(IF_PC), .in1(ALUres), .in2(ja), .in3(ja), .in4(ja), .in5(ja), .in6(ja), .in7(ja),
    .out(multiplexer_1_out), .sel({Bs, exjal, exjalr}));
  Hex_Digit_Display hex_digit_display_1 (.value(LedData[31:28]));  // open: dp
  // Probe on IF_PC[19:0]
  // RiscV_Probe riscv_probe_1: pin names not known; wires that end beside it: riscv_probe_1_p1, IF_IR
  Multiplexer #(.select(1), .width(32), .disabled("Z"), .enable("false")) multiplexer_2 (
    .in0(\预测地址 ), .in1(multiplexer_3_out), .out(\原始PC ), .sel(\分支预测出错 ));
  Register #(.width(32), .trigger("rising"), .Select("low")) PC (
    .D(\下条PC ), .en(and_1_out), .Q(IF_PC), .clk(CLK), .clr(1'b0), .cs(1'b0), .preset(1'b0));
  Multiplexer #(.select(2), .width(32), .disabled("Z"), .enable("false")) multiplexer_3 (
    .in0(adder_1_out), .in1(ALUres), .in2(ja), .out(multiplexer_3_out), .sel({or_7_out[1], exjalr}));  // open: in3
  and and_1 (and_1_out, or_2_out, not_2_out);
  not not_2 (not_2_out, stall);
  \分支历史表  \u_分支历史表_1  (
    .exbranch_ad(multiplexer_1_out), .exPC(EX_PC), .exbranch(or_1_out), .CLK(CLK), .ifPC(IF_PC),
    .\是否跳转 (branch), .\预测结果 (\分支历史表_1_预测结果 ), .\预测跳转 (\分支历史表_1_预测跳转 ));
  Hex_Digit_Display hex_digit_display_2 (.value(LedData[23:20]));  // open: dp
  Hex_Digit_Display hex_digit_display_3 (.value(LedData[27:24]));  // open: dp
  // Probe on ID_PC[19:0]
  // RiscV_Probe riscv_probe_2: pin names not known; wires that end beside it: ID_IR
  Multiplexer #(.select(1), .width(32), .disabled("Z"), .enable("false")) multiplexer_4 (
    .in0(PC_4), .in1(\分支历史表_1_预测结果 ), .out(\预测地址 ), .sel(\分支历史表_1_预测跳转 ));
  Hex_Digit_Display hex_digit_display_4 (.value(LedData[15:12]));  // open: dp
  Hex_Digit_Display hex_digit_display_5 (.value(LedData[19:16]));  // open: dp
  Adder #(.width(32)) adder_2 (.a(IF_PC), .b(32'h4), .out(PC_4), .cin(1'b0));  // open: cout
  Hex_Digit_Display hex_digit_display_6 (.value(LedData[11:8]));  // open: dp
  Hex_Digit_Display hex_digit_display_7 (.value(LedData[7:4]));  // open: dp
  // Probe on EX_PC[19:0]
  // RiscV_Probe riscv_probe_3: pin names not known; wires that end beside it: EX_IR
  or or_3 (branch, or_7_out[1], exjalr);
  // RiscV_Probe riscv_probe_4: pin names not known; wires that end beside it: IF_IR
  ROM #(.addrWidth(10), .dataWidth(32), .Select("high")) rom_1 (.addr(IF_PC[11:2]), .data(IF_IR), .sel(1'b1));
  Hex_Digit_Display hex_digit_display_8 (.value(LedData[3:0]));  // open: dp
  or or_4 (or_4_out, \分支预测出错 , \中断产生 , uret);
  IF_ID if_id_1 (
    .PC(IF_PC), .PC_4(PC_4), .IR(IF_IR), .PC_2(ID_PC), .PC_4_2(if_id_1_pc_4_2), .IR_2(ID_IR), .reset(1'b0),
    .refresh(or_4_out), .en(and_2_out), .CLK(CLK), .\预测跳转 (\分支历史表_1_预测跳转 ), .\预测跳转_2 (\if_id_1_预测跳转_2 ));
  and and_2 (and_2_out, or_5_out, not_4_out);
  or or_5 (or_5_out, not_3_out, Go);
  not not_3 (not_3_out, halt);
  // Probe on \总周期数 
  // Probe on M_PC[19:0]
  // RiscV_Probe riscv_probe_5: pin names not known; wires that end beside it: MEM_IR
  not not_4 (not_4_out, stall);
  // Probe on \总周期数 
  // Probe on \无条件分支数 
  // Probe on \条件分支成功数 
  // Probe on \插入气泡数 
  // Probe on \LoadUse次数 
  Multiplexer #(.select(1), .width(5), .disabled("Z"), .enable("false")) multiplexer_5 (
    .in0(ID_IR[19:15]), .in1(5'b10001), .out(multiplexer_5_out), .sel(idecall));
  Multiplexer #(.select(1), .width(5), .disabled("Z"), .enable("false")) multiplexer_6 (
    .in0(ID_IR[24:20]), .in1(5'b01010), .out(multiplexer_6_out), .sel(idecall));
  // Probe on IF_PC[11:0]
  // Probe on WB_PC[19:0]
  // RiscV_Probe riscv_probe_6: pin names not known; wires that end beside it: WB_IR
  \单周期硬布线控制器  \u_单周期硬布线控制器_1  (
    .Funct({ID_IR[30], ID_IR[25], ID_IR[14:12]}), .OP(ID_IR[6:2]), .ALU_OP(\单周期硬布线控制器_1_alu_op ),
    .MemToReg(\单周期硬布线控制器_1_memtoreg ), .MemWrite(\单周期硬布线控制器_1_memwrite ), .ALU_SRC(\单周期硬布线控制器_1_alu_src ),
    .RegWrite(\单周期硬布线控制器_1_regwrite ), .ecall(idecall), .S_type(S_type), .Jalr(\单周期硬布线控制器_1_jalr ),
    .Beq(\单周期硬布线控制器_1_beq ), .JAL(jal), .Bne(\单周期硬布线控制器_1_bne ), .in_3(ID_IR[21]), .uret(iduret),
    .bgeu(\单周期硬布线控制器_1_bgeu ), .csr(\单周期硬布线控制器_1_csr ), .dasb(\单周期硬布线控制器_1_dasb ),
    .user1(\单周期硬布线控制器_1_user1 ), .user2(\单周期硬布线控制器_1_user2 ));
  Multiplexer #(.select(1), .width(12), .disabled("Z"), .enable("false")) multiplexer_7 (
    .in0(ID_IR[31:20]), .in1({ID_IR[31:25], ID_IR[11:7]}), .out(multiplexer_7_out), .sel(S_type));
  assign bit_extender_1_out = {{20{multiplexer_7_out[11]}}, multiplexer_7_out};  // Bit_Extender bit_extender_1
  assign bit_extender_2_out = {{20{ID_IR[31]}}, {ID_IR[31], ID_IR[7], ID_IR[30:25], ID_IR[11:8]}};  // Bit_Extender bit_extender_2
  assign bit_extender_3_out = {{12{ID_IR[31]}}, {ID_IR[31], ID_IR[19:12], ID_IR[20], ID_IR[30:21]}};  // Bit_Extender bit_extender_3
  // Probe on ID_PC[11:0]
  // Probe on EX_PC[11:0]
  // Probe on M_PC[11:0]
  D_Flip_Flop #(.trigger("high"), .Pre_Clr_Positions("LEGACY"), .NegatePresetClear("false"), .enable("true"), .NewFFLayout("false")) d_ff_1 (.Q(d_ff_1_q));  // open: clk, D, Qn, preset, en, reset
  // Probe on 13'h70
  Multiplexer #(.select(1), .width(32), .disabled("Z"), .enable("false")) multiplexer_8 (
    .in0(bit_extender_2_out), .in1(bit_extender_3_out), .out(multiplexer_8_out), .sel(jal));
  // Probe on WB_PC[11:0]
  Comparator #(.width(13), .mode("twosComplement")) comparator_1 (
    .a(CNT_num), .b(13'h70), .eq(comparator_1_eq), .lt(comparator_1_lt));  // open: gt
  Clock #(.highDuration(1), .lowDuration(1)) clock_1 (.out(clock_1_out));
  or or_6 (or_6_out, stall, \分支预测出错 , \中断产生 , uret);
  not not_5 (not_5_out, CLK);
  Regifile regifile_1 (
    .Din(RDin), .Clk(not_5_out), .R1(regifile_1_r1), .R2(regifile_1_r2), .WE(RegWrite), .W_num(wbrd_a),
    .R1_num(multiplexer_5_out), .R2_num(multiplexer_6_out));
  nand nand_1 (nand_1_out, d_ff_1_q, comparator_1_eq);
  Counter #(.width(13), .max('h1fff), .ongoal("stay"), .trigger("rising"), .behavior("old")) counter_1 (
    .count(comparator_1_lt), .Q(CNT_num), .clk(clock_1_out));  // open: load, D, carry, clr, preset
  \冲突处理_redirect  \u_冲突处理_redirect_1  (
    .exrd(id_ex_1_rd_a_2), .memRegWrite(ex_mem_1_regwrite_2), .ecall(idecall), .user1(\单周期硬布线控制器_1_user1 ),
    .IR(ID_IR), .memrd(ex_mem_1_rd_a_2), .user2(\单周期硬布线控制器_1_user2 ), .exRegWrite(id_ex_1_regwrite_2),
    .\存在分支 (branch), .\阻塞 (stall), .\清空 (refresh), .r1_forward(r1_forward), .r2_forward(r2_forward),
    .exMemToReg(id_ex_1_memtoreg_2));
  or or_7 (or_7_out[1], BranchOK, exjal);
  ID_EX id_ex_1 (
    .Beq(\单周期硬布线控制器_1_beq ), .Bne(\单周期硬布线控制器_1_bne ), .MemToReg(\单周期硬布线控制器_1_memtoreg ),
    .MemWrite(\单周期硬布线控制器_1_memwrite ), .AluSrcB(\单周期硬布线控制器_1_alu_src ), .RegWrite(\单周期硬布线控制器_1_regwrite ),
    .JAL(jal), .JALR(\单周期硬布线控制器_1_jalr ), .URET(iduret), .csr(\单周期硬布线控制器_1_csr ), .bgeu(\单周期硬布线控制器_1_bgeu ),
    .S_type(S_type), .dasb(\单周期硬布线控制器_1_dasb ), .AluOP(\单周期硬布线控制器_1_alu_op ), .r1(regifile_1_r1),
    .r2(regifile_1_r2), .rd_a(ID_IR[11:7]), .imm1(bit_extender_1_out), .imm2(multiplexer_8_out), .PC(ID_PC),
    .PC_4(if_id_1_pc_4_2), .IR(ID_IR), .Beq_2(id_ex_1_beq_2), .Bne_2(id_ex_1_bne_2),
    .MemToReg_2(id_ex_1_memtoreg_2), .MemWrite_2(id_ex_1_memwrite_2), .AluSrcB_2(id_ex_1_alusrcb_2),
    .RegWrite_2(id_ex_1_regwrite_2), .JAL_2(exjal), .JALR_2(exjalr), .URET_2(uret), .csr_2(excsr),
    .bgeu_2(id_ex_1_bgeu_2), .dasb_2(exdasb), .AluOP_2(id_ex_1_aluop_2), .r1_2(exr1), .r2_2(exr2),
    .rd_a_2(id_ex_1_rd_a_2), .imm1_2(id_ex_1_imm1_2), .imm2_2(id_ex_1_imm2_2), .PC_2(EX_PC),
    .PC_4_2(id_ex_1_pc_4_2), .IR_2(EX_IR), .reset(1'b0), .refresh(or_6_out), .en(or_8_out), .CLK(CLK),
    .ecall(idecall), .ecall_2(execall), .r1_forward(r1_forward), .r1_forward_2(id_ex_1_r1_forward_2),
    .r2_forward(r2_forward), .r2_forward_2(id_ex_1_r2_forward_2), .\预测跳转 (\if_id_1_预测跳转_2 ),
    .\预测跳转_2 (\id_ex_1_预测跳转_2 ));  // open: S_type_2
  or or_8 (or_8_out, not_6_out, Go);
  not not_6 (not_6_out, halt);
  assign CLK = nand_1_out ? clock_1_out : 1'bz;  // Controlled_Buffer controlled_buffer_1
  or or_9 (BranchOK, and_6_out, and_4_out, and_3_out);
  Shifter #(.width(32), .shift("ll")) shifter_1 (.in(id_ex_1_imm2_2), .\dist (5'b00001), .out(shifter_1_out));
  Multiplexer #(.select(2), .width(32), .disabled("Z"), .enable("false")) multiplexer_9 (
    .in0(exr1), .in1(RDin), .in2(memALUres), .out(rer1), .sel(id_ex_1_r1_forward_2));  // open: in3
  Multiplexer #(.select(2), .width(32), .disabled("Z"), .enable("false")) multiplexer_10 (
    .in0(exr2), .in1(RDin), .in2(memALUres), .out(rer2), .sel(id_ex_1_r2_forward_2));  // open: in3
  Pull_Resistor #(.pull(1)) pull_resistor_1 (.node(CLK));
  and and_3 (and_3_out, id_ex_1_beq_2, equ);
  Multiplexer #(.select(1), .width(32), .disabled("Z"), .enable("false")) multiplexer_11 (
    .in0(rer2), .in1(id_ex_1_imm1_2), .out(multiplexer_11_out), .sel(id_ex_1_alusrcb_2));
  Register #(.width(32), .trigger("rising"), .Select("low")) register_1 (
    .D(rer2), .en(and_5_out), .Q(LedData), .clk(CLK), .clr(1'b0), .cs(1'b0), .preset(1'b0));
  Adder #(.width(32)) adder_3 (.a(shifter_1_out), .b(EX_PC), .out(ja), .cin(1'b0));  // open: cout
  Counter #(.width(16), .max('hffff), .ongoal("wrap"), .trigger("rising"), .behavior("new")) counter_2 (
    .count(CLK), .Q(\总周期数 ), .clk(and_8_out));  // open: load, D, carry, clr, preset, down
  and and_4 (and_4_out, not_7_out, id_ex_1_bne_2);
  not not_7 (not_7_out, equ);
  ALU alu_1 (
    .X(rer1), .Y(multiplexer_11_out), .AluOP(id_ex_1_aluop_2), .Equal(equ), .Result(ALUres), .out_4(ge));  // open: Result_2, out_6
  Comparator #(.width(32), .mode("twosComplement")) comparator_2 (
    .a(rer1), .b(32'h22), .eq(comparator_2_eq));  // open: gt, lt
  and and_5 (and_5_out, execall, comparator_2_eq);
  xor xor_1 (\分支预测出错 , \id_ex_1_预测跳转_2 , branch);
  and and_6 (and_6_out, id_ex_1_bgeu_2, ge);
  or or_10 (Bs, id_ex_1_bgeu_2, id_ex_1_memtoreg_2, id_ex_1_bne_2);
  and and_7 (exhalt, execall, not_8_out);
  not not_8 (not_8_out, comparator_2_eq);
  Counter #(.width(16), .max('hffff), .ongoal("wrap"), .trigger("rising"), .behavior("new")) counter_3 (
    .count(BranchNum), .Q(\无条件分支数 ), .clk(and_8_out));  // open: load, D, carry, clr, preset, down
  or or_11 (BranchNum, exjalr, exjal);
  EX_MEM ex_mem_1 (
    .MemToReg(id_ex_1_memtoreg_2), .MemWrite(id_ex_1_memwrite_2), .RegWrite(id_ex_1_regwrite_2), .JAL(exjal),
    .JALR(exjalr), .URET(uret), .dasb(exdasb), .halt(exhalt), .res(ALUres), .rd_a(id_ex_1_rd_a_2), .r2(rer2),
    .PC(EX_PC), .PC_4(id_ex_1_pc_4_2), .IR(EX_IR), .MemToReg_2(ex_mem_1_memtoreg_2), .MemWrite_2(MemWrite),
    .RegWrite_2(ex_mem_1_regwrite_2), .JAL_2(ex_mem_1_jal_2), .JALR_2(ex_mem_1_jalr_2),
    .URET_2(ex_mem_1_uret_2), .dasb_2(ex_mem_1_dasb_2), .halt_2(ex_mem_1_halt_2), .res_2(memALUres),
    .rd_a_2(ex_mem_1_rd_a_2), .r2_2(ex_mem_1_r2_2), .PC_2(M_PC), .PC_4_2(ex_mem_1_pc_4_2), .IR_2(MEM_IR),
    .reset(1'b0), .refresh(1'b0), .en(or_8_out), .CLK(CLK));
  Counter #(.width(16), .max('hffff), .ongoal("wrap"), .trigger("rising"), .behavior("new")) counter_4 (
    .count(BranchOK), .Q(\条件分支成功数 ), .clk(and_8_out));  // open: load, D, carry, clr, preset, down
  \专门给SB画的电路  \u_专门给sb画的电路_1  (
    .r2(ex_mem_1_r2_2), .addr(memALUres), .pre_data(ram_1_data), .MDin(MDin), .dasb(ex_mem_1_dasb_2));
  Counter #(.width(16), .max('hffff), .ongoal("wrap"), .trigger("rising"), .behavior("new")) counter_5 (
    .count(refresh), .Q(\插入气泡数 ), .clk(and_8_out));  // open: load, D, carry, clr, preset, down
  RAM #(.addrWidth(10), .dataWidth(32), .bus("separate"), .Select("high")) ram_1 (
    .addr(memALUres[11:2]), .din(MDin), .data(ram_1_data), .str(MemWrite), .sel(1'b1), .clk(CLK), .ld(1'b1),
    .clr(1'b0));
  Counter #(.width(16), .max('hffff), .ongoal("wrap"), .trigger("rising"), .behavior("new")) counter_6 (
    .count(stall), .Q(\LoadUse次数 ), .clk(and_8_out));  // open: load, D, carry, clr, preset, down
  MEM_WB mem_wb_1 (
    .MemToReg(ex_mem_1_memtoreg_2), .RegWrite(ex_mem_1_regwrite_2), .JAL(ex_mem_1_jal_2),
    .JALR(ex_mem_1_jalr_2), .URET(ex_mem_1_uret_2), .dasb(ex_mem_1_dasb_2), .halt(ex_mem_1_halt_2),
    .res(memALUres), .rd_a(ex_mem_1_rd_a_2), .MemData(ram_1_data), .PC(M_PC), .PC_4(ex_mem_1_pc_4_2),
    .IR(MEM_IR), .MemToReg_2(mem_wb_1_memtoreg_2[0]), .RegWrite_2(RegWrite), .JAL_2(mem_wb_1_jal_2),
    .JALR_2(mem_wb_1_jalr_2), .halt_2(mem_wb_1_halt_2), .res_2(mem_wb_1_res_2), .rd_a_2(wbrd_a),
    .MemData_2(mem_wb_1_memdata_2), .PC_2(WB_PC), .PC_4_2(mem_wb_1_pc_4_2), .IR_2(WB_IR), .reset(1'b0),
    .refresh(1'b0), .en(or_8_out), .CLK(CLK));  // open: URET_2, dasb_2
  and and_8 (and_8_out, CLK, not_9_out);
  or or_12 (mem_wb_1_memtoreg_2[1], mem_wb_1_jal_2, mem_wb_1_jalr_2);
  not not_9 (not_9_out, halt);
  Multiplexer #(.select(2), .width(32), .disabled("Z"), .enable("false")) multiplexer_12 (
    .in0(mem_wb_1_res_2), .in1(mem_wb_1_memdata_2), .in2(mem_wb_1_pc_4_2), .out(RDin),
    .sel(mem_wb_1_memtoreg_2));  // open: in3
  D_Flip_Flop #(.trigger("rising"), .Pre_Clr_Positions("ABOVE_BELOW"), .NegatePresetClear("false"), .enable("true"), .NewFFLayout("true")) d_ff_2 (
    .clk(mem_wb_1_halt_2), .D(1'b1), .Q(halt), .preset(1'b0), .en(1'b1), .reset(Go));  // open: Qn
  or or_13 (W1, IR1_q, d_ff_3_q);
  or or_14 (W2, IR1_2_q, d_ff_4_q);
  or or_15 (W3, IR1_3_q, d_ff_5_q);
  D_Flip_Flop #(.trigger("rising"), .Pre_Clr_Positions("LEGACY"), .NegatePresetClear("false"), .enable("true"), .NewFFLayout("false")) d_ff_3 (
    .clk(IR1), .D(1'b1), .Q(d_ff_3_q), .preset(1'b0), .en(1'b1), .reset(IR1_q));  // open: Qn
  D_Flip_Flop #(.trigger("rising"), .Pre_Clr_Positions("LEGACY"), .NegatePresetClear("false"), .enable("true"), .NewFFLayout("false")) d_ff_4 (
    .clk(IR2), .D(1'b1), .Q(d_ff_4_q), .preset(1'b0), .en(1'b1), .reset(IR1_2_q));  // open: Qn
  D_Flip_Flop #(.trigger("rising"), .Pre_Clr_Positions("LEGACY"), .NegatePresetClear("false"), .enable("true"), .NewFFLayout("false")) d_ff_5 (
    .clk(IR3), .D(1'b1), .Q(d_ff_5_q), .preset(1'b0), .en(1'b1), .reset(IR1_3_q));  // open: Qn
  or or_16 (or_16_out, d_ff_3_q, IR1_q);
  or or_17 (or_17_out, d_ff_4_q, IR1_2_q);
  or or_18 (or_18_out, d_ff_5_q, IR1_3_q);
  and and_9 (and_9_out, or_16_out, ~\中断1返回 );  // AND_Gate
  and and_10 (and_10_out, or_17_out, ~\中断2返回 );  // AND_Gate
  and and_11 (and_11_out, or_18_out, ~\中断3返回 );  // AND_Gate
  D_Flip_Flop #(.trigger("rising"), .Pre_Clr_Positions("LEGACY"), .NegatePresetClear("false"), .enable("true"), .NewFFLayout("false")) u_IR1 (
    .clk(CLK), .D(and_9_out), .Q(IR1_q), .preset(1'b0), .en(1'b1), .reset(1'b0));  // open: Qn
  D_Flip_Flop #(.trigger("rising"), .Pre_Clr_Positions("LEGACY"), .NegatePresetClear("false"), .enable("true"), .NewFFLayout("false")) IR1_2 (
    .clk(CLK), .D(and_10_out), .Q(IR1_2_q), .preset(1'b0), .en(1'b1), .reset(1'b0));  // open: Qn
  D_Flip_Flop #(.trigger("rising"), .Pre_Clr_Positions("LEGACY"), .NegatePresetClear("false"), .enable("true"), .NewFFLayout("false")) IR1_3 (
    .clk(CLK), .D(and_11_out), .Q(IR1_3_q), .preset(1'b0), .en(1'b1), .reset(1'b0));  // open: Qn
  Comparator #(.width(3), .mode("twosComplement")) comparator_3 (
    .a(3'b110), .b(EX_IR[14:12]), .eq(comparator_3_eq));  // open: gt, lt
  Comparator #(.width(3), .mode("twosComplement")) comparator_4 (
    .a(EX_IR[14:12]), .b(3'b111), .eq(comparator_4_eq));  // open: gt, lt
  not not_10 (not_10_out, \中断产生 );
  and and_12 (and_12_out, comparator_3_eq, excsr);
  and and_13 (and_13_out, comparator_4_eq, excsr);
  Comparator #(.width(16), .mode("twosComplement")) comparator_5 (
    .a({16{1'b0}}), .b(\总周期数 ), .eq(comparator_5_eq));  // open: gt, lt
  Priority_Encoder #(.select(2), .disabled("Z")) priority_encoder_1 (
    .in0(1'b0), .in1(IR1_q), .in2(IR1_2_q), .in3(IR1_3_q), .out(priority_encoder_1_out),
    .gs(priority_encoder_1_gs), .en_in(1'b1));  // open: en_out
  or or_19 (or_19_out, not_10_out, and_12_out);
  or or_20 (or_20_out, and_12_out, and_13_out, \中断产生 , uret, comparator_5_eq);
  Multiplexer #(.select(2), .width(32), .disabled("Z"), .enable("false")) multiplexer_13 (
    .in1(32'h30ac), .in2(32'h3158), .in3(32'h3204), .out(multiplexer_13_out), .sel(priority_encoder_1_out));  // open: in0
  Register #(.width(1), .trigger("rising"), .Select("low")) \u_中断使能寄存器  (
    .D(or_19_out), .en(or_20_out), .Q(\中断使能寄存器_q ), .clk(CLK), .clr(1'b0), .cs(1'b0), .preset(1'b0));
  and and_14 (\中断产生 , priority_encoder_1_gs, \中断使能寄存器_q , \当前指令优先 );
  Demultiplexer #(.select(2), .width(1), .tristate("false"), .disabled("Z"), .enable("false")) demultiplexer_1 (
    .out1(\中断1返回 ), .out2(\中断2返回 ), .out3(\中断3返回 ), .in(uret), .sel(priority_encoder_1_out));  // open: out0
  Multiplexer #(.select(2), .width(32), .disabled("Z"), .enable("false")) multiplexer_14 (
    .in0(\原始PC ), .in1(EPC), .in2(multiplexer_13_out), .in3(EPC), .out(\下条PC ), .sel({\中断产生 , uret}));
  Pull_Resistor #(.pull(0)) pull_resistor_2 (.node(\中断1返回 ));
  Pull_Resistor #(.pull(0)) pull_resistor_3 (.node(\中断3返回 ));
  or or_21 (or_21_out, \中断产生 , uret);
  not not_11 (not_11_out, \中断产生 );
  Counter #(.width(2), .max('h3), .ongoal("wrap"), .trigger("rising"), .behavior("new")) counter_7 (
    .load(1'b0), .count(or_21_out), .Q(counter_7_q), .clk(CLK), .clr(1'b0), .preset(1'b0), .down(not_11_out));  // open: D, carry
  Pull_Resistor #(.pull(0)) pull_resistor_4 (.node(\中断2返回 ));
  Decoder #(.select(2), .tristate("false"), .disabled("Z"), .enable("false")) decoder_1 (
    .out0(decoder_1_out0), .out1(decoder_1_out1), .out2(decoder_1_out2), .sel(counter_7_q));  // open: out3
  D_Flip_Flop #(.trigger("rising"), .Pre_Clr_Positions("ABOVE_BELOW"), .NegatePresetClear("false"), .enable("false"), .NewFFLayout("true")) d_ff_6 (
    .clk(CLK), .D(branch), .Q(d_ff_6_q[0]), .preset(1'b0), .reset(1'b0));  // open: Qn
  D_Flip_Flop #(.trigger("rising"), .Pre_Clr_Positions("ABOVE_BELOW"), .NegatePresetClear("false"), .enable("false"), .NewFFLayout("true")) d_ff_7 (
    .clk(CLK), .D(uret), .Q(d_ff_6_q[1]), .preset(1'b0), .reset(1'b0));  // open: Qn
  Pull_Resistor #(.pull(0)) pull_resistor_5 (.node(pull_resistor_5_node));
  Pull_Resistor #(.pull(0)) pull_resistor_6 (.node(pull_resistor_6_node));
  Decoder #(.select(2), .tristate("false"), .disabled("Z"), .enable("false")) decoder_2 (
    .out1(pull_resistor_6_node), .out2(pull_resistor_5_node), .out3(decoder_2_out3),
    .sel(priority_encoder_1_out));  // open: out0
  Pull_Resistor #(.pull(0)) pull_resistor_7 (.node(decoder_2_out3));
  and and_15 (and_15_out, \中断产生 , decoder_1_out0);
  and and_16 (and_16_out, decoder_1_out1, \中断产生 );
  and and_17 (and_17_out, decoder_1_out2, \中断产生 );
  Multiplexer #(.select(2), .width(32), .disabled("Z"), .enable("false")) multiplexer_15 (
    .in0(ID_PC), .in1(\原始PC ), .in2(IF_PC), .in3(\原始PC ), .out(multiplexer_15_out), .sel(d_ff_6_q));
  and and_18 (and_18_out, pull_resistor_6_node, \中断产生 );
  and and_19 (and_19_out, pull_resistor_5_node, \中断产生 );
  and and_20 (and_20_out, decoder_2_out3, \中断产生 );
  Register #(.width(2), .trigger("rising"), .Select("low")) IR_id (
    .D(priority_encoder_1_out), .en(and_15_out), .Q(IR_id_q), .clk(CLK), .clr(1'b0), .cs(1'b0), .preset(1'b0));
  Register #(.width(2), .trigger("rising"), .Select("low")) IR_id_2 (
    .D(priority_encoder_1_out), .en(and_16_out), .Q(IR_id_2_q), .clk(CLK), .clr(1'b0), .cs(1'b0),
    .preset(1'b0));
  Register #(.width(2), .trigger("rising"), .Select("low")) IR_id_3 (
    .D(priority_encoder_1_out), .en(and_17_out), .Q(IR_id_3_q), .clk(CLK), .clr(1'b0), .cs(1'b0),
    .preset(1'b0));
  Register #(.width(32), .trigger("rising"), .Select("low")) u_EPC (
    .D(multiplexer_15_out), .en(and_18_out), .Q(EPC_q), .clk(CLK), .clr(1'b0), .cs(1'b0), .preset(1'b0));
  Register #(.width(32), .trigger("rising"), .Select("low")) EPC_2 (
    .D(multiplexer_15_out), .en(and_19_out), .Q(EPC_2_q), .clk(CLK), .clr(1'b0), .cs(1'b0), .preset(1'b0));
  Register #(.width(32), .trigger("rising"), .Select("low")) EPC_3 (
    .D(multiplexer_15_out), .en(and_20_out), .Q(EPC_3_q), .clk(CLK), .clr(1'b0), .cs(1'b0), .preset(1'b0));
  Multiplexer #(.select(2), .width(2), .disabled("Z"), .enable("false")) multiplexer_16 (
    .in1(IR_id_q), .in2(IR_id_2_q), .in3(IR_id_3_q), .out(multiplexer_16_out), .sel(counter_7_q));  // open: in0
  Multiplexer #(.select(2), .width(32), .disabled("Z"), .enable("false")) multiplexer_17 (
    .in1(EPC_q), .in2(EPC_2_q), .in3(EPC_3_q), .out(EPC), .sel(multiplexer_16_out));  // open: in0
  Comparator #(.width(2), .mode("unsigned")) comparator_6 (
    .a(multiplexer_16_out), .b(priority_encoder_1_out), .lt(\当前指令优先 ));  // open: gt, eq
  Pull_Resistor #(.pull(1)) pull_resistor_8 (.node(\当前指令优先 ));

  // Other names for the same wires on the sheet: MEM_PC[31:0] = M_PC

  // Notes on the sheet:
  //   中断源
  //   时空图监测，可删除
  //   中断等待指示
  //   选择PC
  //   数码管输出
  //   取指
  //   指令探针
  //   指令存储器
  //   contents of rom_1 (hex, n*v repeats v):
  //   500493 140006f 100493 200913 300993 400a13 140006f 100493 200913 300993 400a13 140006f 100493 200913
  //   300993 400a13 140006f 100493 200913 300993 400a13 140006f 100493 200913 300993 400a13 140006f 100493
  //   200913 300993 400a13 140006f 100493 200913 300993 400a13 140006f 100493 200913 300993 400a13
  //   fff48493 f80492e3 100413 ff00913 100493 300993 1240c63 840a63 100493 200913 300993 400a13 949a63
  //   1249863 100493 200913 300993 c000ef a00893 73 413 140413 800533 2200893 73 8067
  //   rs1
  //   rs2
  //   I指令
  //   rd
  //   JAL
  //   JALR
  //   URET
  //   bgeu
  //   S指令
  //   B指令
  //   J指令
  //   Beq
  //   Bne
  //   AluOP
  //   AluSrcB
  //   RegWrite
  //   跳转地址生成
  //   控制位
  //   译码
  //   MemToReg
  //   MemWrite
  //   流水调试日志用
  //   暂停节拍，不能为0
  //   可计数暂停的时钟源
  //   计算参数重定向
  //   执行
  //   为方便自动评测，需要输出流水线各段保存的PC值，注意是PC不是PC+4，另外ID段寄存器写入信息，Mem段内存写入信息也要输出
  //   实现sb
  //   存储
  //   数据存储器
  //   写回
  //   选择RDin
  //   Reset 
  //   Reset 
  //   Reset 
  //   中断使能维护
  //   中断PC计算
  //   中断使能维护
  //   中断返回信号
  //   中断数量计数
  //   中断优先级确定
  //   EPC寄存器堆维护
endmodule

module \封装正确性测试  (
);

  wire IR1, IR2, IR3, MemW, RegW;
  wire [31:0] EX_PC, ID_PC, IF_PC, IR, LED, MDin, MDinr, MEM_PC, PC, RDin, RDinr, WB_PC;

  \单周期RISC_V  \u_单周期risc_v_1  (
    .IR1(IR1), .IR2(IR2), .IR3(IR3), .RegWrite(RegW), .MemWrite(MemW), .PC(PC), .IR(IR), .RDin(RDin),
    .MDin(MDin), .LedData(LED));
  \气泡流水线  \u_气泡流水线_1  (
    .RegWrite(RegW), .MemWrite(MemW), .IF_PC(IF_PC), .ID_PC(ID_PC), .EX_PC(EX_PC), .M_PC(MEM_PC),
    .WB_PC(WB_PC), .RDin(RDinr), .MDin(MDinr), .LedData(LED));
  \单周期_单级中断  \u_单周期_单级中断_1  (
    .IR1(IR1), .IR2(IR2), .IR3(IR3), .RegWrite(RegW), .MemWrite(MemW), .PC(PC), .IR(IR), .RDin(RDin),
    .MDin(MDin), .LedData(LED));
  \理想流水线  \u_理想流水线_1  (
    .RegWrite(RegW), .MemWrite(MemW), .IF_PC(IF_PC), .ID_PC(ID_PC), .EX_PC(EX_PC), .M_PC(MEM_PC),
    .WB_PC(WB_PC), .RDin(RDinr), .MDin(MDinr), .LedData(LED));
  \重定向流水线  \u_重定向流水线_1  (
    .RegWrite(RegW), .MemWrite(MemW), .IF_PC(IF_PC), .ID_PC(ID_PC), .EX_PC(EX_PC), .M_PC(MEM_PC),
    .WB_PC(WB_PC), .RDin(RDinr), .MDin(MDinr), .LedData(LED));
  \单周期_多级中断  \u_单周期_多级中断_1  (
    .IR1(IR1), .IR2(IR2), .IR3(IR3), .RegWrite(RegW), .MemWrite(MemW), .PC(PC), .IR(IR), .RDin(RDin),
    .MDin(MDin), .LedData(LED));

  // Notes on the sheet:
  //   单周期封装测试
  //   气泡流水封装测试
  //   单周期+单级中断封装测试
  //   请检查上面封装有无位宽不匹配，引脚标签是否和连接的标签相对应，否则无法在educoder平台上正确测试
  //   理想流水封装测试
  //   重定向流水封装测试
  //   单周期+多级中断封装测试
endmodule
module ID_EX (
  input  Beq,
  input  Bne,
  input  MemToReg,
  input  MemWrite,
  input  AluSrcB,
  input  RegWrite,
  input  JAL,
  input  JALR,
  input  URET,
  input  csr,
  input  bgeu,
  input  S_type,
  input  dasb,
  input  ecall,
  input  [3:0] AluOP,
  input  [31:0] r1,
  input  [31:0] r2,
  input  [4:0] rd_a,
  input  [31:0] imm1,
  input  [31:0] imm2,
  input  [31:0] PC,
  input  [31:0] PC_4,
  input  [31:0] IR,
  input  [1:0] r1_forward,
  input  [1:0] r2_forward,
  input  \预测跳转 ,
  input  reset,
  input  refresh,
  input  en,
  input  CLK,
  output Beq_2,
  output Bne_2,
  output MemToReg_2,
  output MemWrite_2,
  output AluSrcB_2,
  output RegWrite_2,
  output JAL_2,
  output JALR_2,
  output URET_2,
  output csr_2,
  output bgeu_2,
  output S_type_2,
  output dasb_2,
  output ecall_2,
  output [3:0] AluOP_2,
  output [31:0] r1_2,
  output [31:0] r2_2,
  output [4:0] rd_a_2,
  output [31:0] imm1_2,
  output [31:0] imm2_2,
  output [31:0] PC_2,
  output [31:0] PC_4_2,
  output [31:0] IR_2,
  output [1:0] r1_forward_2,
  output [1:0] r2_forward_2,
  output \预测跳转_2 
);

  wire and_1_out, and_2_out, and_3_out, and_4_out, and_5_out, and_6_out, and_7_out, and_8_out, and_9_out,
       and_10_out, and_11_out, and_12_out, and_13_out, and_14_out, and_26_out, nor_1_out;
  wire [1:0] and_24_out, and_25_out, bit_extender_10_out, bit_extender_11_out;
  wire [3:0] and_15_out, bit_extender_1_out;
  wire [4:0] and_18_out, bit_extender_4_out;
  wire [31:0] and_16_out, and_17_out, and_19_out, and_20_out, and_21_out, and_22_out, and_23_out,
       bit_extender_2_out, bit_extender_3_out, bit_extender_5_out, bit_extender_6_out, bit_extender_7_out,
       bit_extender_8_out, bit_extender_9_out;

  nor nor_1 (nor_1_out, reset, refresh);
  assign bit_extender_1_out = {{3{nor_1_out}}, nor_1_out};  // Bit_Extender bit_extender_1
  assign bit_extender_2_out = {{31{nor_1_out}}, nor_1_out};  // Bit_Extender bit_extender_2
  assign bit_extender_3_out = {{31{nor_1_out}}, nor_1_out};  // Bit_Extender bit_extender_3
  assign bit_extender_4_out = {{4{nor_1_out}}, nor_1_out};  // Bit_Extender bit_extender_4
  assign bit_extender_5_out = {{31{nor_1_out}}, nor_1_out};  // Bit_Extender bit_extender_5
  assign bit_extender_6_out = {{31{nor_1_out}}, nor_1_out};  // Bit_Extender bit_extender_6
  assign bit_extender_7_out = {{31{nor_1_out}}, nor_1_out};  // Bit_Extender bit_extender_7
  assign bit_extender_8_out = {{31{nor_1_out}}, nor_1_out};  // Bit_Extender bit_extender_8
  assign bit_extender_9_out = {{31{nor_1_out}}, nor_1_out};  // Bit_Extender bit_extender_9
  assign bit_extender_10_out = {{1{nor_1_out}}, nor_1_out};  // Bit_Extender bit_extender_10
  assign bit_extender_11_out = {{1{nor_1_out}}, nor_1_out};  // Bit_Extender bit_extender_11
  and and_1 (and_1_out, Beq, nor_1_out);
  and and_2 (and_2_out, Bne, nor_1_out);
  and and_3 (and_3_out, MemToReg, nor_1_out);
  and and_4 (and_4_out, MemWrite, nor_1_out);
  and and_5 (and_5_out, AluSrcB, nor_1_out);
  and and_6 (and_6_out, RegWrite, nor_1_out);
  and and_7 (and_7_out, JAL, nor_1_out);
  and and_8 (and_8_out, JALR, nor_1_out);
  and and_9 (and_9_out, URET, nor_1_out);
  and and_10 (and_10_out, csr, nor_1_out);
  and and_11 (and_11_out, bgeu, nor_1_out);
  and and_12 (and_12_out, S_type, nor_1_out);
  and and_13 (and_13_out, dasb, nor_1_out);
  and and_14 (and_14_out, ecall, nor_1_out);
  assign and_15_out = AluOP & bit_extender_1_out;  // AND_Gate and_15, 4 bits wide
  assign and_16_out = r1 & bit_extender_2_out;  // AND_Gate and_16, 32 bits wide
  assign and_17_out = r2 & bit_extender_3_out;  // AND_Gate and_17, 32 bits wide
  assign and_18_out = rd_a & bit_extender_4_out;  // AND_Gate and_18, 5 bits wide
  assign and_19_out = imm1 & bit_extender_5_out;  // AND_Gate and_19, 32 bits wide
  assign and_20_out = imm2 & bit_extender_6_out;  // AND_Gate and_20, 32 bits wide
  assign and_21_out = PC & bit_extender_7_out;  // AND_Gate and_21, 32 bits wide
  assign and_22_out = PC_4 & bit_extender_8_out;  // AND_Gate and_22, 32 bits wide
  assign and_23_out = IR & bit_extender_9_out;  // AND_Gate and_23, 32 bits wide
  assign and_24_out = r1_forward & bit_extender_10_out;  // AND_Gate and_24, 2 bits wide
  assign and_25_out = r2_forward & bit_extender_11_out;  // AND_Gate and_25, 2 bits wide
  and and_26 (and_26_out, \预测跳转 , nor_1_out);
  Register #(.width(1), .trigger("rising"), .Select("low")) register_1 (
    .D(and_1_out), .en(en), .Q(Beq_2), .clk(CLK));  // open: clr
  Register #(.width(1), .trigger("rising"), .Select("low")) register_2 (
    .D(and_2_out), .en(en), .Q(Bne_2), .clk(CLK));  // open: clr
  Register #(.width(1), .trigger("rising"), .Select("low")) register_3 (
    .D(and_3_out), .en(en), .Q(MemToReg_2), .clk(CLK));  // open: clr
  Register #(.width(1), .trigger("rising"), .Select("low")) register_4 (
    .D(and_4_out), .en(en), .Q(MemWrite_2), .clk(CLK));  // open: clr
  Register #(.width(1), .trigger("rising"), .Select("low")) register_5 (
    .D(and_5_out), .en(en), .Q(AluSrcB_2), .clk(CLK));  // open: clr
  Register #(.width(1), .trigger("rising"), .Select("low")) register_6 (
    .D(and_6_out), .en(en), .Q(RegWrite_2), .clk(CLK));  // open: clr
  Register #(.width(1), .trigger("rising"), .Select("low")) register_7 (
    .D(and_7_out), .en(en), .Q(JAL_2), .clk(CLK));  // open: clr
  Register #(.width(1), .trigger("rising"), .Select("low")) register_8 (
    .D(and_8_out), .en(en), .Q(JALR_2), .clk(CLK));  // open: clr
  Register #(.width(1), .trigger("rising"), .Select("low")) register_9 (
    .D(and_9_out), .en(en), .Q(URET_2), .clk(CLK));  // open: clr
  Register #(.width(1), .trigger("rising"), .Select("low")) register_10 (
    .D(and_10_out), .en(en), .Q(csr_2), .clk(CLK));  // open: clr
  Register #(.width(1), .trigger("rising"), .Select("low")) register_11 (
    .D(and_11_out), .en(en), .Q(bgeu_2), .clk(CLK));  // open: clr
  Register #(.width(1), .trigger("rising"), .Select("low")) register_12 (
    .D(and_12_out), .en(en), .Q(S_type_2), .clk(CLK));  // open: clr
  Register #(.width(1), .trigger("rising"), .Select("low")) register_13 (
    .D(and_13_out), .en(en), .Q(dasb_2), .clk(CLK));  // open: clr
  Register #(.width(1), .trigger("rising"), .Select("low")) register_14 (
    .D(and_14_out), .en(en), .Q(ecall_2), .clk(CLK));  // open: clr
  Register #(.width(4), .trigger("rising"), .Select("low")) register_15 (
    .D(and_15_out), .en(en), .Q(AluOP_2), .clk(CLK));  // open: clr
  Register #(.width(32), .trigger("rising"), .Select("low")) register_16 (
    .D(and_16_out), .en(en), .Q(r1_2), .clk(CLK));  // open: clr
  Register #(.width(32), .trigger("rising"), .Select("low")) register_17 (
    .D(and_17_out), .en(en), .Q(r2_2), .clk(CLK));  // open: clr
  Register #(.width(5), .trigger("rising"), .Select("low")) register_18 (
    .D(and_18_out), .en(en), .Q(rd_a_2), .clk(CLK));  // open: clr
  Register #(.width(32), .trigger("rising"), .Select("low")) register_19 (
    .D(and_19_out), .en(en), .Q(imm1_2), .clk(CLK));  // open: clr
  Register #(.width(32), .trigger("rising"), .Select("low")) register_20 (
    .D(and_20_out), .en(en), .Q(imm2_2), .clk(CLK));  // open: clr
  Register #(.width(32), .trigger("rising"), .Select("low")) register_21 (
    .D(and_21_out), .en(en), .Q(PC_2), .clk(CLK));  // open: clr
  Register #(.width(32), .trigger("rising"), .Select("low")) register_22 (
    .D(and_22_out), .en(en), .Q(PC_4_2), .clk(CLK));  // open: clr
  Register #(.width(32), .trigger("rising"), .Select("low")) register_23 (
    .D(and_23_out), .en(en), .Q(IR_2), .clk(CLK));  // open: clr
  Register #(.width(2), .trigger("rising"), .Select("low")) register_24 (
    .D(and_24_out), .en(en), .Q(r1_forward_2), .clk(CLK));  // open: clr
  Register #(.width(2), .trigger("rising"), .Select("low")) register_25 (
    .D(and_25_out), .en(en), .Q(r2_forward_2), .clk(CLK));  // open: clr
  Register #(.width(1), .trigger("rising"), .Select("low")) register_26 (
    .D(and_26_out), .en(en), .Q(\预测跳转_2 ), .clk(CLK));  // open: clr
endmodule

module IF_ID (
  input  [31:0] PC,
  input  [31:0] PC_4,
  input  [31:0] IR,
  input  \预测跳转 ,
  input  reset,
  input  refresh,
  input  en,
  input  CLK,
  output [31:0] PC_2,
  output [31:0] PC_4_2,
  output [31:0] IR_2,
  output \预测跳转_2 
);

  wire and_4_out, nor_1_out;
  wire [31:0] and_1_out, and_2_out, and_3_out, bit_extender_1_out;

  nor nor_1 (nor_1_out, reset, refresh);
  assign bit_extender_1_out = {{31{nor_1_out}}, nor_1_out};  // Bit_Extender bit_extender_1
  assign and_1_out = PC & bit_extender_1_out;  // AND_Gate and_1, 32 bits wide
  assign and_2_out = PC_4 & bit_extender_1_out;  // AND_Gate and_2, 32 bits wide
  assign and_3_out = IR & bit_extender_1_out;  // AND_Gate and_3, 32 bits wide
  and and_4 (and_4_out, \预测跳转 , nor_1_out);
  Register #(.width(32), .trigger("rising"), .Select("low")) register_1 (
    .D(and_1_out), .en(en), .Q(PC_2), .clk(CLK));  // open: clr
  Register #(.width(32), .trigger("rising"), .Select("low")) register_2 (
    .D(and_2_out), .en(en), .Q(PC_4_2), .clk(CLK));  // open: clr
  Register #(.width(32), .trigger("rising"), .Select("low")) register_3 (
    .D(and_3_out), .en(en), .Q(IR_2), .clk(CLK));  // open: clr
  Register #(.width(1), .trigger("rising"), .Select("low")) register_4 (
    .D(and_4_out), .en(en), .Q(\预测跳转_2 ), .clk(CLK));  // open: clr
endmodule

module EX_MEM (
  input  MemToReg,
  input  MemWrite,
  input  RegWrite,
  input  JAL,
  input  JALR,
  input  URET,
  input  dasb,
  input  halt,
  input  [31:0] res,
  input  [4:0] rd_a,
  input  [31:0] r2,
  input  [31:0] PC,
  input  [31:0] PC_4,
  input  [31:0] IR,
  input  reset,
  input  refresh,
  input  en,
  input  CLK,
  output MemToReg_2,
  output MemWrite_2,
  output RegWrite_2,
  output JAL_2,
  output JALR_2,
  output URET_2,
  output dasb_2,
  output halt_2,
  output [31:0] res_2,
  output [4:0] rd_a_2,
  output [31:0] r2_2,
  output [31:0] PC_2,
  output [31:0] PC_4_2,
  output [31:0] IR_2
);

  wire and_1_out, and_2_out, and_3_out, and_4_out, and_5_out, and_6_out, and_7_out, and_8_out, nor_1_out;
  wire [4:0] and_10_out, bit_extender_2_out;
  wire [31:0] and_9_out, and_11_out, and_12_out, and_13_out, and_14_out, bit_extender_1_out,
       bit_extender_3_out, bit_extender_4_out, bit_extender_5_out, bit_extender_6_out;

  nor nor_1 (nor_1_out, reset, refresh);
  assign bit_extender_1_out = {{31{nor_1_out}}, nor_1_out};  // Bit_Extender bit_extender_1
  assign bit_extender_2_out = {{4{nor_1_out}}, nor_1_out};  // Bit_Extender bit_extender_2
  assign bit_extender_3_out = {{31{nor_1_out}}, nor_1_out};  // Bit_Extender bit_extender_3
  assign bit_extender_4_out = {{31{nor_1_out}}, nor_1_out};  // Bit_Extender bit_extender_4
  assign bit_extender_5_out = {{31{nor_1_out}}, nor_1_out};  // Bit_Extender bit_extender_5
  assign bit_extender_6_out = {{31{nor_1_out}}, nor_1_out};  // Bit_Extender bit_extender_6
  and and_1 (and_1_out, MemToReg, nor_1_out);
  and and_2 (and_2_out, MemWrite, nor_1_out);
  and and_3 (and_3_out, RegWrite, nor_1_out);
  and and_4 (and_4_out, JAL, nor_1_out);
  and and_5 (and_5_out, JALR, nor_1_out);
  and and_6 (and_6_out, URET, nor_1_out);
  and and_7 (and_7_out, dasb, nor_1_out);
  and and_8 (and_8_out, halt, nor_1_out);
  assign and_9_out = res & bit_extender_1_out;  // AND_Gate and_9, 32 bits wide
  assign and_10_out = rd_a & bit_extender_2_out;  // AND_Gate and_10, 5 bits wide
  assign and_11_out = r2 & bit_extender_3_out;  // AND_Gate and_11, 32 bits wide
  assign and_12_out = PC & bit_extender_4_out;  // AND_Gate and_12, 32 bits wide
  assign and_13_out = PC_4 & bit_extender_5_out;  // AND_Gate and_13, 32 bits wide
  assign and_14_out = IR & bit_extender_6_out;  // AND_Gate and_14, 32 bits wide
  Register #(.width(1), .trigger("rising"), .Select("low")) register_1 (
    .D(and_1_out), .en(en), .Q(MemToReg_2), .clk(CLK));  // open: clr
  Register #(.width(1), .trigger("rising"), .Select("low")) register_2 (
    .D(and_2_out), .en(en), .Q(MemWrite_2), .clk(CLK));  // open: clr
  Register #(.width(1), .trigger("rising"), .Select("low")) register_3 (
    .D(and_3_out), .en(en), .Q(RegWrite_2), .clk(CLK));  // open: clr
  Register #(.width(1), .trigger("rising"), .Select("low")) register_4 (
    .D(and_4_out), .en(en), .Q(JAL_2), .clk(CLK));  // open: clr
  Register #(.width(1), .trigger("rising"), .Select("low")) register_5 (
    .D(and_5_out), .en(en), .Q(JALR_2), .clk(CLK));  // open: clr
  Register #(.width(1), .trigger("rising"), .Select("low")) register_6 (
    .D(and_6_out), .en(en), .Q(URET_2), .clk(CLK));  // open: clr
  Register #(.width(1), .trigger("rising"), .Select("low")) register_7 (
    .D(and_7_out), .en(en), .Q(dasb_2), .clk(CLK));  // open: clr
  Register #(.width(1), .trigger("rising"), .Select("low")) register_8 (
    .D(and_8_out), .en(en), .Q(halt_2), .clk(CLK));  // open: clr
  Register #(.width(32), .trigger("rising"), .Select("low")) register_9 (
    .D(and_9_out), .en(en), .Q(res_2), .clk(CLK));  // open: clr
  Register #(.width(5), .trigger("rising"), .Select("low")) register_10 (
    .D(and_10_out), .en(en), .Q(rd_a_2), .clk(CLK));  // open: clr
  Register #(.width(32), .trigger("rising"), .Select("low")) register_11 (
    .D(and_11_out), .en(en), .Q(r2_2), .clk(CLK));  // open: clr
  Register #(.width(32), .trigger("rising"), .Select("low")) register_12 (
    .D(and_12_out), .en(en), .Q(PC_2), .clk(CLK));  // open: clr
  Register #(.width(32), .trigger("rising"), .Select("low")) register_13 (
    .D(and_13_out), .en(en), .Q(PC_4_2), .clk(CLK));  // open: clr
  Register #(.width(32), .trigger("rising"), .Select("low")) register_14 (
    .D(and_14_out), .en(en), .Q(IR_2), .clk(CLK));  // open: clr
endmodule

module MEM_WB (
  input  MemToReg,
  input  RegWrite,
  input  JAL,
  input  JALR,
  input  URET,
  input  dasb,
  input  halt,
  input  [31:0] res,
  input  [4:0] rd_a,
  input  [31:0] MemData,
  input  [31:0] PC,
  input  [31:0] PC_4,
  input  [31:0] IR,
  input  reset,
  input  refresh,
  input  en,
  input  CLK,
  output MemToReg_2,
  output RegWrite_2,
  output JAL_2,
  output JALR_2,
  output URET_2,
  output dasb_2,
  output halt_2,
  output [31:0] res_2,
  output [4:0] rd_a_2,
  output [31:0] MemData_2,
  output [31:0] PC_2,
  output [31:0] PC_4_2,
  output [31:0] IR_2
);

  wire and_1_out, and_2_out, and_3_out, and_4_out, and_5_out, and_6_out, and_7_out, nor_1_out;
  wire [4:0] and_9_out, bit_extender_2_out;
  wire [31:0] and_8_out, and_10_out, and_11_out, and_12_out, and_13_out, bit_extender_1_out,
       bit_extender_3_out, bit_extender_4_out, bit_extender_5_out, bit_extender_6_out;

  nor nor_1 (nor_1_out, reset, refresh);
  assign bit_extender_1_out = {{31{nor_1_out}}, nor_1_out};  // Bit_Extender bit_extender_1
  assign bit_extender_2_out = {{4{nor_1_out}}, nor_1_out};  // Bit_Extender bit_extender_2
  assign bit_extender_3_out = {{31{nor_1_out}}, nor_1_out};  // Bit_Extender bit_extender_3
  assign bit_extender_4_out = {{31{nor_1_out}}, nor_1_out};  // Bit_Extender bit_extender_4
  assign bit_extender_5_out = {{31{nor_1_out}}, nor_1_out};  // Bit_Extender bit_extender_5
  assign bit_extender_6_out = {{31{nor_1_out}}, nor_1_out};  // Bit_Extender bit_extender_6
  and and_1 (and_1_out, MemToReg, nor_1_out);
  and and_2 (and_2_out, RegWrite, nor_1_out);
  and and_3 (and_3_out, JAL, nor_1_out);
  and and_4 (and_4_out, JALR, nor_1_out);
  and and_5 (and_5_out, URET, nor_1_out);
  and and_6 (and_6_out, dasb, nor_1_out);
  and and_7 (and_7_out, halt, nor_1_out);
  assign and_8_out = res & bit_extender_1_out;  // AND_Gate and_8, 32 bits wide
  assign and_9_out = rd_a & bit_extender_2_out;  // AND_Gate and_9, 5 bits wide
  assign and_10_out = MemData & bit_extender_3_out;  // AND_Gate and_10, 32 bits wide
  assign and_11_out = PC & bit_extender_4_out;  // AND_Gate and_11, 32 bits wide
  assign and_12_out = PC_4 & bit_extender_5_out;  // AND_Gate and_12, 32 bits wide
  assign and_13_out = IR & bit_extender_6_out;  // AND_Gate and_13, 32 bits wide
  Register #(.width(1), .trigger("rising"), .Select("low")) register_1 (
    .D(and_1_out), .en(en), .Q(MemToReg_2), .clk(CLK));  // open: clr
  Register #(.width(1), .trigger("rising"), .Select("low")) register_2 (
    .D(and_2_out), .en(en), .Q(RegWrite_2), .clk(CLK));  // open: clr
  Register #(.width(1), .trigger("rising"), .Select("low")) register_3 (
    .D(and_3_out), .en(en), .Q(JAL_2), .clk(CLK));  // open: clr
  Register #(.width(1), .trigger("rising"), .Select("low")) register_4 (
    .D(and_4_out), .en(en), .Q(JALR_2), .clk(CLK));  // open: clr
  Register #(.width(1), .trigger("rising"), .Select("low")) register_5 (
    .D(and_5_out), .en(en), .Q(URET_2), .clk(CLK));  // open: clr
  Register #(.width(1), .trigger("rising"), .Select("low")) register_6 (
    .D(and_6_out), .en(en), .Q(dasb_2), .clk(CLK));  // open: clr
  Register #(.width(1), .trigger("rising"), .Select("low")) register_7 (
    .D(and_7_out), .en(en), .Q(halt_2), .clk(CLK));  // open: clr
  Register #(.width(32), .trigger("rising"), .Select("low")) register_8 (
    .D(and_8_out), .en(en), .Q(res_2), .clk(CLK));  // open: clr
  Register #(.width(5), .trigger("rising"), .Select("low")) register_9 (
    .D(and_9_out), .en(en), .Q(rd_a_2), .clk(CLK));  // open: clr
  Register #(.width(32), .trigger("rising"), .Select("low")) register_10 (
    .D(and_10_out), .en(en), .Q(MemData_2), .clk(CLK));  // open: clr
  Register #(.width(32), .trigger("rising"), .Select("low")) register_11 (
    .D(and_11_out), .en(en), .Q(PC_2), .clk(CLK));  // open: clr
  Register #(.width(32), .trigger("rising"), .Select("low")) register_12 (
    .D(and_12_out), .en(en), .Q(PC_4_2), .clk(CLK));  // open: clr
  Register #(.width(32), .trigger("rising"), .Select("low")) register_13 (
    .D(and_13_out), .en(en), .Q(IR_2), .clk(CLK));  // open: clr
endmodule

module \冲突处理_bub  (
  input  [4:0] exrd,
  input  memRegWrite,
  input  user1,
  input  [31:0] IR,
  input  [4:0] memrd,
  input  user2,
  input  exRegWrite,
  input  ecall,
  input  branch,
  output \清空 ,
  output \阻塞 
);

  wire and_1_out, and_2_out, and_3_out, and_4_out, and_5_out, comparator_1_eq, comparator_2_eq,
       comparator_3_eq, comparator_4_eq, comparator_5_eq, comparator_6_eq, comparator_7_eq, comparator_8_eq,
       comparator_9_eq, comparator_10_eq, comparator_11_eq, comparator_12_eq, not_1_out, not_2_out,
       not_3_out, not_4_out, or_1_out;

  Comparator #(.width(5), .mode("twosComplement")) comparator_1 (
    .a({5{1'b0}}), .b(IR[19:15]), .eq(comparator_1_eq));  // open: gt, lt
  Comparator #(.width(5), .mode("twosComplement")) comparator_2 (
    .a(IR[19:15]), .b(exrd), .eq(comparator_2_eq));  // open: gt, lt
  Comparator #(.width(5), .mode("twosComplement")) comparator_3 (
    .a({5{1'b0}}), .b(IR[19:15]), .eq(comparator_3_eq));  // open: gt, lt
  not not_1 (not_1_out, comparator_3_eq);
  Comparator #(.width(5), .mode("twosComplement")) comparator_4 (
    .a(IR[19:15]), .b(memrd), .eq(comparator_4_eq));  // open: gt, lt
  not not_2 (not_2_out, comparator_5_eq);
  Comparator #(.width(5), .mode("twosComplement")) comparator_5 (
    .a({5{1'b0}}), .b(IR[24:20]), .eq(comparator_5_eq));  // open: gt, lt
  Comparator #(.width(5), .mode("twosComplement")) comparator_6 (
    .a(IR[24:20]), .b(exrd), .eq(comparator_6_eq));  // open: gt, lt
  Comparator #(.width(5), .mode("twosComplement")) comparator_7 (
    .a({5{1'b0}}), .b(IR[24:20]), .eq(comparator_7_eq));  // open: gt, lt
  not not_3 (not_3_out, comparator_7_eq);
  Comparator #(.width(5), .mode("twosComplement")) comparator_8 (
    .a(IR[24:20]), .b(memrd), .eq(comparator_8_eq));  // open: gt, lt
  Comparator #(.width(5), .mode("twosComplement")) comparator_9 (
    .a(5'b10001), .b(exrd), .eq(comparator_9_eq));  // open: gt, lt
  Comparator #(.width(5), .mode("twosComplement")) comparator_10 (
    .a(exrd), .b(5'b01010), .eq(comparator_10_eq));  // open: gt, lt
  Comparator #(.width(5), .mode("twosComplement")) comparator_11 (
    .a(5'b10001), .b(memrd), .eq(comparator_11_eq));  // open: gt, lt
  Comparator #(.width(5), .mode("twosComplement")) comparator_12 (
    .a(memrd), .b(5'b01010), .eq(comparator_12_eq));  // open: gt, lt
  not not_4 (not_4_out, comparator_1_eq);
  or or_1 (or_1_out, comparator_9_eq, comparator_10_eq, comparator_11_eq, comparator_12_eq);
  and and_1 (and_1_out, or_1_out, ecall);
  and and_2 (and_2_out, user1, exRegWrite, not_4_out, comparator_2_eq);
  and and_3 (and_3_out, user1, memRegWrite, not_1_out, comparator_4_eq);
  and and_4 (and_4_out, user2, exRegWrite, not_2_out, comparator_6_eq);
  and and_5 (and_5_out, user2, memRegWrite, not_3_out, comparator_8_eq);
  or or_2 (\阻塞 , and_1_out, and_2_out, and_3_out, and_4_out, and_5_out);
  or or_3 (\清空 , branch, \阻塞 );

  // Other names for the same wires on the sheet: r1[4:0] = IR[19:15]; r2[4:0] = IR[24:20]
endmodule

module \专门给SB画的电路  (
  input  [31:0] addr,
  input  [31:0] r2,
  input  [31:0] pre_data,
  input  dasb,
  output [31:0] MDin
);

  wire [4:0] bit_extender_1_out, shifter_1_out;
  wire [31:0] adder_1_out, and_1_out, multiplexer_1_out, r2_data, shifter_2_out;

  assign bit_extender_1_out = {{3{1'b0}}, addr[1:0]};  // Bit_Extender bit_extender_1
  Multiplexer #(.select(2), .width(32), .disabled("Z"), .enable("false")) multiplexer_1 (
    .in0(32'hffffff00), .in1(32'hffff00ff), .in2(32'hff00ffff), .in3(32'hffffff), .out(multiplexer_1_out),
    .sel(addr[1:0]));
  Shifter #(.width(5), .shift("ll")) shifter_1 (.in(bit_extender_1_out), .\dist (3'b011), .out(shifter_1_out));
  assign and_1_out = multiplexer_1_out & pre_data;  // AND_Gate and_1, 32 bits wide
  Shifter #(.width(32), .shift("ll")) shifter_2 (.in(r2_data), .\dist (shifter_1_out), .out(shifter_2_out));
  Adder #(.width(32)) adder_1 (.a(and_1_out), .b(shifter_2_out), .out(adder_1_out));  // open: cin, cout
  Multiplexer #(.select(1), .width(32), .disabled("Z"), .enable("false")) multiplexer_2 (
    .in0(r2), .in1(adder_1_out), .out(MDin), .sel(dasb));
  assign r2_data = {{24{1'b0}}, r2[7:0]};  // Bit_Extender bit_extender_2

  // Other names for the same wires on the sheet: byte_ad[1:0] = addr[1:0]
endmodule

module \冲突处理_redirect  (
  input  [4:0] exrd,
  input  memRegWrite,
  input  ecall,
  input  user1,
  input  [31:0] IR,
  input  [4:0] memrd,
  input  exMemToReg,
  input  user2,
  input  exRegWrite,
  input  \存在分支 ,
  output \阻塞 ,
  output \清空 ,
  output [1:0] r1_forward,
  output [1:0] r2_forward
);

  wire and_1_out, and_2_out, and_3_out, and_4_out, and_5_out, and_6_out, and_7_out, and_8_out, and_9_out,
       and_10_out, comparator_1_eq, comparator_2_eq, comparator_3_eq, comparator_4_eq, comparator_5_eq,
       comparator_6_eq, comparator_7_eq, comparator_8_eq, comparator_9_eq, comparator_10_eq,
       comparator_11_eq, comparator_12_eq, comparator_13_eq, comparator_14_eq, comparator_15_eq,
       comparator_16_eq, not_1_out, not_2_out, not_3_out, not_4_out, not_5_out, not_6_out, not_7_out,
       not_8_out, or_4_out, or_6_out;

  Comparator #(.width(5), .mode("twosComplement")) comparator_1 (
    .a({5{1'b0}}), .b(IR[19:15]), .eq(comparator_1_eq));  // open: gt, lt
  Comparator #(.width(5), .mode("twosComplement")) comparator_2 (
    .a(IR[19:15]), .b(exrd), .eq(comparator_2_eq));  // open: gt, lt
  Comparator #(.width(5), .mode("twosComplement")) comparator_3 (
    .a({5{1'b0}}), .b(IR[24:20]), .eq(comparator_3_eq));  // open: gt, lt
  Comparator #(.width(5), .mode("twosComplement")) comparator_4 (
    .a(IR[24:20]), .b(exrd), .eq(comparator_4_eq));  // open: gt, lt
  not not_1 (not_1_out, comparator_1_eq);
  not not_2 (not_2_out, comparator_3_eq);
  and and_1 (and_1_out, user1, exMemToReg, not_1_out, comparator_2_eq);
  and and_2 (and_2_out, user2, exMemToReg, not_2_out, comparator_4_eq);
  or or_1 (\阻塞 , and_1_out, and_2_out);
  or or_2 (\清空 , \阻塞 , \存在分支 );
  not not_3 (not_3_out, comparator_5_eq);
  Comparator #(.width(5), .mode("twosComplement")) comparator_5 (
    .a({5{1'b0}}), .b(IR[19:15]), .eq(comparator_5_eq));  // open: gt, lt
  Comparator #(.width(5), .mode("twosComplement")) comparator_6 (
    .a(IR[19:15]), .b(exrd), .eq(comparator_6_eq));  // open: gt, lt
  Comparator #(.width(5), .mode("twosComplement")) comparator_7 (
    .a({5{1'b0}}), .b(IR[19:15]), .eq(comparator_7_eq));  // open: gt, lt
  not not_4 (not_4_out, comparator_7_eq);
  Comparator #(.width(5), .mode("twosComplement")) comparator_8 (
    .a(IR[19:15]), .b(memrd), .eq(comparator_8_eq));  // open: gt, lt
  Comparator #(.width(5), .mode("twosComplement")) comparator_9 (
    .a({5{1'b0}}), .b(IR[24:20]), .eq(comparator_9_eq));  // open: gt, lt
  not not_5 (not_5_out, comparator_9_eq);
  Comparator #(.width(5), .mode("twosComplement")) comparator_10 (
    .a(IR[24:20]), .b(exrd), .eq(comparator_10_eq));  // open: gt, lt
  not not_6 (not_6_out, comparator_11_eq);
  Comparator #(.width(5), .mode("twosComplement")) comparator_11 (
    .a({5{1'b0}}), .b(IR[24:20]), .eq(comparator_11_eq));  // open: gt, lt
  Comparator #(.width(5), .mode("twosComplement")) comparator_12 (
    .a(IR[24:20]), .b(memrd), .eq(comparator_12_eq));  // open: gt, lt
  Comparator #(.width(5), .mode("twosComplement")) comparator_13 (
    .a(exrd), .b(5'b10001), .eq(comparator_13_eq));  // open: gt, lt
  Comparator #(.width(5), .mode("twosComplement")) comparator_14 (
    .a(memrd), .b(5'b10001), .eq(comparator_14_eq));  // open: gt, lt
  Comparator #(.width(5), .mode("twosComplement")) comparator_15 (
    .a(exrd), .b(5'b01010), .eq(comparator_15_eq));  // open: gt, lt
  Comparator #(.width(5), .mode("twosComplement")) comparator_16 (
    .a(memrd), .b(5'b01010), .eq(comparator_16_eq));  // open: gt, lt
  and and_3 (and_3_out, comparator_13_eq, exRegWrite, ecall);
  and and_4 (and_4_out, user1, exRegWrite, not_3_out, comparator_6_eq);
  and and_5 (and_5_out, user1, memRegWrite, not_4_out, comparator_8_eq);
  and and_6 (and_6_out, comparator_14_eq, memRegWrite, ecall);
  and and_7 (and_7_out, comparator_15_eq, exRegWrite, ecall);
  and and_8 (and_8_out, user2, exRegWrite, not_5_out, comparator_10_eq);
  and and_9 (and_9_out, user2, memRegWrite, not_6_out, comparator_12_eq);
  and and_10 (and_10_out, comparator_16_eq, memRegWrite, ecall);
  or or_3 (r1_forward[1], and_3_out, and_4_out);
  not not_7 (not_7_out, r1_forward[1]);
  or or_4 (or_4_out, and_5_out, and_6_out);
  or or_5 (r2_forward[1], and_7_out, and_8_out);
  not not_8 (not_8_out, r2_forward[1]);
  or or_6 (or_6_out, and_9_out, and_10_out);
  and and_11 (r1_forward[0], not_7_out, or_4_out);
  and and_12 (r2_forward[0], not_8_out, or_6_out);

  // Other names for the same wires on the sheet: r1[4:0] = IR[19:15]; r2[4:0] = IR[24:20]
endmodule

module \cache归并比较  (
  input  [15:0] Y,
  input  [15:0] X,
  input  [2:0] Y_num,
  input  [2:0] X_num,
  output [15:0] MAX,
  output [2:0] Max_num
);

  wire comparator_1_eq, comparator_1_gt, or_1_out;

  Multiplexer #(.select(1), .width(16), .disabled("Z"), .enable("false")) multiplexer_1 (
    .in0(Y), .in1(X), .out(MAX), .sel(or_1_out));
  Comparator #(.width(16), .mode("unsigned")) comparator_1 (
    .a(X), .b(Y), .gt(comparator_1_gt), .eq(comparator_1_eq));  // open: lt
  or or_1 (or_1_out, comparator_1_gt, comparator_1_eq);
  Multiplexer #(.select(1), .width(3), .disabled("Z"), .enable("false")) multiplexer_2 (
    .in0(Y_num), .in1(X_num), .out(Max_num), .sel(or_1_out));

  // Notes on the sheet:
  //   输出两个输入中的较大值，并输出较大值的3位编号
endmodule

module \分支历史表  (
  input  [31:0] exbranch_ad,
  input  [31:0] exPC,
  input  exbranch,
  input  CLK,
  input  [31:0] ifPC,
  input  \是否跳转 ,
  output [31:0] \预测结果 ,
  output \预测跳转 
);

  wire and_1_out, and_2_out, and_3_out, and_4_out, and_5_out, and_6_out, and_7_out, and_8_out, and_9_out,
       and_10_out, and_11_out, and_12_out, and_13_out, and_14_out, and_15_out, and_16_out, and_17_out,
       and_18_out, and_19_out, and_20_out, and_21_out, and_22_out, and_23_out, and_26_out, and_27_out,
       and_30_out, and_31_out, and_34_out, and_35_out, and_36_out, and_37_out, and_40_out, and_41_out,
       and_42_out, and_43_out, and_44_out, and_45_out, and_46_out, and_47_out, comparator_1_eq,
       comparator_2_eq, comparator_3_eq, comparator_4_eq, comparator_5_eq, comparator_6_eq, comparator_7_eq,
       comparator_8_eq, comparator_9_eq, comparator_10_eq, comparator_11_eq, comparator_12_eq,
       comparator_13_eq, comparator_14_eq, comparator_15_eq, comparator_16_eq, decoder_1_out0,
       decoder_1_out1, decoder_1_out2, decoder_1_out3, decoder_1_out4, decoder_1_out5, decoder_1_out6,
       decoder_1_out7, nor_2_out, not_1_out, not_2_out, not_3_out, not_4_out, not_5_out, not_6_out,
       not_7_out, not_8_out, or_1_out, or_2_out, or_3_out, or_4_out, or_5_out, or_6_out, or_7_out, or_8_out,
       or_9_out, or_10_out, or_11_out, or_12_out, or_13_out, or_14_out, or_15_out, or_16_out, undriven, WE0,
       WE1, WE2, WE3, WE4, WE5, WE6, WE7, \已满 , \有效位_2_q , \有效位_3_q , \有效位_4_q , \有效位_5_q , \有效位_6_q ,
       \有效位_7_q , \有效位_8_q , \有效位_q ;
  wire [0:0] controlled_buffer_9_out, controlled_buffer_10_out, controlled_buffer_11_out,
       controlled_buffer_12_out, controlled_buffer_13_out, controlled_buffer_14_out,
       controlled_buffer_15_out, controlled_buffer_16_out;
  wire [1:0] register_1_q, register_2_q, register_3_q, register_4_q, register_5_q, register_6_q,
       register_7_q, register_8_q, \双位预测状态转换_1_z0 , \双位预测状态转换_2_z0 , \双位预测状态转换_3_z0 , \双位预测状态转换_4_z0 ,
       \双位预测状态转换_5_z0 , \双位预测状态转换_6_z0 , \双位预测状态转换_7_z0 , \双位预测状态转换_8_z0 ;
  wire [2:0] \cache归并比较_1_max_num , \cache归并比较_2_max_num , \cache归并比较_3_max_num , \cache归并比较_4_max_num ,
       \cache归并比较_5_max_num , \cache归并比较_6_max_num , \cache归并比较_7_max_num ;
  wire [15:0] \cache归并比较_1_max , \cache归并比较_2_max , \cache归并比较_3_max , \cache归并比较_4_max , \cache归并比较_5_max ,
       \cache归并比较_6_max , \淘汰计数器_2_q , \淘汰计数器_3_q , \淘汰计数器_4_q , \淘汰计数器_5_q , \淘汰计数器_6_q , \淘汰计数器_7_q ,
       \淘汰计数器_8_q , \淘汰计数器_q ;
  wire [31:0] \区地址_2_q , \区地址_3_q , \区地址_4_q , \区地址_5_q , \区地址_6_q , \区地址_7_q , \区地址_8_q , \区地址_q ,
       \数据缓存_2_q , \数据缓存_3_q , \数据缓存_4_q , \数据缓存_5_q , \数据缓存_6_q , \数据缓存_7_q , \数据缓存_8_q , \数据缓存_q ;

  and and_1 (and_1_out, exbranch, WE7);
  and and_2 (and_2_out, exbranch, WE0);
  and and_3 (and_3_out, exbranch, WE1);
  and and_4 (and_4_out, exbranch, WE2);
  and and_5 (and_5_out, exbranch, WE3);
  and and_6 (and_6_out, exbranch, WE4);
  and and_7 (and_7_out, exbranch, WE5);
  and and_8 (and_8_out, exbranch, WE6);
  Register #(.width(1), .trigger("rising"), .Select("low")) \u_有效位  (
    .D(1'b1), .en(and_2_out), .Q(\有效位_q ), .clk(CLK), .clr(1'b0), .cs(1'b0), .preset(1'b0));
  Register #(.width(1), .trigger("rising"), .Select("low")) \u_有效位_2  (
    .D(1'b1), .en(and_3_out), .Q(\有效位_2_q ), .clk(CLK), .clr(1'b0), .cs(1'b0), .preset(1'b0));
  Register #(.width(1), .trigger("rising"), .Select("low")) \u_有效位_3  (
    .D(1'b1), .en(and_4_out), .Q(\有效位_3_q ), .clk(CLK), .clr(1'b0), .cs(1'b0), .preset(1'b0));
  Register #(.width(1), .trigger("rising"), .Select("low")) \u_有效位_4  (
    .D(1'b1), .en(and_5_out), .Q(\有效位_4_q ), .clk(CLK), .clr(1'b0), .cs(1'b0), .preset(1'b0));
  Register #(.width(1), .trigger("rising"), .Select("low")) \u_有效位_5  (
    .D(1'b1), .en(and_6_out), .Q(\有效位_5_q ), .clk(CLK), .clr(1'b0), .cs(1'b0), .preset(1'b0));
  Register #(.width(1), .trigger("rising"), .Select("low")) \u_有效位_6  (
    .D(1'b1), .en(and_7_out), .Q(\有效位_6_q ), .clk(CLK), .clr(1'b0), .cs(1'b0), .preset(1'b0));
  Register #(.width(1), .trigger("rising"), .Select("low")) \u_有效位_7  (
    .D(1'b1), .en(and_8_out), .Q(\有效位_7_q ), .clk(CLK), .clr(1'b0), .cs(1'b0), .preset(1'b0));
  Register #(.width(1), .trigger("rising"), .Select("low")) \u_有效位_8  (
    .D(1'b1), .en(and_1_out), .Q(\有效位_8_q ), .clk(CLK), .clr(1'b0), .cs(1'b0), .preset(1'b0));
  not not_1 (not_1_out, \有效位_8_q );
  not not_2 (not_2_out, \有效位_7_q );
  not not_3 (not_3_out, \有效位_6_q );
  not not_4 (not_4_out, \有效位_5_q );
  not not_5 (not_5_out, \有效位_4_q );
  not not_6 (not_6_out, \有效位_3_q );
  not not_7 (not_7_out, \有效位_2_q );
  not not_8 (not_8_out, \有效位_q );
  Register #(.width(32), .trigger("rising"), .Select("low")) \u_区地址  (
    .D(exPC), .en(and_2_out), .Q(\区地址_q ), .clk(CLK), .clr(1'b0), .cs(1'b0), .preset(1'b0));
  Register #(.width(32), .trigger("rising"), .Select("low")) \u_区地址_2  (
    .D(exPC), .en(and_3_out), .Q(\区地址_2_q ), .clk(CLK), .clr(1'b0), .cs(1'b0), .preset(1'b0));
  Register #(.width(32), .trigger("rising"), .Select("low")) \u_区地址_3  (
    .D(exPC), .en(and_4_out), .Q(\区地址_3_q ), .clk(CLK), .clr(1'b0), .cs(1'b0), .preset(1'b0));
  Register #(.width(32), .trigger("rising"), .Select("low")) \u_区地址_4  (
    .D(exPC), .en(and_5_out), .Q(\区地址_4_q ), .clk(CLK), .clr(1'b0), .cs(1'b0), .preset(1'b0));
  Register #(.width(32), .trigger("rising"), .Select("low")) \u_区地址_5  (
    .D(exPC), .en(and_6_out), .Q(\区地址_5_q ), .clk(CLK), .clr(1'b0), .cs(1'b0), .preset(1'b0));
  Register #(.width(32), .trigger("rising"), .Select("low")) \u_区地址_6  (
    .D(exPC), .en(and_7_out), .Q(\区地址_6_q ), .clk(CLK), .clr(1'b0), .cs(1'b0), .preset(1'b0));
  Register #(.width(32), .trigger("rising"), .Select("low")) \u_区地址_7  (
    .D(exPC), .en(and_8_out), .Q(\区地址_7_q ), .clk(CLK), .clr(1'b0), .cs(1'b0), .preset(1'b0));
  Register #(.width(32), .trigger("rising"), .Select("low")) \u_区地址_8  (
    .D(exPC), .en(and_1_out), .Q(\区地址_8_q ), .clk(CLK), .clr(1'b0), .cs(1'b0), .preset(1'b0));
  Comparator #(.width(32), .mode("twosComplement")) comparator_1 (
    .a(\区地址_8_q ), .b(exPC), .eq(comparator_1_eq));  // open: gt, lt
  Comparator #(.width(32), .mode("twosComplement")) comparator_2 (
    .a(\区地址_8_q ), .b(ifPC), .eq(comparator_2_eq));  // open: gt, lt
  and and_9 (and_9_out, not_1_out, \有效位_7_q );
  and and_10 (and_10_out, not_2_out, \有效位_6_q );
  and and_11 (and_11_out, not_3_out, \有效位_5_q );
  and and_12 (and_12_out, not_4_out, \有效位_4_q );
  and and_13 (and_13_out, not_5_out, \有效位_3_q );
  and and_14 (and_14_out, not_6_out, \有效位_2_q );
  and and_15 (and_15_out, not_7_out, \有效位_q );
  and and_16 (and_16_out, \有效位_8_q , comparator_1_eq);
  and and_17 (and_17_out, \有效位_8_q , comparator_2_eq);
  Comparator #(.width(32), .mode("twosComplement")) comparator_3 (
    .a(\区地址_7_q ), .b(exPC), .eq(comparator_3_eq));  // open: gt, lt
  Comparator #(.width(32), .mode("twosComplement")) comparator_4 (
    .a(\区地址_7_q ), .b(ifPC), .eq(comparator_4_eq));  // open: gt, lt
  nor nor_1 (\已满 , not_8_out, and_15_out, and_14_out, and_13_out, and_12_out, and_11_out, and_10_out, and_9_out);
  and and_18 (and_18_out, \有效位_7_q , comparator_3_eq);
  and and_19 (and_19_out, \有效位_7_q , comparator_4_eq);
  Comparator #(.width(32), .mode("twosComplement")) comparator_5 (
    .a(\区地址_6_q ), .b(exPC), .eq(comparator_5_eq));  // open: gt, lt
  Comparator #(.width(32), .mode("twosComplement")) comparator_6 (
    .a(\区地址_6_q ), .b(ifPC), .eq(comparator_6_eq));  // open: gt, lt
  and and_20 (and_20_out, \有效位_6_q , comparator_5_eq);
  and and_21 (and_21_out, \有效位_6_q , comparator_6_eq);
  and and_22 (and_22_out, \有效位_5_q , comparator_7_eq);
  Comparator #(.width(32), .mode("twosComplement")) comparator_7 (
    .a(\区地址_5_q ), .b(exPC), .eq(comparator_7_eq));  // open: gt, lt
  and and_23 (and_23_out, \有效位_5_q , comparator_8_eq);
  Comparator #(.width(32), .mode("twosComplement")) comparator_8 (
    .a(\区地址_5_q ), .b(ifPC), .eq(comparator_8_eq));  // open: gt, lt
  Comparator #(.width(32), .mode("twosComplement")) comparator_9 (
    .a(\区地址_4_q ), .b(exPC), .eq(comparator_9_eq));  // open: gt, lt
  Comparator #(.width(32), .mode("twosComplement")) comparator_10 (
    .a(\区地址_4_q ), .b(ifPC), .eq(comparator_10_eq));  // open: gt, lt
  or or_1 (or_1_out, not_8_out, decoder_1_out0);
  or or_2 (or_2_out, and_15_out, decoder_1_out1);
  and and_24 (WE0, nor_2_out, or_1_out);
  and and_25 (WE1, nor_2_out, or_2_out);
  and and_26 (and_26_out, \有效位_4_q , comparator_9_eq);
  and and_27 (and_27_out, \有效位_4_q , comparator_10_eq);
  Comparator #(.width(32), .mode("twosComplement")) comparator_11 (
    .a(\区地址_3_q ), .b(exPC), .eq(comparator_11_eq));  // open: gt, lt
  Comparator #(.width(32), .mode("twosComplement")) comparator_12 (
    .a(\区地址_3_q ), .b(ifPC), .eq(comparator_12_eq));  // open: gt, lt
  or or_3 (or_3_out, and_13_out, decoder_1_out3);
  or or_4 (or_4_out, and_14_out, decoder_1_out2);
  and and_28 (WE3, nor_2_out, or_3_out);
  and and_29 (WE2, nor_2_out, or_4_out);
  and and_30 (and_30_out, \有效位_3_q , comparator_11_eq);
  and and_31 (and_31_out, \有效位_3_q , comparator_12_eq);
  Comparator #(.width(32), .mode("twosComplement")) comparator_13 (
    .a(\区地址_2_q ), .b(exPC), .eq(comparator_13_eq));  // open: gt, lt
  Comparator #(.width(32), .mode("twosComplement")) comparator_14 (
    .a(\区地址_2_q ), .b(ifPC), .eq(comparator_14_eq));  // open: gt, lt
  or or_5 (or_5_out, and_11_out, decoder_1_out5);
  or or_6 (or_6_out, and_12_out, decoder_1_out4);
  and and_32 (WE4, nor_2_out, or_6_out);
  and and_33 (WE5, nor_2_out, or_5_out);
  or or_7 (or_7_out, and_2_out, and_37_out);
  or or_8 (or_8_out, and_3_out, and_35_out);
  or or_9 (or_9_out, and_4_out, and_31_out);
  or or_10 (or_10_out, and_5_out, and_27_out);
  or or_11 (or_11_out, and_6_out, and_23_out);
  or or_12 (or_12_out, and_7_out, and_21_out);
  or or_13 (or_13_out, and_8_out, and_19_out);
  or or_14 (or_14_out, and_1_out, and_17_out);
  and and_34 (and_34_out, \有效位_2_q , comparator_13_eq);
  and and_35 (and_35_out, \有效位_2_q , comparator_14_eq);
  and and_36 (and_36_out, \有效位_q , comparator_15_eq);
  Comparator #(.width(32), .mode("twosComplement")) comparator_15 (
    .a(\区地址_q ), .b(exPC), .eq(comparator_15_eq));  // open: gt, lt
  and and_37 (and_37_out, \有效位_q , comparator_16_eq);
  Comparator #(.width(32), .mode("twosComplement")) comparator_16 (
    .a(\区地址_q ), .b(ifPC), .eq(comparator_16_eq));  // open: gt, lt
  or or_15 (or_15_out, and_10_out, decoder_1_out6);
  or or_16 (or_16_out, and_9_out, decoder_1_out7);
  and and_38 (WE7, nor_2_out, or_16_out);
  and and_39 (WE6, nor_2_out, or_15_out);
  Counter #(.width(16), .max('hffff), .ongoal("wrap"), .trigger("rising"), .behavior("new")) \u_淘汰计数器  (
    .load(or_7_out), .D({16{1'b0}}), .count(\有效位_q ), .Q(\淘汰计数器_q ), .clk(CLK), .clr(1'b0), .preset(1'b0),
    .down(1'b0));  // open: carry
  Counter #(.width(16), .max('hffff), .ongoal("wrap"), .trigger("rising"), .behavior("new")) \u_淘汰计数器_2  (
    .load(or_8_out), .D({16{1'b0}}), .count(\有效位_2_q ), .Q(\淘汰计数器_2_q ), .clk(CLK), .clr(1'b0),
    .preset(1'b0), .down(1'b0));  // open: carry
  Counter #(.width(16), .max('hffff), .ongoal("wrap"), .trigger("rising"), .behavior("new")) \u_淘汰计数器_3  (
    .load(or_9_out), .D({16{1'b0}}), .count(\有效位_3_q ), .Q(\淘汰计数器_3_q ), .clk(CLK), .clr(1'b0),
    .preset(1'b0), .down(1'b0));  // open: carry
  Counter #(.width(16), .max('hffff), .ongoal("wrap"), .trigger("rising"), .behavior("new")) \u_淘汰计数器_4  (
    .load(or_10_out), .D({16{1'b0}}), .count(\有效位_4_q ), .Q(\淘汰计数器_4_q ), .clk(CLK), .clr(1'b0),
    .preset(1'b0), .down(1'b0));  // open: carry
  Counter #(.width(16), .max('hffff), .ongoal("wrap"), .trigger("rising"), .behavior("new")) \u_淘汰计数器_5  (
    .load(or_11_out), .D({16{1'b0}}), .count(\有效位_5_q ), .Q(\淘汰计数器_5_q ), .clk(CLK), .clr(1'b0),
    .preset(1'b0), .down(1'b0));  // open: carry
  Counter #(.width(16), .max('hffff), .ongoal("wrap"), .trigger("rising"), .behavior("new")) \u_淘汰计数器_6  (
    .load(or_12_out), .D({16{1'b0}}), .count(\有效位_6_q ), .Q(\淘汰计数器_6_q ), .clk(CLK), .clr(1'b0),
    .preset(1'b0), .down(1'b0));  // open: carry
  Counter #(.width(16), .max('hffff), .ongoal("wrap"), .trigger("rising"), .behavior("new")) \u_淘汰计数器_7  (
    .load(or_13_out), .D({16{1'b0}}), .count(\有效位_7_q ), .Q(\淘汰计数器_7_q ), .clk(CLK), .clr(1'b0),
    .preset(1'b0), .down(1'b0));  // open: carry
  Counter #(.width(16), .max('hffff), .ongoal("wrap"), .trigger("rising"), .behavior("new")) \u_淘汰计数器_8  (
    .load(or_14_out), .D({16{1'b0}}), .count(\有效位_8_q ), .Q(\淘汰计数器_8_q ), .clk(CLK), .clr(1'b0),
    .preset(1'b0), .down(1'b0));  // open: carry
  \cache归并比较  \cache归并比较_1  (
    .Y(\淘汰计数器_7_q ), .X(\淘汰计数器_8_q ), .Y_num(3'b110), .X_num(3'b111), .MAX(\cache归并比较_1_max ),
    .Max_num(\cache归并比较_1_max_num ));
  \cache归并比较  \cache归并比较_2  (
    .Y(\淘汰计数器_5_q ), .X(\淘汰计数器_6_q ), .Y_num(3'b100), .X_num(3'b101), .MAX(\cache归并比较_2_max ),
    .Max_num(\cache归并比较_2_max_num ));
  \cache归并比较  \cache归并比较_3  (
    .Y(\淘汰计数器_3_q ), .X(\淘汰计数器_4_q ), .Y_num(3'b010), .X_num(3'b011), .MAX(\cache归并比较_3_max ),
    .Max_num(\cache归并比较_3_max_num ));
  \cache归并比较  \cache归并比较_4  (
    .Y(\cache归并比较_2_max ), .X(\cache归并比较_1_max ), .Y_num(\cache归并比较_2_max_num ),
    .X_num(\cache归并比较_1_max_num ), .MAX(\cache归并比较_4_max ), .Max_num(\cache归并比较_4_max_num ));
  \cache归并比较  \cache归并比较_5  (
    .Y(\淘汰计数器_q ), .X(\淘汰计数器_2_q ), .Y_num(3'b000), .X_num(3'b001), .MAX(\cache归并比较_5_max ),
    .Max_num(\cache归并比较_5_max_num ));
  Register #(.width(32), .trigger("rising"), .Select("low")) \u_数据缓存  (
    .D(exbranch_ad), .en(and_2_out), .Q(\数据缓存_q ), .clk(CLK), .clr(1'b0), .cs(1'b0), .preset(1'b0));
  Register #(.width(32), .trigger("rising"), .Select("low")) \u_数据缓存_2  (
    .D(exbranch_ad), .en(and_3_out), .Q(\数据缓存_2_q ), .clk(CLK), .clr(1'b0), .cs(1'b0), .preset(1'b0));
  Register #(.width(32), .trigger("rising"), .Select("low")) \u_数据缓存_3  (
    .D(exbranch_ad), .en(and_4_out), .Q(\数据缓存_3_q ), .clk(CLK), .clr(1'b0), .cs(1'b0), .preset(1'b0));
  Register #(.width(32), .trigger("rising"), .Select("low")) \u_数据缓存_4  (
    .D(exbranch_ad), .en(and_5_out), .Q(\数据缓存_4_q ), .clk(CLK), .clr(1'b0), .cs(undriven), .preset(1'b0));
  Register #(.width(32), .trigger("rising"), .Select("low")) \u_数据缓存_5  (
    .D(exbranch_ad), .en(and_6_out), .Q(\数据缓存_5_q ), .clk(CLK), .clr(1'b0), .cs(1'b0), .preset(1'b0));
  assign \预测结果  = and_23_out ? \数据缓存_5_q  : 32'bz;  // Controlled_Buffer controlled_buffer_1
  assign \预测结果  = and_21_out ? \数据缓存_6_q  : 32'bz;  // Controlled_Buffer controlled_buffer_2
  Register #(.width(32), .trigger("rising"), .Select("low")) \u_数据缓存_6  (
    .D(exbranch_ad), .en(and_7_out), .Q(\数据缓存_6_q ), .clk(CLK), .clr(1'b0), .cs(1'b0), .preset(1'b0));
  Register #(.width(32), .trigger("rising"), .Select("low")) \u_数据缓存_7  (
    .D(exbranch_ad), .en(and_8_out), .Q(\数据缓存_7_q ), .clk(CLK), .clr(1'b0), .cs(1'b0), .preset(1'b0));
  assign \预测结果  = and_19_out ? \数据缓存_7_q  : 32'bz;  // Controlled_Buffer controlled_buffer_3
  Register #(.width(32), .trigger("rising"), .Select("low")) \u_数据缓存_8  (
    .D(exbranch_ad), .en(and_1_out), .Q(\数据缓存_8_q ), .clk(CLK), .clr(1'b0), .cs(1'b0), .preset(1'b0));
  assign \预测结果  = and_17_out ? \数据缓存_8_q  : 32'bz;  // Controlled_Buffer controlled_buffer_4
  \cache归并比较  \cache归并比较_6  (
    .Y(\cache归并比较_5_max ), .X(\cache归并比较_3_max ), .Y_num(\cache归并比较_5_max_num ),
    .X_num(\cache归并比较_3_max_num ), .MAX(\cache归并比较_6_max ), .Max_num(\cache归并比较_6_max_num ));
  Decoder #(.select(3), .tristate("false"), .disabled(0), .enable("true")) decoder_1 (
    .out0(decoder_1_out0), .out1(decoder_1_out1), .out2(decoder_1_out2), .out3(decoder_1_out3),
    .out4(decoder_1_out4), .out5(decoder_1_out5), .out6(decoder_1_out6), .out7(decoder_1_out7),
    .sel(\cache归并比较_7_max_num ), .en(\已满 ));
  assign \预测结果  = and_37_out ? \数据缓存_q  : 32'bz;  // Controlled_Buffer controlled_buffer_5
  assign \预测结果  = and_35_out ? \数据缓存_2_q  : 32'bz;  // Controlled_Buffer controlled_buffer_6
  assign \预测结果  = and_31_out ? \数据缓存_3_q  : 32'bz;  // Controlled_Buffer controlled_buffer_7
  assign \预测结果  = and_27_out ? \数据缓存_4_q  : 32'bz;  // Controlled_Buffer controlled_buffer_8
  nor nor_2 (nor_2_out, and_36_out, and_34_out, and_30_out, and_26_out, and_22_out, and_20_out, and_18_out, and_16_out);
  \cache归并比较  \cache归并比较_7  (
    .Y(\cache归并比较_6_max ), .X(\cache归并比较_4_max ), .Y_num(\cache归并比较_6_max_num ),
    .X_num(\cache归并比较_4_max_num ), .Max_num(\cache归并比较_7_max_num ));  // open: MAX
  \双位预测状态转换  \u_双位预测状态转换_1  (
    .Y1(register_1_q[1]), .Y0(register_1_q[0]), .\跳转 (\是否跳转 ), .Z1(\双位预测状态转换_1_z0 [1]),
    .Z0(\双位预测状态转换_1_z0 [0]));
  \双位预测状态转换  \u_双位预测状态转换_2  (
    .Y1(register_2_q[1]), .Y0(register_2_q[0]), .\跳转 (\是否跳转 ), .Z1(\双位预测状态转换_2_z0 [1]),
    .Z0(\双位预测状态转换_2_z0 [0]));
  \双位预测状态转换  \u_双位预测状态转换_3  (
    .Y1(register_3_q[1]), .Y0(register_3_q[0]), .\跳转 (\是否跳转 ), .Z1(\双位预测状态转换_3_z0 [1]),
    .Z0(\双位预测状态转换_3_z0 [0]));
  \双位预测状态转换  \u_双位预测状态转换_4  (
    .Y1(register_4_q[1]), .Y0(register_4_q[0]), .\跳转 (\是否跳转 ), .Z1(\双位预测状态转换_4_z0 [1]),
    .Z0(\双位预测状态转换_4_z0 [0]));
  \双位预测状态转换  \u_双位预测状态转换_5  (
    .Y1(register_5_q[1]), .Y0(register_5_q[0]), .\跳转 (\是否跳转 ), .Z1(\双位预测状态转换_5_z0 [1]),
    .Z0(\双位预测状态转换_5_z0 [0]));
  \双位预测状态转换  \u_双位预测状态转换_6  (
    .Y1(register_6_q[1]), .Y0(register_6_q[0]), .\跳转 (\是否跳转 ), .Z1(\双位预测状态转换_6_z0 [1]),
    .Z0(\双位预测状态转换_6_z0 [0]));
  \双位预测状态转换  \u_双位预测状态转换_7  (
    .Y1(register_7_q[1]), .Y0(register_7_q[0]), .\跳转 (\是否跳转 ), .Z1(\双位预测状态转换_7_z0 [1]),
    .Z0(\双位预测状态转换_7_z0 [0]));
  \双位预测状态转换  \u_双位预测状态转换_8  (
    .Y1(register_8_q[1]), .Y0(register_8_q[0]), .\跳转 (\是否跳转 ), .Z1(\双位预测状态转换_8_z0 [1]),
    .Z0(\双位预测状态转换_8_z0 [0]));
  and and_40 (and_40_out, exbranch, and_16_out);
  and and_41 (and_41_out, exbranch, and_18_out);
  and and_42 (and_42_out, exbranch, and_20_out);
  and and_43 (and_43_out, exbranch, and_22_out);
  and and_44 (and_44_out, exbranch, and_26_out);
  and and_45 (and_45_out, exbranch, and_30_out);
  and and_46 (and_46_out, exbranch, and_34_out);
  and and_47 (and_47_out, exbranch, and_36_out);
  Register #(.width(2), .trigger("rising"), .Select("low")) register_1 (
    .D(\双位预测状态转换_1_z0 ), .en(and_40_out), .Q(register_1_q), .clk(CLK), .clr(1'b0), .cs(1'b0), .preset(1'b0));
  Register #(.width(2), .trigger("rising"), .Select("low")) register_2 (
    .D(\双位预测状态转换_2_z0 ), .en(and_41_out), .Q(register_2_q), .clk(CLK), .clr(1'b0), .cs(1'b0), .preset(1'b0));
  Register #(.width(2), .trigger("rising"), .Select("low")) register_3 (
    .D(\双位预测状态转换_3_z0 ), .en(and_42_out), .Q(register_3_q), .clk(CLK), .clr(1'b0), .cs(1'b0), .preset(1'b0));
  Register #(.width(2), .trigger("rising"), .Select("low")) register_4 (
    .D(\双位预测状态转换_4_z0 ), .en(and_43_out), .Q(register_4_q), .clk(CLK), .clr(1'b0), .cs(1'b0), .preset(1'b0));
  Register #(.width(2), .trigger("rising"), .Select("low")) register_5 (
    .D(\双位预测状态转换_5_z0 ), .en(and_44_out), .Q(register_5_q), .clk(CLK), .cs(1'b0), .preset(1'b0));  // open: clr
  Register #(.width(2), .trigger("rising"), .Select("low")) register_6 (
    .D(\双位预测状态转换_6_z0 ), .en(and_45_out), .Q(register_6_q), .clk(CLK), .clr(1'b0), .cs(1'b0), .preset(1'b0));
  Register #(.width(2), .trigger("rising"), .Select("low")) register_7 (
    .D(\双位预测状态转换_7_z0 ), .en(and_46_out), .Q(register_7_q), .clk(CLK), .clr(1'b0), .cs(1'b0), .preset(1'b0));
  Register #(.width(2), .trigger("rising"), .Select("low")) register_8 (
    .D(\双位预测状态转换_8_z0 ), .en(and_47_out), .Q(register_8_q), .clk(CLK), .clr(1'b0), .cs(1'b0), .preset(1'b0));
  assign {\预测跳转 , controlled_buffer_9_out[0]} = and_17_out ? register_1_q : 2'bz;  // Controlled_Buffer controlled_buffer_9
  assign {\预测跳转 , controlled_buffer_10_out[0]} = and_19_out ? register_2_q : 2'bz;  // Controlled_Buffer controlled_buffer_10
  assign {\预测跳转 , controlled_buffer_11_out[0]} = and_21_out ? register_3_q : 2'bz;  // Controlled_Buffer controlled_buffer_11
  assign {\预测跳转 , controlled_buffer_12_out[0]} = and_23_out ? register_4_q : 2'bz;  // Controlled_Buffer controlled_buffer_12
  assign {\预测跳转 , controlled_buffer_13_out[0]} = and_27_out ? register_5_q : 2'bz;  // Controlled_Buffer controlled_buffer_13
  assign {\预测跳转 , controlled_buffer_14_out[0]} = and_31_out ? register_6_q : 2'bz;  // Controlled_Buffer controlled_buffer_14
  assign {\预测跳转 , controlled_buffer_15_out[0]} = and_35_out ? register_7_q : 2'bz;  // Controlled_Buffer controlled_buffer_15
  assign {\预测跳转 , controlled_buffer_16_out[0]} = and_37_out ? register_8_q : 2'bz;  // Controlled_Buffer controlled_buffer_16
  Pull_Resistor #(.pull(0)) pull_resistor_1 (.node(\预测跳转 ));

  // Other names for the same wires on the sheet: 分支指令地址[31:0] = exPC; 分支目标地址[31:0] = exbranch_ad; 查询地址[31:0] = ifPC;
  //   表更新 = exbranch

  // Notes on the sheet:
  //   输入引脚区
  //   输出引脚区
endmodule

module \双位预测状态转换  (
  input  Y1,
  input  Y0,
  input  \跳转 ,
  output Z1,
  output Z0
);

  wire and_1_out, and_2_out, and_3_out, and_4_out, not_1_out, not_2_out, not_3_out, not_4_out, not_5_out;

  not not_1 (not_1_out, Y0);
  not not_2 (not_2_out, Y1);
  not not_3 (not_3_out, Y0);
  not not_4 (not_4_out, Y0);
  not not_5 (not_5_out, \跳转 );
  and and_1 (and_1_out, Y0, \跳转 );
  and and_2 (and_2_out, Y1, not_1_out);
  and and_3 (and_3_out, not_2_out, not_3_out, \跳转 );
  and and_4 (and_4_out, Y1, not_4_out, not_5_out);
  or or_1 (Z1, and_1_out, and_2_out);
  or or_2 (Z0, and_3_out, and_4_out);
endmodule
