// Logisim project 团队任务.circ as structural Verilog: 8 circuits, main circuit ◆单周期硬布线控制器
module \单周期_单级中断  (
  input  IR1,
  input  IR2,
  input  IR3,
  output RegWrite,
  output MemWrite,
  output [31:0] PC,
  output [31:0] IR,
  output [31:0] RDin,
  output [31:0] MDin,
  output [31:0] LedData
);

  wire and_1_out, and_2_out, and_3_out, and_4_out, and_5_out, and_6_out, and_7_out, and_8_out, and_9_out,
       and_10_out, and_11_out, and_15_out, Beq, Bge, Blt, Bltu, Bne, CLK, clock_1_out, clr1, clr2, clr3,
       comparator_1_eq, comparator_2_eq, comparator_2_lt, csrrci, csrrsi, d_ff_1_q, d_ff_2_q, d_ff_3_q,
       d_ff_4_q, ecall, en_IE, equ, Go, halt, IE, IE_in, IR1_q, IR1_t, IR2_q, IR2_t, IR3_q, IR3_t, IRA, IRB,
       IRC, JAL, JALR, less, Lui, MemToReg, nand_1_out, not_1_out, not_2_out, not_3_out, not_4_out,
       not_5_out, or_1_out, or_2_out, or_6_out, or_7_out, or_8_out, or_12_out, or_13_out,
       priority_encoder_2_gs, RST, S_type, Sh, uret, W1, W2, W3, \中断请求 , \单周期硬布线控制器_1_alu_src ;
  wire [1:0] priority_encoder_1_out, priority_encoder_3_out, register_1_q, \中断号 ;
  wire [3:0] \单周期硬布线控制器_1_alu_op ;
  wire [4:0] multiplexer_4_out, multiplexer_5_out;
  wire [11:0] multiplexer_3_out;
  wire [12:0] CNT_num;
  wire [15:0] \总周期数 ;
  wire [31:0] adder_2_out, adder_3_out, ALUResult, and_13_out, and_14_out, bit_extender_1_out,
       bit_extender_2_out, bit_extender_3_out, bit_extender_4_out, EPC, imm_U__12, multiplexer_2_out,
       multiplexer_7_out, multiplexer_10_out, multiplexer_11_out, multiplexer_12_out, multiplexer_13_out,
       PC_4, ram_1_data, regifile_1_r1, regifile_1_r2, ShDin, shifter_1_out, shifter_2_out, shifter_4_out,
       \入口地址 , \断点 ;

  Button \u_继续运行  (.out(Go));
  Button _1 (.out(IRA));
  Button _2 (.out(IRB));
  Button _3 (.out(IRC));
  Button \u_总复位  (.out(RST));
  not not_1 (not_1_out, equ);
  and and_1 (and_1_out, Beq, equ);
  LED #(.active("true")) led_1 (.in(W1));
  LED #(.active("true")) led_2 (.in(W2));
  LED #(.active("true")) led_3 (.in(W3));
  and and_2 (and_2_out, not_1_out, Bne);
  and and_3 (and_3_out, less, Bltu);
  or or_1 (or_1_out, and_1_out, and_2_out, and_3_out, and_4_out, and_5_out);
  Priority_Encoder #(.select(2), .disabled("Z")) priority_encoder_1 (
    .in0(1'b1), .in1(or_1_out), .in2(JAL), .in3(JALR), .out(priority_encoder_1_out));  // open: gs, en_out, en_in
  Multiplexer #(.select(2), .width(32), .disabled("Z"), .enable("false")) multiplexer_1 (
    .in0(PC_4), .in1(adder_2_out), .in2(adder_3_out), .in3(ALUResult), .out(\断点 ),
    .sel(priority_encoder_1_out));
  Hex_Digit_Display hex_digit_display_1 (.value(LedData[31:28]));  // open: dp
  not not_2 (not_2_out, less);
  and and_4 (and_4_out, Bge, not_2_out);
  Hex_Digit_Display hex_digit_display_2 (.value(LedData[27:24]));  // open: dp
  Hex_Digit_Display hex_digit_display_3 (.value(LedData[23:20]));  // open: dp
  and and_5 (and_5_out, Blt, less);
  or or_2 (or_2_out, not_3_out, Go);
  Multiplexer #(.select(2), .width(32), .disabled("Z"), .enable("false")) multiplexer_2 (
    .in0(\断点 ), .in1(\入口地址 ), .in2(EPC), .out(multiplexer_2_out), .sel({uret, \中断请求 }));  // open: in3
  not not_3 (not_3_out, halt);
  or or_3 (W1, IR1_q, d_ff_1_q);
  or or_4 (W2, IR2_q, d_ff_2_q);
  or or_5 (W3, IR3_q, d_ff_3_q);
  Hex_Digit_Display hex_digit_display_4 (.value(LedData[15:12]));  // open: dp
  Hex_Digit_Display hex_digit_display_5 (.value(LedData[19:16]));  // open: dp
  Register #(.width(32), .trigger("rising"), .Select("low")) u_PC (
    .D(multiplexer_2_out), .en(or_2_out), .Q(PC), .clk(CLK), .clr(RST));
  D_Flip_Flop #(.trigger("rising"), .Pre_Clr_Positions("LEGACY"), .NegatePresetClear("false"), .enable("true"), .NewFFLayout("false")) d_ff_1 (
    .clk(IRA), .D(1'b1), .Q(d_ff_1_q), .reset(IR1_q));  // open: Qn, preset, en
  D_Flip_Flop #(.trigger("rising"), .Pre_Clr_Positions("LEGACY"), .NegatePresetClear("false"), .enable("true"), .NewFFLayout("false")) d_ff_2 (
    .clk(IRB), .D(1'b1), .Q(d_ff_2_q), .reset(IR2_q));  // open: Qn, preset, en
  D_Flip_Flop #(.trigger("rising"), .Pre_Clr_Positions("LEGACY"), .NegatePresetClear("false"), .enable("true"), .NewFFLayout("false")) d_ff_3 (
    .clk(IRC), .D(1'b1), .Q(d_ff_3_q), .reset(IR3_q));  // open: Qn, preset, en
  Register #(.width(32), .trigger("rising"), .Select("low")) u_EPC (
    .D(\断点 ), .en(\中断请求 ), .Q(EPC), .clk(CLK), .clr(RST));
  Hex_Digit_Display hex_digit_display_6 (.value(LedData[11:8]));  // open: dp
  Hex_Digit_Display hex_digit_display_7 (.value(LedData[7:4]));  // open: dp
  // Probe on \总周期数 
  Adder #(.width(32)) adder_1 (.a(PC), .b(32'h4), .out(PC_4));  // open: cin, cout
  or or_6 (or_6_out, d_ff_1_q, IR1_q);
  and and_6 (and_6_out, clr1, uret);
  or or_7 (or_7_out, d_ff_2_q, IR2_q);
  and and_7 (and_7_out, clr2, uret);
  or or_8 (or_8_out, d_ff_3_q, IR3_q);
  and and_8 (and_8_out, clr3, uret);
  Hex_Digit_Display hex_digit_display_8 (.value(LedData[3:0]));  // open: dp
  and and_9 (and_9_out, or_6_out, ~and_6_out);  // AND_Gate
  and and_10 (and_10_out, or_7_out, ~and_7_out);  // AND_Gate
  and and_11 (and_11_out, or_8_out, ~and_8_out);  // AND_Gate
  // RiscV_Probe riscv_probe_1: pin names not known; wires that end beside it: IR
  ROM #(.addrWidth(10), .dataWidth(32), .Select("high")) rom_1 (.addr(PC[11:2]), .data(IR));
  D_Flip_Flop #(.trigger("rising"), .Pre_Clr_Positions("LEGACY"), .NegatePresetClear("false"), .enable("true"), .NewFFLayout("false")) u_IR1 (
    .clk(CLK), .D(and_9_out), .Q(IR1_q), .reset(RST));  // open: Qn, preset, en
  D_Flip_Flop #(.trigger("rising"), .Pre_Clr_Positions("LEGACY"), .NegatePresetClear("false"), .enable("true"), .NewFFLayout("false")) u_IR2 (
    .clk(CLK), .D(and_10_out), .Q(IR2_q), .reset(RST));  // open: Qn, preset, en
  D_Flip_Flop #(.trigger("rising"), .Pre_Clr_Positions("LEGACY"), .NegatePresetClear("false"), .enable("true"), .NewFFLayout("false")) u_IR3 (
    .clk(CLK), .D(and_11_out), .Q(IR3_q), .reset(RST));  // open: Qn, preset, en
  or or_9 (IR1_t, IR1, IRA);
  D_Flip_Flop #(.trigger("rising"), .Pre_Clr_Positions("LEGACY"), .NegatePresetClear("false"), .enable("true"), .NewFFLayout("false")) u_IE (
    .clk(CLK), .D(IE_in), .Qn(IE), .en(en_IE), .reset(RST));  // open: Q, preset
  or or_10 (IR2_t, IR2, IRB);
  \单周期硬布线控制器  \u_单周期硬布线控制器_1  (
    .Funct({IR[30], IR[25], IR[14:12]}), .OP(IR[6:2]), .ALU_OP(\单周期硬布线控制器_1_alu_op ), .MemToReg(MemToReg),
    .MemWrite(MemWrite), .ALU_SRC(\单周期硬布线控制器_1_alu_src ), .RegWrite(RegWrite), .ecall(ecall),
    .S_type(S_type), .Jalr(JALR), .Beq(Beq), .JAL(JAL), .Bne(Bne), .in_3(IR[21]), .uret(uret), .Lui(Lui),
    .Sh(Sh), .Bltu(Bltu), .csrrsi(csrrsi), .csrrci(csrrci), .Bge(Bge), .Blt(Blt));  // open: rs1used, rs2used
  Multiplexer #(.select(1), .width(12), .disabled("Z"), .enable("false")) multiplexer_3 (
    .in0(IR[31:20]), .in1({IR[31:25], IR[11:7]}), .out(multiplexer_3_out), .sel(S_type));
  assign bit_extender_1_out = {{20{IR[31]}}, {IR[31], IR[7], IR[30:25], IR[11:8]}};  // Bit_Extender bit_extender_1
  assign bit_extender_2_out = {{12{IR[31]}}, {IR[31], IR[19:12], IR[20], IR[30:21]}};  // Bit_Extender bit_extender_2
  assign bit_extender_3_out = {{12{IR[31]}}, IR[31:12]};  // Bit_Extender bit_extender_3
  Multiplexer #(.select(1), .width(5), .disabled("Z"), .enable("false")) multiplexer_4 (
    .in0(IR[19:15]), .in1(5'b10001), .out(multiplexer_4_out), .sel(ecall));
  Multiplexer #(.select(1), .width(5), .disabled("Z"), .enable("false")) multiplexer_5 (
    .in0(IR[24:20]), .in1(5'b01010), .out(multiplexer_5_out), .sel(ecall));
  assign bit_extender_4_out = {{20{multiplexer_3_out[11]}}, multiplexer_3_out};  // Bit_Extender bit_extender_4
  Shifter #(.width(32), .shift("ll")) shifter_1 (.in(bit_extender_1_out), .\dist (5'b00001), .out(shifter_1_out));
  Shifter #(.width(32), .shift("ll")) shifter_2 (.in(bit_extender_2_out), .\dist (5'b00001), .out(shifter_2_out));
  Shifter #(.width(32), .shift("ll")) shifter_3 (.in(bit_extender_3_out), .\dist (5'b01100), .out(imm_U__12));
  Priority_Encoder #(.select(2), .disabled("Z")) priority_encoder_2 (
    .in1(IR1_q), .in2(IR2_q), .in3(IR3_q), .out(\中断号 ), .gs(priority_encoder_2_gs), .en_in(1'b1));  // open: in0, en_out
  or or_11 (IR3_t, IR3, IRC);
  Regifile regifile_1 (
    .Din(RDin), .Clk(CLK), .R1(regifile_1_r1), .R2(regifile_1_r2), .WE(RegWrite), .W_num(IR[11:7]),
    .R1_num(multiplexer_4_out), .R2_num(multiplexer_5_out));
  Adder #(.width(32)) adder_2 (.a(shifter_1_out), .b(PC), .out(adder_2_out));  // open: cin, cout
  Adder #(.width(32)) adder_3 (.a(shifter_2_out), .b(PC), .out(adder_3_out));  // open: cin, cout
  Multiplexer #(.select(2), .width(32), .disabled("Z"), .enable("false")) multiplexer_6 (
    .in1(32'hac), .in2(32'h150), .in3(32'h1f4), .out(\入口地址 ), .sel(\中断号 ));  // open: in0
  Priority_Encoder #(.select(2), .disabled("Z")) priority_encoder_3 (
    .in0(uret), .in1(\中断请求 ), .in2(csrrsi), .in3(csrrci), .out(priority_encoder_3_out), .gs(en_IE),
    .en_in(1'b1));  // open: en_out
  Multiplexer #(.select(1), .width(32), .disabled("Z"), .enable("false")) multiplexer_7 (
    .in0(regifile_1_r2), .in1(bit_extender_4_out), .out(multiplexer_7_out), .sel(\单周期硬布线控制器_1_alu_src ));
  and and_12 (\中断请求 , priority_encoder_2_gs, IE);
  Register #(.width(2), .trigger("rising"), .Select("low")) register_1 (
    .D(\中断号 ), .en(\中断请求 ), .Q(register_1_q), .clk(CLK), .clr(RST));
  Decoder #(.select(2), .tristate("false"), .disabled("Z"), .enable("false")) decoder_1 (
    .out1(clr1), .out2(clr2), .out3(clr3), .sel(register_1_q));  // open: out0
  ALU alu_1 (
    .X(regifile_1_r1), .Y(multiplexer_7_out), .AluOP(\单周期硬布线控制器_1_alu_op ), .Equal(equ), .Result(ALUResult),
    .out_6(less));  // open: Result_2, out_4
  assign and_13_out = 32'hffff & regifile_1_r2;  // AND_Gate and_13, 32 bits wide
  Shifter #(.width(32), .shift("ll")) shifter_4 (.in(regifile_1_r2), .\dist (5'b10000), .out(shifter_4_out));
  Multiplexer #(.select(2), .width(1), .disabled("Z"), .enable("false")) multiplexer_8 (
    .in0(1'b0), .in1(1'b1), .in2(1'b0), .in3(1'b1), .out(IE_in), .sel(priority_encoder_3_out));
  Multiplexer #(.select(1), .width(32), .disabled("Z"), .enable("false")) multiplexer_9 (
    .in0(regifile_1_r2), .in1(ShDin), .out(MDin), .sel(Sh));
  Multiplexer #(.select(1), .width(32), .disabled("Z"), .enable("false")) multiplexer_10 (
    .in0(32'hffff0000), .in1(32'hffff), .out(multiplexer_10_out), .sel(ALUResult[1]));
  Multiplexer #(.select(1), .width(32), .disabled("Z"), .enable("false")) multiplexer_11 (
    .in0(and_13_out), .in1(shifter_4_out), .out(multiplexer_11_out), .sel(ALUResult[1]));
  Comparator #(.width(32), .mode("twosComplement")) comparator_1 (
    .a(regifile_1_r1), .b(32'h22), .eq(comparator_1_eq));  // open: gt, lt
  not not_4 (not_4_out, comparator_1_eq);
  assign and_14_out = ram_1_data & multiplexer_10_out;  // AND_Gate and_14, 32 bits wide
  and and_15 (and_15_out, ecall, comparator_1_eq);
  and and_16 (halt, ecall, not_4_out);
  not not_5 (not_5_out, halt);
  or or_12 (or_12_out, not_5_out, Go);
  Counter #(.width(16), .max('hffff), .ongoal("wrap"), .trigger("rising"), .behavior("new")) counter_1 (
    .count(or_12_out), .Q(\总周期数 ), .clk(CLK), .clr(RST));  // open: load, D, carry, preset, down
  RAM #(.addrWidth(10), .dataWidth(32), .bus("separate"), .Select("high")) ram_1 (
    .addr(ALUResult[11:2]), .din(MDin), .data(ram_1_data), .str(MemWrite), .clk(CLK), .clr(RST));  // open: sel, ld
  Adder #(.width(32)) adder_4 (.a(and_14_out), .b(multiplexer_11_out), .out(ShDin));  // open: cin, cout
  Register #(.width(32), .trigger("rising"), .Select("low")) register_2 (
    .D(regifile_1_r2), .en(and_15_out), .Q(LedData), .clk(CLK), .clr(RST));
  D_Flip_Flop #(.trigger("high"), .Pre_Clr_Positions("LEGACY"), .NegatePresetClear("false"), .enable("true"), .NewFFLayout("false")) d_ff_4 (.Q(d_ff_4_q));  // open: clk, D, Qn, preset, en, reset
  // Probe on 13'hc
  Multiplexer #(.select(1), .width(32), .disabled("Z"), .enable("false")) multiplexer_12 (
    .in0(ALUResult), .in1(ram_1_data), .out(multiplexer_12_out), .sel(MemToReg));
  or or_13 (or_13_out, JAL, JALR);
  Multiplexer #(.select(1), .width(32), .disabled("Z"), .enable("false")) multiplexer_13 (
    .in0(multiplexer_12_out), .in1(PC_4), .out(multiplexer_13_out), .sel(or_13_out));
  Multiplexer #(.select(1), .width(32), .disabled("Z"), .enable("false")) multiplexer_14 (
    .in0(multiplexer_13_out), .in1(imm_U__12), .out(RDin), .sel(Lui));
  Comparator #(.width(13), .mode("twosComplement")) comparator_2 (
    .a(CNT_num), .b(13'hc), .eq(comparator_2_eq), .lt(comparator_2_lt));  // open: gt
  Clock #(.highDuration(1), .lowDuration(1)) clock_1 (.out(clock_1_out));
  Counter #(.width(13), .max('h1fff), .ongoal("stay"), .trigger("rising"), .behavior("old")) counter_2 (
    .count(comparator_2_lt), .Q(CNT_num), .clk(clock_1_out));  // open: load, D, carry, clr, preset
  nand nand_1 (nand_1_out, d_ff_4_q, comparator_2_eq);
  assign CLK = nand_1_out ? clock_1_out : 1'bz;  // Controlled_Buffer controlled_buffer_1
  Pull_Resistor #(.pull(1)) pull_resistor_1 (.node(CLK));

  // Notes on the sheet:
  //   中断源
  //   中断等待指示
  //   总复位信号应将除ROM以外所有存储组件全部清零
  //   三号中断源
  //   一号中断源
  //   一号中断等待指示
  //   二号中断源
  //   二号中断等待指示
  //   三号中断等待指示
  //   保存断点
  //   数码管输出
  //   数码管输出应该用寄存器锁存，否则显示数据只能一闪而过
  //   指令探针
  //   指令存储器
  //   Reset 
  //   Reset 
  //   Reset 
  //   指令字
  //   contents of rom_1 (hex, n*v repeats v):
  //   7d000113 100413 1f41993 41f9d993 433 c00913 800b13 140413 f47413 800293 100313 499993 89e9b3 1300533
  //   2200893 73 406282b3 fe0294e3 140413 f00f93 1f47433 1c41413 800293 100313 49d993 89e9b3 1300533
  //   2200893 73 406282b3 fe0294e3 1c45413 406b0b33 b0463 f95ff06f 2b3 fff2c293 1029293 fff2e293 500533
  //   2200893 73 f5dff06f 1112023 410113 a12023 410113 812023 410113 1312023 410113 1412023 410113 1512023
  //   410113 1612023 410113 100b13 300a13 100a93 1600433 441413 14469b3 1300533 2200893 73 fe0416e3
  //   415a0a33 fe0a10e3 ffc10113 12b03 ffc10113 12a83 ffc10113 12a03 ffc10113 12983 ffc10113 12403
  //   ffc10113 12503 ffc10113 12883 200073 1112023 410113 a12023 410113 812023 410113 1312023 410113
  //   1412023 410113 1512023 410113 1612023 410113 200b13 300a13 100a93 1600433 441413 14469b3 1300533
  //   2200893 73 fe0416e3 415a0a33 fe0a10e3 ffc10113 12b03 ffc10113 12a83 ffc10113 12a03 ffc10113 12983
  //   ffc10113 12403 ffc10113 12503 ffc10113 12883 200073 1112023 410113 a12023 410113 812023 410113
  //   1312023 410113 1412023 410113 1512023 410113 1612023 410113 300b13 300a13 100a93 1600433 441413
  //   14469b3 1300533 2200893 73 fe0416e3 415a0a33 fe0a10e3 ffc10113 12b03 ffc10113 12a83 ffc10113 12a03
  //   ffc10113 12983 ffc10113 12403 ffc10113 12503 ffc10113 12883 200073
  //   中断使能寄存器IE
  //   I
  //   S
  //   B
  //   跳转地址(beq/bne/bltu)
  //   J
  //   跳转地址(jal)
  //   U
  //   在中断响应周期和uret指令周期才可开/关中断
  //   Beq
  //   Bne
  //   MemToReg
  //   MemWrite
  //   AluOP
  //   AluSrcB
  //   RegWrite
  //   $a7编号
  //   $a0编号
  //   INTR
  //   SignImm
  //   选择需要清零的中断号
  //   WriteData
  //   ecall指令输出$a0到Led
  //   为方便自动评测，需要输出PC，IR，寄存器堆写如数据RDin
  //   跳转地址(jalr)
  //   存储器不支持半字访问，因此需要取出一个字的数据特殊处理
  //   RAM写使能MemWrite、RAM写入数据MDin等信号
  //   数据存储器
  //   ReadData
  //   控制位
  //   暂停节拍，不能为0
  //   保存到寄存器中的数据
  //   戳工具置1进入计数暂停模式，ctrl+k时钟自动运行到对应节拍暂停
  //   ctrl+k关闭时钟连续运行，将控制位置零，进入单步调试模式调试
  //   返回地址
  //   左移12位立即数
  //   可计数暂停的时钟源
endmodule

// RISC-V CPU
module \单周期_单级中断游戏版  (
  input  restart,
  input  left,
  input  CLK,
  input  right,
  output RegWrite,
  output MemWrite,
  output [31:0] PC,
  output [31:0] IR,
  output [31:0] RDin,
  output [31:0] MDin,
  output [31:0] flag1,
  output [31:0] flag4,
  output [31:0] start1,
  output [31:0] start4,
  output [31:0] upline1,
  output [31:0] upline4,
  output [31:0] flag2,
  output [31:0] flag5,
  output [31:0] start2,
  output [31:0] start5,
  output [31:0] upline2,
  output [31:0] upline5,
  output [31:0] flag3,
  output [31:0] flag6,
  output [31:0] start3,
  output [31:0] start6,
  output [31:0] upline3,
  output [31:0] upline6,
  output [31:0] bx,
  output [31:0] by,
  output [31:0] life
);

  wire and_1_out, and_2_out, and_3_out, and_4_out, and_5_out, and_6_out, and_7_out, and_8_out, and_9_out,
       and_10_out, and_11_out, and_15_out, and_16_out, and_17_out, and_18_out, and_19_out, and_20_out,
       and_21_out, and_22_out, and_23_out, and_24_out, and_25_out, and_26_out, and_27_out, and_28_out,
       and_29_out, and_30_out, and_31_out, and_32_out, and_33_out, and_34_out, and_35_out, Beq, Bge, Blt,
       Bltu, Bne, CLK_t, clr1, clr2, clr3, comparator_1_eq, comparator_2_eq, comparator_3_eq,
       comparator_4_eq, comparator_5_eq, comparator_6_eq, comparator_7_eq, comparator_8_eq, comparator_9_eq,
       comparator_10_eq, comparator_11_eq, comparator_12_eq, comparator_12_lt, comparator_13_eq,
       comparator_14_eq, comparator_15_eq, comparator_16_eq, comparator_17_eq, comparator_18_eq,
       comparator_19_eq, comparator_20_eq, comparator_21_eq, comparator_22_eq, csrrci, csrrsi, d_ff_1_q,
       d_ff_2_q, d_ff_3_q, d_ff_4_q, ecall, en_IE, equ, Go, IE, IE_in, IR1_q, IR2_q, IR3_q, JAL, JALR, less,
       Lui, MemToReg, nand_1_out, not_1_out, not_2_out, not_3_out, not_4_out, or_1_out, or_2_out, or_6_out,
       or_7_out, or_8_out, or_9_out, or_10_out, priority_encoder_2_gs, RST, S_type, Sh, uret, W1, W2, W3,
       \中断请求 , \单周期硬布线控制器_1_alu_src ;
  wire [1:0] priority_encoder_1_out, priority_encoder_3_out, register_1_q, \中断号 ;
  wire [3:0] \单周期硬布线控制器_1_alu_op ;
  wire [4:0] multiplexer_4_out, multiplexer_5_out;
  wire [11:0] multiplexer_3_out;
  wire [12:0] CNT_num;
  wire [15:0] \总周期数 ;
  wire [31:0] adder_2_out, adder_3_out, ALUResult, and_13_out, and_14_out, bit_extender_1_out,
       bit_extender_2_out, bit_extender_3_out, bit_extender_4_out, EPC, imm_U__12, multiplexer_2_out,
       multiplexer_7_out, multiplexer_10_out, multiplexer_11_out, multiplexer_12_out, multiplexer_13_out,
       PC_4, ram_1_data, regifile_1_r1, regifile_1_r2, ShDin, shifter_1_out, shifter_2_out, shifter_4_out,
       \入口地址 , \断点 ;

  Button \u_继续运行  (.out(Go));
  Button \u_总复位  (.out(RST));
  not not_1 (not_1_out, equ);
  and and_1 (and_1_out, Beq, equ);
  LED #(.active("true")) led_1 (.in(W1));
  LED #(.active("true")) led_2 (.in(W2));
  LED #(.active("true")) led_3 (.in(W3));
  and and_2 (and_2_out, less, Bltu);
  and and_3 (and_3_out, not_1_out, Bne);
  or or_1 (or_1_out, and_1_out, and_3_out, and_2_out, and_4_out, and_5_out);
  Priority_Encoder #(.select(2), .disabled("Z")) priority_encoder_1 (
    .in0(1'b1), .in1(or_1_out), .in2(JAL), .in3(JALR), .out(priority_encoder_1_out));  // open: gs, en_out, en_in
  Multiplexer #(.select(2), .width(32), .disabled("Z"), .enable("false")) multiplexer_1 (
    .in0(PC_4), .in1(adder_2_out), .in2(adder_3_out), .in3(ALUResult), .out(\断点 ),
    .sel(priority_encoder_1_out));
  Hex_Digit_Display hex_digit_display_1 (.value(by[31:28]));  // open: dp
  not not_2 (not_2_out, less);
  and and_4 (and_4_out, Bge, not_2_out);
  Hex_Digit_Display hex_digit_display_2 (.value(by[27:24]));  // open: dp
  Hex_Digit_Display hex_digit_display_3 (.value(by[23:20]));  // open: dp
  and and_5 (and_5_out, Blt, less);
  or or_2 (or_2_out, not_3_out, Go);
  Multiplexer #(.select(2), .width(32), .disabled("Z"), .enable("false")) multiplexer_2 (
    .in0(\断点 ), .in1(\入口地址 ), .in2(EPC), .out(multiplexer_2_out), .sel({uret, \中断请求 }));  // open: in3
  not not_3 (not_3_out, 1'b0);
  or or_3 (W1, IR1_q, d_ff_1_q);
  or or_4 (W2, IR2_q, d_ff_2_q);
  or or_5 (W3, IR3_q, d_ff_3_q);
  Hex_Digit_Display hex_digit_display_4 (.value(by[19:16]));  // open: dp
  Hex_Digit_Display hex_digit_display_5 (.value(by[15:12]));  // open: dp
  Register #(.width(32), .trigger("rising"), .Select("low")) u_PC (
    .D(multiplexer_2_out), .en(or_2_out), .Q(PC), .clk(CLK_t), .clr(RST));
  D_Flip_Flop #(.trigger("rising"), .Pre_Clr_Positions("LEGACY"), .NegatePresetClear("false"), .enable("true"), .NewFFLayout("false")) d_ff_1 (
    .clk(restart), .D(1'b1), .Q(d_ff_1_q), .reset(IR1_q));  // open: Qn, preset, en
  D_Flip_Flop #(.trigger("rising"), .Pre_Clr_Positions("LEGACY"), .NegatePresetClear("false"), .enable("true"), .NewFFLayout("false")) d_ff_2 (
    .clk(left), .D(1'b1), .Q(d_ff_2_q), .reset(IR2_q));  // open: Qn, preset, en
  D_Flip_Flop #(.trigger("rising"), .Pre_Clr_Positions("LEGACY"), .NegatePresetClear("false"), .enable("true"), .NewFFLayout("false")) d_ff_3 (
    .clk(right), .D(1'b1), .Q(d_ff_3_q), .reset(IR3_q));  // open: Qn, preset, en
  Register #(.width(32), .trigger("rising"), .Select("low")) u_EPC (
    .D(\断点 ), .en(\中断请求 ), .Q(EPC), .clk(CLK_t), .clr(RST));
  Hex_Digit_Display hex_digit_display_6 (.value(by[11:8]));  // open: dp
  Hex_Digit_Display hex_digit_display_7 (.value(by[7:4]));  // open: dp
  // Probe on \总周期数 
  Adder #(.width(32)) adder_1 (.a(PC), .b(32'h4), .out(PC_4));  // open: cin, cout
  or or_6 (or_6_out, d_ff_1_q, IR1_q);
  and and_6 (and_6_out, clr1, uret);
  or or_7 (or_7_out, d_ff_2_q, IR2_q);
  and and_7 (and_7_out, clr2, uret);
  or or_8 (or_8_out, d_ff_3_q, IR3_q);
  and and_8 (and_8_out, clr3, uret);
  Hex_Digit_Display hex_digit_display_8 (.value(by[3:0]));  // open: dp
  and and_9 (and_9_out, or_6_out, ~and_6_out);  // AND_Gate
  and and_10 (and_10_out, or_7_out, ~and_7_out);  // AND_Gate
  and and_11 (and_11_out, or_8_out, ~and_8_out);  // AND_Gate
  // RiscV_Probe riscv_probe_1: pin names not known; wires that end beside it: IR
  ROM #(.addrWidth(10), .dataWidth(32), .Select("high")) rom_1 (.addr(PC[11:2]), .data(IR));
  D_Flip_Flop #(.trigger("rising"), .Pre_Clr_Positions("LEGACY"), .NegatePresetClear("false"), .enable("true"), .NewFFLayout("false")) IR1 (
    .clk(CLK_t), .D(and_9_out), .Q(IR1_q), .reset(RST));  // open: Qn, preset, en
  D_Flip_Flop #(.trigger("rising"), .Pre_Clr_Positions("LEGACY"), .NegatePresetClear("false"), .enable("true"), .NewFFLayout("false")) IR2 (
    .clk(CLK_t), .D(and_10_out), .Q(IR2_q), .reset(RST));  // open: Qn, preset, en
  D_Flip_Flop #(.trigger("rising"), .Pre_Clr_Positions("LEGACY"), .NegatePresetClear("false"), .enable("true"), .NewFFLayout("false")) IR3 (
    .clk(CLK_t), .D(and_11_out), .Q(IR3_q), .reset(RST));  // open: Qn, preset, en
  D_Flip_Flop #(.trigger("rising"), .Pre_Clr_Positions("LEGACY"), .NegatePresetClear("false"), .enable("true"), .NewFFLayout("false")) u_IE (
    .clk(CLK_t), .D(IE_in), .Qn(IE), .en(en_IE), .reset(RST));  // open: Q, preset
  \单周期硬布线控制器  \u_单周期硬布线控制器_1  (
    .Funct({IR[30], IR[25], IR[14:12]}), .OP(IR[6:2]), .ALU_OP(\单周期硬布线控制器_1_alu_op ), .MemToReg(MemToReg),
    .MemWrite(MemWrite), .ALU_SRC(\单周期硬布线控制器_1_alu_src ), .RegWrite(RegWrite), .ecall(ecall),
    .S_type(S_type), .Jalr(JALR), .Beq(Beq), .JAL(JAL), .Bne(Bne), .in_3(IR[21]), .uret(uret), .Lui(Lui),
    .Sh(Sh), .Bltu(Bltu), .csrrsi(csrrsi), .csrrci(csrrci), .Bge(Bge), .Blt(Blt));  // open: rs1used, rs2used
  Multiplexer #(.select(1), .width(12), .disabled("Z"), .enable("false")) multiplexer_3 (
    .in0(IR[31:20]), .in1({IR[31:25], IR[11:7]}), .out(multiplexer_3_out), .sel(S_type));
  assign bit_extender_1_out = {{20{IR[31]}}, {IR[31], IR[7], IR[30:25], IR[11:8]}};  // Bit_Extender bit_extender_1
  assign bit_extender_2_out = {{12{IR[31]}}, {IR[31], IR[19:12], IR[20], IR[30:21]}};  // Bit_Extender bit_extender_2
  assign bit_extender_3_out = {{12{IR[31]}}, IR[31:12]};  // Bit_Extender bit_extender_3
  Multiplexer #(.select(1), .width(5), .disabled("Z"), .enable("false")) multiplexer_4 (
    .in0(IR[19:15]), .in1(5'b10001), .out(multiplexer_4_out), .sel(ecall));
  Multiplexer #(.select(1), .width(5), .disabled("Z"), .enable("false")) multiplexer_5 (
    .in0(IR[24:20]), .in1(5'b01010), .out(multiplexer_5_out), .sel(ecall));
  assign bit_extender_4_out = {{20{multiplexer_3_out[11]}}, multiplexer_3_out};  // Bit_Extender bit_extender_4
  Shifter #(.width(32), .shift("ll")) shifter_1 (.in(bit_extender_1_out), .\dist (5'b00001), .out(shifter_1_out));
  Shifter #(.width(32), .shift("ll")) shifter_2 (.in(bit_extender_2_out), .\dist (5'b00001), .out(shifter_2_out));
  Shifter #(.width(32), .shift("ll")) shifter_3 (.in(bit_extender_3_out), .\dist (5'b01100), .out(imm_U__12));
  Priority_Encoder #(.select(2), .disabled("Z")) priority_encoder_2 (
    .in1(IR1_q), .in2(IR2_q), .in3(IR3_q), .out(\中断号 ), .gs(priority_encoder_2_gs), .en_in(1'b1));  // open: in0, en_out
  Regifile regifile_1 (
    .Din(RDin), .Clk(CLK_t), .R1(regifile_1_r1), .R2(regifile_1_r2), .WE(RegWrite), .W_num(IR[11:7]),
    .R1_num(multiplexer_4_out), .R2_num(multiplexer_5_out));
  Adder #(.width(32)) adder_2 (.a(shifter_1_out), .b(PC), .out(adder_2_out));  // open: cin, cout
  Adder #(.width(32)) adder_3 (.a(shifter_2_out), .b(PC), .out(adder_3_out));  // open: cin, cout
  Multiplexer #(.select(2), .width(32), .disabled("Z"), .enable("false")) multiplexer_6 (
    .in1(32'h81c), .in2(32'h8a0), .in3(32'h930), .out(\入口地址 ), .sel(\中断号 ));  // open: in0
  Priority_Encoder #(.select(2), .disabled("Z")) priority_encoder_3 (
    .in0(uret), .in1(\中断请求 ), .in2(csrrsi), .in3(csrrci), .out(priority_encoder_3_out), .gs(en_IE),
    .en_in(1'b1));  // open: en_out
  Multiplexer #(.select(1), .width(32), .disabled("Z"), .enable("false")) multiplexer_7 (
    .in0(regifile_1_r2), .in1(bit_extender_4_out), .out(multiplexer_7_out), .sel(\单周期硬布线控制器_1_alu_src ));
  and and_12 (\中断请求 , priority_encoder_2_gs, IE);
  Register #(.width(2), .trigger("rising"), .Select("low")) register_1 (
    .D(\中断号 ), .en(\中断请求 ), .Q(register_1_q), .clk(CLK_t), .clr(RST));
  Decoder #(.select(2), .tristate("false"), .disabled("Z"), .enable("false")) decoder_1 (
    .out1(clr1), .out2(clr2), .out3(clr3), .sel(register_1_q));  // open: out0
  ALU alu_1 (
    .X(regifile_1_r1), .Y(multiplexer_7_out), .AluOP(\单周期硬布线控制器_1_alu_op ), .Equal(equ), .Result(ALUResult),
    .out_6(less));  // open: Result_2, out_4
  assign and_13_out = 32'hffff & regifile_1_r2;  // AND_Gate and_13, 32 bits wide
  Shifter #(.width(32), .shift("ll")) shifter_4 (.in(regifile_1_r2), .\dist (5'b10000), .out(shifter_4_out));
  Multiplexer #(.select(2), .width(1), .disabled("Z"), .enable("false")) multiplexer_8 (
    .in0(1'b0), .in1(1'b1), .in2(1'b0), .in3(1'b1), .out(IE_in), .sel(priority_encoder_3_out));
  Multiplexer #(.select(1), .width(32), .disabled("Z"), .enable("false")) multiplexer_9 (
    .in0(regifile_1_r2), .in1(ShDin), .out(MDin), .sel(Sh));
  Multiplexer #(.select(1), .width(32), .disabled("Z"), .enable("false")) multiplexer_10 (
    .in0(32'hffff0000), .in1(32'hffff), .out(multiplexer_10_out), .sel(ALUResult[1]));
  Multiplexer #(.select(1), .width(32), .disabled("Z"), .enable("false")) multiplexer_11 (
    .in0(and_13_out), .in1(shifter_4_out), .out(multiplexer_11_out), .sel(ALUResult[1]));
  assign and_14_out = ram_1_data & multiplexer_10_out;  // AND_Gate and_14, 32 bits wide
  not not_4 (not_4_out, 1'b0);
  or or_9 (or_9_out, not_4_out, Go);
  Counter #(.width(16), .max('hffff), .ongoal("wrap"), .trigger("rising"), .behavior("new")) counter_1 (
    .count(or_9_out), .Q(\总周期数 ), .clk(CLK_t), .clr(RST));  // open: load, D, carry, preset, down
  RAM #(.addrWidth(10), .dataWidth(32), .bus("separate"), .Select("high")) ram_1 (
    .addr(ALUResult[11:2]), .din(MDin), .data(ram_1_data), .str(MemWrite), .clk(CLK_t), .clr(RST));  // open: sel, ld
  Adder #(.width(32)) adder_4 (.a(and_14_out), .b(multiplexer_11_out), .out(ShDin));  // open: cin, cout
  Comparator #(.width(32), .mode("twosComplement")) comparator_1 (
    .a(regifile_1_r1), .b(32'h1), .eq(comparator_1_eq));  // open: gt, lt
  Comparator #(.width(32), .mode("twosComplement")) comparator_2 (
    .a(regifile_1_r1), .b(32'hb), .eq(comparator_2_eq));  // open: gt, lt
  Comparator #(.width(32), .mode("twosComplement")) comparator_3 (
    .a(regifile_1_r1), .b(32'h6f), .eq(comparator_3_eq));  // open: gt, lt
  Comparator #(.width(32), .mode("twosComplement")) comparator_4 (
    .a(regifile_1_r1), .b(32'h2), .eq(comparator_4_eq));  // open: gt, lt
  Comparator #(.width(32), .mode("twosComplement")) comparator_5 (
    .a(regifile_1_r1), .b(32'h16), .eq(comparator_5_eq));  // open: gt, lt
  Comparator #(.width(32), .mode("twosComplement")) comparator_6 (
    .a(regifile_1_r1), .b(32'hde), .eq(comparator_6_eq));  // open: gt, lt
  Comparator #(.width(32), .mode("twosComplement")) comparator_7 (
    .a(regifile_1_r1), .b(32'h3), .eq(comparator_7_eq));  // open: gt, lt
  Comparator #(.width(32), .mode("twosComplement")) comparator_8 (
    .a(regifile_1_r1), .b(32'h21), .eq(comparator_8_eq));  // open: gt, lt
  Comparator #(.width(32), .mode("twosComplement")) comparator_9 (
    .a(regifile_1_r1), .b(32'h14d), .eq(comparator_9_eq));  // open: gt, lt
  Comparator #(.width(32), .mode("twosComplement")) comparator_10 (
    .a(regifile_1_r1), .b(32'h7), .eq(comparator_10_eq));  // open: gt, lt
  Comparator #(.width(32), .mode("twosComplement")) comparator_11 (
    .a(regifile_1_r1), .b(32'h9), .eq(comparator_11_eq));  // open: gt, lt
  D_Flip_Flop #(.trigger("high"), .Pre_Clr_Positions("LEGACY"), .NegatePresetClear("false"), .enable("true"), .NewFFLayout("false")) d_ff_4 (.Q(d_ff_4_q));  // open: clk, D, Qn, preset, en, reset
  // Probe on 13'hc
  Multiplexer #(.select(1), .width(32), .disabled("Z"), .enable("false")) multiplexer_12 (
    .in0(ALUResult), .in1(ram_1_data), .out(multiplexer_12_out), .sel(MemToReg));
  or or_10 (or_10_out, JAL, JALR);
  Multiplexer #(.select(1), .width(32), .disabled("Z"), .enable("false")) multiplexer_13 (
    .in0(multiplexer_12_out), .in1(PC_4), .out(multiplexer_13_out), .sel(or_10_out));
  Multiplexer #(.select(1), .width(32), .disabled("Z"), .enable("false")) multiplexer_14 (
    .in0(multiplexer_13_out), .in1(imm_U__12), .out(RDin), .sel(Lui));
  and and_15 (and_15_out, ecall, comparator_1_eq);
  and and_16 (and_16_out, ecall, comparator_2_eq);
  and and_17 (and_17_out, ecall, comparator_3_eq);
  and and_18 (and_18_out, ecall, comparator_4_eq);
  and and_19 (and_19_out, ecall, comparator_5_eq);
  and and_20 (and_20_out, ecall, comparator_6_eq);
  and and_21 (and_21_out, ecall, comparator_7_eq);
  and and_22 (and_22_out, ecall, comparator_8_eq);
  and and_23 (and_23_out, ecall, comparator_9_eq);
  and and_24 (and_24_out, ecall, comparator_10_eq);
  and and_25 (and_25_out, ecall, comparator_11_eq);
  Comparator #(.width(13), .mode("twosComplement")) comparator_12 (
    .a(CNT_num), .b(13'hc), .eq(comparator_12_eq), .lt(comparator_12_lt));  // open: gt
  Register #(.width(32), .trigger("rising"), .Select("low")) register_2 (
    .D(regifile_1_r2), .en(and_15_out), .Q(flag1), .clk(CLK_t), .clr(RST));
  Register #(.width(32), .trigger("rising"), .Select("low")) register_3 (
    .D(regifile_1_r2), .en(and_16_out), .Q(start1), .clk(CLK_t), .clr(RST));
  Register #(.width(32), .trigger("rising"), .Select("low")) register_4 (
    .D(regifile_1_r2), .en(and_17_out), .Q(upline1), .clk(CLK_t), .clr(RST));
  Register #(.width(32), .trigger("rising"), .Select("low")) register_5 (
    .D(regifile_1_r2), .en(and_18_out), .Q(flag2), .clk(CLK_t), .clr(RST));
  Register #(.width(32), .trigger("rising"), .Select("low")) register_6 (
    .D(regifile_1_r2), .en(and_19_out), .Q(start2), .clk(CLK_t), .clr(RST));
  Register #(.width(32), .trigger("rising"), .Select("low")) register_7 (
    .D(regifile_1_r2), .en(and_20_out), .Q(upline2), .clk(CLK_t), .clr(RST));
  Register #(.width(32), .trigger("rising"), .Select("low")) register_8 (
    .D(regifile_1_r2), .en(and_21_out), .Q(flag3), .clk(CLK_t), .clr(RST));
  Register #(.width(32), .trigger("rising"), .Select("low")) register_9 (
    .D(regifile_1_r2), .en(and_22_out), .Q(start3), .clk(CLK_t), .clr(RST));
  Register #(.width(32), .trigger("rising"), .Select("low")) register_10 (
    .D(regifile_1_r2), .en(and_23_out), .Q(upline3), .clk(CLK_t), .clr(RST));
  Register #(.width(32), .trigger("rising"), .Select("low")) register_11 (
    .D(regifile_1_r2), .en(and_24_out), .Q(bx), .clk(CLK_t), .clr(RST));
  Register #(.width(32), .trigger("rising"), .Select("low")) register_12 (
    .D(regifile_1_r2), .en(and_25_out), .Q(life), .clk(CLK_t), .clr(RST));
  Counter #(.width(13), .max('h1fff), .ongoal("stay"), .trigger("rising"), .behavior("old")) counter_2 (
    .count(comparator_12_lt), .Q(CNT_num), .clk(CLK));  // open: load, D, carry, clr, preset
  nand nand_1 (nand_1_out, d_ff_4_q, comparator_12_eq);
  assign CLK_t = nand_1_out ? CLK : 1'bz;  // Controlled_Buffer controlled_buffer_1
  Pull_Resistor #(.pull(1)) pull_resistor_1 (.node(CLK_t));
  Comparator #(.width(32), .mode("twosComplement")) comparator_13 (
    .a(regifile_1_r1), .b(32'h4), .eq(comparator_13_eq));  // open: gt, lt
  Comparator #(.width(32), .mode("twosComplement")) comparator_14 (
    .a(regifile_1_r1), .b(32'h2c), .eq(comparator_14_eq));  // open: gt, lt
  Comparator #(.width(32), .mode("twosComplement")) comparator_15 (
    .a(regifile_1_r1), .b(32'h1bc), .eq(comparator_15_eq));  // open: gt, lt
  Comparator #(.width(32), .mode("twosComplement")) comparator_16 (
    .a(regifile_1_r1), .b(32'h5), .eq(comparator_16_eq));  // open: gt, lt
  Comparator #(.width(32), .mode("twosComplement")) comparator_17 (
    .a(regifile_1_r1), .b(32'h37), .eq(comparator_17_eq));  // open: gt, lt
  Comparator #(.width(32), .mode("twosComplement")) comparator_18 (
    .a(regifile_1_r1), .b(32'h22b), .eq(comparator_18_eq));  // open: gt, lt
  Comparator #(.width(32), .mode("twosComplement")) comparator_19 (
    .a(regifile_1_r1), .b(32'h6), .eq(comparator_19_eq));  // open: gt, lt
  Comparator #(.width(32), .mode("twosComplement")) comparator_20 (
    .a(regifile_1_r1), .b(32'h42), .eq(comparator_20_eq));  // open: gt, lt
  Comparator #(.width(32), .mode("twosComplement")) comparator_21 (
    .a(regifile_1_r1), .b(32'h29a), .eq(comparator_21_eq));  // open: gt, lt
  Comparator #(.width(32), .mode("twosComplement")) comparator_22 (
    .a(regifile_1_r1), .b(32'h8), .eq(comparator_22_eq));  // open: gt, lt
  and and_26 (and_26_out, ecall, comparator_13_eq);
  and and_27 (and_27_out, ecall, comparator_14_eq);
  and and_28 (and_28_out, ecall, comparator_15_eq);
  and and_29 (and_29_out, ecall, comparator_16_eq);
  and and_30 (and_30_out, ecall, comparator_17_eq);
  and and_31 (and_31_out, ecall, comparator_18_eq);
  and and_32 (and_32_out, ecall, comparator_19_eq);
  and and_33 (and_33_out, ecall, comparator_20_eq);
  and and_34 (and_34_out, ecall, comparator_21_eq);
  and and_35 (and_35_out, ecall, comparator_22_eq);
  Register #(.width(32), .trigger("rising"), .Select("low")) register_13 (
    .D(regifile_1_r2), .en(and_26_out), .Q(flag4), .clk(CLK_t), .clr(RST));
  Register #(.width(32), .trigger("rising"), .Select("low")) register_14 (
    .D(regifile_1_r2), .en(and_27_out), .Q(start4), .clk(CLK_t), .clr(RST));
  Register #(.width(32), .trigger("rising"), .Select("low")) register_15 (
    .D(regifile_1_r2), .en(and_28_out), .Q(upline4), .clk(CLK_t), .clr(RST));
  Register #(.width(32), .trigger("rising"), .Select("low")) register_16 (
    .D(regifile_1_r2), .en(and_29_out), .Q(flag5), .clk(CLK_t), .clr(RST));
  Register #(.width(32), .trigger("rising"), .Select("low")) register_17 (
    .D(regifile_1_r2), .en(and_30_out), .Q(start5), .clk(CLK_t), .clr(RST));
  Register #(.width(32), .trigger("rising"), .Select("low")) register_18 (
    .D(regifile_1_r2), .en(and_31_out), .Q(upline5), .clk(CLK_t), .clr(RST));
  Register #(.width(32), .trigger("rising"), .Select("low")) register_19 (
    .D(regifile_1_r2), .en(and_32_out), .Q(flag6), .clk(CLK_t), .clr(RST));
  Register #(.width(32), .trigger("rising"), .Select("low")) register_20 (
    .D(regifile_1_r2), .en(and_33_out), .Q(start6), .clk(CLK_t), .clr(RST));
  Register #(.width(32), .trigger("rising"), .Select("low")) register_21 (
    .D(regifile_1_r2), .en(and_34_out), .Q(upline6), .clk(CLK_t), .clr(RST));
  Register #(.width(32), .trigger("rising"), .Select("low")) register_22 (
    .D(regifile_1_r2), .en(and_35_out), .Q(by), .clk(CLK_t), .clr(RST));

  // Other names for the same wires on the sheet: IRA = restart; IRB = left; IRC = right

  // Notes on the sheet:
  //   中断源
  //   中断等待指示
  //   总复位信号应将除ROM以外所有存储组件全部清零
  //   三号中断源
  //   一号中断源
  //   一号中断等待指示
  //   二号中断源
  //   二号中断等待指示
  //   三号中断等待指示
  //   保存断点
  //   数码管输出
  //   数码管输出应该用寄存器锁存，否则显示数据只能一闪而过
  //   指令探针
  //   指令存储器
  //   Reset 
  //   Reset 
  //   Reset 
  //   指令字
  //   contents of rom_1 (hex, n*v repeats v):
  //   40f073 f000113 f3010113 c112623 c812423 d010413 2000793 fcf42223 2000793 fcf42023 100793 faf42e23
  //   800793 faf42c23 100793 faf42a23 600793 faf42823 400793 faf42623 c00793 faf42423 c00793 faf42223
  //   6f00793 f8f42e23 fe042423 fe842783 fef42623 fe042023 280006f fe042783 479793 ff078793 8787b3
  //   fff00713 f4e7ac23 fe042783 178793 fef42023 fe042703 500793 fce7dae3 800793 fcf42e23 1040006f
  //   f9c40793 f00533 6ec000ef a007b3 37f793 f037b3 ff7f793 f00733 fe842783 479793 ff078793 8787b3
  //   f4e7a623 f9c40793 f00533 6b8000ef fe842783 479793 ff078793 8787b3 c00713 f4e7aa23 fe842783 479793
  //   ff078793 8787b3 fdc42703 f4e7ac23 f9c40793 f00533 67c000ef a00733 41f75793 1b7d793 f70733 1f77713
  //   40f707b3 178713 fe842783 479793 ff078793 8787b3 f4e7a823 fe842783 479793 ff078793 8787b3 f507a703
  //   fe842783 479793 ff078793 8787b3 f547a783 f70733 2100793 f8e7cae3 fe842783 178713 600793 2f767b3
  //   fef42423 fdc42783 878793 fcf42e23 fdc42703 2000793 eee7dce3 fe842783 578713 600793 2f767b3 fcf42c23
  //   180006f fd842783 578713 600793 2f767b3 fcf42c23 fd842783 479793 ff078793 8787b3 f4c7a783 79863
  //   fd842703 fec42783 fcf716e3 fd842783 f2f42c23 f9c40793 f00533 588000ef a00733 fd842783 479793
  //   ff078793 8787b3 f547a783 2f76733 fd842783 479793 ff078793 8787b3 f507a783 f707b3 f2f42823 fd842783
  //   479793 ff078793 8787b3 f587a783 fff78793 f2f42a23 f3442783 def054e3 f3842783 479793 ff078793 8787b3
  //   f4c7a783 79463 dcdff06f 100793 fef42223 fc042a23 40e073 13 40f073 fe842783 578713 600793 2f767b3
  //   479793 ff078793 8787b3 f587a703 1900793 ee7cc63 f9c40793 f00533 4c4000ef a007b3 37f793 f037b3
  //   ff7f793 f00733 fe842783 479793 ff078793 8787b3 f4e7a623 f9c40793 f00533 490000ef fe842783 479793
  //   ff078793 8787b3 c00713 f4e7aa23 fe842783 479793 ff078793 8787b3 2100713 f4e7ac23 f9c40793 f00533
  //   454000ef a00733 41f75793 1b7d793 f70733 1f77713 40f707b3 178713 fe842783 479793 ff078793 8787b3
  //   f4e7a823 fe842783 479793 ff078793 8787b3 f507a703 fe842783 479793 ff078793 8787b3 f547a783 f70733
  //   2100793 f8e7cae3 fe842783 178713 600793 2f767b3 fef42423 f3842703 fff00793 8f70863 f3042703 f3842783
  //   479793 ff078793 8787b3 f507a783 4f76e63 f3842783 479793 ff078793 8787b3 f507a703 f3842783 479793
  //   ff078793 8787b3 f547a783 f70733 f3042783 2e7d463 f3442783 fff78793 f2f42a23 f3442783 16f04863 100793
  //   f2f42a23 fe042223 3380006f f3442783 178793 f2f42a23 fff00793 f2f42c23 1480006f fc042823 fec42783
  //   fcf42623 f80006f f3042703 fcc42783 479793 ff078793 8787b3 f507a783 cf76463 fcc42783 479793 ff078793
  //   8787b3 f507a703 fcc42783 479793 ff078793 8787b3 f547a783 f70733 f3042783 8e7da63 fcc42783 479793
  //   ff078793 8787b3 f587a703 f3442783 40f707b3 6f05a63 fcc42783 479793 ff078793 8787b3 f587a703 f3442783
  //   40f70733 300793 4e7c863 fcc42783 f2f42c23 fcc42783 479793 ff078793 8787b3 f587a783 ffe78793 f2f42a23
  //   100793 fcf42823 fcc42783 479793 ff078793 8787b3 f4c7a783 2079863 fe042223 280006f fcc42783 178713
  //   600793 2f767b3 fcf42623 fcc42703 fe842783 f0f712e3 80006f 13 fd042783 2079463 f3442703 1f00793
  //   e7ca63 f3442783 178793 f2f42a23 c0006f fe042223 1dc0006f fec42783 fcf42423 440006f fc842783 479793
  //   ff078793 8787b3 f587a783 fff78713 fc842783 479793 ff078793 8787b3 f4e7ac23 fc842783 178713 600793
  //   2f767b3 fcf42423 fc842703 fe842783 faf71ce3 fec42783 479793 ff078793 8787b3 f587a783 2f04863
  //   fec42783 479793 ff078793 8787b3 fff00713 f4e7ac23 fec42783 178713 600793 2f767b3 fef42623 100893 793
  //   479793 ff078793 8787b3 f4c7a503 73 b00893 f507a503 73 6f00893 f587a503 73 200893 1078793 f4c7a503 73
  //   1600893 f507a503 73 de00893 f587a503 73 300893 1078793 f4c7a503 73 2100893 f507a503 73 14d00893
  //   f587a503 73 400893 1078793 f4c7a503 73 2c00893 f507a503 73 1bc00893 f587a503 73 500893 1078793
  //   f4c7a503 73 3700893 f507a503 73 22b00893 f587a503 73 600893 1078793 f4c7a503 73 4200893 f507a503 73
  //   29a00893 f587a503 73 700893 f3042503 73 800893 f3442503 73 900893 fe442503 73 fe442783 78a63
  //   fd442783 178793 fcf42a23 b2dff06f 13 900893 fe442503 73 fa042023 40e073 fa042783 fe078ee3 40f073
  //   8c1ff06f fe010113 812e23 2010413 fea42623 fec42783 7a703 41c657b7 78793 e6d78793 2f70733 37b7 78793
  //   3978793 f7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
  //   中断使能寄存器IE
  //   I
  //   S
  //   B
  //   跳转地址(beq/bne/bltu)
  //   J
  //   跳转地址(jal)
  //   U
  //   在中断响应周期和uret指令周期才可开/关中断
  //   Beq
  //   Bne
  //   MemToReg
  //   MemWrite
  //   AluOP
  //   AluSrcB
  //   RegWrite
  //   $a7编号
  //   $a0编号
  //   INTR
  //   SignImm
  //   选择需要清零的中断号
  //   WriteData
  //   ecall指令输出$a0到Led
  //   为方便自动评测，需要输出PC，IR，寄存器堆写如数据RDin
  //   跳转地址(jalr)
  //   存储器不支持半字访问，因此需要取出一个字的数据特殊处理
  //   RAM写使能MemWrite、RAM写入数据MDin等信号
  //   数据存储器
  //   ReadData
  //   控制位
  //   暂停节拍，不能为0
  //   保存到寄存器中的数据
  //   戳工具置1进入计数暂停模式，ctrl+k时钟自动运行到对应节拍暂停
  //   ctrl+k关闭时钟连续运行，将控制位置零，进入单步调试模式调试
  //   返回地址
  //   左移12位立即数
  //   可计数暂停的时钟源
endmodule

// 单周期硬布线控制器
module \单周期硬布线控制器  (
  input  [4:0] OP,
  input  [4:0] Funct,
  input  in_3,
  output [3:0] ALU_OP,
  output uret,
  output MemToReg,
  output ecall,
  output MemWrite,
  output ALU_SRC,
  output RegWrite,
  output S_type,
  output Beq,
  output Bne,
  output Jalr,
  output JAL,
  output Lui,
  output Sh,
  output Bltu,
  output rs1used,
  output rs2used,
  output csrrsi,
  output csrrci,
  output Bge,
  output Blt
);

  wire \控制信号自动生成_1_ecall ;

  \运算控制器自动生成  \u_运算控制器自动生成_1  (
    .OP2(OP[0]), .OP3(OP[1]), .OP4(OP[2]), .OP5(OP[3]), .OP6(OP[4]), .F12(Funct[0]), .F13(Funct[1]),
    .F14(Funct[2]), .F25(Funct[3]), .F30(Funct[4]), .S0(ALU_OP[0]), .S1(ALU_OP[1]), .S2(ALU_OP[2]),
    .S3(ALU_OP[3]));
  \控制信号自动生成  \u_控制信号自动生成_1  (
    .OP2(OP[0]), .OP3(OP[1]), .MemToReg(MemToReg), .OP4(OP[2]), .OP5(OP[3]), .OP6(OP[4]), .F12(Funct[0]),
    .F13(Funct[1]), .F14(Funct[2]), .MemWrite(MemWrite), .F25(Funct[3]), .F30(Funct[4]), .ALU_SRC(ALU_SRC),
    .RegWrite(RegWrite), .ecall(\控制信号自动生成_1_ecall ), .S_Type(S_type), .BEQ(Beq), .BNE(Bne), .JALR(Jalr),
    .JAL(JAL), .LUI(Lui), .SH(Sh), .BLTU(Bltu), .rs1used(rs1used), .rs2used(rs2used), .csrrsi(csrrsi),
    .csrrci(csrrci), .BGE(Bge), .BLT(Blt));
  and and_1 (uret, in_3, \控制信号自动生成_1_ecall );
  and and_2 (ecall, ~in_3, \控制信号自动生成_1_ecall );  // AND_Gate

  // Other names for the same wires on the sheet: IR21 = in_3; OP_CODE[4:0] = OP

  // Notes on the sheet:
  //   运算器控制器，根据指令生成运算器功能选择信号
  //   控制信号生成，产生数据通路需要的其他控制信号
endmodule

// 运算器控制器
module \运算控制器自动生成  (
  input  OP2,
  input  OP3,
  input  OP4,
  input  OP5,
  input  OP6,
  input  F12,
  input  F13,
  input  F14,
  input  F25,
  input  F30,
  output S0,
  output S1,
  output S2,
  output S3
);

  wire and_1_out, and_2_out, and_3_out, and_4_out, and_5_out, and_6_out, and_7_out, and_8_out, and_9_out,
       and_10_out, and_11_out, and_12_out, and_13_out, and_14_out, and_15_out, and_16_out, and_17_out,
       and_18_out, and_19_out, and_20_out, and_21_out, and_22_out, and_23_out, and_24_out, and_25_out,
       and_26_out, and_27_out, and_28_out, and_29_out, and_30_out, and_31_out, and_32_out, and_33_out,
       and_34_out, and_35_out, and_36_out, and_37_out, and_38_out, and_39_out, and_40_out, and_41_out,
       and_42_out, and_43_out, and_44_out, and_45_out, not_1_out, not_2_out, not_3_out, not_4_out, not_5_out,
       not_6_out, not_7_out, not_8_out, not_9_out, not_10_out, not_11_out, not_12_out, not_13_out,
       not_14_out, not_15_out, not_16_out, not_17_out, not_18_out, not_19_out, not_20_out, not_21_out,
       not_22_out, not_23_out, not_24_out, not_25_out, not_26_out, not_27_out, not_28_out, not_29_out,
       not_30_out, not_31_out, not_32_out, not_33_out, not_34_out, not_35_out, not_36_out, not_37_out,
       not_38_out, not_39_out, not_40_out, not_41_out, not_42_out, not_43_out, not_44_out, not_45_out,
       not_46_out, not_47_out, not_48_out, not_49_out, not_50_out, not_51_out, not_52_out, not_53_out,
       not_54_out, not_55_out, not_56_out, not_57_out, not_58_out, not_59_out, not_60_out, not_61_out,
       not_62_out, not_63_out, not_64_out, not_65_out, not_66_out, not_67_out, not_68_out, not_69_out,
       not_70_out, not_71_out, not_72_out, not_73_out, not_74_out, not_75_out, not_76_out, not_77_out,
       not_78_out, not_79_out, not_80_out, not_81_out, not_82_out, not_83_out, not_84_out, not_85_out,
       not_86_out, not_87_out, not_88_out, not_89_out, not_90_out, not_91_out, not_92_out, not_93_out,
       not_94_out, not_95_out, not_96_out, not_97_out, not_98_out, not_99_out, not_100_out, not_101_out,
       not_102_out, not_103_out, not_104_out, not_105_out, not_106_out, not_107_out, not_108_out,
       not_109_out, not_110_out, not_111_out, not_112_out, not_113_out, not_114_out, not_115_out,
       not_116_out, not_117_out, not_118_out, not_119_out, not_120_out, not_121_out, not_122_out,
       not_123_out, not_124_out, not_125_out, not_126_out, not_127_out, not_128_out, not_129_out,
       not_130_out, not_131_out, not_132_out, not_133_out, not_134_out, not_135_out, not_136_out,
       not_137_out, not_138_out, not_139_out, not_140_out, not_141_out, not_142_out, not_143_out,
       not_144_out, not_145_out, not_146_out, not_147_out, not_148_out, not_149_out, not_150_out,
       not_151_out, not_152_out, not_153_out, not_154_out, not_155_out, not_156_out, not_157_out,
       not_158_out, not_159_out, not_160_out, not_161_out, not_162_out, not_163_out, not_164_out,
       not_165_out, not_166_out, not_167_out, not_168_out, not_169_out, not_170_out, not_171_out,
       not_172_out, not_173_out, not_174_out, not_175_out, not_176_out, not_177_out, not_178_out,
       not_179_out, not_180_out, not_181_out, not_182_out, not_183_out, not_184_out, not_185_out,
       not_186_out, not_187_out, not_188_out, not_189_out, not_190_out, not_191_out, not_192_out,
       not_193_out, not_194_out, not_195_out, not_196_out, not_197_out, not_198_out, not_199_out,
       not_200_out, not_201_out, not_202_out, not_203_out, not_204_out, not_205_out, not_206_out,
       not_207_out, not_208_out, not_209_out, not_210_out, not_211_out, not_212_out, not_213_out,
       not_214_out, not_215_out, not_216_out, not_217_out, not_218_out, not_219_out, not_220_out,
       not_221_out, not_222_out, not_223_out, not_224_out, not_225_out, not_226_out, not_227_out,
       not_228_out, not_229_out, not_230_out, not_231_out, not_232_out, not_233_out, not_234_out,
       not_235_out, not_236_out, not_237_out, not_238_out, not_239_out, not_240_out, not_241_out,
       not_242_out, not_243_out, not_244_out, not_245_out, not_246_out, not_247_out, not_248_out,
       not_249_out, not_250_out, not_251_out, not_252_out, not_253_out, not_254_out, not_255_out,
       not_256_out, not_257_out, not_258_out, not_259_out, not_260_out;

  not not_1 (not_1_out, F30);
  not not_2 (not_2_out, F25);
  not not_3 (not_3_out, F14);
  not not_4 (not_4_out, F13);
  not not_5 (not_5_out, F12);
  not not_6 (not_6_out, OP6);
  not not_7 (not_7_out, OP3);
  not not_8 (not_8_out, OP2);
  not not_9 (not_9_out, F30);
  not not_10 (not_10_out, F25);
  not not_11 (not_11_out, OP6);
  not not_12 (not_12_out, OP3);
  not not_13 (not_13_out, OP2);
  not not_14 (not_14_out, F30);
  not not_15 (not_15_out, F25);
  not not_16 (not_16_out, F14);
  not not_17 (not_17_out, F12);
  not not_18 (not_18_out, OP6);
  not not_19 (not_19_out, OP3);
  not not_20 (not_20_out, OP2);
  not not_21 (not_21_out, F14);
  not not_22 (not_22_out, F13);
  not not_23 (not_23_out, F12);
  not not_24 (not_24_out, OP6);
  not not_25 (not_25_out, OP5);
  not not_26 (not_26_out, OP3);
  not not_27 (not_27_out, OP2);
  not not_28 (not_28_out, OP6);
  not not_29 (not_29_out, OP5);
  not not_30 (not_30_out, OP3);
  not not_31 (not_31_out, OP2);
  not not_32 (not_32_out, F13);
  not not_33 (not_33_out, F12);
  not not_34 (not_34_out, OP6);
  not not_35 (not_35_out, OP5);
  not not_36 (not_36_out, OP3);
  not not_37 (not_37_out, OP2);
  not not_38 (not_38_out, F14);
  not not_39 (not_39_out, F12);
  not not_40 (not_40_out, OP6);
  not not_41 (not_41_out, OP5);
  not not_42 (not_42_out, OP3);
  not not_43 (not_43_out, OP2);
  not not_44 (not_44_out, F25);
  not not_45 (not_45_out, F13);
  not not_46 (not_46_out, OP6);
  not not_47 (not_47_out, OP5);
  not not_48 (not_48_out, OP3);
  not not_49 (not_49_out, OP2);
  not not_50 (not_50_out, F14);
  not not_51 (not_51_out, F12);
  not not_52 (not_52_out, OP6);
  not not_53 (not_53_out, OP5);
  not not_54 (not_54_out, OP4);
  not not_55 (not_55_out, OP3);
  not not_56 (not_56_out, OP2);
  not not_57 (not_57_out, F14);
  not not_58 (not_58_out, F12);
  not not_59 (not_59_out, OP6);
  not not_60 (not_60_out, OP4);
  not not_61 (not_61_out, OP3);
  not not_62 (not_62_out, OP2);
  not not_63 (not_63_out, F14);
  not not_64 (not_64_out, F13);
  not not_65 (not_65_out, F12);
  not not_66 (not_66_out, OP4);
  not not_67 (not_67_out, OP3);
  not not_68 (not_68_out, F14);
  not not_69 (not_69_out, F13);
  not not_70 (not_70_out, OP6);
  not not_71 (not_71_out, OP4);
  not not_72 (not_72_out, OP3);
  not not_73 (not_73_out, OP2);
  not not_74 (not_74_out, F30);
  not not_75 (not_75_out, F14);
  not not_76 (not_76_out, F13);
  not not_77 (not_77_out, F12);
  not not_78 (not_78_out, OP6);
  not not_79 (not_79_out, OP3);
  not not_80 (not_80_out, OP2);
  not not_81 (not_81_out, F13);
  not not_82 (not_82_out, OP4);
  not not_83 (not_83_out, OP3);
  not not_84 (not_84_out, OP2);
  not not_85 (not_85_out, F13);
  not not_86 (not_86_out, F12);
  not not_87 (not_87_out, OP4);
  not not_88 (not_88_out, OP3);
  not not_89 (not_89_out, OP2);
  not not_90 (not_90_out, F25);
  not not_91 (not_91_out, F14);
  not not_92 (not_92_out, F13);
  not not_93 (not_93_out, F12);
  not not_94 (not_94_out, OP6);
  not not_95 (not_95_out, OP3);
  not not_96 (not_96_out, OP2);
  not not_97 (not_97_out, F30);
  not not_98 (not_98_out, F25);
  not not_99 (not_99_out, OP6);
  not not_100 (not_100_out, OP3);
  not not_101 (not_101_out, OP2);
  not not_102 (not_102_out, F30);
  not not_103 (not_103_out, F25);
  not not_104 (not_104_out, F14);
  not not_105 (not_105_out, F12);
  not not_106 (not_106_out, OP6);
  not not_107 (not_107_out, OP3);
  not not_108 (not_108_out, OP2);
  not not_109 (not_109_out, OP6);
  not not_110 (not_110_out, OP5);
  not not_111 (not_111_out, OP3);
  not not_112 (not_112_out, OP2);
  not not_113 (not_113_out, F14);
  not not_114 (not_114_out, F12);
  not not_115 (not_115_out, OP6);
  not not_116 (not_116_out, OP5);
  not not_117 (not_117_out, OP3);
  not not_118 (not_118_out, OP2);
  not not_119 (not_119_out, F30);
  not not_120 (not_120_out, F25);
  not not_121 (not_121_out, F13);
  not not_122 (not_122_out, OP6);
  not not_123 (not_123_out, OP5);
  not not_124 (not_124_out, OP3);
  not not_125 (not_125_out, OP2);
  not not_126 (not_126_out, F30);
  not not_127 (not_127_out, F14);
  not not_128 (not_128_out, F13);
  not not_129 (not_129_out, F12);
  not not_130 (not_130_out, OP6);
  not not_131 (not_131_out, OP3);
  not not_132 (not_132_out, OP2);
  not not_133 (not_133_out, F13);
  not not_134 (not_134_out, OP4);
  not not_135 (not_135_out, OP3);
  not not_136 (not_136_out, OP2);
  not not_137 (not_137_out, F13);
  not not_138 (not_138_out, F12);
  not not_139 (not_139_out, OP4);
  not not_140 (not_140_out, OP3);
  not not_141 (not_141_out, OP2);
  not not_142 (not_142_out, F30);
  not not_143 (not_143_out, F25);
  not not_144 (not_144_out, F14);
  not not_145 (not_145_out, F13);
  not not_146 (not_146_out, F12);
  not not_147 (not_147_out, OP6);
  not not_148 (not_148_out, OP3);
  not not_149 (not_149_out, OP2);
  not not_150 (not_150_out, F25);
  not not_151 (not_151_out, F14);
  not not_152 (not_152_out, F13);
  not not_153 (not_153_out, F12);
  not not_154 (not_154_out, OP6);
  not not_155 (not_155_out, OP3);
  not not_156 (not_156_out, OP2);
  not not_157 (not_157_out, F30);
  not not_158 (not_158_out, F25);
  not not_159 (not_159_out, OP6);
  not not_160 (not_160_out, OP3);
  not not_161 (not_161_out, OP2);
  not not_162 (not_162_out, F30);
  not not_163 (not_163_out, F25);
  not not_164 (not_164_out, F14);
  not not_165 (not_165_out, OP6);
  not not_166 (not_166_out, OP3);
  not not_167 (not_167_out, OP2);
  not not_168 (not_168_out, F14);
  not not_169 (not_169_out, F13);
  not not_170 (not_170_out, F12);
  not not_171 (not_171_out, OP6);
  not not_172 (not_172_out, OP5);
  not not_173 (not_173_out, OP3);
  not not_174 (not_174_out, OP2);
  not not_175 (not_175_out, OP6);
  not not_176 (not_176_out, OP5);
  not not_177 (not_177_out, OP3);
  not not_178 (not_178_out, OP2);
  not not_179 (not_179_out, F14);
  not not_180 (not_180_out, F12);
  not not_181 (not_181_out, OP6);
  not not_182 (not_182_out, OP5);
  not not_183 (not_183_out, OP4);
  not not_184 (not_184_out, OP3);
  not not_185 (not_185_out, OP2);
  not not_186 (not_186_out, F14);
  not not_187 (not_187_out, F12);
  not not_188 (not_188_out, OP6);
  not not_189 (not_189_out, OP4);
  not not_190 (not_190_out, OP3);
  not not_191 (not_191_out, OP2);
  not not_192 (not_192_out, F14);
  not not_193 (not_193_out, F13);
  not not_194 (not_194_out, F12);
  not not_195 (not_195_out, OP4);
  not not_196 (not_196_out, OP3);
  not not_197 (not_197_out, F14);
  not not_198 (not_198_out, F13);
  not not_199 (not_199_out, OP6);
  not not_200 (not_200_out, OP4);
  not not_201 (not_201_out, OP3);
  not not_202 (not_202_out, OP2);
  not not_203 (not_203_out, F12);
  not not_204 (not_204_out, OP4);
  not not_205 (not_205_out, OP3);
  not not_206 (not_206_out, OP2);
  not not_207 (not_207_out, F30);
  not not_208 (not_208_out, F12);
  not not_209 (not_209_out, OP6);
  not not_210 (not_210_out, OP3);
  not not_211 (not_211_out, OP2);
  not not_212 (not_212_out, F30);
  not not_213 (not_213_out, F25);
  not not_214 (not_214_out, F12);
  not not_215 (not_215_out, OP6);
  not not_216 (not_216_out, OP3);
  not not_217 (not_217_out, OP2);
  not not_218 (not_218_out, F30);
  not not_219 (not_219_out, F25);
  not not_220 (not_220_out, F14);
  not not_221 (not_221_out, F12);
  not not_222 (not_222_out, OP6);
  not not_223 (not_223_out, OP3);
  not not_224 (not_224_out, OP2);
  not not_225 (not_225_out, F30);
  not not_226 (not_226_out, F25);
  not not_227 (not_227_out, F14);
  not not_228 (not_228_out, OP6);
  not not_229 (not_229_out, OP3);
  not not_230 (not_230_out, OP2);
  not not_231 (not_231_out, F12);
  not not_232 (not_232_out, OP6);
  not not_233 (not_233_out, OP5);
  not not_234 (not_234_out, OP3);
  not not_235 (not_235_out, OP2);
  not not_236 (not_236_out, F13);
  not not_237 (not_237_out, F12);
  not not_238 (not_238_out, OP6);
  not not_239 (not_239_out, OP5);
  not not_240 (not_240_out, OP3);
  not not_241 (not_241_out, OP2);
  not not_242 (not_242_out, F14);
  not not_243 (not_243_out, F12);
  not not_244 (not_244_out, OP6);
  not not_245 (not_245_out, OP5);
  not not_246 (not_246_out, OP3);
  not not_247 (not_247_out, OP2);
  not not_248 (not_248_out, F12);
  not not_249 (not_249_out, OP4);
  not not_250 (not_250_out, OP3);
  not not_251 (not_251_out, OP2);
  not not_252 (not_252_out, F13);
  not not_253 (not_253_out, OP4);
  not not_254 (not_254_out, OP3);
  not not_255 (not_255_out, OP2);
  not not_256 (not_256_out, F13);
  not not_257 (not_257_out, F12);
  not not_258 (not_258_out, OP4);
  not not_259 (not_259_out, OP3);
  not not_260 (not_260_out, OP2);
  and and_1 (and_1_out, not_1_out, not_2_out, not_3_out, not_4_out, not_5_out, not_6_out, OP5, OP4, not_7_out, not_8_out);
  and and_2 (and_2_out, not_9_out, not_10_out, F14, F13, F12, not_11_out, OP5, OP4, not_12_out, not_13_out);
  and and_3 (and_3_out, not_14_out, not_15_out, not_16_out, F13, not_17_out, not_18_out, OP5, OP4, not_19_out, not_20_out);
  and and_4 (and_4_out, not_21_out, not_22_out, not_23_out, not_24_out, not_25_out, OP4, not_26_out, not_27_out);
  and and_5 (and_5_out, F14, F13, F12, not_28_out, not_29_out, OP4, not_30_out, not_31_out);
  and and_6 (and_6_out, F14, not_32_out, not_33_out, not_34_out, not_35_out, OP4, not_36_out, not_37_out);
  and and_7 (and_7_out, not_38_out, F13, not_39_out, not_40_out, not_41_out, OP4, not_42_out, not_43_out);
  and and_8 (and_8_out, F30, not_44_out, F14, not_45_out, F12, not_46_out, not_47_out, OP4, not_48_out, not_49_out);
  and and_9 (and_9_out, not_50_out, F13, not_51_out, not_52_out, not_53_out, not_54_out, not_55_out, not_56_out);
  and and_10 (and_10_out, not_57_out, F13, not_58_out, not_59_out, OP5, not_60_out, not_61_out, not_62_out);
  and and_11 (and_11_out, not_63_out, not_64_out, not_65_out, OP6, OP5, not_66_out, not_67_out, OP2);
  and and_12 (and_12_out, not_68_out, not_69_out, F12, not_70_out, OP5, not_71_out, not_72_out, not_73_out);
  and and_13 (and_13_out, not_74_out, F25, not_75_out, not_76_out, not_77_out, not_78_out, OP5, OP4, not_79_out, not_80_out);
  and and_14 (and_14_out, F14, not_81_out, F12, OP6, OP5, not_82_out, not_83_out, not_84_out);
  and and_15 (and_15_out, F14, not_85_out, not_86_out, OP6, OP5, not_87_out, not_88_out, not_89_out);
  and and_16 (and_16_out, F30, not_90_out, not_91_out, not_92_out, not_93_out, not_94_out, OP5, OP4, not_95_out, not_96_out);
  and and_17 (and_17_out, not_97_out, not_98_out, F14, F13, F12, not_99_out, OP5, OP4, not_100_out, not_101_out);
  and and_18 (and_18_out, not_102_out, not_103_out, not_104_out, F13, not_105_out, not_106_out, OP5, OP4, not_107_out, not_108_out);
  and and_19 (and_19_out, F14, F13, F12, not_109_out, not_110_out, OP4, not_111_out, not_112_out);
  and and_20 (and_20_out, not_113_out, F13, not_114_out, not_115_out, not_116_out, OP4, not_117_out, not_118_out);
  and and_21 (and_21_out, not_119_out, not_120_out, F14, not_121_out, F12, not_122_out, not_123_out, OP4, not_124_out, not_125_out);
  and and_22 (and_22_out, not_126_out, F25, not_127_out, not_128_out, not_129_out, not_130_out, OP5, OP4, not_131_out, not_132_out);
  and and_23 (and_23_out, F14, not_133_out, F12, OP6, OP5, not_134_out, not_135_out, not_136_out);
  and and_24 (and_24_out, F14, not_137_out, not_138_out, OP6, OP5, not_139_out, not_140_out, not_141_out);
  and and_25 (and_25_out, not_142_out, not_143_out, not_144_out, not_145_out, not_146_out, not_147_out, OP5, OP4, not_148_out, not_149_out);
  and and_26 (and_26_out, F30, not_150_out, not_151_out, not_152_out, not_153_out, not_154_out, OP5, OP4, not_155_out, not_156_out);
  and and_27 (and_27_out, not_157_out, not_158_out, F14, F13, F12, not_159_out, OP5, OP4, not_160_out, not_161_out);
  and and_28 (and_28_out, not_162_out, not_163_out, not_164_out, F13, F12, not_165_out, OP5, OP4, not_166_out, not_167_out);
  and and_29 (and_29_out, not_168_out, not_169_out, not_170_out, not_171_out, not_172_out, OP4, not_173_out, not_174_out);
  and and_30 (and_30_out, F14, F13, F12, not_175_out, not_176_out, OP4, not_177_out, not_178_out);
  and and_31 (and_31_out, not_179_out, F13, not_180_out, not_181_out, not_182_out, not_183_out, not_184_out, not_185_out);
  and and_32 (and_32_out, not_186_out, F13, not_187_out, not_188_out, OP5, not_189_out, not_190_out, not_191_out);
  and and_33 (and_33_out, not_192_out, not_193_out, not_194_out, OP6, OP5, not_195_out, not_196_out, OP2);
  and and_34 (and_34_out, not_197_out, not_198_out, F12, not_199_out, OP5, not_200_out, not_201_out, not_202_out);
  and and_35 (and_35_out, F14, F13, not_203_out, OP6, OP5, not_204_out, not_205_out, not_206_out);
  and and_36 (and_36_out, not_207_out, F25, F14, F13, not_208_out, not_209_out, OP5, OP4, not_210_out, not_211_out);
  and and_37 (and_37_out, not_212_out, not_213_out, F14, F13, not_214_out, not_215_out, OP5, OP4, not_216_out, not_217_out);
  and and_38 (and_38_out, not_218_out, not_219_out, not_220_out, F13, not_221_out, not_222_out, OP5, OP4, not_223_out, not_224_out);
  and and_39 (and_39_out, not_225_out, not_226_out, not_227_out, F13, F12, not_228_out, OP5, OP4, not_229_out, not_230_out);
  and and_40 (and_40_out, F14, F13, not_231_out, not_232_out, not_233_out, OP4, not_234_out, not_235_out);
  and and_41 (and_41_out, F14, not_236_out, not_237_out, not_238_out, not_239_out, OP4, not_240_out, not_241_out);
  and and_42 (and_42_out, not_242_out, F13, not_243_out, not_244_out, not_245_out, OP4, not_246_out, not_247_out);
  and and_43 (and_43_out, F14, F13, not_248_out, OP6, OP5, not_249_out, not_250_out, not_251_out);
  and and_44 (and_44_out, F14, not_252_out, F12, OP6, OP5, not_253_out, not_254_out, not_255_out);
  and and_45 (and_45_out, F14, not_256_out, not_257_out, OP6, OP5, not_258_out, not_259_out, not_260_out);
  or or_1 (S0, and_1_out, and_2_out, and_3_out, and_4_out, and_5_out, and_6_out, and_7_out, and_8_out, and_9_out, and_10_out, and_11_out, and_12_out, and_13_out, and_14_out, and_15_out);
  or or_2 (S1, and_16_out, and_17_out, and_18_out, and_19_out, and_20_out, and_21_out, and_22_out, and_23_out, and_24_out);
  or or_3 (S2, and_25_out, and_26_out, and_27_out, and_28_out, and_29_out, and_30_out, and_31_out, and_32_out, and_33_out, and_34_out, and_35_out, and_36_out);
  or or_4 (S3, and_37_out, and_38_out, and_39_out, and_40_out, and_41_out, and_42_out, and_43_out, and_44_out, and_45_out);
endmodule
// 控制信号生成
module \控制信号自动生成  (
  input  OP2,
  input  OP3,
  input  OP4,
  input  OP5,
  input  OP6,
  input  F12,
  input  F13,
  input  F14,
  input  F25,
  input  F30,
  output MemToReg,
  output MemWrite,
  output ALU_SRC,
  output RegWrite,
  output ecall,
  output S_Type,
  output BEQ,
  output BNE,
  output JALR,
  output JAL,
  output LUI,
  output SH,
  output BLTU,
  output rs1used,
  output rs2used,
  output csrrsi,
  output csrrci,
  output BGE,
  output BLT
);

  wire and_2_out, and_3_out, and_4_out, and_5_out, and_6_out, and_7_out, and_8_out, and_9_out, and_10_out,
       and_11_out, and_12_out, and_13_out, and_14_out, and_15_out, and_16_out, and_17_out, and_18_out,
       and_19_out, and_20_out, and_21_out, and_22_out, and_23_out, and_24_out, and_25_out, and_26_out,
       and_27_out, and_28_out, and_29_out, and_30_out, and_31_out, and_32_out, and_33_out, and_34_out,
       and_35_out, and_36_out, and_37_out, and_38_out, and_39_out, and_40_out, and_48_out, and_49_out,
       and_50_out, and_51_out, and_52_out, and_53_out, and_54_out, and_55_out, and_56_out, and_57_out,
       and_58_out, and_59_out, and_60_out, and_61_out, and_62_out, and_63_out, and_64_out, and_65_out,
       and_66_out, and_67_out, and_68_out, and_69_out, and_70_out, and_71_out, and_72_out, and_73_out,
       and_74_out, and_75_out, and_76_out, and_77_out, and_78_out, and_79_out, and_80_out, and_81_out,
       and_82_out, and_83_out, and_84_out, and_85_out, and_86_out, and_87_out, and_88_out, and_89_out,
       and_90_out, and_91_out, not_1_out, not_2_out, not_3_out, not_4_out, not_5_out, not_6_out, not_7_out,
       not_8_out, not_9_out, not_10_out, not_11_out, not_12_out, not_13_out, not_14_out, not_15_out,
       not_16_out, not_17_out, not_18_out, not_19_out, not_20_out, not_21_out, not_22_out, not_23_out,
       not_24_out, not_25_out, not_26_out, not_27_out, not_28_out, not_29_out, not_30_out, not_31_out,
       not_32_out, not_33_out, not_34_out, not_35_out, not_36_out, not_37_out, not_38_out, not_39_out,
       not_40_out, not_41_out, not_42_out, not_43_out, not_44_out, not_45_out, not_46_out, not_47_out,
       not_48_out, not_49_out, not_50_out, not_51_out, not_52_out, not_53_out, not_54_out, not_55_out,
       not_56_out, not_57_out, not_58_out, not_59_out, not_60_out, not_61_out, not_62_out, not_63_out,
       not_64_out, not_65_out, not_66_out, not_67_out, not_68_out, not_69_out, not_70_out, not_71_out,
       not_72_out, not_73_out, not_74_out, not_75_out, not_76_out, not_77_out, not_78_out, not_79_out,
       not_80_out, not_81_out, not_82_out, not_83_out, not_84_out, not_85_out, not_86_out, not_87_out,
       not_88_out, not_89_out, not_90_out, not_91_out, not_92_out, not_93_out, not_94_out, not_95_out,
       not_96_out, not_97_out, not_98_out, not_99_out, not_100_out, not_101_out, not_102_out, not_103_out,
       not_104_out, not_105_out, not_106_out, not_107_out, not_108_out, not_109_out, not_110_out,
       not_111_out, not_112_out, not_113_out, not_114_out, not_115_out, not_116_out, not_117_out,
       not_118_out, not_119_out, not_120_out, not_121_out, not_122_out, not_123_out, not_124_out,
       not_125_out, not_126_out, not_127_out, not_128_out, not_129_out, not_130_out, not_131_out,
       not_132_out, not_133_out, not_134_out, not_135_out, not_136_out, not_137_out, not_138_out,
       not_139_out, not_140_out, not_141_out, not_142_out, not_143_out, not_144_out, not_145_out,
       not_146_out, not_147_out, not_148_out, not_149_out, not_150_out, not_151_out, not_152_out,
       not_153_out, not_154_out, not_155_out, not_156_out, not_157_out, not_158_out, not_159_out,
       not_160_out, not_161_out, not_162_out, not_163_out, not_164_out, not_165_out, not_166_out,
       not_167_out, not_168_out, not_169_out, not_170_out, not_171_out, not_172_out, not_173_out,
       not_174_out, not_175_out, not_176_out, not_177_out, not_178_out, not_179_out, not_180_out,
       not_181_out, not_182_out, not_183_out, not_184_out, not_185_out, not_186_out, not_187_out,
       not_188_out, not_189_out, not_190_out, not_191_out, not_192_out, not_193_out, not_194_out,
       not_195_out, not_196_out, not_197_out, not_198_out, not_199_out, not_200_out, not_201_out,
       not_202_out, not_203_out, not_204_out, not_205_out, not_206_out, not_207_out, not_208_out,
       not_209_out, not_210_out, not_211_out, not_212_out, not_213_out, not_214_out, not_215_out,
       not_216_out, not_217_out, not_218_out, not_219_out, not_220_out, not_221_out, not_222_out,
       not_223_out, not_224_out, not_225_out, not_226_out, not_227_out, not_228_out, not_229_out,
       not_230_out, not_231_out, not_232_out, not_233_out, not_234_out, not_235_out, not_236_out,
       not_237_out, not_238_out, not_239_out, not_240_out, not_241_out, not_242_out, not_243_out,
       not_244_out, not_245_out, not_246_out, not_247_out, not_248_out, not_249_out, not_250_out,
       not_251_out, not_252_out, not_253_out, not_254_out, not_255_out, not_256_out, not_257_out,
       not_258_out, not_259_out, not_260_out, not_261_out, not_262_out, not_263_out, not_264_out,
       not_265_out, not_266_out, not_267_out, not_268_out, not_269_out, not_270_out, not_271_out,
       not_272_out, not_273_out, not_274_out, not_275_out, not_276_out, not_277_out, not_278_out,
       not_279_out, not_280_out, not_281_out, not_282_out, not_283_out, not_284_out, not_285_out,
       not_286_out, not_287_out, not_288_out, not_289_out, not_290_out, not_291_out, not_292_out,
       not_293_out, not_294_out, not_295_out, not_296_out, not_297_out, not_298_out, not_299_out,
       not_300_out, not_301_out, not_302_out, not_303_out, not_304_out, not_305_out, not_306_out,
       not_307_out, not_308_out, not_309_out, not_310_out, not_311_out, not_312_out, not_313_out,
       not_314_out, not_315_out, not_316_out, not_317_out, not_318_out, not_319_out, not_320_out,
       not_321_out, not_322_out, not_323_out, not_324_out, not_325_out, not_326_out, not_327_out,
       not_328_out, not_329_out, not_330_out, not_331_out, not_332_out, not_333_out, not_334_out,
       not_335_out, not_336_out, not_337_out, not_338_out, not_339_out, not_340_out, not_341_out,
       not_342_out, not_343_out, not_344_out, not_345_out, not_346_out, not_347_out, not_348_out,
       not_349_out, not_350_out, not_351_out, not_352_out, not_353_out, not_354_out, not_355_out,
       not_356_out, not_357_out, not_358_out, not_359_out, not_360_out, not_361_out, not_362_out,
       not_363_out, not_364_out, not_365_out, not_366_out, not_367_out, not_368_out, not_369_out,
       not_370_out, not_371_out, not_372_out, not_373_out, not_374_out, not_375_out, not_376_out,
       not_377_out, not_378_out, not_379_out, not_380_out, not_381_out, not_382_out, not_383_out,
       not_384_out, not_385_out, not_386_out, not_387_out, not_388_out, not_389_out, not_390_out,
       not_391_out, not_392_out, not_393_out, not_394_out, not_395_out, not_396_out, not_397_out,
       not_398_out, not_399_out, not_400_out, not_401_out, not_402_out, not_403_out, not_404_out,
       not_405_out, not_406_out, not_407_out, not_408_out, not_409_out, not_410_out, not_411_out,
       not_412_out, not_413_out, not_414_out, not_415_out, not_416_out, not_417_out, not_418_out,
       not_419_out, not_420_out, not_421_out, not_422_out, not_423_out, not_424_out, not_425_out,
       not_426_out, not_427_out, not_428_out, not_429_out, not_430_out, not_431_out, not_432_out,
       not_433_out, not_434_out, not_435_out, not_436_out, not_437_out, not_438_out, not_439_out,
       not_440_out, not_441_out, not_442_out, not_443_out, not_444_out, not_445_out, not_446_out,
       not_447_out, not_448_out, not_449_out, not_450_out, not_451_out, not_452_out, not_453_out,
       not_454_out, not_455_out, not_456_out, not_457_out, not_458_out, not_459_out, not_460_out,
       not_461_out, not_462_out, not_463_out, not_464_out, not_465_out, not_466_out, not_467_out,
       not_468_out, not_469_out, not_470_out, not_471_out, not_472_out, not_473_out, not_474_out,
       not_475_out, not_476_out, not_477_out, not_478_out, not_479_out, not_480_out, not_481_out,
       not_482_out, not_483_out, not_484_out, not_485_out, not_486_out, not_487_out, not_488_out,
       not_489_out, not_490_out, not_491_out, not_492_out, not_493_out, not_494_out, not_495_out,
       not_496_out, not_497_out, not_498_out, not_499_out, not_500_out, not_501_out, not_502_out,
       not_503_out, not_504_out, not_505_out, not_506_out, not_507_out, not_508_out, not_509_out,
       not_510_out, not_511_out, not_512_out, not_513_out, not_514_out, not_515_out, not_516_out,
       not_517_out, not_518_out, not_519_out, not_520_out, not_521_out, not_522_out, not_523_out,
       not_524_out, not_525_out, not_526_out, not_527_out, not_528_out, not_529_out, not_530_out,
       not_531_out, not_532_out, not_533_out, not_534_out, not_535_out, not_536_out, not_537_out,
       not_538_out, not_539_out, not_540_out;

  not not_1 (not_1_out, F14);
  not not_2 (not_2_out, F12);
  not not_3 (not_3_out, OP6);
  not not_4 (not_4_out, OP5);
  not not_5 (not_5_out, OP4);
  not not_6 (not_6_out, OP3);
  not not_7 (not_7_out, OP2);
  not not_8 (not_8_out, F14);
  not not_9 (not_9_out, F12);
  not not_10 (not_10_out, OP6);
  not not_11 (not_11_out, OP4);
  not not_12 (not_12_out, OP3);
  not not_13 (not_13_out, OP2);
  not not_14 (not_14_out, F14);
  not not_15 (not_15_out, F13);
  not not_16 (not_16_out, OP6);
  not not_17 (not_17_out, OP4);
  not not_18 (not_18_out, OP3);
  not not_19 (not_19_out, OP2);
  not not_20 (not_20_out, F14);
  not not_21 (not_21_out, F13);
  not not_22 (not_22_out, F12);
  not not_23 (not_23_out, OP6);
  not not_24 (not_24_out, OP5);
  not not_25 (not_25_out, OP3);
  not not_26 (not_26_out, OP2);
  not not_27 (not_27_out, OP6);
  not not_28 (not_28_out, OP5);
  not not_29 (not_29_out, OP3);
  not not_30 (not_30_out, OP2);
  not not_31 (not_31_out, F12);
  not not_32 (not_32_out, OP6);
  not not_33 (not_33_out, OP5);
  not not_34 (not_34_out, OP3);
  not not_35 (not_35_out, OP2);
  not not_36 (not_36_out, F13);
  not not_37 (not_37_out, F12);
  not not_38 (not_38_out, OP6);
  not not_39 (not_39_out, OP5);
  not not_40 (not_40_out, OP3);
  not not_41 (not_41_out, OP2);
  not not_42 (not_42_out, F14);
  not not_43 (not_43_out, F12);
  not not_44 (not_44_out, OP6);
  not not_45 (not_45_out, OP5);
  not not_46 (not_46_out, OP3);
  not not_47 (not_47_out, OP2);
  not not_48 (not_48_out, F14);
  not not_49 (not_49_out, F13);
  not not_50 (not_50_out, OP6);
  not not_51 (not_51_out, OP5);
  not not_52 (not_52_out, OP3);
  not not_53 (not_53_out, OP2);
  not not_54 (not_54_out, F30);
  not not_55 (not_55_out, F25);
  not not_56 (not_56_out, F13);
  not not_57 (not_57_out, OP6);
  not not_58 (not_58_out, OP5);
  not not_59 (not_59_out, OP3);
  not not_60 (not_60_out, OP2);
  not not_61 (not_61_out, F25);
  not not_62 (not_62_out, F13);
  not not_63 (not_63_out, OP6);
  not not_64 (not_64_out, OP5);
  not not_65 (not_65_out, OP3);
  not not_66 (not_66_out, OP2);
  not not_67 (not_67_out, F14);
  not not_68 (not_68_out, F12);
  not not_69 (not_69_out, OP6);
  not not_70 (not_70_out, OP5);
  not not_71 (not_71_out, OP4);
  not not_72 (not_72_out, OP3);
  not not_73 (not_73_out, OP2);
  not not_74 (not_74_out, F14);
  not not_75 (not_75_out, F12);
  not not_76 (not_76_out, OP6);
  not not_77 (not_77_out, OP4);
  not not_78 (not_78_out, OP3);
  not not_79 (not_79_out, OP2);
  not not_80 (not_80_out, F14);
  not not_81 (not_81_out, F13);
  not not_82 (not_82_out, F12);
  not not_83 (not_83_out, OP4);
  not not_84 (not_84_out, OP3);
  not not_85 (not_85_out, F14);
  not not_86 (not_86_out, F13);
  not not_87 (not_87_out, OP6);
  not not_88 (not_88_out, OP4);
  not not_89 (not_89_out, OP3);
  not not_90 (not_90_out, OP2);
  not not_91 (not_91_out, F30);
  not not_92 (not_92_out, F25);
  not not_93 (not_93_out, F14);
  not not_94 (not_94_out, F13);
  not not_95 (not_95_out, F12);
  not not_96 (not_96_out, OP6);
  not not_97 (not_97_out, OP3);
  not not_98 (not_98_out, OP2);
  not not_99 (not_99_out, F25);
  not not_100 (not_100_out, F14);
  not not_101 (not_101_out, F13);
  not not_102 (not_102_out, F12);
  not not_103 (not_103_out, OP6);
  not not_104 (not_104_out, OP3);
  not not_105 (not_105_out, OP2);
  not not_106 (not_106_out, F30);
  not not_107 (not_107_out, F25);
  not not_108 (not_108_out, OP6);
  not not_109 (not_109_out, OP3);
  not not_110 (not_110_out, OP2);
  not not_111 (not_111_out, F30);
  not not_112 (not_112_out, F25);
  not not_113 (not_113_out, F12);
  not not_114 (not_114_out, OP6);
  not not_115 (not_115_out, OP3);
  not not_116 (not_116_out, OP2);
  not not_117 (not_117_out, F30);
  not not_118 (not_118_out, F25);
  not not_119 (not_119_out, F14);
  not not_120 (not_120_out, F12);
  not not_121 (not_121_out, OP6);
  not not_122 (not_122_out, OP3);
  not not_123 (not_123_out, OP2);
  not not_124 (not_124_out, F30);
  not not_125 (not_125_out, F25);
  not not_126 (not_126_out, F14);
  not not_127 (not_127_out, OP6);
  not not_128 (not_128_out, OP3);
  not not_129 (not_129_out, OP2);
  not not_130 (not_130_out, F14);
  not not_131 (not_131_out, F13);
  not not_132 (not_132_out, F12);
  not not_133 (not_133_out, OP6);
  not not_134 (not_134_out, OP5);
  not not_135 (not_135_out, OP3);
  not not_136 (not_136_out, OP2);
  not not_137 (not_137_out, OP6);
  not not_138 (not_138_out, OP5);
  not not_139 (not_139_out, OP3);
  not not_140 (not_140_out, OP2);
  not not_141 (not_141_out, F12);
  not not_142 (not_142_out, OP6);
  not not_143 (not_143_out, OP5);
  not not_144 (not_144_out, OP3);
  not not_145 (not_145_out, OP2);
  not not_146 (not_146_out, F13);
  not not_147 (not_147_out, F12);
  not not_148 (not_148_out, OP6);
  not not_149 (not_149_out, OP5);
  not not_150 (not_150_out, OP3);
  not not_151 (not_151_out, OP2);
  not not_152 (not_152_out, F14);
  not not_153 (not_153_out, F12);
  not not_154 (not_154_out, OP6);
  not not_155 (not_155_out, OP5);
  not not_156 (not_156_out, OP3);
  not not_157 (not_157_out, OP2);
  not not_158 (not_158_out, F14);
  not not_159 (not_159_out, F13);
  not not_160 (not_160_out, OP6);
  not not_161 (not_161_out, OP5);
  not not_162 (not_162_out, OP3);
  not not_163 (not_163_out, OP2);
  not not_164 (not_164_out, F30);
  not not_165 (not_165_out, F25);
  not not_166 (not_166_out, F13);
  not not_167 (not_167_out, OP6);
  not not_168 (not_168_out, OP5);
  not not_169 (not_169_out, OP3);
  not not_170 (not_170_out, OP2);
  not not_171 (not_171_out, F25);
  not not_172 (not_172_out, F13);
  not not_173 (not_173_out, OP6);
  not not_174 (not_174_out, OP5);
  not not_175 (not_175_out, OP3);
  not not_176 (not_176_out, OP2);
  not not_177 (not_177_out, F14);
  not not_178 (not_178_out, F12);
  not not_179 (not_179_out, OP6);
  not not_180 (not_180_out, OP5);
  not not_181 (not_181_out, OP4);
  not not_182 (not_182_out, OP3);
  not not_183 (not_183_out, OP2);
  not not_184 (not_184_out, OP4);
  not not_185 (not_185_out, F14);
  not not_186 (not_186_out, F13);
  not not_187 (not_187_out, F12);
  not not_188 (not_188_out, OP4);
  not not_189 (not_189_out, OP3);
  not not_190 (not_190_out, F30);
  not not_191 (not_191_out, F25);
  not not_192 (not_192_out, F14);
  not not_193 (not_193_out, F13);
  not not_194 (not_194_out, OP6);
  not not_195 (not_195_out, OP3);
  not not_196 (not_196_out, OP2);
  not not_197 (not_197_out, OP6);
  not not_198 (not_198_out, OP3);
  not not_199 (not_199_out, F30);
  not not_200 (not_200_out, F12);
  not not_201 (not_201_out, OP6);
  not not_202 (not_202_out, OP3);
  not not_203 (not_203_out, OP2);
  not not_204 (not_204_out, F30);
  not not_205 (not_205_out, F14);
  not not_206 (not_206_out, F13);
  not not_207 (not_207_out, F12);
  not not_208 (not_208_out, OP6);
  not not_209 (not_209_out, OP3);
  not not_210 (not_210_out, OP2);
  not not_211 (not_211_out, F30);
  not not_212 (not_212_out, F25);
  not not_213 (not_213_out, F14);
  not not_214 (not_214_out, F13);
  not not_215 (not_215_out, F12);
  not not_216 (not_216_out, OP3);
  not not_217 (not_217_out, OP2);
  not not_218 (not_218_out, F30);
  not not_219 (not_219_out, F25);
  not not_220 (not_220_out, F14);
  not not_221 (not_221_out, F13);
  not not_222 (not_222_out, F12);
  not not_223 (not_223_out, OP3);
  not not_224 (not_224_out, OP2);
  not not_225 (not_225_out, F14);
  not not_226 (not_226_out, F12);
  not not_227 (not_227_out, OP6);
  not not_228 (not_228_out, OP4);
  not not_229 (not_229_out, OP3);
  not not_230 (not_230_out, OP2);
  not not_231 (not_231_out, F14);
  not not_232 (not_232_out, F13);
  not not_233 (not_233_out, OP6);
  not not_234 (not_234_out, OP4);
  not not_235 (not_235_out, OP3);
  not not_236 (not_236_out, OP2);
  not not_237 (not_237_out, F14);
  not not_238 (not_238_out, F13);
  not not_239 (not_239_out, F12);
  not not_240 (not_240_out, OP4);
  not not_241 (not_241_out, OP3);
  not not_242 (not_242_out, OP2);
  not not_243 (not_243_out, F14);
  not not_244 (not_244_out, F13);
  not not_245 (not_245_out, OP4);
  not not_246 (not_246_out, OP3);
  not not_247 (not_247_out, OP2);
  not not_248 (not_248_out, F14);
  not not_249 (not_249_out, F13);
  not not_250 (not_250_out, F12);
  not not_251 (not_251_out, OP4);
  not not_252 (not_252_out, OP3);
  not not_253 (not_253_out, OP4);
  not not_254 (not_254_out, OP6);
  not not_255 (not_255_out, OP3);
  not not_256 (not_256_out, F14);
  not not_257 (not_257_out, F13);
  not not_258 (not_258_out, OP6);
  not not_259 (not_259_out, OP4);
  not not_260 (not_260_out, OP3);
  not not_261 (not_261_out, OP2);
  not not_262 (not_262_out, F12);
  not not_263 (not_263_out, OP4);
  not not_264 (not_264_out, OP3);
  not not_265 (not_265_out, OP2);
  not not_266 (not_266_out, F30);
  not not_267 (not_267_out, F25);
  not not_268 (not_268_out, F14);
  not not_269 (not_269_out, F13);
  not not_270 (not_270_out, F12);
  not not_271 (not_271_out, OP6);
  not not_272 (not_272_out, OP3);
  not not_273 (not_273_out, OP2);
  not not_274 (not_274_out, F25);
  not not_275 (not_275_out, F14);
  not not_276 (not_276_out, F13);
  not not_277 (not_277_out, F12);
  not not_278 (not_278_out, OP6);
  not not_279 (not_279_out, OP3);
  not not_280 (not_280_out, OP2);
  not not_281 (not_281_out, F30);
  not not_282 (not_282_out, F25);
  not not_283 (not_283_out, OP6);
  not not_284 (not_284_out, OP3);
  not not_285 (not_285_out, OP2);
  not not_286 (not_286_out, F30);
  not not_287 (not_287_out, F25);
  not not_288 (not_288_out, F12);
  not not_289 (not_289_out, OP6);
  not not_290 (not_290_out, OP3);
  not not_291 (not_291_out, OP2);
  not not_292 (not_292_out, F30);
  not not_293 (not_293_out, F25);
  not not_294 (not_294_out, F14);
  not not_295 (not_295_out, F12);
  not not_296 (not_296_out, OP6);
  not not_297 (not_297_out, OP3);
  not not_298 (not_298_out, OP2);
  not not_299 (not_299_out, F30);
  not not_300 (not_300_out, F25);
  not not_301 (not_301_out, F14);
  not not_302 (not_302_out, OP6);
  not not_303 (not_303_out, OP3);
  not not_304 (not_304_out, OP2);
  not not_305 (not_305_out, F14);
  not not_306 (not_306_out, F13);
  not not_307 (not_307_out, F12);
  not not_308 (not_308_out, OP6);
  not not_309 (not_309_out, OP5);
  not not_310 (not_310_out, OP3);
  not not_311 (not_311_out, OP2);
  not not_312 (not_312_out, OP6);
  not not_313 (not_313_out, OP5);
  not not_314 (not_314_out, OP3);
  not not_315 (not_315_out, OP2);
  not not_316 (not_316_out, F12);
  not not_317 (not_317_out, OP6);
  not not_318 (not_318_out, OP5);
  not not_319 (not_319_out, OP3);
  not not_320 (not_320_out, OP2);
  not not_321 (not_321_out, F13);
  not not_322 (not_322_out, F12);
  not not_323 (not_323_out, OP6);
  not not_324 (not_324_out, OP5);
  not not_325 (not_325_out, OP3);
  not not_326 (not_326_out, OP2);
  not not_327 (not_327_out, F14);
  not not_328 (not_328_out, F12);
  not not_329 (not_329_out, OP6);
  not not_330 (not_330_out, OP5);
  not not_331 (not_331_out, OP3);
  not not_332 (not_332_out, OP2);
  not not_333 (not_333_out, F14);
  not not_334 (not_334_out, F13);
  not not_335 (not_335_out, OP6);
  not not_336 (not_336_out, OP5);
  not not_337 (not_337_out, OP3);
  not not_338 (not_338_out, OP2);
  not not_339 (not_339_out, F30);
  not not_340 (not_340_out, F25);
  not not_341 (not_341_out, F13);
  not not_342 (not_342_out, OP6);
  not not_343 (not_343_out, OP5);
  not not_344 (not_344_out, OP3);
  not not_345 (not_345_out, OP2);
  not not_346 (not_346_out, F25);
  not not_347 (not_347_out, F13);
  not not_348 (not_348_out, OP6);
  not not_349 (not_349_out, OP5);
  not not_350 (not_350_out, OP3);
  not not_351 (not_351_out, OP2);
  not not_352 (not_352_out, F14);
  not not_353 (not_353_out, F12);
  not not_354 (not_354_out, OP6);
  not not_355 (not_355_out, OP5);
  not not_356 (not_356_out, OP4);
  not not_357 (not_357_out, OP3);
  not not_358 (not_358_out, OP2);
  not not_359 (not_359_out, F14);
  not not_360 (not_360_out, F12);
  not not_361 (not_361_out, OP6);
  not not_362 (not_362_out, OP4);
  not not_363 (not_363_out, OP3);
  not not_364 (not_364_out, OP2);
  not not_365 (not_365_out, F30);
  not not_366 (not_366_out, F25);
  not not_367 (not_367_out, F14);
  not not_368 (not_368_out, F13);
  not not_369 (not_369_out, F12);
  not not_370 (not_370_out, OP3);
  not not_371 (not_371_out, OP2);
  not not_372 (not_372_out, F14);
  not not_373 (not_373_out, F13);
  not not_374 (not_374_out, F12);
  not not_375 (not_375_out, OP4);
  not not_376 (not_376_out, OP3);
  not not_377 (not_377_out, OP2);
  not not_378 (not_378_out, F14);
  not not_379 (not_379_out, F13);
  not not_380 (not_380_out, OP4);
  not not_381 (not_381_out, OP3);
  not not_382 (not_382_out, OP2);
  not not_383 (not_383_out, F14);
  not not_384 (not_384_out, F13);
  not not_385 (not_385_out, F12);
  not not_386 (not_386_out, OP4);
  not not_387 (not_387_out, OP3);
  not not_388 (not_388_out, F30);
  not not_389 (not_389_out, F25);
  not not_390 (not_390_out, F14);
  not not_391 (not_391_out, F13);
  not not_392 (not_392_out, OP6);
  not not_393 (not_393_out, OP3);
  not not_394 (not_394_out, OP2);
  not not_395 (not_395_out, F14);
  not not_396 (not_396_out, F13);
  not not_397 (not_397_out, OP6);
  not not_398 (not_398_out, OP4);
  not not_399 (not_399_out, OP3);
  not not_400 (not_400_out, OP2);
  not not_401 (not_401_out, F12);
  not not_402 (not_402_out, OP4);
  not not_403 (not_403_out, OP3);
  not not_404 (not_404_out, OP2);
  not not_405 (not_405_out, F30);
  not not_406 (not_406_out, F12);
  not not_407 (not_407_out, OP6);
  not not_408 (not_408_out, OP3);
  not not_409 (not_409_out, OP2);
  not not_410 (not_410_out, F30);
  not not_411 (not_411_out, F14);
  not not_412 (not_412_out, F13);
  not not_413 (not_413_out, F12);
  not not_414 (not_414_out, OP6);
  not not_415 (not_415_out, OP3);
  not not_416 (not_416_out, OP2);
  not not_417 (not_417_out, F13);
  not not_418 (not_418_out, OP4);
  not not_419 (not_419_out, OP3);
  not not_420 (not_420_out, OP2);
  not not_421 (not_421_out, F13);
  not not_422 (not_422_out, F12);
  not not_423 (not_423_out, OP4);
  not not_424 (not_424_out, OP3);
  not not_425 (not_425_out, OP2);
  not not_426 (not_426_out, F30);
  not not_427 (not_427_out, F25);
  not not_428 (not_428_out, F14);
  not not_429 (not_429_out, F13);
  not not_430 (not_430_out, F12);
  not not_431 (not_431_out, OP6);
  not not_432 (not_432_out, OP3);
  not not_433 (not_433_out, OP2);
  not not_434 (not_434_out, F25);
  not not_435 (not_435_out, F14);
  not not_436 (not_436_out, F13);
  not not_437 (not_437_out, F12);
  not not_438 (not_438_out, OP6);
  not not_439 (not_439_out, OP3);
  not not_440 (not_440_out, OP2);
  not not_441 (not_441_out, F30);
  not not_442 (not_442_out, F25);
  not not_443 (not_443_out, OP6);
  not not_444 (not_444_out, OP3);
  not not_445 (not_445_out, OP2);
  not not_446 (not_446_out, F30);
  not not_447 (not_447_out, F25);
  not not_448 (not_448_out, F12);
  not not_449 (not_449_out, OP6);
  not not_450 (not_450_out, OP3);
  not not_451 (not_451_out, OP2);
  not not_452 (not_452_out, F30);
  not not_453 (not_453_out, F25);
  not not_454 (not_454_out, F14);
  not not_455 (not_455_out, F12);
  not not_456 (not_456_out, OP6);
  not not_457 (not_457_out, OP3);
  not not_458 (not_458_out, OP2);
  not not_459 (not_459_out, F30);
  not not_460 (not_460_out, F25);
  not not_461 (not_461_out, F14);
  not not_462 (not_462_out, OP6);
  not not_463 (not_463_out, OP3);
  not not_464 (not_464_out, OP2);
  not not_465 (not_465_out, F14);
  not not_466 (not_466_out, F12);
  not not_467 (not_467_out, OP6);
  not not_468 (not_468_out, OP4);
  not not_469 (not_469_out, OP3);
  not not_470 (not_470_out, OP2);
  not not_471 (not_471_out, F30);
  not not_472 (not_472_out, F25);
  not not_473 (not_473_out, F14);
  not not_474 (not_474_out, F13);
  not not_475 (not_475_out, F12);
  not not_476 (not_476_out, OP3);
  not not_477 (not_477_out, OP2);
  not not_478 (not_478_out, F14);
  not not_479 (not_479_out, F13);
  not not_480 (not_480_out, F12);
  not not_481 (not_481_out, OP4);
  not not_482 (not_482_out, OP3);
  not not_483 (not_483_out, OP2);
  not not_484 (not_484_out, F14);
  not not_485 (not_485_out, F13);
  not not_486 (not_486_out, OP4);
  not not_487 (not_487_out, OP3);
  not not_488 (not_488_out, OP2);
  not not_489 (not_489_out, F30);
  not not_490 (not_490_out, F25);
  not not_491 (not_491_out, F14);
  not not_492 (not_492_out, F13);
  not not_493 (not_493_out, OP6);
  not not_494 (not_494_out, OP3);
  not not_495 (not_495_out, OP2);
  not not_496 (not_496_out, F14);
  not not_497 (not_497_out, F13);
  not not_498 (not_498_out, OP6);
  not not_499 (not_499_out, OP4);
  not not_500 (not_500_out, OP3);
  not not_501 (not_501_out, OP2);
  not not_502 (not_502_out, F12);
  not not_503 (not_503_out, OP4);
  not not_504 (not_504_out, OP3);
  not not_505 (not_505_out, OP2);
  not not_506 (not_506_out, F30);
  not not_507 (not_507_out, F12);
  not not_508 (not_508_out, OP6);
  not not_509 (not_509_out, OP3);
  not not_510 (not_510_out, OP2);
  not not_511 (not_511_out, F30);
  not not_512 (not_512_out, F14);
  not not_513 (not_513_out, F13);
  not not_514 (not_514_out, F12);
  not not_515 (not_515_out, OP6);
  not not_516 (not_516_out, OP3);
  not not_517 (not_517_out, OP2);
  not not_518 (not_518_out, F13);
  not not_519 (not_519_out, OP4);
  not not_520 (not_520_out, OP3);
  not not_521 (not_521_out, OP2);
  not not_522 (not_522_out, F13);
  not not_523 (not_523_out, F12);
  not not_524 (not_524_out, OP4);
  not not_525 (not_525_out, OP3);
  not not_526 (not_526_out, OP2);
  not not_527 (not_527_out, F12);
  not not_528 (not_528_out, OP3);
  not not_529 (not_529_out, OP2);
  not not_530 (not_530_out, OP3);
  not not_531 (not_531_out, OP2);
  not not_532 (not_532_out, F13);
  not not_533 (not_533_out, OP4);
  not not_534 (not_534_out, OP3);
  not not_535 (not_535_out, OP2);
  not not_536 (not_536_out, F13);
  not not_537 (not_537_out, F12);
  not not_538 (not_538_out, OP4);
  not not_539 (not_539_out, OP3);
  not not_540 (not_540_out, OP2);
  and and_1 (MemToReg, not_1_out, F13, not_2_out, not_3_out, not_4_out, not_5_out, not_6_out, not_7_out);
  and and_2 (and_2_out, not_8_out, F13, not_9_out, not_10_out, OP5, not_11_out, not_12_out, not_13_out);
  and and_3 (and_3_out, not_14_out, not_15_out, F12, not_16_out, OP5, not_17_out, not_18_out, not_19_out);
  and and_4 (and_4_out, not_20_out, not_21_out, not_22_out, not_23_out, not_24_out, OP4, not_25_out, not_26_out);
  and and_5 (and_5_out, F14, F13, F12, not_27_out, not_28_out, OP4, not_29_out, not_30_out);
  and and_6 (and_6_out, F14, F13, not_31_out, not_32_out, not_33_out, OP4, not_34_out, not_35_out);
  and and_7 (and_7_out, F14, not_36_out, not_37_out, not_38_out, not_39_out, OP4, not_40_out, not_41_out);
  and and_8 (and_8_out, not_42_out, F13, not_43_out, not_44_out, not_45_out, OP4, not_46_out, not_47_out);
  and and_9 (and_9_out, not_48_out, not_49_out, F12, not_50_out, not_51_out, OP4, not_52_out, not_53_out);
  and and_10 (and_10_out, not_54_out, not_55_out, F14, not_56_out, F12, not_57_out, not_58_out, OP4, not_59_out, not_60_out);
  and and_11 (and_11_out, F30, not_61_out, F14, not_62_out, F12, not_63_out, not_64_out, OP4, not_65_out, not_66_out);
  and and_12 (and_12_out, not_67_out, F13, not_68_out, not_69_out, not_70_out, not_71_out, not_72_out, not_73_out);
  and and_13 (and_13_out, not_74_out, F13, not_75_out, not_76_out, OP5, not_77_out, not_78_out, not_79_out);
  and and_14 (and_14_out, not_80_out, not_81_out, not_82_out, OP6, OP5, not_83_out, not_84_out, OP2);
  and and_15 (and_15_out, not_85_out, not_86_out, F12, not_87_out, OP5, not_88_out, not_89_out, not_90_out);
  and and_16 (and_16_out, not_91_out, not_92_out, not_93_out, not_94_out, not_95_out, not_96_out, OP5, OP4, not_97_out, not_98_out);
  and and_17 (and_17_out, F30, not_99_out, not_100_out, not_101_out, not_102_out, not_103_out, OP5, OP4, not_104_out, not_105_out);
  and and_18 (and_18_out, not_106_out, not_107_out, F14, F13, F12, not_108_out, OP5, OP4, not_109_out, not_110_out);
  and and_19 (and_19_out, not_111_out, not_112_out, F14, F13, not_113_out, not_114_out, OP5, OP4, not_115_out, not_116_out);
  and and_20 (and_20_out, not_117_out, not_118_out, not_119_out, F13, not_120_out, not_121_out, OP5, OP4, not_122_out, not_123_out);
  and and_21 (and_21_out, not_124_out, not_125_out, not_126_out, F13, F12, not_127_out, OP5, OP4, not_128_out, not_129_out);
  and and_22 (and_22_out, not_130_out, not_131_out, not_132_out, not_133_out, not_134_out, OP4, not_135_out, not_136_out);
  and and_23 (and_23_out, F14, F13, F12, not_137_out, not_138_out, OP4, not_139_out, not_140_out);
  and and_24 (and_24_out, F14, F13, not_141_out, not_142_out, not_143_out, OP4, not_144_out, not_145_out);
  and and_25 (and_25_out, F14, not_146_out, not_147_out, not_148_out, not_149_out, OP4, not_150_out, not_151_out);
  and and_26 (and_26_out, not_152_out, F13, not_153_out, not_154_out, not_155_out, OP4, not_156_out, not_157_out);
  and and_27 (and_27_out, not_158_out, not_159_out, F12, not_160_out, not_161_out, OP4, not_162_out, not_163_out);
  and and_28 (and_28_out, not_164_out, not_165_out, F14, not_166_out, F12, not_167_out, not_168_out, OP4, not_169_out, not_170_out);
  and and_29 (and_29_out, F30, not_171_out, F14, not_172_out, F12, not_173_out, not_174_out, OP4, not_175_out, not_176_out);
  and and_30 (and_30_out, not_177_out, F13, not_178_out, not_179_out, not_180_out, not_181_out, not_182_out, not_183_out);
  and and_31 (and_31_out, OP6, OP5, not_184_out, OP3, OP2);
  and and_32 (and_32_out, not_185_out, not_186_out, not_187_out, OP6, OP5, not_188_out, not_189_out, OP2);
  and and_33 (and_33_out, not_190_out, not_191_out, not_192_out, not_193_out, F12, not_194_out, OP5, OP4, not_195_out, not_196_out);
  and and_34 (and_34_out, not_197_out, OP5, OP4, not_198_out, OP2);
  and and_35 (and_35_out, not_199_out, F25, F14, F13, not_200_out, not_201_out, OP5, OP4, not_202_out, not_203_out);
  and and_36 (and_36_out, not_204_out, F25, not_205_out, not_206_out, not_207_out, not_208_out, OP5, OP4, not_209_out, not_210_out);
  and and_37 (and_37_out, not_211_out, not_212_out, not_213_out, not_214_out, not_215_out, OP6, OP5, OP4, not_216_out, not_217_out);
  and and_38 (and_38_out, not_218_out, not_219_out, not_220_out, not_221_out, not_222_out, OP6, OP5, OP4, not_223_out, not_224_out);
  and and_39 (and_39_out, not_225_out, F13, not_226_out, not_227_out, OP5, not_228_out, not_229_out, not_230_out);
  and and_40 (and_40_out, not_231_out, not_232_out, F12, not_233_out, OP5, not_234_out, not_235_out, not_236_out);
  and and_41 (BEQ, not_237_out, not_238_out, not_239_out, OP6, OP5, not_240_out, not_241_out, not_242_out);
  and and_42 (BNE, not_243_out, not_244_out, F12, OP6, OP5, not_245_out, not_246_out, not_247_out);
  and and_43 (JALR, not_248_out, not_249_out, not_250_out, OP6, OP5, not_251_out, not_252_out, OP2);
  and and_44 (JAL, OP6, OP5, not_253_out, OP3, OP2);
  and and_45 (LUI, not_254_out, OP5, OP4, not_255_out, OP2);
  and and_46 (SH, not_256_out, not_257_out, F12, not_258_out, OP5, not_259_out, not_260_out, not_261_out);
  and and_47 (BLTU, F14, F13, not_262_out, OP6, OP5, not_263_out, not_264_out, not_265_out);
  and and_48 (and_48_out, not_266_out, not_267_out, not_268_out, not_269_out, not_270_out, not_271_out, OP5, OP4, not_272_out, not_273_out);
  and and_49 (and_49_out, F30, not_274_out, not_275_out, not_276_out, not_277_out, not_278_out, OP5, OP4, not_279_out, not_280_out);
  and and_50 (and_50_out, not_281_out, not_282_out, F14, F13, F12, not_283_out, OP5, OP4, not_284_out, not_285_out);
  and and_51 (and_51_out, not_286_out, not_287_out, F14, F13, not_288_out, not_289_out, OP5, OP4, not_290_out, not_291_out);
  and and_52 (and_52_out, not_292_out, not_293_out, not_294_out, F13, not_295_out, not_296_out, OP5, OP4, not_297_out, not_298_out);
  and and_53 (and_53_out, not_299_out, not_300_out, not_301_out, F13, F12, not_302_out, OP5, OP4, not_303_out, not_304_out);
  and and_54 (and_54_out, not_305_out, not_306_out, not_307_out, not_308_out, not_309_out, OP4, not_310_out, not_311_out);
  and and_55 (and_55_out, F14, F13, F12, not_312_out, not_313_out, OP4, not_314_out, not_315_out);
  and and_56 (and_56_out, F14, F13, not_316_out, not_317_out, not_318_out, OP4, not_319_out, not_320_out);
  and and_57 (and_57_out, F14, not_321_out, not_322_out, not_323_out, not_324_out, OP4, not_325_out, not_326_out);
  and and_58 (and_58_out, not_327_out, F13, not_328_out, not_329_out, not_330_out, OP4, not_331_out, not_332_out);
  and and_59 (and_59_out, not_333_out, not_334_out, F12, not_335_out, not_336_out, OP4, not_337_out, not_338_out);
  and and_60 (and_60_out, not_339_out, not_340_out, F14, not_341_out, F12, not_342_out, not_343_out, OP4, not_344_out, not_345_out);
  and and_61 (and_61_out, F30, not_346_out, F14, not_347_out, F12, not_348_out, not_349_out, OP4, not_350_out, not_351_out);
  and and_62 (and_62_out, not_352_out, F13, not_353_out, not_354_out, not_355_out, not_356_out, not_357_out, not_358_out);
  and and_63 (and_63_out, not_359_out, F13, not_360_out, not_361_out, OP5, not_362_out, not_363_out, not_364_out);
  and and_64 (and_64_out, not_365_out, not_366_out, not_367_out, not_368_out, not_369_out, OP6, OP5, OP4, not_370_out, not_371_out);
  and and_65 (and_65_out, not_372_out, not_373_out, not_374_out, OP6, OP5, not_375_out, not_376_out, not_377_out);
  and and_66 (and_66_out, not_378_out, not_379_out, F12, OP6, OP5, not_380_out, not_381_out, not_382_out);
  and and_67 (and_67_out, not_383_out, not_384_out, not_385_out, OP6, OP5, not_386_out, not_387_out, OP2);
  and and_68 (and_68_out, not_388_out, not_389_out, not_390_out, not_391_out, F12, not_392_out, OP5, OP4, not_393_out, not_394_out);
  and and_69 (and_69_out, not_395_out, not_396_out, F12, not_397_out, OP5, not_398_out, not_399_out, not_400_out);
  and and_70 (and_70_out, F14, F13, not_401_out, OP6, OP5, not_402_out, not_403_out, not_404_out);
  and and_71 (and_71_out, not_405_out, F25, F14, F13, not_406_out, not_407_out, OP5, OP4, not_408_out, not_409_out);
  and and_72 (and_72_out, not_410_out, F25, not_411_out, not_412_out, not_413_out, not_414_out, OP5, OP4, not_415_out, not_416_out);
  and and_73 (and_73_out, F14, not_417_out, F12, OP6, OP5, not_418_out, not_419_out, not_420_out);
  and and_74 (and_74_out, F14, not_421_out, not_422_out, OP6, OP5, not_423_out, not_424_out, not_425_out);
  and and_75 (and_75_out, not_426_out, not_427_out, not_428_out, not_429_out, not_430_out, not_431_out, OP5, OP4, not_432_out, not_433_out);
  and and_76 (and_76_out, F30, not_434_out, not_435_out, not_436_out, not_437_out, not_438_out, OP5, OP4, not_439_out, not_440_out);
  and and_77 (and_77_out, not_441_out, not_442_out, F14, F13, F12, not_443_out, OP5, OP4, not_444_out, not_445_out);
  and and_78 (and_78_out, not_446_out, not_447_out, F14, F13, not_448_out, not_449_out, OP5, OP4, not_450_out, not_451_out);
  and and_79 (and_79_out, not_452_out, not_453_out, not_454_out, F13, not_455_out, not_456_out, OP5, OP4, not_457_out, not_458_out);
  and and_80 (and_80_out, not_459_out, not_460_out, not_461_out, F13, F12, not_462_out, OP5, OP4, not_463_out, not_464_out);
  and and_81 (and_81_out, not_465_out, F13, not_466_out, not_467_out, OP5, not_468_out, not_469_out, not_470_out);
  and and_82 (and_82_out, not_471_out, not_472_out, not_473_out, not_474_out, not_475_out, OP6, OP5, OP4, not_476_out, not_477_out);
  and and_83 (and_83_out, not_478_out, not_479_out, not_480_out, OP6, OP5, not_481_out, not_482_out, not_483_out);
  and and_84 (and_84_out, not_484_out, not_485_out, F12, OP6, OP5, not_486_out, not_487_out, not_488_out);
  and and_85 (and_85_out, not_489_out, not_490_out, not_491_out, not_492_out, F12, not_493_out, OP5, OP4, not_494_out, not_495_out);
  and and_86 (and_86_out, not_496_out, not_497_out, F12, not_498_out, OP5, not_499_out, not_500_out, not_501_out);
  and and_87 (and_87_out, F14, F13, not_502_out, OP6, OP5, not_503_out, not_504_out, not_505_out);
  and and_88 (and_88_out, not_506_out, F25, F14, F13, not_507_out, not_508_out, OP5, OP4, not_509_out, not_510_out);
  and and_89 (and_89_out, not_511_out, F25, not_512_out, not_513_out, not_514_out, not_515_out, OP5, OP4, not_516_out, not_517_out);
  and and_90 (and_90_out, F14, not_518_out, F12, OP6, OP5, not_519_out, not_520_out, not_521_out);
  and and_91 (and_91_out, F14, not_522_out, not_523_out, OP6, OP5, not_524_out, not_525_out, not_526_out);
  and and_92 (csrrsi, F14, F13, not_527_out, OP6, OP5, OP4, not_528_out, not_529_out);
  and and_93 (csrrci, F14, F13, F12, OP6, OP5, OP4, not_530_out, not_531_out);
  and and_94 (BGE, F14, not_532_out, F12, OP6, OP5, not_533_out, not_534_out, not_535_out);
  and and_95 (BLT, F14, not_536_out, not_537_out, OP6, OP5, not_538_out, not_539_out, not_540_out);
  or or_1 (MemWrite, and_2_out, and_3_out);
  or or_2 (ecall, and_37_out, and_38_out);
  or or_3 (S_Type, and_39_out, and_40_out);
  or or_4 (ALU_SRC, and_4_out, and_5_out, and_6_out, and_7_out, and_8_out, and_9_out, and_10_out, and_11_out, and_12_out, and_13_out, and_14_out, and_15_out);
  or or_5 (RegWrite, and_16_out, and_17_out, and_18_out, and_19_out, and_20_out, and_21_out, and_22_out, and_23_out, and_24_out, and_25_out, and_26_out, and_27_out, and_28_out, and_29_out, and_30_out, and_31_out, and_32_out, and_33_out, and_34_out, and_35_out, and_36_out);
  or or_6 (rs2used, and_75_out, and_76_out, and_77_out, and_78_out, and_79_out, and_80_out, and_81_out, and_82_out, and_83_out, and_84_out, and_85_out, and_86_out, and_87_out, and_88_out, and_89_out, and_90_out, and_91_out);
  or or_7 (rs1used, and_48_out, and_49_out, and_50_out, and_51_out, and_52_out, and_53_out, and_54_out, and_55_out, and_56_out, and_57_out, and_58_out, and_59_out, and_60_out, and_61_out, and_62_out, and_63_out, and_64_out, and_65_out, and_66_out, and_67_out, and_68_out, and_69_out, and_70_out, and_71_out, and_72_out, and_73_out, and_74_out);
endmodule

// ALU
module ALU (
  input  [31:0] X,
  input  [31:0] Y,
  input  [3:0] AluOP,
  output out_4,
  output Equal,
  output out_6,
  output [31:0] Result,
  output [31:0] Result_2
);

  wire [0:0] comparator_1_lt, comparator_2_lt;
  wire [31:0] adder_1_out, AND_out, divider_1_out, divider_1_rem, multiplier_1_cout, multiplier_1_out,
       NOR_out, OR_out, shifter_1_out, shifter_2_out, shifter_3_out, subtractor_1_out, XOR_out;

  assign AND_out = X & Y;  // AND_Gate AND, 32 bits wide
  assign OR_out = X | Y;  // OR_Gate OR, 32 bits wide
  Shifter #(.width(32), .shift("ll")) shifter_1 (.in(X), .\dist (Y[4:0]), .out(shifter_1_out));
  Shifter #(.width(32), .shift("ar")) shifter_2 (.in(X), .\dist (Y[4:0]), .out(shifter_2_out));
  Shifter #(.width(32), .shift("lr")) shifter_3 (.in(X), .\dist (Y[4:0]), .out(shifter_3_out));
  Multiplier #(.width(32)) multiplier_1 (.a(X), .b(Y), .out(multiplier_1_out), .cout(multiplier_1_cout));  // open: cin
  Divider #(.width(32)) divider_1 (.a(X), .b(Y), .out(divider_1_out), .rem(divider_1_rem));  // open: upper
  Adder #(.width(32)) adder_1 (.a(X), .b(Y), .out(adder_1_out));  // open: cin, cout
  Subtractor #(.width(32)) subtractor_1 (.a(X), .b(Y), .out(subtractor_1_out));  // open: bin, bout
  assign XOR_out = X ^ Y;  // XOR_Gate XOR, 32 bits wide
  assign NOR_out = ~(X | Y);  // NOR_Gate NOR, 32 bits wide
  Comparator #(.width(32), .mode("twosComplement")) comparator_1 (
    .a(X), .b(Y), .eq(Equal), .lt(comparator_1_lt[0]));  // open: gt
  Comparator #(.width(32), .mode("unsigned")) comparator_2 (.a(X), .b(Y), .lt(comparator_2_lt[0]));  // open: gt, eq
  Multiplexer #(.select(4), .width(32), .disabled("Z"), .enable("false")) multiplexer_1 (
    .in0(shifter_1_out), .in1(shifter_2_out), .in2(shifter_3_out), .in3(multiplier_1_out),
    .in4(divider_1_rem), .in5(adder_1_out), .in6(subtractor_1_out), .in7(AND_out), .in8(OR_out),
    .in9(XOR_out), .in10(NOR_out), .in11({{31{1'b0}}, comparator_1_lt[0]}),
    .in12({{31{1'b0}}, comparator_2_lt[0]}), .in13({32{1'b0}}), .in14({32{1'b0}}), .in15({32{1'b0}}),
    .out(Result), .sel(AluOP));
  Multiplexer #(.select(4), .width(32), .disabled("Z"), .enable("false")) multiplexer_2 (
    .in0({32{1'b0}}), .in1({32{1'b0}}), .in2({32{1'b0}}), .in3(multiplier_1_cout), .in4(divider_1_out),
    .in5({32{1'b0}}), .in6({32{1'b0}}), .in7({32{1'b0}}), .in8({32{1'b0}}), .in9({32{1'b0}}),
    .in10({32{1'b0}}), .in11({32{1'b0}}), .in12({32{1'b0}}), .in13({32{1'b0}}), .in14({32{1'b0}}),
    .in15({32{1'b0}}), .out(Result_2), .sel(AluOP));
  Multiplexer #(.select(4), .width(1), .disabled("Z"), .enable("false")) multiplexer_3 (
    .in0(1'b0), .in1(1'b0), .in2(1'b0), .in3(1'b0), .in4(1'b0), .in5(1'b0), .in6(1'b0), .in7(1'b0),
    .in8(1'b0), .in9(1'b0), .in10(1'b0), .in11(comparator_1_lt[0]), .in12(comparator_2_lt[0]), .in13(1'b0),
    .in14(1'b0), .in15(1'b0), .out(out_6), .sel(AluOP));
  not not_1 (out_4, out_6);

  // Other names for the same wires on the sheet: Result2[31:0] = Result_2; S[3:0] = AluOP; tunnel = out_6;
  //   tunnel_t = out_4

  // Notes on the sheet:
  //   不要改变此引脚区域内容，也不要改变ALU封装形式
  //   输入引脚
  //   有符号比较
  //   无符号比较
  //   输出引脚
endmodule

module Regifile (
  input  [31:0] Din,
  input  Clk,
  input  WE,
  input  [4:0] R1_num,
  input  [4:0] W_num,
  input  [4:0] R2_num,
  output [31:0] R1,
  output [31:0] R2
);

  // RegisterFile registerfile_1: pin names not known; wires that end beside it: Din, Clk, WE, W_num, R1_num, R2_num, R1, R2
endmodule

module Rapid_Roll (
);

  wire clock_1_out, left_out, restart_out, right_out;
  wire [31:0] all_1_row1, all_1_row2, all_1_row3, all_1_row4, all_1_row5, all_1_row6, all_1_row7, all_1_row8,
       all_1_row9, all_1_row10, all_1_row11, all_1_row12, all_1_row13, all_1_row14, all_1_row15, all_1_row16,
       all_1_row17, all_1_row18, all_1_row19, all_1_row20, all_1_row21, all_1_row22, all_1_row23,
       all_1_row24, all_1_row25, all_1_row26, all_1_row27, all_1_row28, all_1_row29, all_1_row30,
       all_1_row31, all_1_row32, \单周期_单级中断游戏版_1_bx , \单周期_单级中断游戏版_1_by , \单周期_单级中断游戏版_1_flag1 ,
       \单周期_单级中断游戏版_1_flag2 , \单周期_单级中断游戏版_1_flag3 , \单周期_单级中断游戏版_1_flag4 , \单周期_单级中断游戏版_1_flag5 ,
       \单周期_单级中断游戏版_1_flag6 , \单周期_单级中断游戏版_1_life , \单周期_单级中断游戏版_1_start1 , \单周期_单级中断游戏版_1_start2 ,
       \单周期_单级中断游戏版_1_start3 , \单周期_单级中断游戏版_1_start4 , \单周期_单级中断游戏版_1_start5 , \单周期_单级中断游戏版_1_start6 ,
       \单周期_单级中断游戏版_1_upline1 , \单周期_单级中断游戏版_1_upline2 , \单周期_单级中断游戏版_1_upline3 , \单周期_单级中断游戏版_1_upline4 ,
       \单周期_单级中断游戏版_1_upline5 , \单周期_单级中断游戏版_1_upline6 ;

  Button restart (.out(restart_out));
  Button right (.out(right_out));
  Button left (.out(left_out));
  \单周期_单级中断游戏版  \u_单周期_单级中断游戏版_1  (
    .restart(restart_out), .left(left_out), .right(right_out), .flag1(\单周期_单级中断游戏版_1_flag1 ),
    .flag4(\单周期_单级中断游戏版_1_flag4 ), .start1(\单周期_单级中断游戏版_1_start1 ), .start4(\单周期_单级中断游戏版_1_start4 ),
    .upline1(\单周期_单级中断游戏版_1_upline1 ), .upline4(\单周期_单级中断游戏版_1_upline4 ), .flag2(\单周期_单级中断游戏版_1_flag2 ),
    .flag5(\单周期_单级中断游戏版_1_flag5 ), .start2(\单周期_单级中断游戏版_1_start2 ), .start5(\单周期_单级中断游戏版_1_start5 ),
    .upline2(\单周期_单级中断游戏版_1_upline2 ), .upline5(\单周期_单级中断游戏版_1_upline5 ), .flag3(\单周期_单级中断游戏版_1_flag3 ),
    .flag6(\单周期_单级中断游戏版_1_flag6 ), .start3(\单周期_单级中断游戏版_1_start3 ), .start6(\单周期_单级中断游戏版_1_start6 ),
    .upline3(\单周期_单级中断游戏版_1_upline3 ), .upline6(\单周期_单级中断游戏版_1_upline6 ), .bx(\单周期_单级中断游戏版_1_bx ),
    .by(\单周期_单级中断游戏版_1_by ), .life(\单周期_单级中断游戏版_1_life ), .CLK(clock_1_out));  // open: RegWrite, MemWrite, PC, IR, RDin, MDin
  Clock #(.highDuration(1), .lowDuration(1)) clock_1 (.out(clock_1_out));
  all all_1 (
    .flag1(\单周期_单级中断游戏版_1_flag1 ), .start1(\单周期_单级中断游戏版_1_start1 ), .upline1(\单周期_单级中断游戏版_1_upline1 ),
    .flag4(\单周期_单级中断游戏版_1_flag4 ), .upline4(\单周期_单级中断游戏版_1_upline4 ), .flag2(\单周期_单级中断游戏版_1_flag2 ),
    .start2(\单周期_单级中断游戏版_1_start2 ), .upline2(\单周期_单级中断游戏版_1_upline2 ), .flag5(\单周期_单级中断游戏版_1_flag5 ),
    .start5(\单周期_单级中断游戏版_1_start5 ), .upline5(\单周期_单级中断游戏版_1_upline5 ), .flag3(\单周期_单级中断游戏版_1_flag3 ),
    .start3(\单周期_单级中断游戏版_1_start3 ), .upline3(\单周期_单级中断游戏版_1_upline3 ), .flag6(\单周期_单级中断游戏版_1_flag6 ),
    .start6(\单周期_单级中断游戏版_1_start6 ), .upline6(\单周期_单级中断游戏版_1_upline6 ), .x(\单周期_单级中断游戏版_1_bx ),
    .y(\单周期_单级中断游戏版_1_by ), .row1(all_1_row1), .row9(all_1_row9), .row17(all_1_row17), .row25(all_1_row25),
    .row2(all_1_row2), .row10(all_1_row10), .row18(all_1_row18), .row26(all_1_row26), .row3(all_1_row3),
    .row11(all_1_row11), .row19(all_1_row19), .row27(all_1_row27), .row4(all_1_row4), .row12(all_1_row12),
    .row20(all_1_row20), .row28(all_1_row28), .row5(all_1_row5), .row13(all_1_row13), .row21(all_1_row21),
    .row29(all_1_row29), .row6(all_1_row6), .row14(all_1_row14), .row22(all_1_row22), .row30(all_1_row30),
    .row7(all_1_row7), .row15(all_1_row15), .row23(all_1_row23), .row31(all_1_row31), .row8(all_1_row8),
    .row16(all_1_row16), .row24(all_1_row24), .row32(all_1_row32), .start4(\单周期_单级中断游戏版_1_start4 ),
    .life(\单周期_单级中断游戏版_1_life ));
  DotMatrix #(.inputtype("row"), .matrixcols(32), .matrixrows(32), .persist(0), .dotshape("square")) dotmatrix_1 (
    .row0(all_1_row1), .row1(all_1_row2), .row2(all_1_row3), .row3(all_1_row4), .row4(all_1_row5),
    .row5(all_1_row6), .row6(all_1_row7), .row7(all_1_row8), .row8(all_1_row9), .row9(all_1_row10),
    .row10(all_1_row11), .row11(all_1_row12), .row12(all_1_row13), .row13(all_1_row14), .row14(all_1_row15),
    .row15(all_1_row16), .row16(all_1_row17), .row17(all_1_row18), .row18(all_1_row19), .row19(all_1_row20),
    .row20(all_1_row21), .row21(all_1_row22), .row22(all_1_row23), .row23(all_1_row24), .row24(all_1_row25),
    .row25(all_1_row26), .row26(all_1_row27), .row27(all_1_row28), .row28(all_1_row29), .row29(all_1_row30),
    .row30(all_1_row31), .row31(all_1_row32));
endmodule
