// Logisim project 动态分支预测.circ as structural Verilog: 24 circuits, main circuit ◇单周期RISC-V
module \单周期RISC_V  (
  input  IR1,
  input  IR2,
  input  IR3,
  output RegWrite,
  output MemWrite,
  output [31:0] PC,
  output [31:0] IR,
  output [31:0] RDin,
  output [31:0] MDin,
  output [31:0] LedData
);

  wire and_1_out, and_2_out, and_3_out, and_6_out, Beq, Bltu, Bne, CLK, clock_1_out, comparator_1_eq,
       comparator_2_eq, comparator_2_lt, d_ff_1_q, ecall, equ, Go, halt, IR1_t, IR2_t, IR3_t, IRA, IRB, IRC,
       JAL, JALR, less, Lui, MemToReg, nand_1_out, not_1_out, not_2_out, not_3_out, not_4_out, or_1_out,
       or_2_out, or_6_out, or_7_out, riscv_probe_1_p2, RST, S_type, Sh, W1, W2, W3, \单周期硬布线控制器_1_alu_src ;
  wire [1:0] priority_encoder_1_out;
  wire [3:0] \单周期硬布线控制器_1_alu_op ;
  wire [4:0] multiplexer_3_out, multiplexer_4_out;
  wire [11:0] multiplexer_2_out;
  wire [12:0] CNT_num;
  wire [15:0] \总周期数 ;
  wire [31:0] adder_2_out, adder_3_out, ALUResult, and_4_out, and_5_out, bit_extender_1_out,
       bit_extender_2_out, bit_extender_3_out, bit_extender_4_out, imm_U__12, multiplexer_1_out,
       multiplexer_5_out, multiplexer_7_out, multiplexer_8_out, multiplexer_9_out, multiplexer_10_out, PC_4,
       ram_1_data, regifile_1_r1, regifile_1_r2, ShDin, shifter_1_out, shifter_2_out, shifter_4_out;

  Button \u_继续运行  (.out(Go));
  Button _1 (.out(IRA));
  Button _2 (.out(IRB));
  Button _3 (.out(IRC));
  Button \u_置位  (.out(RST));
  LED #(.active("true")) led_1 (.in(W1));
  LED #(.active("true")) led_2 (.in(W2));
  LED #(.active("true")) led_3 (.in(W3));
  Priority_Encoder #(.select(2), .disabled("Z")) priority_encoder_1 (
    .in0(1'b1), .in1(or_1_out), .in2(JAL), .in3(JALR), .out(priority_encoder_1_out));  // open: gs, en_out, en_in
  Multiplexer #(.select(2), .width(32), .disabled("Z"), .enable("false")) multiplexer_1 (
    .in0(PC_4), .in1(adder_2_out), .in2(adder_3_out), .in3(ALUResult), .out(multiplexer_1_out),
    .sel(priority_encoder_1_out));
  not not_1 (not_1_out, halt);
  Hex_Digit_Display hex_digit_display_1 (.value(LedData[31:28]));  // open: dp
  not not_2 (not_2_out, equ);
  and and_1 (and_1_out, Beq, equ);
  and and_2 (and_2_out, not_2_out, Bne);
  or or_1 (or_1_out, and_1_out, and_2_out, and_3_out);
  Register #(.width(32), .trigger("rising"), .Select("low")) u_PC (
    .D(multiplexer_1_out), .en(or_2_out), .Q(PC), .clk(CLK), .clr(RST));
  or or_2 (or_2_out, not_1_out, Go);
  Hex_Digit_Display hex_digit_display_2 (.value(LedData[23:20]));  // open: dp
  Hex_Digit_Display hex_digit_display_3 (.value(LedData[27:24]));  // open: dp
  and and_3 (and_3_out, less, Bltu);
  Adder #(.width(32)) adder_1 (.a(PC), .b(32'h4), .out(PC_4));  // open: cin, cout
  Hex_Digit_Display hex_digit_display_4 (.value(LedData[19:16]));  // open: dp
  Hex_Digit_Display hex_digit_display_5 (.value(LedData[15:12]));  // open: dp
  Hex_Digit_Display hex_digit_display_6 (.value(LedData[7:4]));  // open: dp
  Hex_Digit_Display hex_digit_display_7 (.value(LedData[11:8]));  // open: dp
  // Probe on \总周期数 
  // RiscV_Probe riscv_probe_1: pin names not known; wires that end beside it: IR, riscv_probe_1_p2
  ROM #(.addrWidth(10), .dataWidth(32), .Select("high")) rom_1 (.addr(PC[11:2]), .data(IR));
  Hex_Digit_Display hex_digit_display_8 (.value(LedData[3:0]));  // open: dp
  \单周期硬布线控制器  \u_单周期硬布线控制器_1  (
    .Funct({IR[30], IR[25], IR[14:12]}), .OP(IR[6:2]), .ALU_OP(\单周期硬布线控制器_1_alu_op ), .MemToReg(MemToReg),
    .MemWrite(MemWrite), .ALU_SRC(\单周期硬布线控制器_1_alu_src ), .RegWrite(RegWrite), .ecall(ecall),
    .S_type(S_type), .Jalr(JALR), .Beq(Beq), .JAL(JAL), .Bne(Bne), .in_3(IR[21]), .uret(riscv_probe_1_p2),
    .Lui(Lui), .Sh(Sh), .Bltu(Bltu));  // open: rs1used, rs2used, csr
  Multiplexer #(.select(1), .width(12), .disabled("Z"), .enable("false")) multiplexer_2 (
    .in0(IR[31:20]), .in1({IR[31:25], IR[11:7]}), .out(multiplexer_2_out), .sel(S_type));
  assign bit_extender_1_out = {{20{IR[31]}}, {IR[31], IR[7], IR[30:25], IR[11:8]}};  // Bit_Extender bit_extender_1
  assign bit_extender_2_out = {{12{IR[31]}}, {IR[31], IR[19:12], IR[20], IR[30:21]}};  // Bit_Extender bit_extender_2
  assign bit_extender_3_out = {{12{IR[31]}}, IR[31:12]};  // Bit_Extender bit_extender_3
  or or_3 (IR1_t, IR1, IRA);
  Multiplexer #(.select(1), .width(5), .disabled("Z"), .enable("false")) multiplexer_3 (
    .in0(IR[19:15]), .in1(5'b10001), .out(multiplexer_3_out), .sel(ecall));
  Multiplexer #(.select(1), .width(5), .disabled("Z"), .enable("false")) multiplexer_4 (
    .in0(IR[24:20]), .in1(5'b01010), .out(multiplexer_4_out), .sel(ecall));
  assign bit_extender_4_out = {{20{multiplexer_2_out[11]}}, multiplexer_2_out};  // Bit_Extender bit_extender_4
  Shifter #(.width(32), .shift("ll")) shifter_1 (.in(bit_extender_1_out), .\dist (5'b00001), .out(shifter_1_out));
  Shifter #(.width(32), .shift("ll")) shifter_2 (.in(bit_extender_2_out), .\dist (5'b00001), .out(shifter_2_out));
  Shifter #(.width(32), .shift("ll")) shifter_3 (.in(bit_extender_3_out), .\dist (5'b01100), .out(imm_U__12));
  or or_4 (IR2_t, IR2, IRB);
  Regifile regifile_1 (
    .Din(RDin), .Clk(CLK), .R1(regifile_1_r1), .R2(regifile_1_r2), .WE(RegWrite), .W_num(IR[11:7]),
    .R1_num(multiplexer_3_out), .R2_num(multiplexer_4_out));
  Adder #(.width(32)) adder_2 (.a(shifter_1_out), .b(PC), .out(adder_2_out));  // open: cin, cout
  Adder #(.width(32)) adder_3 (.a(shifter_2_out), .b(PC), .out(adder_3_out));  // open: cin, cout
  or or_5 (IR3_t, IR3, IRC);
  Multiplexer #(.select(1), .width(32), .disabled("Z"), .enable("false")) multiplexer_5 (
    .in0(regifile_1_r2), .in1(bit_extender_4_out), .out(multiplexer_5_out), .sel(\单周期硬布线控制器_1_alu_src ));
  assign and_4_out = 32'hffff & regifile_1_r2;  // AND_Gate and_4, 32 bits wide
  Shifter #(.width(32), .shift("ll")) shifter_4 (.in(regifile_1_r2), .\dist (5'b10000), .out(shifter_4_out));
  ALU alu_1 (
    .X(regifile_1_r1), .Y(multiplexer_5_out), .AluOP(\单周期硬布线控制器_1_alu_op ), .Equal(equ), .Result(ALUResult),
    .out_6(less));  // open: Result_2, out_4
  Multiplexer #(.select(1), .width(32), .disabled("Z"), .enable("false")) multiplexer_6 (
    .in0(regifile_1_r2), .in1(ShDin), .out(MDin), .sel(Sh));
  Multiplexer #(.select(1), .width(32), .disabled("Z"), .enable("false")) multiplexer_7 (
    .in0(32'hffff0000), .in1(32'hffff), .out(multiplexer_7_out), .sel(ALUResult[1]));
  Multiplexer #(.select(1), .width(32), .disabled("Z"), .enable("false")) multiplexer_8 (
    .in0(and_4_out), .in1(shifter_4_out), .out(multiplexer_8_out), .sel(ALUResult[1]));
  Comparator #(.width(32), .mode("twosComplement")) comparator_1 (
    .a(regifile_1_r1), .b(32'h22), .eq(comparator_1_eq));  // open: gt, lt
  not not_3 (not_3_out, comparator_1_eq);
  not not_4 (not_4_out, halt);
  or or_6 (or_6_out, not_4_out, Go);
  Counter #(.width(16), .max('hffff), .ongoal("wrap"), .trigger("rising"), .behavior("new")) counter_1 (
    .count(or_6_out), .Q(\总周期数 ), .clk(CLK), .clr(RST));  // open: load, D, carry, preset, down
  assign and_5_out = ram_1_data & multiplexer_7_out;  // AND_Gate and_5, 32 bits wide
  and and_6 (and_6_out, ecall, comparator_1_eq);
  and and_7 (halt, ecall, not_3_out);
  RAM #(.addrWidth(10), .dataWidth(32), .bus("separate"), .Select("high")) ram_1 (
    .addr(ALUResult[11:2]), .din(MDin), .data(ram_1_data), .str(MemWrite), .clk(CLK), .clr(RST));  // open: sel, ld
  Adder #(.width(32)) adder_4 (.a(and_5_out), .b(multiplexer_8_out), .out(ShDin));  // open: cin, cout
  Register #(.width(32), .trigger("rising"), .Select("low")) register_1 (
    .D(regifile_1_r2), .en(and_6_out), .Q(LedData), .clk(CLK), .clr(RST));
  Multiplexer #(.select(1), .width(32), .disabled("Z"), .enable("false")) multiplexer_9 (
    .in0(ALUResult), .in1(ram_1_data), .out(multiplexer_9_out), .sel(MemToReg));
  or or_7 (or_7_out, JAL, JALR);
  Multiplexer #(.select(1), .width(32), .disabled("Z"), .enable("false")) multiplexer_10 (
    .in0(multiplexer_9_out), .in1(PC_4), .out(multiplexer_10_out), .sel(or_7_out));
  Multiplexer #(.select(1), .width(32), .disabled("Z"), .enable("false")) multiplexer_11 (
    .in0(multiplexer_10_out), .in1(imm_U__12), .out(RDin), .sel(Lui));
  D_Flip_Flop #(.trigger("high"), .Pre_Clr_Positions("LEGACY"), .NegatePresetClear("false"), .enable("true"), .NewFFLayout("false")) d_ff_1 (.Q(d_ff_1_q));  // open: clk, D, Qn, preset, en, reset
  // Probe on 13'h31
  Comparator #(.width(13), .mode("twosComplement")) comparator_2 (
    .a(CNT_num), .b(13'h31), .eq(comparator_2_eq), .lt(comparator_2_lt));  // open: gt
  Clock #(.highDuration(1), .lowDuration(1)) clock_1 (.out(clock_1_out));
  Counter #(.width(13), .max('h1fff), .ongoal("stay"), .trigger("rising"), .behavior("old")) counter_2 (
    .count(comparator_2_lt), .Q(CNT_num), .clk(clock_1_out));  // open: load, D, carry, clr, preset
  nand nand_1 (nand_1_out, d_ff_1_q, comparator_2_eq);
  assign CLK = nand_1_out ? clock_1_out : 1'bz;  // Controlled_Buffer controlled_buffer_1
  Pull_Resistor #(.pull(1)) pull_resistor_1 (.node(CLK));

  // Notes on the sheet:
  //   中断源
  //   中断等待指示
  //   数码管输出应该用寄存器锁存，否则显示数据只能一闪而过
  //   数码管输出
  //   指令探针
  //   指令存储器
  //   指令字
  //   contents of rom_1 (hex, n*v repeats v):
  //   100493 100006f 100493 200913 300993 100006f 100493 200913 300993 100006f 100493 200913 300993
  //   100006f 100493 200913 300993 3c0000ef 100413 100493 1f49493 900533 2200893 73 24d493 48463 fedff06f
  //   900533 2200893 73 100493 249493 900533 2200893 73 48463 fedff06f 100493 1f49493 900533 2200893 73
  //   4034d493 900533 2200893 73 4044d493 900533 2200893 73 4044d493 900533 2200893 73 4044d493 900533
  //   2200893 73 4044d493 900533 2200893 73 4044d493 900533 2200893 73 4044d493 900533 2200893 73 4044d493
  //   900533 2200893 73 100413 1f41993 41f9d993 433 c00913 300b13 140413 f47413 800293 100313 499993
  //   89e9b3 1300533 2200893 73 406282b3 fe0294e3 140413 f00f93 1f47433 1c41413 800293 100313 49d993
  //   89e9b3 1300533 2200893 73 406282b3 fe0294e3 1c45413 406b0b33 b0463 f95ff06f 2b3 fff2c293 829293
  //   ff2e293 500533 2200893 73 fff00413 493 84a023 140413 448493 84a023 140413 448493 84a023 140413
  //   448493 84a023 140413 448493 84a023 140413 448493 84a023 140413 448493 84a023 140413 448493 84a023
  //   140413 448493 84a023 140413 448493 84a023 140413 448493 84a023 140413 448493 84a023 140413 448493
  //   84a023 140413 448493 84a023 140413 448493 84a023 140413 448493 84a023 140413 448493 140413 433
  //   3c00493 42983 4aa03 149a2b3 28663 134a023 1442023 ffc48493 fe9412e3 800533 2200893 73 440413 3c00493
  //   fc9416e3 a00893 73 100293 300313 800493 849493 7648493 900533 2200893 73 800e13 5494b3 6494b3 900533
  //   2200893 73 fffe0e13 fe0e14e3 a00893 73 800e13 fedc04b7 fff00413 1045413 84e4b3 900533 2200893 73
  //   ba984b7 900533 73 76544b7 900533 73 32104b7 900533 73 fffe0e13 fa0e1ee3 a00893 73 313 2000e13 100493
  //   100913 931023 900533 2200893 73 12484b3 230313 fffe0e13 fe0e12e3 1000e13 313 32483 900533 2200893 73
  //   430313 fffe0e13 fe0e14e3 a00893 73 ff100493 900533 2200893 73 148493 fe9068e3 900533 2200893 73
  //   a00893 73 413 140413 800533 2200893 73 240413 800533 2200893 73 340413 800533 2200893 73 440413
  //   800533 2200893 73 540413 800533 2200893 73 640413 800533 2200893 73 740413 800533 2200893 73 840413
  //   800533 2200893 2200893 73 8067
  //   I
  //   S
  //   B
  //   J
  //   跳转地址(jal)
  //   U
  //   Beq
  //   Bne
  //   MemToReg
  //   MemWrite
  //   AluOP
  //   AluSrcB
  //   RegWrite
  //   $a7编号
  //   $a0编号
  //   跳转地址(beq/bne/bltu)
  //   SignImm
  //   WriteData
  //   ecall指令输出$a0到Led
  //   跳转地址(jalr)
  //   存储器不支持半字访问，因此需要取出一个字的数据特殊处理
  //   数据存储器
  //   为方便自动评测，需要输出PC，IR，寄存器堆写如数据RDin
  //   ReadData
  //   RAM写使能MemWrite、RAM写入数据MDin等信号
  //   保存到寄存器中的数据
  //   返回地址
  //   左移12位立即数
  //   控制位
  //   暂停节拍，不能为0
  //   戳工具置1进入计数暂停模式，ctrl+k时钟自动运行到对应节拍暂停
  //   ctrl+k关闭时钟连续运行，将控制位置零，进入单步调试模式调试
  //   用这个时钟源需要去掉电路中的其他时钟源
  //   可计数暂停的时钟源
endmodule

// 单周期硬布线控制器
module \单周期硬布线控制器  (
  input  [4:0] OP,
  input  [4:0] Funct,
  input  in_3,
  output [3:0] ALU_OP,
  output uret,
  output MemToReg,
  output ecall,
  output MemWrite,
  output ALU_SRC,
  output RegWrite,
  output S_type,
  output Beq,
  output Bne,
  output Jalr,
  output JAL,
  output Lui,
  output Sh,
  output Bltu,
  output rs1used,
  output rs2used,
  output csr
);

  wire \控制信号自动生成_1_ecall ;

  \运算控制器自动生成  \u_运算控制器自动生成_1  (
    .OP2(OP[0]), .OP3(OP[1]), .OP4(OP[2]), .OP5(OP[3]), .OP6(OP[4]), .F12(Funct[0]), .F13(Funct[1]),
    .F14(Funct[2]), .F25(Funct[3]), .F30(Funct[4]), .S0(ALU_OP[0]), .S1(ALU_OP[1]), .S2(ALU_OP[2]),
    .S3(ALU_OP[3]));
  \控制信号自动生成  \u_控制信号自动生成_1  (
    .OP2(OP[0]), .OP3(OP[1]), .MemToReg(MemToReg), .OP4(OP[2]), .OP5(OP[3]), .OP6(OP[4]), .F12(Funct[0]),
    .F13(Funct[1]), .F14(Funct[2]), .F25(Funct[3]), .MemWrite(MemWrite), .F30(Funct[4]), .ALU_SRC(ALU_SRC),
    .RegWrite(RegWrite), .ecall(\控制信号自动生成_1_ecall ), .S_Type(S_type), .BEQ(Beq), .BNE(Bne), .JALR(Jalr),
    .JAL(JAL), .LUI(Lui), .SH(Sh), .BLTU(Bltu), .rs1used(rs1used), .rs2used(rs2used), .csr(csr));
  and and_1 (uret, in_3, \控制信号自动生成_1_ecall );
  and and_2 (ecall, ~in_3, \控制信号自动生成_1_ecall );  // AND_Gate

  // Other names for the same wires on the sheet: IR21 = in_3; OP_CODE[4:0] = OP

  // Notes on the sheet:
  //   运算器控制器，根据指令生成运算器功能选择信号
  //   控制信号生成，产生数据通路需要的其他控制信号
endmodule

// 运算器控制器
module \运算控制器自动生成  (
  input  OP2,
  input  OP3,
  input  OP4,
  input  OP5,
  input  OP6,
  input  F12,
  input  F13,
  input  F14,
  input  F25,
  input  F30,
  output S0,
  output S1,
  output S2,
  output S3
);

  wire and_1_out, and_2_out, and_3_out, and_4_out, and_5_out, and_6_out, and_7_out, and_8_out, and_9_out,
       and_10_out, and_11_out, and_12_out, and_13_out, and_14_out, and_15_out, and_16_out, and_17_out,
       and_18_out, and_19_out, and_20_out, and_21_out, and_22_out, and_23_out, and_24_out, and_25_out,
       and_26_out, and_27_out, and_28_out, and_29_out, and_30_out, and_31_out, and_32_out, and_33_out,
       and_34_out, and_35_out, and_36_out, not_1_out, not_2_out, not_3_out, not_4_out, not_5_out, not_6_out,
       not_7_out, not_8_out, not_9_out, not_10_out, not_11_out, not_12_out, not_13_out, not_14_out,
       not_15_out, not_16_out, not_17_out, not_18_out, not_19_out, not_20_out, not_21_out, not_22_out,
       not_23_out, not_24_out, not_25_out, not_26_out, not_27_out, not_28_out, not_29_out, not_30_out,
       not_31_out, not_32_out, not_33_out, not_34_out, not_35_out, not_36_out, not_37_out, not_38_out,
       not_39_out, not_40_out, not_41_out, not_42_out, not_43_out, not_44_out, not_45_out, not_46_out,
       not_47_out, not_48_out, not_49_out, not_50_out, not_51_out, not_52_out, not_53_out, not_54_out,
       not_55_out, not_56_out, not_57_out, not_58_out, not_59_out, not_60_out, not_61_out, not_62_out,
       not_63_out, not_64_out, not_65_out, not_66_out, not_67_out, not_68_out, not_69_out, not_70_out,
       not_71_out, not_72_out, not_73_out, not_74_out, not_75_out, not_76_out, not_77_out, not_78_out,
       not_79_out, not_80_out, not_81_out, not_82_out, not_83_out, not_84_out, not_85_out, not_86_out,
       not_87_out, not_88_out, not_89_out, not_90_out, not_91_out, not_92_out, not_93_out, not_94_out,
       not_95_out, not_96_out, not_97_out, not_98_out, not_99_out, not_100_out, not_101_out, not_102_out,
       not_103_out, not_104_out, not_105_out, not_106_out, not_107_out, not_108_out, not_109_out,
       not_110_out, not_111_out, not_112_out, not_113_out, not_114_out, not_115_out, not_116_out,
       not_117_out, not_118_out, not_119_out, not_120_out, not_121_out, not_122_out, not_123_out,
       not_124_out, not_125_out, not_126_out, not_127_out, not_128_out, not_129_out, not_130_out,
       not_131_out, not_132_out, not_133_out, not_134_out, not_135_out, not_136_out, not_137_out,
       not_138_out, not_139_out, not_140_out, not_141_out, not_142_out, not_143_out, not_144_out,
       not_145_out, not_146_out, not_147_out, not_148_out, not_149_out, not_150_out, not_151_out,
       not_152_out, not_153_out, not_154_out, not_155_out, not_156_out, not_157_out, not_158_out,
       not_159_out, not_160_out, not_161_out, not_162_out, not_163_out, not_164_out, not_165_out,
       not_166_out, not_167_out, not_168_out, not_169_out, not_170_out, not_171_out, not_172_out,
       not_173_out, not_174_out, not_175_out, not_176_out, not_177_out, not_178_out, not_179_out,
       not_180_out, not_181_out, not_182_out, not_183_out, not_184_out, not_185_out, not_186_out,
       not_187_out, not_188_out, not_189_out, not_190_out, not_191_out, not_192_out, not_193_out,
       not_194_out, not_195_out, not_196_out, not_197_out, not_198_out, not_199_out, not_200_out,
       not_201_out, not_202_out, not_203_out, not_204_out, not_205_out, not_206_out, not_207_out,
       not_208_out, not_209_out, not_210_out, not_211_out, not_212_out, not_213_out, not_214_out;

  not not_1 (not_1_out, F30);
  not not_2 (not_2_out, F25);
  not not_3 (not_3_out, F14);
  not not_4 (not_4_out, F13);
  not not_5 (not_5_out, F12);
  not not_6 (not_6_out, OP6);
  not not_7 (not_7_out, OP3);
  not not_8 (not_8_out, OP2);
  not not_9 (not_9_out, F30);
  not not_10 (not_10_out, F25);
  not not_11 (not_11_out, OP6);
  not not_12 (not_12_out, OP3);
  not not_13 (not_13_out, OP2);
  not not_14 (not_14_out, F30);
  not not_15 (not_15_out, F25);
  not not_16 (not_16_out, F14);
  not not_17 (not_17_out, F12);
  not not_18 (not_18_out, OP6);
  not not_19 (not_19_out, OP3);
  not not_20 (not_20_out, OP2);
  not not_21 (not_21_out, F14);
  not not_22 (not_22_out, F13);
  not not_23 (not_23_out, F12);
  not not_24 (not_24_out, OP6);
  not not_25 (not_25_out, OP5);
  not not_26 (not_26_out, OP3);
  not not_27 (not_27_out, OP2);
  not not_28 (not_28_out, OP6);
  not not_29 (not_29_out, OP5);
  not not_30 (not_30_out, OP3);
  not not_31 (not_31_out, OP2);
  not not_32 (not_32_out, F13);
  not not_33 (not_33_out, F12);
  not not_34 (not_34_out, OP6);
  not not_35 (not_35_out, OP5);
  not not_36 (not_36_out, OP3);
  not not_37 (not_37_out, OP2);
  not not_38 (not_38_out, F14);
  not not_39 (not_39_out, F12);
  not not_40 (not_40_out, OP6);
  not not_41 (not_41_out, OP5);
  not not_42 (not_42_out, OP3);
  not not_43 (not_43_out, OP2);
  not not_44 (not_44_out, F25);
  not not_45 (not_45_out, F13);
  not not_46 (not_46_out, OP6);
  not not_47 (not_47_out, OP5);
  not not_48 (not_48_out, OP3);
  not not_49 (not_49_out, OP2);
  not not_50 (not_50_out, F14);
  not not_51 (not_51_out, F12);
  not not_52 (not_52_out, OP6);
  not not_53 (not_53_out, OP5);
  not not_54 (not_54_out, OP4);
  not not_55 (not_55_out, OP3);
  not not_56 (not_56_out, OP2);
  not not_57 (not_57_out, F14);
  not not_58 (not_58_out, F12);
  not not_59 (not_59_out, OP6);
  not not_60 (not_60_out, OP4);
  not not_61 (not_61_out, OP3);
  not not_62 (not_62_out, OP2);
  not not_63 (not_63_out, F14);
  not not_64 (not_64_out, F13);
  not not_65 (not_65_out, F12);
  not not_66 (not_66_out, OP4);
  not not_67 (not_67_out, OP3);
  not not_68 (not_68_out, F14);
  not not_69 (not_69_out, F13);
  not not_70 (not_70_out, OP6);
  not not_71 (not_71_out, OP4);
  not not_72 (not_72_out, OP3);
  not not_73 (not_73_out, OP2);
  not not_74 (not_74_out, F25);
  not not_75 (not_75_out, F14);
  not not_76 (not_76_out, F13);
  not not_77 (not_77_out, F12);
  not not_78 (not_78_out, OP6);
  not not_79 (not_79_out, OP3);
  not not_80 (not_80_out, OP2);
  not not_81 (not_81_out, F30);
  not not_82 (not_82_out, F25);
  not not_83 (not_83_out, OP6);
  not not_84 (not_84_out, OP3);
  not not_85 (not_85_out, OP2);
  not not_86 (not_86_out, F30);
  not not_87 (not_87_out, F25);
  not not_88 (not_88_out, F14);
  not not_89 (not_89_out, F12);
  not not_90 (not_90_out, OP6);
  not not_91 (not_91_out, OP3);
  not not_92 (not_92_out, OP2);
  not not_93 (not_93_out, OP6);
  not not_94 (not_94_out, OP5);
  not not_95 (not_95_out, OP3);
  not not_96 (not_96_out, OP2);
  not not_97 (not_97_out, F14);
  not not_98 (not_98_out, F12);
  not not_99 (not_99_out, OP6);
  not not_100 (not_100_out, OP5);
  not not_101 (not_101_out, OP3);
  not not_102 (not_102_out, OP2);
  not not_103 (not_103_out, F30);
  not not_104 (not_104_out, F25);
  not not_105 (not_105_out, F13);
  not not_106 (not_106_out, OP6);
  not not_107 (not_107_out, OP5);
  not not_108 (not_108_out, OP3);
  not not_109 (not_109_out, OP2);
  not not_110 (not_110_out, F30);
  not not_111 (not_111_out, F25);
  not not_112 (not_112_out, F14);
  not not_113 (not_113_out, F13);
  not not_114 (not_114_out, F12);
  not not_115 (not_115_out, OP6);
  not not_116 (not_116_out, OP3);
  not not_117 (not_117_out, OP2);
  not not_118 (not_118_out, F25);
  not not_119 (not_119_out, F14);
  not not_120 (not_120_out, F13);
  not not_121 (not_121_out, F12);
  not not_122 (not_122_out, OP6);
  not not_123 (not_123_out, OP3);
  not not_124 (not_124_out, OP2);
  not not_125 (not_125_out, F30);
  not not_126 (not_126_out, F25);
  not not_127 (not_127_out, OP6);
  not not_128 (not_128_out, OP3);
  not not_129 (not_129_out, OP2);
  not not_130 (not_130_out, F30);
  not not_131 (not_131_out, F25);
  not not_132 (not_132_out, F14);
  not not_133 (not_133_out, OP6);
  not not_134 (not_134_out, OP3);
  not not_135 (not_135_out, OP2);
  not not_136 (not_136_out, F14);
  not not_137 (not_137_out, F13);
  not not_138 (not_138_out, F12);
  not not_139 (not_139_out, OP6);
  not not_140 (not_140_out, OP5);
  not not_141 (not_141_out, OP3);
  not not_142 (not_142_out, OP2);
  not not_143 (not_143_out, OP6);
  not not_144 (not_144_out, OP5);
  not not_145 (not_145_out, OP3);
  not not_146 (not_146_out, OP2);
  not not_147 (not_147_out, F14);
  not not_148 (not_148_out, F12);
  not not_149 (not_149_out, OP6);
  not not_150 (not_150_out, OP5);
  not not_151 (not_151_out, OP4);
  not not_152 (not_152_out, OP3);
  not not_153 (not_153_out, OP2);
  not not_154 (not_154_out, F14);
  not not_155 (not_155_out, F12);
  not not_156 (not_156_out, OP6);
  not not_157 (not_157_out, OP4);
  not not_158 (not_158_out, OP3);
  not not_159 (not_159_out, OP2);
  not not_160 (not_160_out, F14);
  not not_161 (not_161_out, F13);
  not not_162 (not_162_out, F12);
  not not_163 (not_163_out, OP4);
  not not_164 (not_164_out, OP3);
  not not_165 (not_165_out, F14);
  not not_166 (not_166_out, F13);
  not not_167 (not_167_out, OP6);
  not not_168 (not_168_out, OP4);
  not not_169 (not_169_out, OP3);
  not not_170 (not_170_out, OP2);
  not not_171 (not_171_out, F12);
  not not_172 (not_172_out, OP4);
  not not_173 (not_173_out, OP3);
  not not_174 (not_174_out, OP2);
  not not_175 (not_175_out, F30);
  not not_176 (not_176_out, F25);
  not not_177 (not_177_out, F12);
  not not_178 (not_178_out, OP6);
  not not_179 (not_179_out, OP3);
  not not_180 (not_180_out, OP2);
  not not_181 (not_181_out, F30);
  not not_182 (not_182_out, F25);
  not not_183 (not_183_out, F14);
  not not_184 (not_184_out, F12);
  not not_185 (not_185_out, OP6);
  not not_186 (not_186_out, OP3);
  not not_187 (not_187_out, OP2);
  not not_188 (not_188_out, F30);
  not not_189 (not_189_out, F25);
  not not_190 (not_190_out, F14);
  not not_191 (not_191_out, OP6);
  not not_192 (not_192_out, OP3);
  not not_193 (not_193_out, OP2);
  not not_194 (not_194_out, F12);
  not not_195 (not_195_out, OP6);
  not not_196 (not_196_out, OP5);
  not not_197 (not_197_out, OP3);
  not not_198 (not_198_out, OP2);
  not not_199 (not_199_out, F13);
  not not_200 (not_200_out, F12);
  not not_201 (not_201_out, OP6);
  not not_202 (not_202_out, OP5);
  not not_203 (not_203_out, OP3);
  not not_204 (not_204_out, OP2);
  not not_205 (not_205_out, F14);
  not not_206 (not_206_out, F12);
  not not_207 (not_207_out, OP6);
  not not_208 (not_208_out, OP5);
  not not_209 (not_209_out, OP3);
  not not_210 (not_210_out, OP2);
  not not_211 (not_211_out, F12);
  not not_212 (not_212_out, OP4);
  not not_213 (not_213_out, OP3);
  not not_214 (not_214_out, OP2);
  and and_1 (and_1_out, not_1_out, not_2_out, not_3_out, not_4_out, not_5_out, not_6_out, OP5, OP4, not_7_out, not_8_out);
  and and_2 (and_2_out, not_9_out, not_10_out, F14, F13, F12, not_11_out, OP5, OP4, not_12_out, not_13_out);
  and and_3 (and_3_out, not_14_out, not_15_out, not_16_out, F13, not_17_out, not_18_out, OP5, OP4, not_19_out, not_20_out);
  and and_4 (and_4_out, not_21_out, not_22_out, not_23_out, not_24_out, not_25_out, OP4, not_26_out, not_27_out);
  and and_5 (and_5_out, F14, F13, F12, not_28_out, not_29_out, OP4, not_30_out, not_31_out);
  and and_6 (and_6_out, F14, not_32_out, not_33_out, not_34_out, not_35_out, OP4, not_36_out, not_37_out);
  and and_7 (and_7_out, not_38_out, F13, not_39_out, not_40_out, not_41_out, OP4, not_42_out, not_43_out);
  and and_8 (and_8_out, F30, not_44_out, F14, not_45_out, F12, not_46_out, not_47_out, OP4, not_48_out, not_49_out);
  and and_9 (and_9_out, not_50_out, F13, not_51_out, not_52_out, not_53_out, not_54_out, not_55_out, not_56_out);
  and and_10 (and_10_out, not_57_out, F13, not_58_out, not_59_out, OP5, not_60_out, not_61_out, not_62_out);
  and and_11 (and_11_out, not_63_out, not_64_out, not_65_out, OP6, OP5, not_66_out, not_67_out, OP2);
  and and_12 (and_12_out, not_68_out, not_69_out, F12, not_70_out, OP5, not_71_out, not_72_out, not_73_out);
  and and_13 (and_13_out, F30, not_74_out, not_75_out, not_76_out, not_77_out, not_78_out, OP5, OP4, not_79_out, not_80_out);
  and and_14 (and_14_out, not_81_out, not_82_out, F14, F13, F12, not_83_out, OP5, OP4, not_84_out, not_85_out);
  and and_15 (and_15_out, not_86_out, not_87_out, not_88_out, F13, not_89_out, not_90_out, OP5, OP4, not_91_out, not_92_out);
  and and_16 (and_16_out, F14, F13, F12, not_93_out, not_94_out, OP4, not_95_out, not_96_out);
  and and_17 (and_17_out, not_97_out, F13, not_98_out, not_99_out, not_100_out, OP4, not_101_out, not_102_out);
  and and_18 (and_18_out, not_103_out, not_104_out, F14, not_105_out, F12, not_106_out, not_107_out, OP4, not_108_out, not_109_out);
  and and_19 (and_19_out, not_110_out, not_111_out, not_112_out, not_113_out, not_114_out, not_115_out, OP5, OP4, not_116_out, not_117_out);
  and and_20 (and_20_out, F30, not_118_out, not_119_out, not_120_out, not_121_out, not_122_out, OP5, OP4, not_123_out, not_124_out);
  and and_21 (and_21_out, not_125_out, not_126_out, F14, F13, F12, not_127_out, OP5, OP4, not_128_out, not_129_out);
  and and_22 (and_22_out, not_130_out, not_131_out, not_132_out, F13, F12, not_133_out, OP5, OP4, not_134_out, not_135_out);
  and and_23 (and_23_out, not_136_out, not_137_out, not_138_out, not_139_out, not_140_out, OP4, not_141_out, not_142_out);
  and and_24 (and_24_out, F14, F13, F12, not_143_out, not_144_out, OP4, not_145_out, not_146_out);
  and and_25 (and_25_out, not_147_out, F13, not_148_out, not_149_out, not_150_out, not_151_out, not_152_out, not_153_out);
  and and_26 (and_26_out, not_154_out, F13, not_155_out, not_156_out, OP5, not_157_out, not_158_out, not_159_out);
  and and_27 (and_27_out, not_160_out, not_161_out, not_162_out, OP6, OP5, not_163_out, not_164_out, OP2);
  and and_28 (and_28_out, not_165_out, not_166_out, F12, not_167_out, OP5, not_168_out, not_169_out, not_170_out);
  and and_29 (and_29_out, F14, F13, not_171_out, OP6, OP5, not_172_out, not_173_out, not_174_out);
  and and_30 (and_30_out, not_175_out, not_176_out, F14, F13, not_177_out, not_178_out, OP5, OP4, not_179_out, not_180_out);
  and and_31 (and_31_out, not_181_out, not_182_out, not_183_out, F13, not_184_out, not_185_out, OP5, OP4, not_186_out, not_187_out);
  and and_32 (and_32_out, not_188_out, not_189_out, not_190_out, F13, F12, not_191_out, OP5, OP4, not_192_out, not_193_out);
  and and_33 (and_33_out, F14, F13, not_194_out, not_195_out, not_196_out, OP4, not_197_out, not_198_out);
  and and_34 (and_34_out, F14, not_199_out, not_200_out, not_201_out, not_202_out, OP4, not_203_out, not_204_out);
  and and_35 (and_35_out, not_205_out, F13, not_206_out, not_207_out, not_208_out, OP4, not_209_out, not_210_out);
  and and_36 (and_36_out, F14, F13, not_211_out, OP6, OP5, not_212_out, not_213_out, not_214_out);
  or or_1 (S0, and_1_out, and_2_out, and_3_out, and_4_out, and_5_out, and_6_out, and_7_out, and_8_out, and_9_out, and_10_out, and_11_out, and_12_out);
  or or_2 (S1, and_13_out, and_14_out, and_15_out, and_16_out, and_17_out, and_18_out);
  or or_3 (S2, and_19_out, and_20_out, and_21_out, and_22_out, and_23_out, and_24_out, and_25_out, and_26_out, and_27_out, and_28_out, and_29_out);
  or or_4 (S3, and_30_out, and_31_out, and_32_out, and_33_out, and_34_out, and_35_out, and_36_out);
endmodule

// 控制信号生成
module \控制信号自动生成  (
  input  OP2,
  input  OP3,
  input  OP4,
  input  OP5,
  input  OP6,
  input  F12,
  input  F13,
  input  F14,
  input  F25,
  input  F30,
  output MemToReg,
  output MemWrite,
  output ALU_SRC,
  output RegWrite,
  output ecall,
  output S_Type,
  output BEQ,
  output BNE,
  output JALR,
  output JAL,
  output LUI,
  output SH,
  output BLTU,
  output rs1used,
  output rs2used,
  output csr
);

  wire and_2_out, and_3_out, and_4_out, and_5_out, and_6_out, and_7_out, and_8_out, and_9_out, and_10_out,
       and_11_out, and_12_out, and_13_out, and_14_out, and_15_out, and_16_out, and_17_out, and_18_out,
       and_19_out, and_20_out, and_21_out, and_23_out, and_24_out, and_32_out, and_33_out, and_34_out,
       and_35_out, and_36_out, and_37_out, and_38_out, and_39_out, and_40_out, and_41_out, and_42_out,
       and_43_out, and_44_out, and_45_out, and_46_out, and_47_out, and_48_out, and_49_out, and_50_out,
       and_51_out, and_52_out, and_53_out, not_1_out, not_2_out, not_3_out, not_4_out, not_5_out, not_6_out,
       not_7_out, not_8_out, not_9_out, not_10_out, not_11_out, not_12_out, not_13_out, not_14_out,
       not_15_out, not_16_out, not_17_out, not_18_out, not_19_out, not_20_out, not_21_out, not_22_out,
       not_23_out, not_24_out, not_25_out, not_26_out, not_27_out, not_28_out, not_29_out, not_30_out,
       not_31_out, not_32_out, not_33_out, not_34_out, not_35_out, not_36_out, not_37_out, not_38_out,
       not_39_out, not_40_out, not_41_out, not_42_out, not_43_out, not_44_out, not_45_out, not_46_out,
       not_47_out, not_48_out, not_49_out, not_50_out, not_51_out, not_52_out, not_53_out, not_54_out,
       not_55_out, not_56_out, not_57_out, not_58_out, not_59_out, not_60_out, not_61_out, not_62_out,
       not_63_out, not_64_out, not_65_out, not_66_out, not_67_out, not_68_out, not_69_out, not_70_out,
       not_71_out, not_72_out, not_73_out, not_74_out, not_75_out, not_76_out, not_77_out, not_78_out,
       not_79_out, not_80_out, not_81_out, not_82_out, not_83_out, not_84_out, not_85_out, not_86_out,
       not_87_out, not_88_out, not_89_out, not_90_out, not_91_out, not_92_out, not_93_out, not_94_out,
       not_95_out, not_96_out, not_97_out, not_98_out, not_99_out, not_100_out, not_101_out, not_102_out,
       not_103_out, not_104_out, not_105_out, not_106_out, not_107_out, not_108_out, not_109_out,
       not_110_out, not_111_out, not_112_out, not_113_out, not_114_out, not_115_out, not_116_out,
       not_117_out, not_118_out, not_119_out, not_120_out, not_121_out, not_122_out, not_123_out,
       not_124_out, not_125_out, not_126_out, not_127_out, not_128_out, not_129_out, not_130_out,
       not_131_out, not_132_out, not_133_out, not_134_out, not_135_out, not_136_out, not_137_out,
       not_138_out, not_139_out, not_140_out, not_141_out, not_142_out, not_143_out, not_144_out,
       not_145_out, not_146_out, not_147_out, not_148_out, not_149_out, not_150_out, not_151_out,
       not_152_out, not_153_out, not_154_out, not_155_out, not_156_out, not_157_out, not_158_out,
       not_159_out, not_160_out, not_161_out, not_162_out, not_163_out, not_164_out, not_165_out,
       not_166_out, not_167_out, not_168_out, not_169_out, not_170_out, not_171_out, not_172_out,
       not_173_out, not_174_out, not_175_out, not_176_out, not_177_out, not_178_out, not_179_out,
       not_180_out, not_181_out, not_182_out, not_183_out, not_184_out, not_185_out, not_186_out,
       not_187_out, not_188_out, not_189_out, not_190_out, not_191_out, not_192_out, not_193_out,
       not_194_out, not_195_out, not_196_out, not_197_out, not_198_out, not_199_out, not_200_out,
       not_201_out, not_202_out, not_203_out, not_204_out, not_205_out, not_206_out, not_207_out,
       not_208_out, not_209_out, not_210_out, not_211_out, not_212_out, not_213_out, not_214_out,
       not_215_out, not_216_out, not_217_out, not_218_out, not_219_out, not_220_out, not_221_out,
       not_222_out, not_223_out, not_224_out, not_225_out, not_226_out, not_227_out, not_228_out,
       not_229_out, not_230_out, not_231_out, not_232_out, not_233_out, not_234_out, not_235_out,
       not_236_out, not_237_out, not_238_out, not_239_out, not_240_out, not_241_out, not_242_out,
       not_243_out, not_244_out, not_245_out, not_246_out, not_247_out, not_248_out, not_249_out,
       not_250_out, not_251_out, not_252_out, not_253_out, not_254_out, not_255_out, not_256_out,
       not_257_out, not_258_out, not_259_out, not_260_out, not_261_out, not_262_out, not_263_out,
       not_264_out, not_265_out, not_266_out, not_267_out, not_268_out, not_269_out, not_270_out,
       not_271_out, not_272_out;

  not not_1 (not_1_out, OP2);
  not not_2 (not_2_out, OP3);
  not not_3 (not_3_out, OP4);
  not not_4 (not_4_out, OP5);
  not not_5 (not_5_out, OP6);
  not not_6 (not_6_out, F12);
  not not_7 (not_7_out, F14);
  not not_8 (not_8_out, OP2);
  not not_9 (not_9_out, OP3);
  not not_10 (not_10_out, OP4);
  not not_11 (not_11_out, OP6);
  not not_12 (not_12_out, F12);
  not not_13 (not_13_out, F14);
  not not_14 (not_14_out, OP2);
  not not_15 (not_15_out, OP3);
  not not_16 (not_16_out, OP4);
  not not_17 (not_17_out, OP6);
  not not_18 (not_18_out, F13);
  not not_19 (not_19_out, F14);
  not not_20 (not_20_out, OP2);
  not not_21 (not_21_out, OP3);
  not not_22 (not_22_out, OP4);
  not not_23 (not_23_out, OP6);
  not not_24 (not_24_out, F12);
  not not_25 (not_25_out, F14);
  not not_26 (not_26_out, OP2);
  not not_27 (not_27_out, OP3);
  not not_28 (not_28_out, OP4);
  not not_29 (not_29_out, OP6);
  not not_30 (not_30_out, F13);
  not not_31 (not_31_out, F14);
  not not_32 (not_32_out, OP2);
  not not_33 (not_33_out, OP3);
  not not_34 (not_34_out, OP5);
  not not_35 (not_35_out, OP6);
  not not_36 (not_36_out, F12);
  not not_37 (not_37_out, OP2);
  not not_38 (not_38_out, OP3);
  not not_39 (not_39_out, OP5);
  not not_40 (not_40_out, OP6);
  not not_41 (not_41_out, F13);
  not not_42 (not_42_out, F14);
  not not_43 (not_43_out, OP2);
  not not_44 (not_44_out, OP3);
  not not_45 (not_45_out, OP5);
  not not_46 (not_46_out, OP6);
  not not_47 (not_47_out, F13);
  not not_48 (not_48_out, F25);
  not not_49 (not_49_out, OP2);
  not not_50 (not_50_out, OP3);
  not not_51 (not_51_out, OP5);
  not not_52 (not_52_out, OP6);
  not not_53 (not_53_out, OP3);
  not not_54 (not_54_out, OP4);
  not not_55 (not_55_out, F12);
  not not_56 (not_56_out, F13);
  not not_57 (not_57_out, F14);
  not not_58 (not_58_out, OP2);
  not not_59 (not_59_out, OP3);
  not not_60 (not_60_out, OP5);
  not not_61 (not_61_out, OP6);
  not not_62 (not_62_out, F12);
  not not_63 (not_63_out, F14);
  not not_64 (not_64_out, OP2);
  not not_65 (not_65_out, OP3);
  not not_66 (not_66_out, OP5);
  not not_67 (not_67_out, OP6);
  not not_68 (not_68_out, F12);
  not not_69 (not_69_out, OP2);
  not not_70 (not_70_out, OP3);
  not not_71 (not_71_out, OP5);
  not not_72 (not_72_out, OP6);
  not not_73 (not_73_out, F13);
  not not_74 (not_74_out, F14);
  not not_75 (not_75_out, OP2);
  not not_76 (not_76_out, OP3);
  not not_77 (not_77_out, OP5);
  not not_78 (not_78_out, OP6);
  not not_79 (not_79_out, F13);
  not not_80 (not_80_out, F25);
  not not_81 (not_81_out, OP2);
  not not_82 (not_82_out, OP3);
  not not_83 (not_83_out, OP6);
  not not_84 (not_84_out, F12);
  not not_85 (not_85_out, F13);
  not not_86 (not_86_out, F14);
  not not_87 (not_87_out, F25);
  not not_88 (not_88_out, OP2);
  not not_89 (not_89_out, OP3);
  not not_90 (not_90_out, OP5);
  not not_91 (not_91_out, OP6);
  not not_92 (not_92_out, OP3);
  not not_93 (not_93_out, OP6);
  not not_94 (not_94_out, F14);
  not not_95 (not_95_out, F25);
  not not_96 (not_96_out, F30);
  not not_97 (not_97_out, OP3);
  not not_98 (not_98_out, OP6);
  not not_99 (not_99_out, F25);
  not not_100 (not_100_out, F30);
  not not_101 (not_101_out, OP4);
  not not_102 (not_102_out, F12);
  not not_103 (not_103_out, F13);
  not not_104 (not_104_out, F14);
  not not_105 (not_105_out, OP3);
  not not_106 (not_106_out, OP6);
  not not_107 (not_107_out, OP4);
  not not_108 (not_108_out, OP2);
  not not_109 (not_109_out, OP3);
  not not_110 (not_110_out, F12);
  not not_111 (not_111_out, F13);
  not not_112 (not_112_out, F14);
  not not_113 (not_113_out, F25);
  not not_114 (not_114_out, F30);
  not not_115 (not_115_out, OP2);
  not not_116 (not_116_out, OP3);
  not not_117 (not_117_out, OP4);
  not not_118 (not_118_out, OP6);
  not not_119 (not_119_out, F12);
  not not_120 (not_120_out, F14);
  not not_121 (not_121_out, OP2);
  not not_122 (not_122_out, OP3);
  not not_123 (not_123_out, OP4);
  not not_124 (not_124_out, OP6);
  not not_125 (not_125_out, F13);
  not not_126 (not_126_out, F14);
  not not_127 (not_127_out, OP2);
  not not_128 (not_128_out, OP3);
  not not_129 (not_129_out, OP4);
  not not_130 (not_130_out, F12);
  not not_131 (not_131_out, F13);
  not not_132 (not_132_out, F14);
  not not_133 (not_133_out, OP2);
  not not_134 (not_134_out, OP3);
  not not_135 (not_135_out, OP4);
  not not_136 (not_136_out, F13);
  not not_137 (not_137_out, F14);
  not not_138 (not_138_out, OP3);
  not not_139 (not_139_out, OP4);
  not not_140 (not_140_out, F12);
  not not_141 (not_141_out, F13);
  not not_142 (not_142_out, F14);
  not not_143 (not_143_out, OP4);
  not not_144 (not_144_out, OP3);
  not not_145 (not_145_out, OP6);
  not not_146 (not_146_out, OP2);
  not not_147 (not_147_out, OP3);
  not not_148 (not_148_out, OP4);
  not not_149 (not_149_out, OP6);
  not not_150 (not_150_out, F13);
  not not_151 (not_151_out, F14);
  not not_152 (not_152_out, OP2);
  not not_153 (not_153_out, OP3);
  not not_154 (not_154_out, OP4);
  not not_155 (not_155_out, F12);
  not not_156 (not_156_out, OP2);
  not not_157 (not_157_out, OP3);
  not not_158 (not_158_out, OP4);
  not not_159 (not_159_out, OP6);
  not not_160 (not_160_out, F12);
  not not_161 (not_161_out, F14);
  not not_162 (not_162_out, OP2);
  not not_163 (not_163_out, OP3);
  not not_164 (not_164_out, OP4);
  not not_165 (not_165_out, F13);
  not not_166 (not_166_out, F14);
  not not_167 (not_167_out, OP3);
  not not_168 (not_168_out, OP4);
  not not_169 (not_169_out, F12);
  not not_170 (not_170_out, F13);
  not not_171 (not_171_out, F14);
  not not_172 (not_172_out, OP2);
  not not_173 (not_173_out, OP3);
  not not_174 (not_174_out, OP4);
  not not_175 (not_175_out, F12);
  not not_176 (not_176_out, OP2);
  not not_177 (not_177_out, OP3);
  not not_178 (not_178_out, OP5);
  not not_179 (not_179_out, OP6);
  not not_180 (not_180_out, F12);
  not not_181 (not_181_out, OP2);
  not not_182 (not_182_out, OP3);
  not not_183 (not_183_out, OP5);
  not not_184 (not_184_out, OP6);
  not not_185 (not_185_out, F13);
  not not_186 (not_186_out, F14);
  not not_187 (not_187_out, OP2);
  not not_188 (not_188_out, OP3);
  not not_189 (not_189_out, OP5);
  not not_190 (not_190_out, OP6);
  not not_191 (not_191_out, F13);
  not not_192 (not_192_out, F25);
  not not_193 (not_193_out, OP2);
  not not_194 (not_194_out, OP3);
  not not_195 (not_195_out, OP6);
  not not_196 (not_196_out, F12);
  not not_197 (not_197_out, F13);
  not not_198 (not_198_out, F14);
  not not_199 (not_199_out, F25);
  not not_200 (not_200_out, OP2);
  not not_201 (not_201_out, OP3);
  not not_202 (not_202_out, OP6);
  not not_203 (not_203_out, F13);
  not not_204 (not_204_out, F14);
  not not_205 (not_205_out, F25);
  not not_206 (not_206_out, F30);
  not not_207 (not_207_out, OP2);
  not not_208 (not_208_out, OP3);
  not not_209 (not_209_out, OP5);
  not not_210 (not_210_out, OP6);
  not not_211 (not_211_out, OP2);
  not not_212 (not_212_out, OP3);
  not not_213 (not_213_out, F12);
  not not_214 (not_214_out, F13);
  not not_215 (not_215_out, F14);
  not not_216 (not_216_out, F25);
  not not_217 (not_217_out, F30);
  not not_218 (not_218_out, OP2);
  not not_219 (not_219_out, OP3);
  not not_220 (not_220_out, OP6);
  not not_221 (not_221_out, F25);
  not not_222 (not_222_out, F30);
  not not_223 (not_223_out, OP2);
  not not_224 (not_224_out, OP3);
  not not_225 (not_225_out, OP4);
  not not_226 (not_226_out, OP6);
  not not_227 (not_227_out, F12);
  not not_228 (not_228_out, F14);
  not not_229 (not_229_out, OP2);
  not not_230 (not_230_out, OP3);
  not not_231 (not_231_out, OP4);
  not not_232 (not_232_out, F13);
  not not_233 (not_233_out, F14);
  not not_234 (not_234_out, OP2);
  not not_235 (not_235_out, OP3);
  not not_236 (not_236_out, OP4);
  not not_237 (not_237_out, F13);
  not not_238 (not_238_out, F14);
  not not_239 (not_239_out, OP2);
  not not_240 (not_240_out, OP3);
  not not_241 (not_241_out, OP4);
  not not_242 (not_242_out, F12);
  not not_243 (not_243_out, OP2);
  not not_244 (not_244_out, OP3);
  not not_245 (not_245_out, OP6);
  not not_246 (not_246_out, F12);
  not not_247 (not_247_out, F13);
  not not_248 (not_248_out, F14);
  not not_249 (not_249_out, F25);
  not not_250 (not_250_out, OP2);
  not not_251 (not_251_out, OP3);
  not not_252 (not_252_out, OP6);
  not not_253 (not_253_out, F14);
  not not_254 (not_254_out, F25);
  not not_255 (not_255_out, F30);
  not not_256 (not_256_out, OP2);
  not not_257 (not_257_out, OP3);
  not not_258 (not_258_out, F12);
  not not_259 (not_259_out, F13);
  not not_260 (not_260_out, F14);
  not not_261 (not_261_out, F25);
  not not_262 (not_262_out, F30);
  not not_263 (not_263_out, OP2);
  not not_264 (not_264_out, OP3);
  not not_265 (not_265_out, OP6);
  not not_266 (not_266_out, F25);
  not not_267 (not_267_out, F30);
  not not_268 (not_268_out, F12);
  not not_269 (not_269_out, OP3);
  not not_270 (not_270_out, OP2);
  not not_271 (not_271_out, OP3);
  not not_272 (not_272_out, OP2);
  and and_1 (MemToReg, not_1_out, not_2_out, not_3_out, not_4_out, not_5_out, not_6_out, F13, not_7_out);
  and and_2 (and_2_out, not_8_out, not_9_out, not_10_out, OP5, not_11_out, not_12_out, F13, not_13_out);
  and and_3 (and_3_out, not_14_out, not_15_out, not_16_out, OP5, not_17_out, F12, not_18_out, not_19_out);
  and and_4 (and_4_out, not_20_out, not_21_out, not_22_out, not_23_out, not_24_out, F13, not_25_out);
  and and_5 (and_5_out, not_26_out, not_27_out, not_28_out, OP5, not_29_out, F12, not_30_out, not_31_out);
  and and_6 (and_6_out, not_32_out, not_33_out, OP4, not_34_out, not_35_out, not_36_out);
  and and_7 (and_7_out, not_37_out, not_38_out, OP4, not_39_out, not_40_out, not_41_out, not_42_out);
  and and_8 (and_8_out, not_43_out, not_44_out, OP4, not_45_out, not_46_out, not_47_out, not_48_out);
  and and_9 (and_9_out, not_49_out, not_50_out, OP4, not_51_out, not_52_out, F13, F14);
  and and_10 (and_10_out, OP2, not_53_out, not_54_out, OP5, OP6, not_55_out, not_56_out, not_57_out);
  and and_11 (and_11_out, not_58_out, not_59_out, not_60_out, not_61_out, not_62_out, F13, not_63_out);
  and and_12 (and_12_out, not_64_out, not_65_out, OP4, not_66_out, not_67_out, not_68_out);
  and and_13 (and_13_out, not_69_out, not_70_out, OP4, not_71_out, not_72_out, not_73_out, not_74_out);
  and and_14 (and_14_out, not_75_out, not_76_out, OP4, not_77_out, not_78_out, not_79_out, not_80_out);
  and and_15 (and_15_out, not_81_out, not_82_out, OP4, not_83_out, not_84_out, not_85_out, not_86_out, not_87_out);
  and and_16 (and_16_out, not_88_out, not_89_out, OP4, not_90_out, not_91_out, F13, F14);
  and and_17 (and_17_out, not_92_out, OP4, OP5, not_93_out, not_94_out, not_95_out, not_96_out);
  and and_18 (and_18_out, not_97_out, OP4, OP5, not_98_out, F13, not_99_out, not_100_out);
  and and_19 (and_19_out, OP2, not_101_out, OP5, OP6, not_102_out, not_103_out, not_104_out);
  and and_20 (and_20_out, OP2, not_105_out, OP4, OP5, not_106_out);
  and and_21 (and_21_out, OP2, OP3, not_107_out, OP5, OP6);
  and and_22 (ecall, not_108_out, not_109_out, OP4, OP5, OP6, not_110_out, not_111_out, not_112_out, not_113_out, not_114_out);
  and and_23 (and_23_out, not_115_out, not_116_out, not_117_out, OP5, not_118_out, not_119_out, F13, not_120_out);
  and and_24 (and_24_out, not_121_out, not_122_out, not_123_out, OP5, not_124_out, F12, not_125_out, not_126_out);
  and and_25 (BEQ, not_127_out, not_128_out, not_129_out, OP5, OP6, not_130_out, not_131_out, not_132_out);
  and and_26 (BNE, not_133_out, not_134_out, not_135_out, OP5, OP6, F12, not_136_out, not_137_out);
  and and_27 (JALR, OP2, not_138_out, not_139_out, OP5, OP6, not_140_out, not_141_out, not_142_out);
  and and_28 (JAL, OP2, OP3, not_143_out, OP5, OP6);
  and and_29 (LUI, OP2, not_144_out, OP4, OP5, not_145_out);
  and and_30 (SH, not_146_out, not_147_out, not_148_out, OP5, not_149_out, F12, not_150_out, not_151_out);
  and and_31 (BLTU, not_152_out, not_153_out, not_154_out, OP5, OP6, not_155_out, F13, F14);
  and and_32 (and_32_out, not_156_out, not_157_out, not_158_out, not_159_out, not_160_out, F13, not_161_out);
  and and_33 (and_33_out, not_162_out, not_163_out, not_164_out, OP5, F12, not_165_out, not_166_out);
  and and_34 (and_34_out, not_167_out, not_168_out, OP5, OP6, not_169_out, not_170_out, not_171_out);
  and and_35 (and_35_out, not_172_out, not_173_out, not_174_out, OP5, OP6, not_175_out, F13, F14);
  and and_36 (and_36_out, not_176_out, not_177_out, OP4, not_178_out, not_179_out, not_180_out);
  and and_37 (and_37_out, not_181_out, not_182_out, OP4, not_183_out, not_184_out, not_185_out, not_186_out);
  and and_38 (and_38_out, not_187_out, not_188_out, OP4, not_189_out, not_190_out, not_191_out, not_192_out);
  and and_39 (and_39_out, not_193_out, not_194_out, OP4, not_195_out, not_196_out, not_197_out, not_198_out, not_199_out);
  and and_40 (and_40_out, not_200_out, not_201_out, OP4, not_202_out, not_203_out, not_204_out, not_205_out, not_206_out);
  and and_41 (and_41_out, not_207_out, not_208_out, OP4, not_209_out, not_210_out, F13, F14);
  and and_42 (and_42_out, not_211_out, not_212_out, OP4, OP5, not_213_out, not_214_out, not_215_out, not_216_out, not_217_out);
  and and_43 (and_43_out, not_218_out, not_219_out, OP4, OP5, not_220_out, F13, not_221_out, not_222_out);
  and and_44 (and_44_out, not_223_out, not_224_out, not_225_out, OP5, not_226_out, not_227_out, F13, not_228_out);
  and and_45 (and_45_out, not_229_out, not_230_out, not_231_out, OP5, F12, not_232_out, not_233_out);
  and and_46 (and_46_out, not_234_out, not_235_out, not_236_out, OP5, OP6, not_237_out, not_238_out);
  and and_47 (and_47_out, not_239_out, not_240_out, not_241_out, OP5, OP6, not_242_out, F13, F14);
  and and_48 (and_48_out, not_243_out, not_244_out, OP4, OP5, not_245_out, not_246_out, not_247_out, not_248_out, not_249_out);
  and and_49 (and_49_out, not_250_out, not_251_out, OP4, OP5, not_252_out, not_253_out, not_254_out, not_255_out);
  and and_50 (and_50_out, not_256_out, not_257_out, OP4, OP5, not_258_out, not_259_out, not_260_out, not_261_out, not_262_out);
  and and_51 (and_51_out, not_263_out, not_264_out, OP4, OP5, not_265_out, F13, not_266_out, not_267_out);
  and and_52 (and_52_out, F14, F13, not_268_out, OP6, OP5, OP4, not_269_out, not_270_out);
  and and_53 (and_53_out, F14, F13, F12, OP6, OP5, OP4, not_271_out, not_272_out);
  or or_1 (MemWrite, and_2_out, and_3_out);
  or or_2 (ALU_SRC, and_4_out, and_5_out, and_6_out, and_7_out, and_8_out, and_9_out, and_10_out);
  or or_3 (S_Type, and_23_out, and_24_out);
  or or_4 (csr, and_52_out, and_53_out);
  or or_5 (RegWrite, and_11_out, and_12_out, and_13_out, and_14_out, and_15_out, and_16_out, and_17_out, and_18_out, and_19_out, and_20_out, and_21_out);
  or or_6 (rs1used, and_32_out, and_33_out, and_34_out, and_35_out, and_36_out, and_37_out, and_38_out, and_39_out, and_40_out, and_41_out, and_42_out, and_43_out);
  or or_7 (rs2used, and_44_out, and_45_out, and_46_out, and_47_out, and_48_out, and_49_out, and_50_out, and_51_out);
endmodule

// ALU
module ALU (
  input  [31:0] X,
  input  [31:0] Y,
  input  [3:0] AluOP,
  output out_4,
  output Equal,
  output out_6,
  output [31:0] Result,
  output [31:0] Result_2
);

  wire [0:0] comparator_1_lt, comparator_2_lt;
  wire [31:0] adder_1_out, AND_out, divider_1_out, divider_1_rem, multiplier_1_cout, multiplier_1_out,
       NOR_out, OR_out, shifter_1_out, shifter_2_out, shifter_3_out, subtractor_1_out, XOR_out;

  assign AND_out = X & Y;  // AND_Gate AND, 32 bits wide
  assign OR_out = X | Y;  // OR_Gate OR, 32 bits wide
  Shifter #(.width(32), .shift("ll")) shifter_1 (.in(X), .\dist (Y[4:0]), .out(shifter_1_out));
  Shifter #(.width(32), .shift("ar")) shifter_2 (.in(X), .\dist (Y[4:0]), .out(shifter_2_out));
  Shifter #(.width(32), .shift("lr")) shifter_3 (.in(X), .\dist (Y[4:0]), .out(shifter_3_out));
  Multiplier #(.width(32)) multiplier_1 (.a(X), .b(Y), .out(multiplier_1_out), .cout(multiplier_1_cout));  // open: cin
  Divider #(.width(32)) divider_1 (.a(X), .b(Y), .out(divider_1_out), .rem(divider_1_rem));  // open: upper
  Adder #(.width(32)) adder_1 (.a(X), .b(Y), .out(adder_1_out));  // open: cin, cout
  Subtractor #(.width(32)) subtractor_1 (.a(X), .b(Y), .out(subtractor_1_out));  // open: bin, bout
  assign XOR_out = X ^ Y;  // XOR_Gate XOR, 32 bits wide
  assign NOR_out = ~(X | Y);  // NOR_Gate NOR, 32 bits wide
  Comparator #(.width(32), .mode("twosComplement")) comparator_1 (
    .a(X), .b(Y), .eq(Equal), .lt(comparator_1_lt[0]));  // open: gt
  Comparator #(.width(32), .mode("unsigned")) comparator_2 (.a(X), .b(Y), .lt(comparator_2_lt[0]));  // open: gt, eq
  Multiplexer #(.select(4), .width(32), .disabled("Z"), .enable("false")) multiplexer_1 (
    .in0(shifter_1_out), .in1(shifter_2_out), .in2(shifter_3_out), .in3(multiplier_1_out),
    .in4(divider_1_out), .in5(adder_1_out), .in6(subtractor_1_out), .in7(AND_out), .in8(OR_out),
    .in9(XOR_out), .in10(NOR_out), .in11({{31{1'b0}}, comparator_1_lt[0]}),
    .in12({{31{1'b0}}, comparator_2_lt[0]}), .in13({32{1'b0}}), .in14({32{1'b0}}), .in15({32{1'b0}}),
    .out(Result), .sel(AluOP));
  Multiplexer #(.select(4), .width(32), .disabled("Z"), .enable("false")) multiplexer_2 (
    .in0({32{1'b0}}), .in1({32{1'b0}}), .in2({32{1'b0}}), .in3(multiplier_1_cout), .in4(divider_1_rem),
    .in5({32{1'b0}}), .in6({32{1'b0}}), .in7({32{1'b0}}), .in8({32{1'b0}}), .in9({32{1'b0}}),
    .in10({32{1'b0}}), .in11({32{1'b0}}), .in12({32{1'b0}}), .in13({32{1'b0}}), .in14({32{1'b0}}),
    .in15({32{1'b0}}), .out(Result_2), .sel(AluOP));
  Multiplexer #(.select(4), .width(1), .disabled("Z"), .enable("false")) multiplexer_3 (
    .in0(1'b0), .in1(1'b0), .in2(1'b0), .in3(1'b0), .in4(1'b0), .in5(1'b0), .in6(1'b0), .in7(1'b0),
    .in8(1'b0), .in9(1'b0), .in10(1'b0), .in11(comparator_1_lt[0]), .in12(comparator_2_lt[0]), .in13(1'b0),
    .in14(1'b0), .in15(1'b0), .out(out_6), .sel(AluOP));
  not not_1 (out_4, out_6);

  // Other names for the same wires on the sheet: Result2[31:0] = Result_2; S[3:0] = AluOP; tunnel = out_6;
  //   tunnel_t = out_4

  // Notes on the sheet:
  //   不要改变此引脚区域内容，也不要改变ALU封装形式
  //   输入引脚
  //   有符号比较
  //   无符号比较
  //   输出引脚
endmodule

module Regifile (
  input  [31:0] Din,
  input  Clk,
  input  WE,
  input  [4:0] R1_num,
  input  [4:0] W_num,
  input  [4:0] R2_num,
  output [31:0] R1,
  output [31:0] R2
);

  // RegisterFile registerfile_1: pin names not known; wires that end beside it: Din, Clk, WE, W_num, R1_num, R2_num, R1, R2
endmodule

module IF_ID (
  input  clr,
  input  rst,
  input  en,
  input  clk,
  input  [31:0] IR,
  input  [31:0] PC,
  input  PredictJump,
  output [31:0] IR_2,
  output [31:0] PC_2,
  output PredictJump_2
);

  wire and_3_out, not_1_out;
  wire [31:0] and_1_out, and_2_out, bit_extender_1_out;

  not not_1 (not_1_out, clr);
  assign bit_extender_1_out = {{31{not_1_out}}, not_1_out};  // Bit_Extender bit_extender_1
  assign and_1_out = bit_extender_1_out & IR;  // AND_Gate and_1, 32 bits wide
  assign and_2_out = bit_extender_1_out & PC;  // AND_Gate and_2, 32 bits wide
  and and_3 (and_3_out, not_1_out, PredictJump);
  Register #(.width(32), .trigger("rising"), .Select("low")) register_1 (
    .D(and_1_out), .en(en), .Q(IR_2), .clk(clk), .clr(rst));
  Register #(.width(32), .trigger("rising"), .Select("low")) register_2 (
    .D(and_2_out), .en(en), .Q(PC_2), .clk(clk), .clr(rst));
  Register #(.width(1), .trigger("rising"), .Select("low")) register_3 (
    .D(and_3_out), .en(en), .Q(PredictJump_2), .clk(clk), .clr(rst));
endmodule

module ID_EX (
  input  clr,
  input  rst,
  input  en,
  input  clk,
  input  Beq,
  input  Bne,
  input  MemToReg,
  input  MemWrite,
  input  [3:0] AluOP,
  input  AluSrcB,
  input  RegWrite,
  input  Ecall,
  input  JAL,
  input  JALR,
  input  Lui,
  input  Sh,
  input  Bltu,
  input  [31:0] rs1,
  input  [31:0] rs2,
  input  [31:0] imm_IS,
  input  [31:0] imm_B,
  input  [31:0] imm_J,
  input  [31:0] imm_U,
  input  [4:0] rd,
  input  [31:0] IR,
  input  [31:0] PC,
  input  [1:0] rs1Fwd,
  input  [1:0] rs2Fwd,
  input  uret,
  input  PredictJump,
  output Beq_2,
  output Bne_2,
  output MemToReg_2,
  output MemWrite_2,
  output [3:0] AluOP_2,
  output AluSrcB_2,
  output RegWrite_2,
  output Ecall_2,
  output JAL_2,
  output JALR_2,
  output Lui_2,
  output Sh_2,
  output Bltu_2,
  output [31:0] rs1_2,
  output [31:0] rs2_2,
  output [31:0] imm_IS_2,
  output [31:0] imm_B_2,
  output [31:0] imm_J_2,
  output [31:0] imm_U_2,
  output [4:0] rd_2,
  output [31:0] IR_2,
  output [31:0] PC_2,
  output [1:0] rs1Fwd_2,
  output [1:0] rs2Fwd_2,
  output uret_2,
  output PredictJump_2
);

  wire and_1_out, and_2_out, and_3_out, and_4_out, and_5_out, and_6_out, and_7_out, and_8_out, and_9_out,
       and_10_out, and_11_out, and_12_out, and_25_out, and_26_out, not_1_out;
  wire [1:0] and_23_out, and_24_out, bit_extender_4_out, bit_extender_5_out;
  wire [3:0] and_13_out, bit_extender_1_out;
  wire [4:0] and_20_out, bit_extender_3_out;
  wire [31:0] and_14_out, and_15_out, and_16_out, and_17_out, and_18_out, and_19_out, and_21_out, and_22_out,
       bit_extender_2_out;

  not not_1 (not_1_out, clr);
  and and_1 (and_1_out, not_1_out, Beq);
  and and_2 (and_2_out, not_1_out, Bne);
  and and_3 (and_3_out, not_1_out, MemToReg);
  and and_4 (and_4_out, not_1_out, MemWrite);
  assign bit_extender_1_out = {{3{not_1_out}}, not_1_out};  // Bit_Extender bit_extender_1
  and and_5 (and_5_out, not_1_out, AluSrcB);
  and and_6 (and_6_out, not_1_out, RegWrite);
  and and_7 (and_7_out, not_1_out, Ecall);
  and and_8 (and_8_out, not_1_out, JAL);
  and and_9 (and_9_out, not_1_out, JALR);
  and and_10 (and_10_out, not_1_out, Lui);
  and and_11 (and_11_out, not_1_out, Sh);
  and and_12 (and_12_out, not_1_out, Bltu);
  assign and_13_out = bit_extender_1_out & AluOP;  // AND_Gate and_13, 4 bits wide
  assign bit_extender_2_out = {{31{not_1_out}}, not_1_out};  // Bit_Extender bit_extender_2
  assign bit_extender_3_out = {{4{not_1_out}}, not_1_out};  // Bit_Extender bit_extender_3
  assign bit_extender_4_out = {{1{not_1_out}}, not_1_out};  // Bit_Extender bit_extender_4
  assign bit_extender_5_out = {{1{not_1_out}}, not_1_out};  // Bit_Extender bit_extender_5
  assign and_14_out = bit_extender_2_out & rs1;  // AND_Gate and_14, 32 bits wide
  assign and_15_out = bit_extender_2_out & rs2;  // AND_Gate and_15, 32 bits wide
  assign and_16_out = bit_extender_2_out & imm_IS;  // AND_Gate and_16, 32 bits wide
  assign and_17_out = bit_extender_2_out & imm_B;  // AND_Gate and_17, 32 bits wide
  assign and_18_out = bit_extender_2_out & imm_J;  // AND_Gate and_18, 32 bits wide
  assign and_19_out = bit_extender_2_out & imm_U;  // AND_Gate and_19, 32 bits wide
  assign and_20_out = bit_extender_3_out & rd;  // AND_Gate and_20, 5 bits wide
  assign and_21_out = bit_extender_2_out & IR;  // AND_Gate and_21, 32 bits wide
  assign and_22_out = bit_extender_2_out & PC;  // AND_Gate and_22, 32 bits wide
  assign and_23_out = bit_extender_4_out & rs1Fwd;  // AND_Gate and_23, 2 bits wide
  assign and_24_out = bit_extender_5_out & rs2Fwd;  // AND_Gate and_24, 2 bits wide
  and and_25 (and_25_out, not_1_out, uret);
  and and_26 (and_26_out, not_1_out, PredictJump);
  Register #(.width(1), .trigger("rising"), .Select("low")) register_1 (
    .D(and_1_out), .en(en), .Q(Beq_2), .clk(clk), .clr(rst));
  Register #(.width(1), .trigger("rising"), .Select("low")) register_2 (
    .D(and_2_out), .en(en), .Q(Bne_2), .clk(clk), .clr(rst));
  Register #(.width(1), .trigger("rising"), .Select("low")) register_3 (
    .D(and_3_out), .en(en), .Q(MemToReg_2), .clk(clk), .clr(rst));
  Register #(.width(1), .trigger("rising"), .Select("low")) register_4 (
    .D(and_4_out), .en(en), .Q(MemWrite_2), .clk(clk), .clr(rst));
  Register #(.width(4), .trigger("rising"), .Select("low")) register_5 (
    .D(and_13_out), .en(en), .Q(AluOP_2), .clk(clk), .clr(rst));
  Register #(.width(1), .trigger("rising"), .Select("low")) register_6 (
    .D(and_5_out), .en(en), .Q(AluSrcB_2), .clk(clk), .clr(rst));
  Register #(.width(1), .trigger("rising"), .Select("low")) register_7 (
    .D(and_6_out), .en(en), .Q(RegWrite_2), .clk(clk), .clr(rst));
  Register #(.width(1), .trigger("rising"), .Select("low")) register_8 (
    .D(and_7_out), .en(en), .Q(Ecall_2), .clk(clk), .clr(rst));
  Register #(.width(1), .trigger("rising"), .Select("low")) register_9 (
    .D(and_8_out), .en(en), .Q(JAL_2), .clk(clk), .clr(rst));
  Register #(.width(1), .trigger("rising"), .Select("low")) register_10 (
    .D(and_9_out), .en(en), .Q(JALR_2), .clk(clk), .clr(rst));
  Register #(.width(1), .trigger("rising"), .Select("low")) register_11 (
    .D(and_10_out), .en(en), .Q(Lui_2), .clk(clk), .clr(rst));
  Register #(.width(1), .trigger("rising"), .Select("low")) register_12 (
    .D(and_11_out), .en(en), .Q(Sh_2), .clk(clk), .clr(rst));
  Register #(.width(1), .trigger("rising"), .Select("low")) register_13 (
    .D(and_12_out), .en(en), .Q(Bltu_2), .clk(clk), .clr(rst));
  Register #(.width(32), .trigger("rising"), .Select("low")) register_14 (
    .D(and_14_out), .en(en), .Q(rs1_2), .clk(clk), .clr(rst));
  Register #(.width(32), .trigger("rising"), .Select("low")) register_15 (
    .D(and_15_out), .en(en), .Q(rs2_2), .clk(clk), .clr(rst));
  Register #(.width(32), .trigger("rising"), .Select("low")) register_16 (
    .D(and_16_out), .en(en), .Q(imm_IS_2), .clk(clk), .clr(rst));
  Register #(.width(32), .trigger("rising"), .Select("low")) register_17 (
    .D(and_17_out), .en(en), .Q(imm_B_2), .clk(clk), .clr(rst));
  Register #(.width(32), .trigger("rising"), .Select("low")) register_18 (
    .D(and_18_out), .en(en), .Q(imm_J_2), .clk(clk), .clr(rst));
  Register #(.width(32), .trigger("rising"), .Select("low")) register_19 (
    .D(and_19_out), .en(en), .Q(imm_U_2), .clk(clk), .clr(rst));
  Register #(.width(5), .trigger("rising"), .Select("low")) register_20 (
    .D(and_20_out), .en(en), .Q(rd_2), .clk(clk), .clr(rst));
  Register #(.width(32), .trigger("rising"), .Select("low")) register_21 (
    .D(and_21_out), .en(en), .Q(IR_2), .clk(clk), .clr(rst));
  Register #(.width(32), .trigger("rising"), .Select("low")) register_22 (
    .D(and_22_out), .en(en), .Q(PC_2), .clk(clk), .clr(rst));
  Register #(.width(2), .trigger("rising"), .Select("low")) register_23 (
    .D(and_23_out), .en(en), .Q(rs1Fwd_2), .clk(clk), .clr(rst));
  Register #(.width(2), .trigger("rising"), .Select("low")) register_24 (
    .D(and_24_out), .en(en), .Q(rs2Fwd_2), .clk(clk), .clr(rst));
  Register #(.width(1), .trigger("rising"), .Select("low")) register_25 (
    .D(and_25_out), .en(en), .Q(uret_2), .clk(clk), .clr(rst));
  Register #(.width(1), .trigger("rising"), .Select("low")) register_26 (
    .D(and_26_out), .en(en), .Q(PredictJump_2), .clk(clk), .clr(rst));
endmodule

module EX_MEM (
  input  rst,
  input  en,
  input  clk,
  input  MemToReg,
  input  MemWrite,
  input  RegWrite,
  input  JAL,
  input  JALR,
  input  Lui,
  input  Sh,
  input  [31:0] ALUResult,
  input  [31:0] rs2,
  input  [31:0] imm_U,
  input  halt,
  input  [4:0] rd,
  input  [31:0] IR,
  input  [31:0] PC,
  output MemToReg_2,
  output MemWrite_2,
  output RegWrite_2,
  output JAL_2,
  output JALR_2,
  output Lui_2,
  output Sh_2,
  output [31:0] ALUResult_2,
  output [31:0] rs2_2,
  output [31:0] imm_U_2,
  output halt_2,
  output [4:0] rd_2,
  output [31:0] IR_2,
  output [31:0] PC_2
);

  Register #(.width(1), .trigger("rising"), .Select("low")) register_1 (
    .D(MemToReg), .en(en), .Q(MemToReg_2), .clk(clk), .clr(rst));
  Register #(.width(1), .trigger("rising"), .Select("low")) register_2 (
    .D(MemWrite), .en(en), .Q(MemWrite_2), .clk(clk), .clr(rst));
  Register #(.width(1), .trigger("rising"), .Select("low")) register_3 (
    .D(RegWrite), .en(en), .Q(RegWrite_2), .clk(clk), .clr(rst));
  Register #(.width(1), .trigger("rising"), .Select("low")) register_4 (
    .D(JAL), .en(en), .Q(JAL_2), .clk(clk), .clr(rst));
  Register #(.width(1), .trigger("rising"), .Select("low")) register_5 (
    .D(JALR), .en(en), .Q(JALR_2), .clk(clk), .clr(rst));
  Register #(.width(1), .trigger("rising"), .Select("low")) register_6 (
    .D(Lui), .en(en), .Q(Lui_2), .clk(clk), .clr(rst));
  Register #(.width(1), .trigger("rising"), .Select("low")) register_7 (
    .D(Sh), .en(en), .Q(Sh_2), .clk(clk), .clr(rst));
  Register #(.width(32), .trigger("rising"), .Select("low")) register_8 (
    .D(ALUResult), .en(en), .Q(ALUResult_2), .clk(clk), .clr(rst));
  Register #(.width(32), .trigger("rising"), .Select("low")) register_9 (
    .D(rs2), .en(en), .Q(rs2_2), .clk(clk), .clr(rst));
  Register #(.width(32), .trigger("rising"), .Select("low")) register_10 (
    .D(imm_U), .en(en), .Q(imm_U_2), .clk(clk), .clr(rst));
  Register #(.width(1), .trigger("rising"), .Select("low")) register_11 (
    .D(halt), .en(en), .Q(halt_2), .clk(clk), .clr(rst));
  Register #(.width(5), .trigger("rising"), .Select("low")) register_12 (
    .D(rd), .en(en), .Q(rd_2), .clk(clk), .clr(rst));
  Register #(.width(32), .trigger("rising"), .Select("low")) register_13 (
    .D(IR), .en(en), .Q(IR_2), .clk(clk), .clr(rst));
  Register #(.width(32), .trigger("rising"), .Select("low")) register_14 (
    .D(PC), .en(en), .Q(PC_2), .clk(clk), .clr(rst));
endmodule

module MEM_WB (
  input  rst,
  input  en,
  input  clk,
  input  MemToReg,
  input  RegWrite,
  input  JAL,
  input  JALR,
  input  Lui,
  input  [31:0] ALUResult,
  input  [31:0] ReadData,
  input  [31:0] imm_U,
  input  halt,
  input  [4:0] rd,
  input  [31:0] IR,
  input  [31:0] PC,
  output MemToReg_2,
  output RegWrite_2,
  output JAL_2,
  output JALR_2,
  output Lui_2,
  output [31:0] ALUResult_2,
  output [31:0] ReadData_2,
  output [31:0] imm_U_2,
  output halt_2,
  output [4:0] rd_2,
  output [31:0] IR_2,
  output [31:0] PC_2
);

  Register #(.width(1), .trigger("rising"), .Select("low")) register_1 (
    .D(MemToReg), .en(en), .Q(MemToReg_2), .clk(clk), .clr(rst));
  Register #(.width(1), .trigger("rising"), .Select("low")) register_2 (
    .D(RegWrite), .en(en), .Q(RegWrite_2), .clk(clk), .clr(rst));
  Register #(.width(1), .trigger("rising"), .Select("low")) register_3 (
    .D(JAL), .en(en), .Q(JAL_2), .clk(clk), .clr(rst));
  Register #(.width(1), .trigger("rising"), .Select("low")) register_4 (
    .D(JALR), .en(en), .Q(JALR_2), .clk(clk), .clr(rst));
  Register #(.width(1), .trigger("rising"), .Select("low")) register_5 (
    .D(Lui), .en(en), .Q(Lui_2), .clk(clk), .clr(rst));
  Register #(.width(32), .trigger("rising"), .Select("low")) register_6 (
    .D(ALUResult), .en(en), .Q(ALUResult_2), .clk(clk), .clr(rst));
  Register #(.width(32), .trigger("rising"), .Select("low")) register_7 (
    .D(ReadData), .en(en), .Q(ReadData_2), .clk(clk), .clr(rst));
  Register #(.width(32), .trigger("rising"), .Select("low")) register_8 (
    .D(imm_U), .en(en), .Q(imm_U_2), .clk(clk), .clr(rst));
  Register #(.width(1), .trigger("rising"), .Select("low")) register_9 (
    .D(halt), .en(en), .Q(halt_2), .clk(clk), .clr(rst));
  Register #(.width(5), .trigger("rising"), .Select("low")) register_10 (
    .D(rd), .en(en), .Q(rd_2), .clk(clk), .clr(rst));
  Register #(.width(32), .trigger("rising"), .Select("low")) register_11 (
    .D(IR), .en(en), .Q(IR_2), .clk(clk), .clr(rst));
  Register #(.width(32), .trigger("rising"), .Select("low")) register_12 (
    .D(PC), .en(en), .Q(PC_2), .clk(clk), .clr(rst));
endmodule

module \理想流水线  (
  output RegWrite,
  output MemWrite,
  output [31:0] IF_PC,
  output [31:0] ID_PC,
  output [31:0] EX_PC,
  output [31:0] M_PC,
  output [31:0] WB_PC,
  output [31:0] RDin,
  output [31:0] MDin,
  output [31:0] LedData
);

  wire and_1_out, and_2_out, and_3_out, and_4_out, and_5_out, Beq, Bltu, Bne, CLK, clock_1_out,
       comparator_1_eq, comparator_1_lt, comparator_2_eq, d_ff_1_q, ecall_EX, ecall_ID, equ, ex_mem_1_halt_2,
       ex_mem_1_jal_2, ex_mem_1_jalr_2, ex_mem_1_lui_2, ex_mem_1_memtoreg_2, ex_mem_1_regwrite_2,
       ex_mem_1_sh_2, Go, halt, id_ex_1_alusrcb_2, id_ex_1_lui_2, id_ex_1_memtoreg_2, id_ex_1_memwrite_2,
       id_ex_1_regwrite_2, id_ex_1_sh_2, IR1, IR2, IR3, JAL, JALR, less, mem_wb_1_jal_2, mem_wb_1_jalr_2,
       mem_wb_1_lui_2, mem_wb_1_memtoreg_2, nand_1_out, not_1_out, not_2_out, not_3_out, not_4_out,
       not_5_out, or_1_out, or_2_out, or_3_out, or_4_out, or_5_out, RST, S_type, W1, W2, W3,
       \单周期硬布线控制器_1_alu_src , \单周期硬布线控制器_1_beq , \单周期硬布线控制器_1_bltu , \单周期硬布线控制器_1_bne , \单周期硬布线控制器_1_jal ,
       \单周期硬布线控制器_1_jalr , \单周期硬布线控制器_1_lui , \单周期硬布线控制器_1_memtoreg , \单周期硬布线控制器_1_memwrite ,
       \单周期硬布线控制器_1_regwrite , \单周期硬布线控制器_1_sh ;
  wire [1:0] priority_encoder_1_out;
  wire [3:0] id_ex_1_aluop_2, \单周期硬布线控制器_1_alu_op ;
  wire [4:0] ex_mem_1_rd_2, id_ex_1_rd_2, multiplexer_3_out, multiplexer_4_out, rd;
  wire [11:0] multiplexer_2_out;
  wire [12:0] CNT_num;
  wire [15:0] \LoadUse次数 , \总周期数 , \插入气泡数 , \无条件分支数 , \条件分支成功数 ;
  wire [31:0] adder_1_out, adder_2_out, adder_3_out, adder_5_out, ALUResult_EX, ALUResult_MEM, and_6_out,
       and_7_out, bit_extender_1_out, bit_extender_2_out, bit_extender_3_out, bit_extender_4_out, EX_IR,
       ex_mem_1_imm_u_2, ex_mem_1_rs2_2, id_ex_1_imm_b_2, id_ex_1_imm_is_2, id_ex_1_imm_j_2, id_ex_1_imm_u_2,
       id_ex_1_rs1_2, id_ex_1_rs2_2, ID_IR, IF_IR, MEM_IR, mem_wb_1_aluresult_2, mem_wb_1_imm_u_2,
       mem_wb_1_readdata_2, multiplexer_1_out, multiplexer_5_out, multiplexer_7_out, multiplexer_8_out,
       multiplexer_9_out, multiplexer_10_out, ram_1_data, regifile_1_r1, regifile_1_r2, ShDin, shifter_1_out,
       shifter_2_out, shifter_3_out, shifter_4_out, WB_IR;

  Button \u_总复位  (.out(RST));
  Button _1 (.out(IR1));
  Button _2 (.out(IR2));
  Button _3 (.out(IR3));
  // Probe on \总周期数 
  // Probe on \总周期数 
  Button \u_继续运行  (.out(Go));
  LED #(.active("true")) led_1 (.in(W1));
  LED #(.active("true")) led_2 (.in(W2));
  LED #(.active("true")) led_3 (.in(W3));
  Hex_Digit_Display hex_digit_display_1 (.value(LedData[31:28]));  // open: dp
  // Probe on IF_PC[19:0]
  // RiscV_Probe riscv_probe_1: pin names not known; wires that end beside it: IF_IR
  Priority_Encoder #(.select(2), .disabled("Z")) priority_encoder_1 (
    .in0(1'b1), .in1(or_3_out), .in2(JAL), .in3(JALR), .out(priority_encoder_1_out));  // open: gs, en_out, en_in
  Hex_Digit_Display hex_digit_display_2 (.value(LedData[27:24]));  // open: dp
  Hex_Digit_Display hex_digit_display_3 (.value(LedData[23:20]));  // open: dp
  // Probe on ID_PC[19:0]
  // RiscV_Probe riscv_probe_2: pin names not known; wires that end beside it: ID_IR
  not not_1 (not_1_out, halt);
  and and_1 (and_1_out, Beq, equ);
  Multiplexer #(.select(2), .width(32), .disabled("Z"), .enable("false")) multiplexer_1 (
    .in0(adder_1_out), .in1(adder_2_out), .in2(adder_3_out), .in3(ALUResult_EX), .out(multiplexer_1_out),
    .sel(priority_encoder_1_out));
  or or_1 (or_1_out, not_2_out, Go);
  not not_2 (not_2_out, halt);
  Hex_Digit_Display hex_digit_display_4 (.value(LedData[15:12]));  // open: dp
  Hex_Digit_Display hex_digit_display_5 (.value(LedData[19:16]));  // open: dp
  or or_2 (or_2_out, not_1_out, Go);
  not not_3 (not_3_out, equ);
  and and_2 (and_2_out, less, Bltu);
  and and_3 (and_3_out, not_3_out, Bne);
  or or_3 (or_3_out, and_1_out, and_3_out, and_2_out);
  Register #(.width(32), .trigger("rising"), .Select("low")) PC (
    .D(multiplexer_1_out), .en(or_1_out), .Q(IF_PC), .clk(CLK), .clr(RST));
  Hex_Digit_Display hex_digit_display_6 (.value(LedData[7:4]));  // open: dp
  Hex_Digit_Display hex_digit_display_7 (.value(LedData[11:8]));  // open: dp
  // Probe on EX_PC[19:0]
  // RiscV_Probe riscv_probe_3: pin names not known; wires that end beside it: EX_IR
  Adder #(.width(32)) adder_1 (.a(IF_PC), .b(32'h4), .out(adder_1_out));  // open: cin, cout
  Hex_Digit_Display hex_digit_display_8 (.value(LedData[3:0]));  // open: dp
  // Probe on \总周期数 
  // Probe on M_PC[19:0]
  // RiscV_Probe riscv_probe_4: pin names not known; wires that end beside it: MEM_IR
  ROM #(.addrWidth(10), .dataWidth(32), .Select("high")) rom_1 (.addr(IF_PC[11:2]), .data(IF_IR));
  // Probe on \总周期数 
  // Probe on \无条件分支数 
  // Probe on \条件分支成功数 
  // Probe on \插入气泡数 
  // Probe on \LoadUse次数 
  IF_ID if_id_1 (
    .IR(IF_IR), .PC(IF_PC), .IR_2(ID_IR), .PC_2(ID_PC), .en(or_2_out), .clk(CLK), .clr(1'b0), .rst(RST));  // open: PredictJump, PredictJump_2
  // Probe on IF_PC[11:0]
  // Probe on WB_PC[19:0]
  // RiscV_Probe riscv_probe_5: pin names not known; wires that end beside it: WB_IR
  // Probe on EX_PC[11:0]
  // Probe on ID_PC[11:0]
  // Probe on M_PC[11:0]
  D_Flip_Flop #(.trigger("high"), .Pre_Clr_Positions("LEGACY"), .NegatePresetClear("false"), .enable("true"), .NewFFLayout("false")) d_ff_1 (.Q(d_ff_1_q));  // open: clk, D, Qn, preset, en, reset
  // Probe on 13'hc
  \单周期硬布线控制器  \u_单周期硬布线控制器_1  (
    .Funct({ID_IR[30], ID_IR[25], ID_IR[14:12]}), .OP(ID_IR[6:2]), .ALU_OP(\单周期硬布线控制器_1_alu_op ),
    .MemToReg(\单周期硬布线控制器_1_memtoreg ), .MemWrite(\单周期硬布线控制器_1_memwrite ), .ALU_SRC(\单周期硬布线控制器_1_alu_src ),
    .RegWrite(\单周期硬布线控制器_1_regwrite ), .ecall(ecall_ID), .S_type(S_type), .Jalr(\单周期硬布线控制器_1_jalr ),
    .Beq(\单周期硬布线控制器_1_beq ), .JAL(\单周期硬布线控制器_1_jal ), .Bne(\单周期硬布线控制器_1_bne ), .in_3(ID_IR[21]),
    .Lui(\单周期硬布线控制器_1_lui ), .Sh(\单周期硬布线控制器_1_sh ), .Bltu(\单周期硬布线控制器_1_bltu ));  // open: uret, rs1used, rs2used, csr
  Multiplexer #(.select(1), .width(12), .disabled("Z"), .enable("false")) multiplexer_2 (
    .in0(ID_IR[31:20]), .in1({ID_IR[31:25], ID_IR[11:7]}), .out(multiplexer_2_out), .sel(S_type));
  assign bit_extender_1_out = {{20{ID_IR[31]}}, {ID_IR[31], ID_IR[7], ID_IR[30:25], ID_IR[11:8]}};  // Bit_Extender bit_extender_1
  assign bit_extender_2_out = {{12{ID_IR[31]}}, {ID_IR[31], ID_IR[19:12], ID_IR[20], ID_IR[30:21]}};  // Bit_Extender bit_extender_2
  assign bit_extender_3_out = {{12{ID_IR[31]}}, ID_IR[31:12]};  // Bit_Extender bit_extender_3
  // Probe on WB_PC[11:0]
  Comparator #(.width(13), .mode("twosComplement")) comparator_1 (
    .a(CNT_num), .b(13'hc), .eq(comparator_1_eq), .lt(comparator_1_lt));  // open: gt
  Clock #(.highDuration(1), .lowDuration(1)) clock_1 (.out(clock_1_out));
  Multiplexer #(.select(1), .width(5), .disabled("Z"), .enable("false")) multiplexer_3 (
    .in0(ID_IR[19:15]), .in1(5'b10001), .out(multiplexer_3_out), .sel(ecall_ID));
  Multiplexer #(.select(1), .width(5), .disabled("Z"), .enable("false")) multiplexer_4 (
    .in0(ID_IR[24:20]), .in1(5'b01010), .out(multiplexer_4_out), .sel(ecall_ID));
  assign bit_extender_4_out = {{20{multiplexer_2_out[11]}}, multiplexer_2_out};  // Bit_Extender bit_extender_4
  nand nand_1 (nand_1_out, d_ff_1_q, comparator_1_eq);
  Counter #(.width(13), .max('h1fff), .ongoal("stay"), .trigger("rising"), .behavior("old")) counter_1 (
    .count(comparator_1_lt), .Q(CNT_num), .clk(clock_1_out));  // open: load, D, carry, clr, preset
  Regifile regifile_1 (
    .Din(RDin), .Clk(CLK), .R1(regifile_1_r1), .R2(regifile_1_r2), .WE(RegWrite), .W_num(rd),
    .R1_num(multiplexer_3_out), .R2_num(multiplexer_4_out));
  assign CLK = nand_1_out ? clock_1_out : 1'bz;  // Controlled_Buffer controlled_buffer_1
  Pull_Resistor #(.pull(1)) pull_resistor_1 (.node(CLK));
  ID_EX id_ex_1 (
    .Beq(\单周期硬布线控制器_1_beq ), .Bne(\单周期硬布线控制器_1_bne ), .MemToReg(\单周期硬布线控制器_1_memtoreg ),
    .MemWrite(\单周期硬布线控制器_1_memwrite ), .AluOP(\单周期硬布线控制器_1_alu_op ), .AluSrcB(\单周期硬布线控制器_1_alu_src ),
    .RegWrite(\单周期硬布线控制器_1_regwrite ), .Ecall(ecall_ID), .JAL(\单周期硬布线控制器_1_jal ), .JALR(\单周期硬布线控制器_1_jalr ),
    .Lui(\单周期硬布线控制器_1_lui ), .Sh(\单周期硬布线控制器_1_sh ), .Bltu(\单周期硬布线控制器_1_bltu ), .rs1(regifile_1_r1),
    .rs2(regifile_1_r2), .imm_IS(bit_extender_4_out), .imm_B(bit_extender_1_out), .imm_J(bit_extender_2_out),
    .imm_U(bit_extender_3_out), .rd(ID_IR[11:7]), .IR(ID_IR), .PC(ID_PC), .Beq_2(Beq), .Bne_2(Bne),
    .MemToReg_2(id_ex_1_memtoreg_2), .MemWrite_2(id_ex_1_memwrite_2), .AluOP_2(id_ex_1_aluop_2),
    .AluSrcB_2(id_ex_1_alusrcb_2), .RegWrite_2(id_ex_1_regwrite_2), .Ecall_2(ecall_EX), .JAL_2(JAL),
    .JALR_2(JALR), .Lui_2(id_ex_1_lui_2), .Sh_2(id_ex_1_sh_2), .Bltu_2(Bltu), .rs1_2(id_ex_1_rs1_2),
    .rs2_2(id_ex_1_rs2_2), .imm_IS_2(id_ex_1_imm_is_2), .imm_B_2(id_ex_1_imm_b_2), .imm_J_2(id_ex_1_imm_j_2),
    .imm_U_2(id_ex_1_imm_u_2), .rd_2(id_ex_1_rd_2), .IR_2(EX_IR), .PC_2(EX_PC), .en(or_2_out), .clk(CLK),
    .clr(1'b0), .rst(RST));  // open: rs1Fwd, rs2Fwd, rs1Fwd_2, rs2Fwd_2, uret, uret_2, PredictJump, PredictJump_2
  Shifter #(.width(32), .shift("ll")) shifter_1 (.in(id_ex_1_imm_b_2), .\dist (5'b00001), .out(shifter_1_out));
  Shifter #(.width(32), .shift("ll")) shifter_2 (.in(id_ex_1_imm_j_2), .\dist (5'b00001), .out(shifter_2_out));
  Shifter #(.width(32), .shift("ll")) shifter_3 (.in(id_ex_1_imm_u_2), .\dist (5'b01100), .out(shifter_3_out));
  not not_4 (not_4_out, halt);
  Adder #(.width(32)) adder_2 (.a(shifter_1_out), .b(EX_PC), .out(adder_2_out));  // open: cin, cout
  Adder #(.width(32)) adder_3 (.a(shifter_2_out), .b(EX_PC), .out(adder_3_out));  // open: cin, cout
  or or_4 (or_4_out, not_4_out, Go);
  Counter #(.width(16), .max('hffff), .ongoal("wrap"), .trigger("rising"), .behavior("new")) counter_2 (
    .count(or_4_out), .Q(\总周期数 ), .clk(CLK), .clr(RST));  // open: load, D, carry, preset, down
  Multiplexer #(.select(1), .width(32), .disabled("Z"), .enable("false")) multiplexer_5 (
    .in0(id_ex_1_rs2_2), .in1(id_ex_1_imm_is_2), .out(multiplexer_5_out), .sel(id_ex_1_alusrcb_2));
  Comparator #(.width(32), .mode("twosComplement")) comparator_2 (
    .a(id_ex_1_rs1_2), .b(32'h22), .eq(comparator_2_eq));  // open: gt, lt
  not not_5 (not_5_out, comparator_2_eq);
  ALU alu_1 (
    .X(id_ex_1_rs1_2), .Y(multiplexer_5_out), .AluOP(id_ex_1_aluop_2), .Equal(equ), .Result(ALUResult_EX),
    .out_6(less));  // open: Result_2, out_4
  and and_4 (and_4_out, ecall_EX, comparator_2_eq);
  and and_5 (and_5_out, ecall_EX, not_5_out);
  Register #(.width(32), .trigger("rising"), .Select("low")) register_1 (
    .D(id_ex_1_rs2_2), .en(and_4_out), .Q(LedData), .clk(CLK), .clr(RST));
  EX_MEM ex_mem_1 (
    .MemToReg(id_ex_1_memtoreg_2), .MemWrite(id_ex_1_memwrite_2), .RegWrite(id_ex_1_regwrite_2), .JAL(JAL),
    .JALR(JALR), .Lui(id_ex_1_lui_2), .Sh(id_ex_1_sh_2), .ALUResult(ALUResult_EX), .rs2(id_ex_1_rs2_2),
    .imm_U(shifter_3_out), .halt(and_5_out), .rd(id_ex_1_rd_2), .IR(EX_IR), .PC(EX_PC),
    .MemToReg_2(ex_mem_1_memtoreg_2), .MemWrite_2(MemWrite), .RegWrite_2(ex_mem_1_regwrite_2),
    .JAL_2(ex_mem_1_jal_2), .JALR_2(ex_mem_1_jalr_2), .Lui_2(ex_mem_1_lui_2), .Sh_2(ex_mem_1_sh_2),
    .ALUResult_2(ALUResult_MEM), .rs2_2(ex_mem_1_rs2_2), .imm_U_2(ex_mem_1_imm_u_2),
    .halt_2(ex_mem_1_halt_2), .rd_2(ex_mem_1_rd_2), .IR_2(MEM_IR), .PC_2(M_PC), .en(or_2_out), .clk(CLK),
    .rst(RST));
  Multiplexer #(.select(1), .width(32), .disabled("Z"), .enable("false")) multiplexer_6 (
    .in0(ex_mem_1_rs2_2), .in1(ShDin), .out(MDin), .sel(ex_mem_1_sh_2));
  assign and_6_out = 32'hffff & ex_mem_1_rs2_2;  // AND_Gate and_6, 32 bits wide
  Shifter #(.width(32), .shift("ll")) shifter_4 (.in(ex_mem_1_rs2_2), .\dist (5'b10000), .out(shifter_4_out));
  assign and_7_out = ram_1_data & multiplexer_7_out;  // AND_Gate and_7, 32 bits wide
  Multiplexer #(.select(1), .width(32), .disabled("Z"), .enable("false")) multiplexer_7 (
    .in0(32'hffff0000), .in1(32'hffff), .out(multiplexer_7_out), .sel(ALUResult_MEM[1]));
  Multiplexer #(.select(1), .width(32), .disabled("Z"), .enable("false")) multiplexer_8 (
    .in0(and_6_out), .in1(shifter_4_out), .out(multiplexer_8_out), .sel(ALUResult_MEM[1]));
  RAM #(.addrWidth(10), .dataWidth(32), .bus("separate"), .Select("high")) ram_1 (
    .addr(ALUResult_MEM[11:2]), .din(MDin), .data(ram_1_data), .str(MemWrite), .clk(CLK), .clr(RST));  // open: sel, ld
  Adder #(.width(32)) adder_4 (.a(and_7_out), .b(multiplexer_8_out), .out(ShDin));  // open: cin, cout
  MEM_WB mem_wb_1 (
    .MemToReg(ex_mem_1_memtoreg_2), .RegWrite(ex_mem_1_regwrite_2), .JAL(ex_mem_1_jal_2),
    .JALR(ex_mem_1_jalr_2), .Lui(ex_mem_1_lui_2), .ALUResult(ALUResult_MEM), .ReadData(ram_1_data),
    .imm_U(ex_mem_1_imm_u_2), .halt(ex_mem_1_halt_2), .rd(ex_mem_1_rd_2), .IR(MEM_IR), .PC(M_PC),
    .MemToReg_2(mem_wb_1_memtoreg_2), .RegWrite_2(RegWrite), .JAL_2(mem_wb_1_jal_2),
    .JALR_2(mem_wb_1_jalr_2), .Lui_2(mem_wb_1_lui_2), .ALUResult_2(mem_wb_1_aluresult_2),
    .ReadData_2(mem_wb_1_readdata_2), .imm_U_2(mem_wb_1_imm_u_2), .halt_2(halt), .rd_2(rd), .IR_2(WB_IR),
    .PC_2(WB_PC), .en(or_2_out), .clk(CLK), .rst(RST));
  Multiplexer #(.select(1), .width(32), .disabled("Z"), .enable("false")) multiplexer_9 (
    .in0(mem_wb_1_aluresult_2), .in1(mem_wb_1_readdata_2), .out(multiplexer_9_out), .sel(mem_wb_1_memtoreg_2));
  or or_5 (or_5_out, mem_wb_1_jalr_2, mem_wb_1_jal_2);
  Multiplexer #(.select(1), .width(32), .disabled("Z"), .enable("false")) multiplexer_10 (
    .in0(multiplexer_9_out), .in1(adder_5_out), .out(multiplexer_10_out), .sel(or_5_out));
  Adder #(.width(32)) adder_5 (.a(32'h4), .b(WB_PC), .out(adder_5_out));  // open: cin, cout
  Multiplexer #(.select(1), .width(32), .disabled("Z"), .enable("false")) multiplexer_11 (
    .in0(multiplexer_10_out), .in1(mem_wb_1_imm_u_2), .out(RDin), .sel(mem_wb_1_lui_2));

  // Other names for the same wires on the sheet: MEM_PC[31:0] = M_PC

  // Notes on the sheet:
  //   中断源
  //   时空图监测，可删除
  //   中断等待指示
  //   数码管输出
  //   取指(IF)
  //   指令存储器
  //   contents of rom_1 (hex, n*v repeats v):
  //   413 493 913 993 46413 14e493 296913 39e993 842023 942223 1242423 1342623 a00893 493 913 993 73
  //   Lui
  //   Sh
  //   Bltu
  //   控制位
  //   JAL
  //   JALR
  //   $a7编号
  //   $a0编号
  //   I
  //   S
  //   B
  //   J
  //   U
  //   流水调试日志用
  //   暂停节拍，不能为0
  //   Beq
  //   Bne
  //   MemToReg
  //   MemWrite
  //   AluOP
  //   AluSrcB
  //   RegWrite
  //   译码取数(ID)
  //   戳工具置1进入计数暂停模式，ctrl+k时钟自动运行到对应节拍暂停
  //   ctrl+k关闭时钟连续运行，将控制位置零，进入单步调试模式调试
  //   用这个时钟源需要去掉电路中的其他时钟源
  //   SignImm
  //   可计数暂停的时钟源
  //   跳转地址(beq/bne/bltu)
  //   跳转地址(jal)
  //   为方便自动评测，需要输出流水线各段保存的PC值，注意是PC不是PC+4，另外ID段寄存器写入信息，Mem段内存写入信息也要输出
  //   指令执行(EX)
  //   ecall指令输出$a0到Led
  //   跳转地址(jalr)
  //   WriteData
  //   数据存储器
  //   存储器不支持半字访问，因此需要取出一个字的数据特殊处理
  //   访存(MEM)
  //   ReadData
  //   返回地址
  //   左移12位立即数
  //   写回(WB)
  //   保存到寄存器中的数据
endmodule

module \相关处理逻辑_气泡  (
  input  rs1used,
  input  rs2used,
  input  BranchTaken,
  input  EX_RegWrite,
  input  [4:0] EX_WriteReg_num,
  input  MEM_RegWrite,
  input  [4:0] MEM_WriteReg_num,
  input  ecall,
  input  [31:0] Instr,
  output Stall,
  output Flush
);

  wire and_1_out, and_2_out, and_3_out, and_4_out, comparator_1_eq, comparator_2_eq, comparator_3_eq,
       comparator_4_eq, comparator_5_eq, comparator_6_eq, comparator_7_eq, comparator_8_eq, not_1_out,
       not_2_out, not_3_out, not_4_out, not_5_out, or_1_out;
  wire [4:0] rs1, rs2;

  Comparator #(.width(5), .mode("twosComplement")) comparator_1 (
    .a(rs1), .b({5{1'b0}}), .eq(comparator_1_eq));  // open: gt, lt
  Comparator #(.width(5), .mode("twosComplement")) comparator_2 (
    .a(rs1), .b(EX_WriteReg_num), .eq(comparator_2_eq));  // open: gt, lt
  Comparator #(.width(5), .mode("twosComplement")) comparator_3 (
    .a(rs2), .b({5{1'b0}}), .eq(comparator_3_eq));  // open: gt, lt
  Comparator #(.width(5), .mode("twosComplement")) comparator_4 (
    .a(rs2), .b(EX_WriteReg_num), .eq(comparator_4_eq));  // open: gt, lt
  Comparator #(.width(5), .mode("twosComplement")) comparator_5 (
    .a(rs1), .b({5{1'b0}}), .eq(comparator_5_eq));  // open: gt, lt
  Comparator #(.width(5), .mode("twosComplement")) comparator_6 (
    .a(rs1), .b(MEM_WriteReg_num), .eq(comparator_6_eq));  // open: gt, lt
  Comparator #(.width(5), .mode("twosComplement")) comparator_7 (
    .a(rs2), .b({5{1'b0}}), .eq(comparator_7_eq));  // open: gt, lt
  Comparator #(.width(5), .mode("twosComplement")) comparator_8 (
    .a(rs2), .b(MEM_WriteReg_num), .eq(comparator_8_eq));  // open: gt, lt
  not not_1 (not_1_out, comparator_1_eq);
  not not_2 (not_2_out, comparator_3_eq);
  not not_3 (not_3_out, comparator_5_eq);
  not not_4 (not_4_out, comparator_7_eq);
  Multiplexer #(.select(1), .width(5), .disabled("Z"), .enable("false")) multiplexer_1 (
    .in0(Instr[19:15]), .in1(5'b10001), .out(rs1), .sel(ecall));
  Multiplexer #(.select(1), .width(5), .disabled("Z"), .enable("false")) multiplexer_2 (
    .in0(Instr[24:20]), .in1(5'b01010), .out(rs2), .sel(ecall));
  and and_1 (and_1_out, rs1used, not_1_out, EX_RegWrite, comparator_2_eq);
  and and_2 (and_2_out, rs2used, not_2_out, EX_RegWrite, comparator_4_eq);
  and and_3 (and_3_out, rs1used, not_3_out, MEM_RegWrite, comparator_6_eq);
  and and_4 (and_4_out, rs2used, not_4_out, MEM_RegWrite, comparator_8_eq);
  or or_1 (or_1_out, and_1_out, and_2_out, and_3_out, and_4_out);
  or or_2 (Flush, Stall, BranchTaken);
  not not_5 (not_5_out, BranchTaken);
  and and_5 (Stall, or_1_out, not_5_out);

  // Other names for the same wires on the sheet: DataHazzard = Stall
endmodule
module \气泡流水线  (
  output RegWrite,
  output MemWrite,
  output [31:0] IF_PC,
  output [31:0] ID_PC,
  output [31:0] EX_PC,
  output [31:0] M_PC,
  output [31:0] WB_PC,
  output [31:0] RDin,
  output [31:0] MDin,
  output [31:0] LedData
);

  wire and_1_out, and_2_out, and_3_out, and_5_out, and_6_out, and_7_out, and_8_out, Beq, Bltu, Bne,
       BranchTaken, CLK, clock_1_out, comparator_1_eq, comparator_2_eq, comparator_2_lt, comparator_3_eq,
       Conditional, d_ff_1_q, en, equ, EX_ecall, ex_mem_1_halt_2, ex_mem_1_jal_2, ex_mem_1_jalr_2,
       ex_mem_1_lui_2, ex_mem_1_memtoreg_2, ex_mem_1_regwrite_2, ex_mem_1_sh_2, Go, halt, ID_ecall,
       id_ex_1_alusrcb_2, id_ex_1_lui_2, id_ex_1_memtoreg_2, id_ex_1_memwrite_2, id_ex_1_regwrite_2,
       id_ex_1_sh_2, IR1, IR2, IR3, JAL, JALR, less, mem_wb_1_jal_2, mem_wb_1_jalr_2, mem_wb_1_lui_2,
       mem_wb_1_memtoreg_2, nand_1_out, not_1_out, not_2_out, not_3_out, not_5_out, not_6_out, not_7_out,
       or_2_out, or_3_out, or_4_out, RST, S_type, Stall, W1, W2, W3, \单周期硬布线控制器_1_alu_src ,
       \单周期硬布线控制器_1_beq , \单周期硬布线控制器_1_bltu , \单周期硬布线控制器_1_bne , \单周期硬布线控制器_1_jal , \单周期硬布线控制器_1_jalr ,
       \单周期硬布线控制器_1_lui , \单周期硬布线控制器_1_memtoreg , \单周期硬布线控制器_1_memwrite , \单周期硬布线控制器_1_regwrite ,
       \单周期硬布线控制器_1_rs1used , \单周期硬布线控制器_1_rs2used , \单周期硬布线控制器_1_sh , \相关处理逻辑_气泡_1_flush ;
  wire [1:0] priority_encoder_1_out;
  wire [3:0] id_ex_1_aluop_2, \单周期硬布线控制器_1_alu_op ;
  wire [4:0] ex_mem_1_rd_2, id_ex_1_rd_2, multiplexer_2_out, multiplexer_3_out, rd;
  wire [11:0] multiplexer_4_out;
  wire [12:0] CNT_num;
  wire [15:0] \LoadUse次数 , \总周期数 , \插入气泡数 , \无条件分支数 , \条件分支成功数 ;
  wire [31:0] adder_1_out, adder_2_out, adder_3_out, adder_5_out, and_9_out, and_10_out, bit_extender_1_out,
       bit_extender_2_out, bit_extender_3_out, bit_extender_4_out, EX_ALUResult, EX_IR, ex_mem_1_imm_u_2,
       ex_mem_1_rs2_2, id_ex_1_imm_b_2, id_ex_1_imm_is_2, id_ex_1_imm_j_2, id_ex_1_imm_u_2, id_ex_1_rs1_2,
       id_ex_1_rs2_2, ID_IR, IF_IR, MEM_ALUResult, MEM_IR, mem_wb_1_aluresult_2, mem_wb_1_imm_u_2,
       mem_wb_1_readdata_2, multiplexer_1_out, multiplexer_5_out, multiplexer_7_out, multiplexer_8_out,
       multiplexer_9_out, multiplexer_10_out, ram_1_data, regifile_1_r1, regifile_1_r2, ShDin, shifter_1_out,
       shifter_2_out, shifter_3_out, shifter_4_out, WB_IR;

  Button \u_总复位  (.out(RST));
  Button _1 (.out(IR1));
  Button _2 (.out(IR2));
  Button _3 (.out(IR3));
  // Probe on \总周期数 
  // Probe on \总周期数 
  Button \u_继续运行  (.out(Go));
  LED #(.active("true")) led_1 (.in(W1));
  LED #(.active("true")) led_2 (.in(W2));
  LED #(.active("true")) led_3 (.in(W3));
  Hex_Digit_Display hex_digit_display_1 (.value(LedData[31:28]));  // open: dp
  // Probe on IF_PC[19:0]
  // RiscV_Probe riscv_probe_1: pin names not known; wires that end beside it: IF_IR
  not not_1 (not_1_out, equ);
  and and_1 (and_1_out, not_1_out, Bne);
  and and_2 (and_2_out, Beq, equ);
  or or_1 (Conditional, and_2_out, and_1_out, and_3_out);
  Priority_Encoder #(.select(2), .disabled("Z")) priority_encoder_1 (
    .in0(1'b1), .in1(Conditional), .in2(JAL), .in3(JALR), .out(priority_encoder_1_out));  // open: gs, en_out, en_in
  Multiplexer #(.select(2), .width(32), .disabled("Z"), .enable("false")) multiplexer_1 (
    .in0(adder_1_out), .in1(adder_2_out), .in2(adder_3_out), .in3(EX_ALUResult), .out(multiplexer_1_out),
    .sel(priority_encoder_1_out));
  Hex_Digit_Display hex_digit_display_2 (.value(LedData[23:20]));  // open: dp
  Hex_Digit_Display hex_digit_display_3 (.value(LedData[27:24]));  // open: dp
  // Probe on ID_PC[19:0]
  // RiscV_Probe riscv_probe_2: pin names not known; wires that end beside it: ID_IR
  not not_2 (not_2_out, halt);
  or or_2 (or_2_out, not_2_out, Go);
  and and_3 (and_3_out, less, Bltu);
  Hex_Digit_Display hex_digit_display_4 (.value(LedData[15:12]));  // open: dp
  Hex_Digit_Display hex_digit_display_5 (.value(LedData[19:16]));  // open: dp
  \相关处理逻辑_气泡  \u_相关处理逻辑_气泡_1  (
    .rs1used(\单周期硬布线控制器_1_rs1used ), .rs2used(\单周期硬布线控制器_1_rs2used ), .EX_RegWrite(id_ex_1_regwrite_2),
    .EX_WriteReg_num(id_ex_1_rd_2), .MEM_RegWrite(ex_mem_1_regwrite_2), .MEM_WriteReg_num(ex_mem_1_rd_2),
    .Instr(ID_IR), .Stall(Stall), .Flush(\相关处理逻辑_气泡_1_flush ), .ecall(ID_ecall), .BranchTaken(BranchTaken));
  not not_3 (not_3_out, Stall);
  and and_4 (en, not_3_out, or_2_out);
  Comparator #(.width(2), .mode("twosComplement")) comparator_1 (
    .a(2'b00), .b(priority_encoder_1_out), .eq(comparator_1_eq));  // open: gt, lt
  not not_4 (BranchTaken, comparator_1_eq);
  Register #(.width(32), .trigger("rising"), .Select("low")) PC (
    .D(multiplexer_1_out), .en(en), .Q(IF_PC), .clk(CLK), .clr(RST));
  Hex_Digit_Display hex_digit_display_6 (.value(LedData[7:4]));  // open: dp
  Hex_Digit_Display hex_digit_display_7 (.value(LedData[11:8]));  // open: dp
  // Probe on EX_PC[19:0]
  // RiscV_Probe riscv_probe_3: pin names not known; wires that end beside it: EX_IR
  Adder #(.width(32)) adder_1 (.a(IF_PC), .b(32'h4), .out(adder_1_out));  // open: cin, cout
  Hex_Digit_Display hex_digit_display_8 (.value(LedData[3:0]));  // open: dp
  ROM #(.addrWidth(10), .dataWidth(32), .Select("high")) rom_1 (.addr(IF_PC[11:2]), .data(IF_IR));
  // Probe on \总周期数 
  // Probe on M_PC[19:0]
  // RiscV_Probe riscv_probe_4: pin names not known; wires that end beside it: MEM_IR
  IF_ID if_id_1 (
    .IR(IF_IR), .PC(IF_PC), .IR_2(ID_IR), .PC_2(ID_PC), .en(en), .clk(CLK), .clr(BranchTaken), .rst(RST));  // open: PredictJump, PredictJump_2
  // Probe on \总周期数 
  // Probe on \无条件分支数 
  // Probe on \条件分支成功数 
  // Probe on \插入气泡数 
  // Probe on \LoadUse次数 
  // Probe on IF_PC[11:0]
  // Probe on WB_PC[19:0]
  // RiscV_Probe riscv_probe_5: pin names not known; wires that end beside it: WB_IR
  // Probe on ID_PC[11:0]
  // Probe on EX_PC[11:0]
  \单周期硬布线控制器  \u_单周期硬布线控制器_1  (
    .Funct({ID_IR[30], ID_IR[25], ID_IR[14:12]}), .OP(ID_IR[6:2]), .ALU_OP(\单周期硬布线控制器_1_alu_op ),
    .MemToReg(\单周期硬布线控制器_1_memtoreg ), .MemWrite(\单周期硬布线控制器_1_memwrite ), .ALU_SRC(\单周期硬布线控制器_1_alu_src ),
    .RegWrite(\单周期硬布线控制器_1_regwrite ), .ecall(ID_ecall), .S_type(S_type), .Jalr(\单周期硬布线控制器_1_jalr ),
    .Beq(\单周期硬布线控制器_1_beq ), .JAL(\单周期硬布线控制器_1_jal ), .Bne(\单周期硬布线控制器_1_bne ), .in_3(ID_IR[21]),
    .Lui(\单周期硬布线控制器_1_lui ), .Sh(\单周期硬布线控制器_1_sh ), .Bltu(\单周期硬布线控制器_1_bltu ),
    .rs1used(\单周期硬布线控制器_1_rs1used ), .rs2used(\单周期硬布线控制器_1_rs2used ));  // open: uret, csr
  // Probe on M_PC[11:0]
  D_Flip_Flop #(.trigger("high"), .Pre_Clr_Positions("LEGACY"), .NegatePresetClear("false"), .enable("true"), .NewFFLayout("false")) d_ff_1 (.Q(d_ff_1_q));  // open: clk, D, Qn, preset, en, reset
  // Probe on 13'he27
  Multiplexer #(.select(1), .width(5), .disabled("Z"), .enable("false")) multiplexer_2 (
    .in0(ID_IR[19:15]), .in1(5'b10001), .out(multiplexer_2_out), .sel(ID_ecall));
  Multiplexer #(.select(1), .width(5), .disabled("Z"), .enable("false")) multiplexer_3 (
    .in0(ID_IR[24:20]), .in1(5'b01010), .out(multiplexer_3_out), .sel(ID_ecall));
  assign bit_extender_1_out = {{20{multiplexer_4_out[11]}}, multiplexer_4_out};  // Bit_Extender bit_extender_1
  Multiplexer #(.select(1), .width(12), .disabled("Z"), .enable("false")) multiplexer_4 (
    .in0(ID_IR[31:20]), .in1({ID_IR[31:25], ID_IR[11:7]}), .out(multiplexer_4_out), .sel(S_type));
  assign bit_extender_2_out = {{20{ID_IR[31]}}, {ID_IR[31], ID_IR[7], ID_IR[30:25], ID_IR[11:8]}};  // Bit_Extender bit_extender_2
  assign bit_extender_3_out = {{12{ID_IR[31]}}, {ID_IR[31], ID_IR[19:12], ID_IR[20], ID_IR[30:21]}};  // Bit_Extender bit_extender_3
  assign bit_extender_4_out = {{12{ID_IR[31]}}, ID_IR[31:12]};  // Bit_Extender bit_extender_4
  // Probe on WB_PC[11:0]
  Comparator #(.width(13), .mode("twosComplement")) comparator_2 (
    .a(CNT_num), .b(13'he27), .eq(comparator_2_eq), .lt(comparator_2_lt));  // open: gt
  Clock #(.highDuration(1), .lowDuration(1)) clock_1 (.out(clock_1_out));
  nand nand_1 (nand_1_out, d_ff_1_q, comparator_2_eq);
  Counter #(.width(13), .max('h1fff), .ongoal("stay"), .trigger("rising"), .behavior("old")) counter_1 (
    .count(comparator_2_lt), .Q(CNT_num), .clk(clock_1_out));  // open: load, D, carry, clr, preset
  Regifile regifile_1 (
    .Din(RDin), .Clk(CLK), .R1(regifile_1_r1), .R2(regifile_1_r2), .WE(RegWrite), .W_num(rd),
    .R1_num(multiplexer_2_out), .R2_num(multiplexer_3_out));
  assign CLK = nand_1_out ? clock_1_out : 1'bz;  // Controlled_Buffer controlled_buffer_1
  ID_EX id_ex_1 (
    .Beq(\单周期硬布线控制器_1_beq ), .Bne(\单周期硬布线控制器_1_bne ), .MemToReg(\单周期硬布线控制器_1_memtoreg ),
    .MemWrite(\单周期硬布线控制器_1_memwrite ), .AluOP(\单周期硬布线控制器_1_alu_op ), .AluSrcB(\单周期硬布线控制器_1_alu_src ),
    .RegWrite(\单周期硬布线控制器_1_regwrite ), .Ecall(ID_ecall), .JAL(\单周期硬布线控制器_1_jal ), .JALR(\单周期硬布线控制器_1_jalr ),
    .Lui(\单周期硬布线控制器_1_lui ), .Sh(\单周期硬布线控制器_1_sh ), .Bltu(\单周期硬布线控制器_1_bltu ), .rs1(regifile_1_r1),
    .rs2(regifile_1_r2), .imm_IS(bit_extender_1_out), .imm_B(bit_extender_2_out), .imm_J(bit_extender_3_out),
    .imm_U(bit_extender_4_out), .rd(ID_IR[11:7]), .IR(ID_IR), .PC(ID_PC), .Beq_2(Beq), .Bne_2(Bne),
    .MemToReg_2(id_ex_1_memtoreg_2), .MemWrite_2(id_ex_1_memwrite_2), .AluOP_2(id_ex_1_aluop_2),
    .AluSrcB_2(id_ex_1_alusrcb_2), .RegWrite_2(id_ex_1_regwrite_2), .Ecall_2(EX_ecall), .JAL_2(JAL),
    .JALR_2(JALR), .Lui_2(id_ex_1_lui_2), .Sh_2(id_ex_1_sh_2), .Bltu_2(Bltu), .rs1_2(id_ex_1_rs1_2),
    .rs2_2(id_ex_1_rs2_2), .imm_IS_2(id_ex_1_imm_is_2), .imm_B_2(id_ex_1_imm_b_2), .imm_J_2(id_ex_1_imm_j_2),
    .imm_U_2(id_ex_1_imm_u_2), .rd_2(id_ex_1_rd_2), .IR_2(EX_IR), .PC_2(EX_PC), .en(or_2_out), .clk(CLK),
    .clr(\相关处理逻辑_气泡_1_flush ), .rst(RST));  // open: rs1Fwd, rs2Fwd, rs1Fwd_2, rs2Fwd_2, uret, uret_2, PredictJump, PredictJump_2
  Pull_Resistor #(.pull(1)) pull_resistor_1 (.node(CLK));
  Shifter #(.width(32), .shift("ll")) shifter_1 (.in(id_ex_1_imm_b_2), .\dist (5'b00001), .out(shifter_1_out));
  Shifter #(.width(32), .shift("ll")) shifter_2 (.in(id_ex_1_imm_j_2), .\dist (5'b00001), .out(shifter_2_out));
  Shifter #(.width(32), .shift("ll")) shifter_3 (.in(id_ex_1_imm_u_2), .\dist (5'b01100), .out(shifter_3_out));
  not not_5 (not_5_out, halt);
  Adder #(.width(32)) adder_2 (.a(shifter_1_out), .b(EX_PC), .out(adder_2_out));  // open: cin, cout
  Adder #(.width(32)) adder_3 (.a(shifter_2_out), .b(EX_PC), .out(adder_3_out));  // open: cin, cout
  or or_3 (or_3_out, not_5_out, Go);
  Counter #(.width(16), .max('hffff), .ongoal("wrap"), .trigger("rising"), .behavior("new")) counter_2 (
    .count(or_3_out), .Q(\总周期数 ), .clk(CLK), .clr(RST));  // open: load, D, carry, preset, down
  Multiplexer #(.select(1), .width(32), .disabled("Z"), .enable("false")) multiplexer_5 (
    .in0(id_ex_1_rs2_2), .in1(id_ex_1_imm_is_2), .out(multiplexer_5_out), .sel(id_ex_1_alusrcb_2));
  ALU alu_1 (
    .X(id_ex_1_rs1_2), .Y(multiplexer_5_out), .AluOP(id_ex_1_aluop_2), .Equal(equ), .Result(EX_ALUResult),
    .out_6(less));  // open: Result_2, out_4
  Comparator #(.width(32), .mode("twosComplement")) comparator_3 (
    .a(id_ex_1_rs1_2), .b(32'h22), .eq(comparator_3_eq));  // open: gt, lt
  not not_6 (not_6_out, comparator_3_eq);
  Counter #(.width(16), .max('hffff), .ongoal("wrap"), .trigger("rising"), .behavior("new")) counter_3 (
    .count(Stall), .Q(\插入气泡数 ), .clk(CLK), .clr(RST));  // open: load, D, carry, preset, down
  Register #(.width(32), .trigger("rising"), .Select("low")) register_1 (
    .D(id_ex_1_rs2_2), .en(and_5_out), .Q(LedData), .clk(CLK), .clr(RST));
  and and_5 (and_5_out, EX_ecall, comparator_3_eq);
  and and_6 (and_6_out, EX_ecall, not_6_out);
  not not_7 (not_7_out, Conditional);
  and and_7 (and_7_out, BranchTaken, not_7_out);
  Counter #(.width(16), .max('hffff), .ongoal("wrap"), .trigger("rising"), .behavior("new")) counter_4 (
    .count(and_7_out), .Q(\无条件分支数 ), .clk(CLK), .clr(RST));  // open: load, D, carry, preset, down
  EX_MEM ex_mem_1 (
    .MemToReg(id_ex_1_memtoreg_2), .MemWrite(id_ex_1_memwrite_2), .RegWrite(id_ex_1_regwrite_2), .JAL(JAL),
    .JALR(JALR), .Lui(id_ex_1_lui_2), .Sh(id_ex_1_sh_2), .ALUResult(EX_ALUResult), .rs2(id_ex_1_rs2_2),
    .imm_U(shifter_3_out), .halt(and_6_out), .rd(id_ex_1_rd_2), .IR(EX_IR), .PC(EX_PC),
    .MemToReg_2(ex_mem_1_memtoreg_2), .MemWrite_2(MemWrite), .RegWrite_2(ex_mem_1_regwrite_2),
    .JAL_2(ex_mem_1_jal_2), .JALR_2(ex_mem_1_jalr_2), .Lui_2(ex_mem_1_lui_2), .Sh_2(ex_mem_1_sh_2),
    .ALUResult_2(MEM_ALUResult), .rs2_2(ex_mem_1_rs2_2), .imm_U_2(ex_mem_1_imm_u_2),
    .halt_2(ex_mem_1_halt_2), .rd_2(ex_mem_1_rd_2), .IR_2(MEM_IR), .PC_2(M_PC), .en(or_2_out), .clk(CLK),
    .rst(RST));
  Multiplexer #(.select(1), .width(32), .disabled("Z"), .enable("false")) multiplexer_6 (
    .in0(ex_mem_1_rs2_2), .in1(ShDin), .out(MDin), .sel(ex_mem_1_sh_2));
  Shifter #(.width(32), .shift("ll")) shifter_4 (.in(ex_mem_1_rs2_2), .\dist (5'b10000), .out(shifter_4_out));
  and and_8 (and_8_out, BranchTaken, Conditional);
  Counter #(.width(16), .max('hffff), .ongoal("wrap"), .trigger("rising"), .behavior("new")) counter_5 (
    .count(and_8_out), .Q(\条件分支成功数 ), .clk(CLK), .clr(RST));  // open: load, D, carry, preset, down
  Multiplexer #(.select(1), .width(32), .disabled("Z"), .enable("false")) multiplexer_7 (
    .in0(32'hffff0000), .in1(32'hffff), .out(multiplexer_7_out), .sel(MEM_ALUResult[1]));
  assign and_9_out = 32'hffff & ex_mem_1_rs2_2;  // AND_Gate and_9, 32 bits wide
  Multiplexer #(.select(1), .width(32), .disabled("Z"), .enable("false")) multiplexer_8 (
    .in0(and_9_out), .in1(shifter_4_out), .out(multiplexer_8_out), .sel(MEM_ALUResult[1]));
  assign and_10_out = ram_1_data & multiplexer_7_out;  // AND_Gate and_10, 32 bits wide
  RAM #(.addrWidth(10), .dataWidth(32), .bus("separate"), .Select("high")) ram_1 (
    .addr(MEM_ALUResult[11:2]), .din(MDin), .data(ram_1_data), .str(MemWrite), .clk(CLK), .clr(RST));  // open: sel, ld
  Adder #(.width(32)) adder_4 (.a(and_10_out), .b(multiplexer_8_out), .out(ShDin));  // open: cin, cout
  MEM_WB mem_wb_1 (
    .MemToReg(ex_mem_1_memtoreg_2), .RegWrite(ex_mem_1_regwrite_2), .JAL(ex_mem_1_jal_2),
    .JALR(ex_mem_1_jalr_2), .Lui(ex_mem_1_lui_2), .ALUResult(MEM_ALUResult), .ReadData(ram_1_data),
    .imm_U(ex_mem_1_imm_u_2), .halt(ex_mem_1_halt_2), .rd(ex_mem_1_rd_2), .IR(MEM_IR), .PC(M_PC),
    .MemToReg_2(mem_wb_1_memtoreg_2), .RegWrite_2(RegWrite), .JAL_2(mem_wb_1_jal_2),
    .JALR_2(mem_wb_1_jalr_2), .Lui_2(mem_wb_1_lui_2), .ALUResult_2(mem_wb_1_aluresult_2),
    .ReadData_2(mem_wb_1_readdata_2), .imm_U_2(mem_wb_1_imm_u_2), .halt_2(halt), .rd_2(rd), .IR_2(WB_IR),
    .PC_2(WB_PC), .en(or_2_out), .clk(CLK), .rst(RST));
  Multiplexer #(.select(1), .width(32), .disabled("Z"), .enable("false")) multiplexer_9 (
    .in0(mem_wb_1_aluresult_2), .in1(mem_wb_1_readdata_2), .out(multiplexer_9_out), .sel(mem_wb_1_memtoreg_2));
  Adder #(.width(32)) adder_5 (.a(32'h4), .b(WB_PC), .out(adder_5_out));  // open: cin, cout
  or or_4 (or_4_out, mem_wb_1_jalr_2, mem_wb_1_jal_2);
  Multiplexer #(.select(1), .width(32), .disabled("Z"), .enable("false")) multiplexer_10 (
    .in0(multiplexer_9_out), .in1(adder_5_out), .out(multiplexer_10_out), .sel(or_4_out));
  Multiplexer #(.select(1), .width(32), .disabled("Z"), .enable("false")) multiplexer_11 (
    .in0(multiplexer_10_out), .in1(mem_wb_1_imm_u_2), .out(RDin), .sel(mem_wb_1_lui_2));

  // Other names for the same wires on the sheet: MEM_PC[31:0] = M_PC

  // Notes on the sheet:
  //   中断源
  //   时空图监测，可删除
  //   中断等待指示
  //   数码管输出
  //   BranchTaken
  //   Stall
  //   BranchTaken
  //   取指(IF)
  //   指令存储器
  //   contents of rom_1 (hex, n*v repeats v):
  //   100493 100006f 100493 200913 300993 100006f 100493 200913 300993 100006f 100493 200913 300993
  //   100006f 100493 200913 300993 3c0000ef 100413 100493 1f49493 900533 2200893 73 24d493 48463 fedff06f
  //   900533 2200893 73 100493 249493 900533 2200893 73 48463 fedff06f 100493 1f49493 900533 2200893 73
  //   4034d493 900533 2200893 73 4044d493 900533 2200893 73 4044d493 900533 2200893 73 4044d493 900533
  //   2200893 73 4044d493 900533 2200893 73 4044d493 900533 2200893 73 4044d493 900533 2200893 73 4044d493
  //   900533 2200893 73 100413 1f41993 41f9d993 433 c00913 300b13 140413 f47413 800293 100313 499993
  //   89e9b3 1300533 2200893 73 406282b3 fe0294e3 140413 f00f93 1f47433 1c41413 800293 100313 49d993
  //   89e9b3 1300533 2200893 73 406282b3 fe0294e3 1c45413 406b0b33 b0463 f95ff06f 2b3 fff2c293 829293
  //   ff2e293 500533 2200893 73 fff00413 493 84a023 140413 448493 84a023 140413 448493 84a023 140413
  //   448493 84a023 140413 448493 84a023 140413 448493 84a023 140413 448493 84a023 140413 448493 84a023
  //   140413 448493 84a023 140413 448493 84a023 140413 448493 84a023 140413 448493 84a023 140413 448493
  //   84a023 140413 448493 84a023 140413 448493 84a023 140413 448493 84a023 140413 448493 140413 433
  //   3c00493 42983 4aa03 149a2b3 28663 134a023 1442023 ffc48493 fe9412e3 800533 2200893 73 440413 3c00493
  //   fc9416e3 a00893 73 100293 300313 800493 849493 7648493 900533 2200893 73 800e13 5494b3 6494b3 900533
  //   2200893 73 fffe0e13 fe0e14e3 a00893 73 800e13 fedc04b7 fff00413 1045413 84e4b3 900533 2200893 73
  //   ba984b7 900533 73 76544b7 900533 73 32104b7 900533 73 fffe0e13 fa0e1ee3 a00893 73 313 2000e13 100493
  //   100913 931023 900533 2200893 73 12484b3 230313 fffe0e13 fe0e12e3 1000e13 313 32483 900533 2200893 73
  //   430313 fffe0e13 fe0e14e3 a00893 73 ff100493 900533 2200893 73 148493 fe9068e3 900533 2200893 73
  //   a00893 73 413 140413 800533 2200893 73 240413 800533 2200893 73 340413 800533 2200893 73 440413
  //   800533 2200893 73 540413 800533 2200893 73 640413 800533 2200893 73 740413 800533 2200893 73 840413
  //   800533 2200893 2200893 73 8067
  //   Lui
  //   Sh
  //   Bltu
  //   I
  //   S
  //   B
  //   J
  //   U
  //   控制位
  //   Instr
  //   rs1used
  //   JAL
  //   JALR
  //   $a7编号
  //   $a0编号
  //   流水调试日志用
  //   暂停节拍，不能为0
  //   rs2used
  //   Beq
  //   Bne
  //   MemToReg
  //   MemWrite
  //   AluOP
  //   AluSrcB
  //   RegWrite
  //   译码取数(ID)
  //   戳工具置1进入计数暂停模式，ctrl+k时钟自动运行到对应节拍暂停
  //   ctrl+k关闭时钟连续运行，将控制位置零，进入单步调试模式调试
  //   SignImm
  //   可计数暂停的时钟源
  //   Flush
  //   跳转地址(beq/bne/bltu)
  //   跳转地址(jal)
  //   为方便自动评测，需要输出流水线各段保存的PC值，注意是PC不是PC+4，另外ID段寄存器写入信息，Mem段内存写入信息也要输出
  //   指令执行(EX)
  //   ecall指令输出$a0到Led
  //   跳转地址(jalr)
  //   WriteData
  //   存储器不支持半字访问，因此需要取出一个字的数据特殊处理
  //   数据存储器
  //   访存(MEM)
  //   ReadData
  //   返回地址
  //   左移12位立即数
  //   写回(WB)
  //   保存到寄存器中的数据
endmodule

module \相关处理逻辑_重定向  (
  input  rs1used,
  input  rs2used,
  input  BranchTaken,
  input  \中断请求 ,
  input  EX_RegWrite,
  input  [4:0] EX_WriteReg_num,
  input  EX_MemToReg,
  input  MEM_RegWrite,
  input  [4:0] MEM_WriteReg_num,
  input  EX_Lui,
  input  ecall,
  input  [31:0] Instr,
  output [1:0] rs1Fwd,
  output Stall,
  output Flush,
  output [1:0] rs2Fwd
);

  wire and_1_out, and_2_out, and_4_out, and_5_out, and_6_out, and_7_out, and_8_out, and_9_out,
       comparator_1_eq, comparator_2_eq, comparator_3_eq, comparator_4_eq, comparator_5_eq, comparator_6_eq,
       comparator_7_eq, comparator_8_eq, comparator_9_eq, comparator_10_eq, comparator_11_eq,
       comparator_12_eq, not_1_out, not_2_out, not_3_out, not_4_out, not_5_out, not_6_out, not_7_out,
       not_8_out, or_1_out;
  wire [4:0] rs1, rs2;

  Comparator #(.width(5), .mode("twosComplement")) comparator_1 (
    .a(rs1), .b({5{1'b0}}), .eq(comparator_1_eq));  // open: gt, lt
  Comparator #(.width(5), .mode("twosComplement")) comparator_2 (
    .a(rs1), .b(EX_WriteReg_num), .eq(comparator_2_eq));  // open: gt, lt
  Comparator #(.width(5), .mode("twosComplement")) comparator_3 (
    .a(rs2), .b({5{1'b0}}), .eq(comparator_3_eq));  // open: gt, lt
  Comparator #(.width(5), .mode("twosComplement")) comparator_4 (
    .a(rs2), .b(EX_WriteReg_num), .eq(comparator_4_eq));  // open: gt, lt
  not not_1 (not_1_out, comparator_1_eq);
  not not_2 (not_2_out, comparator_3_eq);
  Multiplexer #(.select(1), .width(5), .disabled("Z"), .enable("false")) multiplexer_1 (
    .in0(Instr[19:15]), .in1(5'b10001), .out(rs1), .sel(ecall));
  Multiplexer #(.select(1), .width(5), .disabled("Z"), .enable("false")) multiplexer_2 (
    .in0(Instr[24:20]), .in1(5'b01010), .out(rs2), .sel(ecall));
  and and_1 (and_1_out, rs1used, not_1_out, EX_MemToReg, comparator_2_eq);
  and and_2 (and_2_out, rs2used, not_2_out, EX_MemToReg, comparator_4_eq);
  or or_1 (or_1_out, and_1_out, and_2_out);
  not not_3 (not_3_out, \中断请求 );
  or or_2 (Flush, Stall, BranchTaken);
  and and_3 (Stall, or_1_out, not_3_out, not_4_out);
  not not_4 (not_4_out, BranchTaken);
  Comparator #(.width(5), .mode("twosComplement")) comparator_5 (
    .a(rs1), .b({5{1'b0}}), .eq(comparator_5_eq));  // open: gt, lt
  Comparator #(.width(5), .mode("twosComplement")) comparator_6 (
    .a(rs1), .b(MEM_WriteReg_num), .eq(comparator_6_eq));  // open: gt, lt
  Comparator #(.width(5), .mode("twosComplement")) comparator_7 (
    .a(rs1), .b({5{1'b0}}), .eq(comparator_7_eq));  // open: gt, lt
  Comparator #(.width(5), .mode("twosComplement")) comparator_8 (
    .a(rs1), .b(EX_WriteReg_num), .eq(comparator_8_eq));  // open: gt, lt
  Comparator #(.width(5), .mode("twosComplement")) comparator_9 (
    .a(rs2), .b({5{1'b0}}), .eq(comparator_9_eq));  // open: gt, lt
  Comparator #(.width(5), .mode("twosComplement")) comparator_10 (
    .a(rs2), .b(MEM_WriteReg_num), .eq(comparator_10_eq));  // open: gt, lt
  Comparator #(.width(5), .mode("twosComplement")) comparator_11 (
    .a(rs2), .b({5{1'b0}}), .eq(comparator_11_eq));  // open: gt, lt
  Comparator #(.width(5), .mode("twosComplement")) comparator_12 (
    .a(rs2), .b(EX_WriteReg_num), .eq(comparator_12_eq));  // open: gt, lt
  not not_5 (not_5_out, comparator_5_eq);
  not not_6 (not_6_out, comparator_7_eq);
  not not_7 (not_7_out, comparator_9_eq);
  not not_8 (not_8_out, comparator_11_eq);
  and and_4 (and_4_out, rs1used, not_5_out, MEM_RegWrite, comparator_6_eq);
  and and_5 (and_5_out, rs1used, not_6_out, EX_RegWrite, comparator_8_eq);
  and and_6 (and_6_out, rs2used, not_7_out, MEM_RegWrite, comparator_10_eq);
  and and_7 (and_7_out, rs2used, not_8_out, EX_RegWrite, comparator_12_eq);
  and and_8 (and_8_out, and_5_out, EX_Lui);
  and and_9 (and_9_out, and_7_out, EX_Lui);
  Priority_Encoder #(.select(2), .disabled("Z")) priority_encoder_1 (
    .in0(1'b1), .in1(and_4_out), .in2(and_5_out), .in3(and_8_out), .out(rs1Fwd));  // open: gs, en_out, en_in
  Priority_Encoder #(.select(2), .disabled("Z")) priority_encoder_2 (
    .in0(1'b1), .in1(and_6_out), .in2(and_7_out), .in3(and_9_out), .out(rs2Fwd));  // open: gs, en_out, en_in

  // Other names for the same wires on the sheet: LoadUse = Stall

  // Notes on the sheet:
  //   无数据相关
  //   ID段和MEM段数据相关
  //   ID段和EX段数据相关
  //   无数据相关
  //   ID段和MEM段数据相关
  //   ID段和EX段数据相关
  //   ID段和EX段Lui指令的数据相关
  //   ID段和EX段Lui指令的数据相关
endmodule

module \重定向流水线  (
  output RegWrite,
  output MemWrite,
  output [31:0] IF_PC,
  output [31:0] ID_PC,
  output [31:0] EX_PC,
  output [31:0] M_PC,
  output [31:0] WB_PC,
  output [31:0] RDin,
  output [31:0] MDin,
  output [31:0] LedData
);

  wire and_1_out, and_2_out, and_3_out, and_5_out, and_6_out, and_7_out, and_8_out, Beq, Bltu, Bne,
       BranchTaken, CLK, clock_1_out, comparator_1_eq, comparator_2_eq, comparator_2_lt, comparator_3_eq,
       Conditional, d_ff_1_q, en, equ, EX_ecall, ex_mem_1_halt_2, ex_mem_1_jal_2, ex_mem_1_jalr_2,
       ex_mem_1_lui_2, ex_mem_1_memtoreg_2, ex_mem_1_regwrite_2, ex_mem_1_sh_2, Go, halt, ID_ecall,
       id_ex_1_alusrcb_2, id_ex_1_lui_2, id_ex_1_memtoreg_2, id_ex_1_memwrite_2, id_ex_1_regwrite_2,
       id_ex_1_sh_2, IR1, IR2, IR3, JAL, JALR, less, mem_wb_1_jal_2, mem_wb_1_jalr_2, mem_wb_1_lui_2,
       mem_wb_1_memtoreg_2, nand_1_out, not_1_out, not_2_out, not_3_out, not_5_out, not_6_out, not_7_out,
       or_2_out, or_3_out, or_4_out, RST, S_type, Stall, W1, W2, W3, \单周期硬布线控制器_1_alu_src ,
       \单周期硬布线控制器_1_beq , \单周期硬布线控制器_1_bltu , \单周期硬布线控制器_1_bne , \单周期硬布线控制器_1_jal , \单周期硬布线控制器_1_jalr ,
       \单周期硬布线控制器_1_lui , \单周期硬布线控制器_1_memtoreg , \单周期硬布线控制器_1_memwrite , \单周期硬布线控制器_1_regwrite ,
       \单周期硬布线控制器_1_rs1used , \单周期硬布线控制器_1_rs2used , \单周期硬布线控制器_1_sh , \相关处理逻辑_重定向_1_flush ;
  wire [1:0] id_ex_1_rs1fwd_2, id_ex_1_rs2fwd_2, priority_encoder_1_out, \相关处理逻辑_重定向_1_rs1fwd ,
       \相关处理逻辑_重定向_1_rs2fwd ;
  wire [3:0] id_ex_1_aluop_2, \单周期硬布线控制器_1_alu_op ;
  wire [4:0] ex_mem_1_rd_2, id_ex_1_rd_2, multiplexer_2_out, multiplexer_3_out, rd;
  wire [11:0] multiplexer_4_out;
  wire [12:0] CNT_num;
  wire [15:0] \LoadUse次数 , \总周期数 , \无条件分支数 , \条件分支成功数 ;
  wire [31:0] adder_1_out, adder_2_out, adder_3_out, adder_5_out, and_9_out, and_10_out, bit_extender_1_out,
       bit_extender_2_out, bit_extender_3_out, bit_extender_4_out, EX_ALUResult, EX_IR, ex_mem_1_rs2_2,
       id_ex_1_imm_b_2, id_ex_1_imm_is_2, id_ex_1_imm_j_2, id_ex_1_imm_u_2, id_ex_1_rs1_2, id_ex_1_rs2_2,
       ID_IR, IF_IR, imm_U, MEM_ALUResult, MEM_IR, mem_wb_1_aluresult_2, mem_wb_1_imm_u_2,
       mem_wb_1_readdata_2, multiplexer_1_out, multiplexer_5_out, multiplexer_6_out, multiplexer_7_out,
       multiplexer_9_out, multiplexer_10_out, multiplexer_11_out, multiplexer_12_out, ram_1_data,
       regifile_1_r1, regifile_1_r2, ShDin, shifter_1_out, shifter_2_out, shifter_3_out, shifter_4_out, WB_IR;

  Button \u_总复位  (.out(RST));
  Button _1 (.out(IR1));
  Button _2 (.out(IR2));
  Button _3 (.out(IR3));
  // Probe on \总周期数 
  // Probe on \总周期数 
  Button \u_继续运行  (.out(Go));
  LED #(.active("true")) led_1 (.in(W1));
  LED #(.active("true")) led_2 (.in(W2));
  LED #(.active("true")) led_3 (.in(W3));
  Hex_Digit_Display hex_digit_display_1 (.value(LedData[31:28]));  // open: dp
  // Probe on IF_PC[19:0]
  // RiscV_Probe riscv_probe_1: pin names not known; wires that end beside it: IF_IR
  not not_1 (not_1_out, equ);
  and and_1 (and_1_out, Beq, equ);
  and and_2 (and_2_out, not_1_out, Bne);
  or or_1 (Conditional, and_1_out, and_2_out, and_3_out);
  Priority_Encoder #(.select(2), .disabled("Z")) priority_encoder_1 (
    .in0(1'b1), .in1(Conditional), .in2(JAL), .in3(JALR), .out(priority_encoder_1_out));  // open: gs, en_out, en_in
  Multiplexer #(.select(2), .width(32), .disabled("Z"), .enable("false")) multiplexer_1 (
    .in0(adder_1_out), .in1(adder_2_out), .in2(adder_3_out), .in3(EX_ALUResult), .out(multiplexer_1_out),
    .sel(priority_encoder_1_out));
  Hex_Digit_Display hex_digit_display_2 (.value(LedData[23:20]));  // open: dp
  Hex_Digit_Display hex_digit_display_3 (.value(LedData[27:24]));  // open: dp
  // Probe on ID_PC[19:0]
  // RiscV_Probe riscv_probe_2: pin names not known; wires that end beside it: ID_IR
  \相关处理逻辑_重定向  \u_相关处理逻辑_重定向_1  (
    .rs1used(\单周期硬布线控制器_1_rs1used ), .rs2used(\单周期硬布线控制器_1_rs2used ), .BranchTaken(BranchTaken),
    .EX_RegWrite(id_ex_1_regwrite_2), .EX_WriteReg_num(id_ex_1_rd_2), .MEM_RegWrite(ex_mem_1_regwrite_2),
    .MEM_WriteReg_num(ex_mem_1_rd_2), .Instr(ID_IR), .Stall(Stall), .Flush(\相关处理逻辑_重定向_1_flush ),
    .ecall(ID_ecall), .EX_MemToReg(id_ex_1_memtoreg_2), .rs1Fwd(\相关处理逻辑_重定向_1_rs1fwd ),
    .EX_Lui(id_ex_1_lui_2), .rs2Fwd(\相关处理逻辑_重定向_1_rs2fwd ), .\中断请求 (1'b0));
  not not_2 (not_2_out, halt);
  or or_2 (or_2_out, not_2_out, Go);
  and and_3 (and_3_out, less, Bltu);
  Hex_Digit_Display hex_digit_display_4 (.value(LedData[15:12]));  // open: dp
  Hex_Digit_Display hex_digit_display_5 (.value(LedData[19:16]));  // open: dp
  not not_3 (not_3_out, Stall);
  and and_4 (en, not_3_out, or_2_out);
  not not_4 (BranchTaken, comparator_1_eq);
  Comparator #(.width(2), .mode("twosComplement")) comparator_1 (
    .a(2'b00), .b(priority_encoder_1_out), .eq(comparator_1_eq));  // open: gt, lt
  Register #(.width(32), .trigger("rising"), .Select("low")) PC (
    .D(multiplexer_1_out), .en(en), .Q(IF_PC), .clk(CLK), .clr(RST));
  Hex_Digit_Display hex_digit_display_6 (.value(LedData[11:8]));  // open: dp
  Hex_Digit_Display hex_digit_display_7 (.value(LedData[7:4]));  // open: dp
  // Probe on EX_PC[19:0]
  // RiscV_Probe riscv_probe_3: pin names not known; wires that end beside it: EX_IR
  Adder #(.width(32)) adder_1 (.a(IF_PC), .b(32'h4), .out(adder_1_out));  // open: cin, cout
  Hex_Digit_Display hex_digit_display_8 (.value(LedData[3:0]));  // open: dp
  ROM #(.addrWidth(10), .dataWidth(32), .Select("high")) rom_1 (.addr(IF_PC[11:2]), .data(IF_IR));
  // Probe on \总周期数 
  // Probe on M_PC[19:0]
  // RiscV_Probe riscv_probe_4: pin names not known; wires that end beside it: MEM_IR
  IF_ID if_id_1 (
    .IR(IF_IR), .PC(IF_PC), .IR_2(ID_IR), .PC_2(ID_PC), .en(en), .clk(CLK), .clr(BranchTaken), .rst(RST));  // open: PredictJump, PredictJump_2
  // Probe on \总周期数 
  // Probe on \无条件分支数 
  // Probe on \条件分支成功数 
  // Probe on \LoadUse次数 
  // Probe on \LoadUse次数 
  // Probe on IF_PC[11:0]
  // Probe on WB_PC[19:0]
  // RiscV_Probe riscv_probe_5: pin names not known; wires that end beside it: WB_IR
  // Probe on ID_PC[11:0]
  // Probe on EX_PC[11:0]
  \单周期硬布线控制器  \u_单周期硬布线控制器_1  (
    .Funct({ID_IR[30], ID_IR[25], ID_IR[14:12]}), .OP(ID_IR[6:2]), .ALU_OP(\单周期硬布线控制器_1_alu_op ),
    .MemToReg(\单周期硬布线控制器_1_memtoreg ), .MemWrite(\单周期硬布线控制器_1_memwrite ), .ALU_SRC(\单周期硬布线控制器_1_alu_src ),
    .RegWrite(\单周期硬布线控制器_1_regwrite ), .ecall(ID_ecall), .S_type(S_type), .Jalr(\单周期硬布线控制器_1_jalr ),
    .Beq(\单周期硬布线控制器_1_beq ), .JAL(\单周期硬布线控制器_1_jal ), .Bne(\单周期硬布线控制器_1_bne ), .in_3(ID_IR[21]),
    .Lui(\单周期硬布线控制器_1_lui ), .Sh(\单周期硬布线控制器_1_sh ), .Bltu(\单周期硬布线控制器_1_bltu ),
    .rs1used(\单周期硬布线控制器_1_rs1used ), .rs2used(\单周期硬布线控制器_1_rs2used ));  // open: uret, csr
  // Probe on M_PC[11:0]
  D_Flip_Flop #(.trigger("high"), .Pre_Clr_Positions("LEGACY"), .NegatePresetClear("false"), .enable("true"), .NewFFLayout("false")) d_ff_1 (.Q(d_ff_1_q));  // open: clk, D, Qn, preset, en, reset
  // Probe on 13'he27
  Multiplexer #(.select(1), .width(5), .disabled("Z"), .enable("false")) multiplexer_2 (
    .in0(ID_IR[19:15]), .in1(5'b10001), .out(multiplexer_2_out), .sel(ID_ecall));
  Multiplexer #(.select(1), .width(5), .disabled("Z"), .enable("false")) multiplexer_3 (
    .in0(ID_IR[24:20]), .in1(5'b01010), .out(multiplexer_3_out), .sel(ID_ecall));
  Multiplexer #(.select(1), .width(12), .disabled("Z"), .enable("false")) multiplexer_4 (
    .in0(ID_IR[31:20]), .in1({ID_IR[31:25], ID_IR[11:7]}), .out(multiplexer_4_out), .sel(S_type));
  assign bit_extender_1_out = {{20{multiplexer_4_out[11]}}, multiplexer_4_out};  // Bit_Extender bit_extender_1
  assign bit_extender_2_out = {{20{ID_IR[31]}}, {ID_IR[31], ID_IR[7], ID_IR[30:25], ID_IR[11:8]}};  // Bit_Extender bit_extender_2
  assign bit_extender_3_out = {{12{ID_IR[31]}}, {ID_IR[31], ID_IR[19:12], ID_IR[20], ID_IR[30:21]}};  // Bit_Extender bit_extender_3
  assign bit_extender_4_out = {{12{ID_IR[31]}}, ID_IR[31:12]};  // Bit_Extender bit_extender_4
  // Probe on WB_PC[11:0]
  Comparator #(.width(13), .mode("twosComplement")) comparator_2 (
    .a(CNT_num), .b(13'he27), .eq(comparator_2_eq), .lt(comparator_2_lt));  // open: gt
  Clock #(.highDuration(1), .lowDuration(1)) clock_1 (.out(clock_1_out));
  nand nand_1 (nand_1_out, d_ff_1_q, comparator_2_eq);
  Counter #(.width(13), .max('h1fff), .ongoal("stay"), .trigger("rising"), .behavior("old")) counter_1 (
    .count(comparator_2_lt), .Q(CNT_num), .clk(clock_1_out));  // open: load, D, carry, clr, preset
  Regifile regifile_1 (
    .Din(RDin), .Clk(CLK), .R1(regifile_1_r1), .R2(regifile_1_r2), .WE(RegWrite), .W_num(rd),
    .R1_num(multiplexer_2_out), .R2_num(multiplexer_3_out));
  assign CLK = nand_1_out ? clock_1_out : 1'bz;  // Controlled_Buffer controlled_buffer_1
  ID_EX id_ex_1 (
    .Beq(\单周期硬布线控制器_1_beq ), .Bne(\单周期硬布线控制器_1_bne ), .MemToReg(\单周期硬布线控制器_1_memtoreg ),
    .MemWrite(\单周期硬布线控制器_1_memwrite ), .AluOP(\单周期硬布线控制器_1_alu_op ), .AluSrcB(\单周期硬布线控制器_1_alu_src ),
    .RegWrite(\单周期硬布线控制器_1_regwrite ), .Ecall(ID_ecall), .JAL(\单周期硬布线控制器_1_jal ), .JALR(\单周期硬布线控制器_1_jalr ),
    .Lui(\单周期硬布线控制器_1_lui ), .Sh(\单周期硬布线控制器_1_sh ), .Bltu(\单周期硬布线控制器_1_bltu ), .rs1(regifile_1_r1),
    .rs2(regifile_1_r2), .imm_IS(bit_extender_1_out), .imm_B(bit_extender_2_out), .imm_J(bit_extender_3_out),
    .imm_U(bit_extender_4_out), .rd(ID_IR[11:7]), .IR(ID_IR), .PC(ID_PC), .Beq_2(Beq), .Bne_2(Bne),
    .MemToReg_2(id_ex_1_memtoreg_2), .MemWrite_2(id_ex_1_memwrite_2), .AluOP_2(id_ex_1_aluop_2),
    .AluSrcB_2(id_ex_1_alusrcb_2), .RegWrite_2(id_ex_1_regwrite_2), .Ecall_2(EX_ecall), .JAL_2(JAL),
    .JALR_2(JALR), .Lui_2(id_ex_1_lui_2), .Sh_2(id_ex_1_sh_2), .Bltu_2(Bltu), .rs1_2(id_ex_1_rs1_2),
    .rs2_2(id_ex_1_rs2_2), .imm_IS_2(id_ex_1_imm_is_2), .imm_B_2(id_ex_1_imm_b_2), .imm_J_2(id_ex_1_imm_j_2),
    .imm_U_2(id_ex_1_imm_u_2), .rd_2(id_ex_1_rd_2), .IR_2(EX_IR), .PC_2(EX_PC), .en(or_2_out), .clk(CLK),
    .clr(\相关处理逻辑_重定向_1_flush ), .rs1Fwd(\相关处理逻辑_重定向_1_rs1fwd ), .rs2Fwd(\相关处理逻辑_重定向_1_rs2fwd ),
    .rs1Fwd_2(id_ex_1_rs1fwd_2), .rs2Fwd_2(id_ex_1_rs2fwd_2), .rst(RST));  // open: uret, uret_2, PredictJump, PredictJump_2
  Pull_Resistor #(.pull(1)) pull_resistor_1 (.node(CLK));
  Shifter #(.width(32), .shift("ll")) shifter_1 (.in(id_ex_1_imm_b_2), .\dist (5'b00001), .out(shifter_1_out));
  Shifter #(.width(32), .shift("ll")) shifter_2 (.in(id_ex_1_imm_j_2), .\dist (5'b00001), .out(shifter_2_out));
  Shifter #(.width(32), .shift("ll")) shifter_3 (.in(id_ex_1_imm_u_2), .\dist (5'b01100), .out(shifter_3_out));
  not not_5 (not_5_out, halt);
  Multiplexer #(.select(2), .width(32), .disabled("Z"), .enable("false")) multiplexer_5 (
    .in0(id_ex_1_rs1_2), .in1(RDin), .in2(MEM_ALUResult), .in3(imm_U), .out(multiplexer_5_out),
    .sel(id_ex_1_rs1fwd_2));
  Multiplexer #(.select(2), .width(32), .disabled("Z"), .enable("false")) multiplexer_6 (
    .in0(id_ex_1_rs2_2), .in1(RDin), .in2(MEM_ALUResult), .in3(imm_U), .out(multiplexer_6_out),
    .sel(id_ex_1_rs2fwd_2));
  Adder #(.width(32)) adder_2 (.a(shifter_1_out), .b(EX_PC), .out(adder_2_out));  // open: cin, cout
  Adder #(.width(32)) adder_3 (.a(shifter_2_out), .b(EX_PC), .out(adder_3_out));  // open: cin, cout
  or or_3 (or_3_out, not_5_out, Go);
  Counter #(.width(16), .max('hffff), .ongoal("wrap"), .trigger("rising"), .behavior("new")) counter_2 (
    .count(or_3_out), .Q(\总周期数 ), .clk(CLK), .clr(RST));  // open: load, D, carry, preset, down
  Multiplexer #(.select(1), .width(32), .disabled("Z"), .enable("false")) multiplexer_7 (
    .in0(multiplexer_6_out), .in1(id_ex_1_imm_is_2), .out(multiplexer_7_out), .sel(id_ex_1_alusrcb_2));
  ALU alu_1 (
    .X(multiplexer_5_out), .Y(multiplexer_7_out), .AluOP(id_ex_1_aluop_2), .Equal(equ),
    .Result(EX_ALUResult), .out_6(less));  // open: Result_2, out_4
  Comparator #(.width(32), .mode("twosComplement")) comparator_3 (
    .a(multiplexer_5_out), .b(32'h22), .eq(comparator_3_eq));  // open: gt, lt
  not not_6 (not_6_out, comparator_3_eq);
  Counter #(.width(16), .max('hffff), .ongoal("wrap"), .trigger("rising"), .behavior("new")) counter_3 (
    .count(Stall), .Q(\LoadUse次数 ), .clk(CLK), .clr(RST));  // open: load, D, carry, preset, down
  Register #(.width(32), .trigger("rising"), .Select("low")) register_1 (
    .D(multiplexer_6_out), .en(and_5_out), .Q(LedData), .clk(CLK), .clr(RST));
  and and_5 (and_5_out, EX_ecall, comparator_3_eq);
  and and_6 (and_6_out, EX_ecall, not_6_out);
  not not_7 (not_7_out, Conditional);
  and and_7 (and_7_out, BranchTaken, not_7_out);
  Counter #(.width(16), .max('hffff), .ongoal("wrap"), .trigger("rising"), .behavior("new")) counter_4 (
    .count(and_7_out), .Q(\无条件分支数 ), .clk(CLK), .clr(RST));  // open: load, D, carry, preset, down
  EX_MEM ex_mem_1 (
    .MemToReg(id_ex_1_memtoreg_2), .MemWrite(id_ex_1_memwrite_2), .RegWrite(id_ex_1_regwrite_2), .JAL(JAL),
    .JALR(JALR), .Lui(id_ex_1_lui_2), .Sh(id_ex_1_sh_2), .ALUResult(EX_ALUResult), .rs2(multiplexer_6_out),
    .imm_U(shifter_3_out), .halt(and_6_out), .rd(id_ex_1_rd_2), .IR(EX_IR), .PC(EX_PC),
    .MemToReg_2(ex_mem_1_memtoreg_2), .MemWrite_2(MemWrite), .RegWrite_2(ex_mem_1_regwrite_2),
    .JAL_2(ex_mem_1_jal_2), .JALR_2(ex_mem_1_jalr_2), .Lui_2(ex_mem_1_lui_2), .Sh_2(ex_mem_1_sh_2),
    .ALUResult_2(MEM_ALUResult), .rs2_2(ex_mem_1_rs2_2), .imm_U_2(imm_U), .halt_2(ex_mem_1_halt_2),
    .rd_2(ex_mem_1_rd_2), .IR_2(MEM_IR), .PC_2(M_PC), .en(or_2_out), .clk(CLK), .rst(RST));
  Multiplexer #(.select(1), .width(32), .disabled("Z"), .enable("false")) multiplexer_8 (
    .in0(ex_mem_1_rs2_2), .in1(ShDin), .out(MDin), .sel(ex_mem_1_sh_2));
  Shifter #(.width(32), .shift("ll")) shifter_4 (.in(ex_mem_1_rs2_2), .\dist (5'b10000), .out(shifter_4_out));
  and and_8 (and_8_out, BranchTaken, Conditional);
  Counter #(.width(16), .max('hffff), .ongoal("wrap"), .trigger("rising"), .behavior("new")) counter_5 (
    .count(and_8_out), .Q(\条件分支成功数 ), .clk(CLK), .clr(RST));  // open: load, D, carry, preset, down
  Multiplexer #(.select(1), .width(32), .disabled("Z"), .enable("false")) multiplexer_9 (
    .in0(32'hffff0000), .in1(32'hffff), .out(multiplexer_9_out), .sel(MEM_ALUResult[1]));
  assign and_9_out = 32'hffff & ex_mem_1_rs2_2;  // AND_Gate and_9, 32 bits wide
  Multiplexer #(.select(1), .width(32), .disabled("Z"), .enable("false")) multiplexer_10 (
    .in0(and_9_out), .in1(shifter_4_out), .out(multiplexer_10_out), .sel(MEM_ALUResult[1]));
  assign and_10_out = ram_1_data & multiplexer_9_out;  // AND_Gate and_10, 32 bits wide
  RAM #(.addrWidth(10), .dataWidth(32), .bus("separate"), .Select("high")) ram_1 (
    .addr(MEM_ALUResult[11:2]), .din(MDin), .data(ram_1_data), .str(MemWrite), .clk(CLK), .clr(RST));  // open: sel, ld
  Adder #(.width(32)) adder_4 (.a(and_10_out), .b(multiplexer_10_out), .out(ShDin));  // open: cin, cout
  MEM_WB mem_wb_1 (
    .MemToReg(ex_mem_1_memtoreg_2), .RegWrite(ex_mem_1_regwrite_2), .JAL(ex_mem_1_jal_2),
    .JALR(ex_mem_1_jalr_2), .Lui(ex_mem_1_lui_2), .ALUResult(MEM_ALUResult), .ReadData(ram_1_data),
    .imm_U(imm_U), .halt(ex_mem_1_halt_2), .rd(ex_mem_1_rd_2), .IR(MEM_IR), .PC(M_PC),
    .MemToReg_2(mem_wb_1_memtoreg_2), .RegWrite_2(RegWrite), .JAL_2(mem_wb_1_jal_2),
    .JALR_2(mem_wb_1_jalr_2), .Lui_2(mem_wb_1_lui_2), .ALUResult_2(mem_wb_1_aluresult_2),
    .ReadData_2(mem_wb_1_readdata_2), .imm_U_2(mem_wb_1_imm_u_2), .halt_2(halt), .rd_2(rd), .IR_2(WB_IR),
    .PC_2(WB_PC), .en(or_2_out), .clk(CLK), .rst(RST));
  Multiplexer #(.select(1), .width(32), .disabled("Z"), .enable("false")) multiplexer_11 (
    .in0(mem_wb_1_aluresult_2), .in1(mem_wb_1_readdata_2), .out(multiplexer_11_out), .sel(mem_wb_1_memtoreg_2));
  Adder #(.width(32)) adder_5 (.a(32'h4), .b(WB_PC), .out(adder_5_out));  // open: cin, cout
  or or_4 (or_4_out, mem_wb_1_jalr_2, mem_wb_1_jal_2);
  Multiplexer #(.select(1), .width(32), .disabled("Z"), .enable("false")) multiplexer_12 (
    .in0(multiplexer_11_out), .in1(adder_5_out), .out(multiplexer_12_out), .sel(or_4_out));
  Multiplexer #(.select(1), .width(32), .disabled("Z"), .enable("false")) multiplexer_13 (
    .in0(multiplexer_12_out), .in1(mem_wb_1_imm_u_2), .out(RDin), .sel(mem_wb_1_lui_2));

  // Other names for the same wires on the sheet: MEM_PC[31:0] = M_PC; 插入气泡数[15:0] = \LoadUse次数 

  // Notes on the sheet:
  //   中断源
  //   时空图监测，可删除
  //   中断等待指示
  //   Stall
  //   数码管输出
  //   BranchTaken
  //   BranchTaken
  //   取指(IF)
  //   指令存储器
  //   contents of rom_1 (hex, n*v repeats v):
  //   100493 100006f 100493 200913 300993 100006f 100493 200913 300993 100006f 100493 200913 300993
  //   100006f 100493 200913 300993 3c0000ef 100413 100493 1f49493 900533 2200893 73 24d493 48463 fedff06f
  //   900533 2200893 73 100493 249493 900533 2200893 73 48463 fedff06f 100493 1f49493 900533 2200893 73
  //   4034d493 900533 2200893 73 4044d493 900533 2200893 73 4044d493 900533 2200893 73 4044d493 900533
  //   2200893 73 4044d493 900533 2200893 73 4044d493 900533 2200893 73 4044d493 900533 2200893 73 4044d493
  //   900533 2200893 73 100413 1f41993 41f9d993 433 c00913 300b13 140413 f47413 800293 100313 499993
  //   89e9b3 1300533 2200893 73 406282b3 fe0294e3 140413 f00f93 1f47433 1c41413 800293 100313 49d993
  //   89e9b3 1300533 2200893 73 406282b3 fe0294e3 1c45413 406b0b33 b0463 f95ff06f 2b3 fff2c293 829293
  //   ff2e293 500533 2200893 73 fff00413 493 84a023 140413 448493 84a023 140413 448493 84a023 140413
  //   448493 84a023 140413 448493 84a023 140413 448493 84a023 140413 448493 84a023 140413 448493 84a023
  //   140413 448493 84a023 140413 448493 84a023 140413 448493 84a023 140413 448493 84a023 140413 448493
  //   84a023 140413 448493 84a023 140413 448493 84a023 140413 448493 84a023 140413 448493 140413 433
  //   3c00493 42983 4aa03 149a2b3 28663 134a023 1442023 ffc48493 fe9412e3 800533 2200893 73 440413 3c00493
  //   fc9416e3 a00893 73 100293 300313 800493 849493 7648493 900533 2200893 73 800e13 5494b3 6494b3 900533
  //   2200893 73 fffe0e13 fe0e14e3 a00893 73 800e13 fedc04b7 fff00413 1045413 84e4b3 900533 2200893 73
  //   ba984b7 900533 73 76544b7 900533 73 32104b7 900533 73 fffe0e13 fa0e1ee3 a00893 73 313 2000e13 100493
  //   100913 931023 900533 2200893 73 12484b3 230313 fffe0e13 fe0e12e3 1000e13 313 32483 900533 2200893 73
  //   430313 fffe0e13 fe0e14e3 a00893 73 ff100493 900533 2200893 73 148493 fe9068e3 900533 2200893 73
  //   a00893 73 413 140413 800533 2200893 73 240413 800533 2200893 73 340413 800533 2200893 73 440413
  //   800533 2200893 73 540413 800533 2200893 73 640413 800533 2200893 73 740413 800533 2200893 73 840413
  //   800533 2200893 2200893 73 8067
  //   Lui
  //   Sh
  //   Bltu
  //   I
  //   S
  //   B
  //   J
  //   U
  //   控制位
  //   Instr
  //   rs1used
  //   JAL
  //   JALR
  //   $a7编号
  //   $a0编号
  //   流水调试日志用
  //   暂停节拍，不能为0
  //   rs2used
  //   Beq
  //   Bne
  //   MemToReg
  //   MemWrite
  //   AluOP
  //   AluSrcB
  //   RegWrite
  //   译码取数(ID)
  //   戳工具置1进入计数暂停模式，ctrl+k时钟自动运行到对应节拍暂停
  //   ctrl+k关闭时钟连续运行，将控制位置零，进入单步调试模式调试
  //   SignImm
  //   rs1Fwd
  //   rs2Fwd
  //   可计数暂停的时钟源
  //   Flush
  //   跳转地址(beq/bne/bltu)
  //   跳转地址(jal)
  //   为方便自动评测，需要输出流水线各段保存的PC值，注意是PC不是PC+4，另外ID段寄存器写入信息，Mem段内存写入信息也要输出
  //   指令执行(EX)
  //   EX.Lui
  //   ecall指令输出$a0到Led
  //   跳转地址(jalr)
  //   WriteData
  //   存储器不支持半字访问，因此需要取出一个字的数据特殊处理
  //   数据存储器
  //   访存(MEM)
  //   ReadData
  //   返回地址
  //   左移12位立即数
  //   写回(WB)
  //   保存到寄存器中的数据
endmodule

module \中断按键参考电路  (
  input  \同步清零信号 ,
  output \与中断屏蔽位与 
);

  wire \_1号中断_out , and_1_out, clock_1_out, d_ff_1_q, or_1_out, or_2_out;

  Clock #(.highDuration(1), .lowDuration(1)) clock_1 (.out(clock_1_out));
  Button \_1号中断  (.out(\_1号中断_out ));
  LED #(.active("true")) \_1号中断等待指示灯  (.in(or_1_out));
  or or_1 (or_1_out, \与中断屏蔽位与 , d_ff_1_q);
  D_Flip_Flop #(.trigger("rising"), .Pre_Clr_Positions("LEGACY"), .NegatePresetClear("false"), .enable("true"), .NewFFLayout("false")) d_ff_1 (
    .clk(\_1号中断_out ), .D(1'b1), .Q(d_ff_1_q), .reset(\与中断屏蔽位与 ));  // open: Qn, preset, en
  or or_2 (or_2_out, d_ff_1_q, \与中断屏蔽位与 );
  and and_1 (and_1_out, or_2_out, ~\同步清零信号 );  // AND_Gate
  D_Flip_Flop #(.trigger("rising"), .Pre_Clr_Positions("LEGACY"), .NegatePresetClear("false"), .enable("true"), .NewFFLayout("false")) IR1 (
    .clk(clock_1_out), .D(and_1_out), .Q(\与中断屏蔽位与 ));  // open: Qn, preset, en, reset

  // Notes on the sheet:
  //   中断信号采样参考电路
  //   Reset 
endmodule

module \单周期_单级中断  (
  input  IR1,
  input  IR2,
  input  IR3,
  output RegWrite,
  output MemWrite,
  output [31:0] PC,
  output [31:0] IR,
  output [31:0] RDin,
  output [31:0] MDin,
  output [31:0] LedData
);

  wire and_1_out, and_2_out, and_3_out, and_4_out, and_5_out, and_6_out, and_7_out, and_8_out, and_9_out,
       and_13_out, Beq, Bltu, Bne, CLK, clock_1_out, clr1, clr2, clr3, comparator_1_eq, comparator_2_eq,
       comparator_2_lt, comparator_3_eq, comparator_4_eq, comparator_5_eq, comparator_6_eq,
       controlled_inverter_1_out, controlled_inverter_2_out, controlled_inverter_3_out, d_ff_1_q, d_ff_2_q,
       d_ff_3_q, d_ff_4_q, ecall, equ, Go, halt, IE, IR1_q, IR1_t, IR2_q, IR2_t, IR3_q, IR3_t, IRA, IRB, IRC,
       JAL, JALR, less, Lui, MemToReg, nand_1_out, not_1_out, not_2_out, not_3_out, not_4_out, or_1_out,
       or_2_out, or_6_out, or_7_out, or_8_out, or_10_out, or_13_out, or_14_out, or_15_out,
       priority_encoder_2_gs, RST, S_type, Sh, uret, W1, W2, W3, \中断请求 , \单周期硬布线控制器_1_alu_src ;
  wire [1:0] priority_encoder_1_out, register_1_q, \中断号 ;
  wire [3:0] \单周期硬布线控制器_1_alu_op ;
  wire [4:0] multiplexer_4_out, multiplexer_5_out;
  wire [11:0] multiplexer_3_out;
  wire [12:0] CNT_num;
  wire [15:0] \总周期数 ;
  wire [31:0] adder_2_out, adder_3_out, ALUResult, and_11_out, and_12_out, bit_extender_1_out,
       bit_extender_2_out, bit_extender_3_out, bit_extender_4_out, EPC, imm_U__12, multiplexer_2_out,
       multiplexer_7_out, multiplexer_9_out, multiplexer_10_out, multiplexer_11_out, multiplexer_12_out,
       PC_4, ram_1_data, regifile_1_r1, regifile_1_r2, ShDin, shifter_1_out, shifter_2_out, shifter_4_out,
       \入口地址 , \断点 ;

  Button \u_继续运行  (.out(Go));
  Button _1 (.out(IRA));
  Button _2 (.out(IRB));
  Button _3 (.out(IRC));
  Button \u_总复位  (.out(RST));
  and and_1 (and_1_out, Beq, equ);
  LED #(.active("true")) led_1 (.in(W1));
  LED #(.active("true")) led_2 (.in(W2));
  LED #(.active("true")) led_3 (.in(W3));
  not not_1 (not_1_out, equ);
  and and_2 (and_2_out, not_1_out, Bne);
  and and_3 (and_3_out, less, Bltu);
  or or_1 (or_1_out, and_1_out, and_2_out, and_3_out);
  Priority_Encoder #(.select(2), .disabled("Z")) priority_encoder_1 (
    .in0(1'b1), .in1(or_1_out), .in2(JAL), .in3(JALR), .out(priority_encoder_1_out));  // open: gs, en_out, en_in
  Multiplexer #(.select(2), .width(32), .disabled("Z"), .enable("false")) multiplexer_1 (
    .in0(PC_4), .in1(adder_2_out), .in2(adder_3_out), .in3(ALUResult), .out(\断点 ),
    .sel(priority_encoder_1_out));
  Hex_Digit_Display hex_digit_display_1 (.value(LedData[31:28]));  // open: dp
  Hex_Digit_Display hex_digit_display_2 (.value(LedData[23:20]));  // open: dp
  Hex_Digit_Display hex_digit_display_3 (.value(LedData[27:24]));  // open: dp
  or or_2 (or_2_out, not_2_out, Go);
  Multiplexer #(.select(2), .width(32), .disabled("Z"), .enable("false")) multiplexer_2 (
    .in0(\断点 ), .in1(\入口地址 ), .in2(EPC), .out(multiplexer_2_out), .sel({uret, \中断请求 }));  // open: in3
  not not_2 (not_2_out, halt);
  or or_3 (W1, IR1_q, d_ff_1_q);
  or or_4 (W2, IR2_q, d_ff_2_q);
  or or_5 (W3, IR3_q, d_ff_3_q);
  Hex_Digit_Display hex_digit_display_4 (.value(LedData[15:12]));  // open: dp
  Hex_Digit_Display hex_digit_display_5 (.value(LedData[19:16]));  // open: dp
  Register #(.width(32), .trigger("rising"), .Select("low")) u_PC (
    .D(multiplexer_2_out), .en(or_2_out), .Q(PC), .clk(CLK), .clr(RST));
  D_Flip_Flop #(.trigger("rising"), .Pre_Clr_Positions("LEGACY"), .NegatePresetClear("false"), .enable("true"), .NewFFLayout("false")) d_ff_1 (
    .clk(IRA), .D(1'b1), .Q(d_ff_1_q), .reset(IR1_q));  // open: Qn, preset, en
  D_Flip_Flop #(.trigger("rising"), .Pre_Clr_Positions("LEGACY"), .NegatePresetClear("false"), .enable("true"), .NewFFLayout("false")) d_ff_2 (
    .clk(IRB), .D(1'b1), .Q(d_ff_2_q), .reset(IR2_q));  // open: Qn, preset, en
  D_Flip_Flop #(.trigger("rising"), .Pre_Clr_Positions("LEGACY"), .NegatePresetClear("false"), .enable("true"), .NewFFLayout("false")) d_ff_3 (
    .clk(IRC), .D(1'b1), .Q(d_ff_3_q), .reset(IR3_q));  // open: Qn, preset, en
  Register #(.width(32), .trigger("rising"), .Select("low")) u_EPC (
    .D(\断点 ), .en(\中断请求 ), .Q(EPC), .clk(CLK), .clr(RST));
  Hex_Digit_Display hex_digit_display_6 (.value(LedData[7:4]));  // open: dp
  Hex_Digit_Display hex_digit_display_7 (.value(LedData[11:8]));  // open: dp
  // Probe on \总周期数 
  Adder #(.width(32)) adder_1 (.a(PC), .b(32'h4), .out(PC_4));  // open: cin, cout
  or or_6 (or_6_out, d_ff_1_q, IR1_q);
  and and_4 (and_4_out, clr1, uret);
  or or_7 (or_7_out, d_ff_2_q, IR2_q);
  and and_5 (and_5_out, clr2, uret);
  or or_8 (or_8_out, d_ff_3_q, IR3_q);
  and and_6 (and_6_out, clr3, uret);
  Hex_Digit_Display hex_digit_display_8 (.value(LedData[3:0]));  // open: dp
  and and_7 (and_7_out, or_6_out, ~and_4_out);  // AND_Gate
  and and_8 (and_8_out, or_7_out, ~and_5_out);  // AND_Gate
  and and_9 (and_9_out, or_8_out, ~and_6_out);  // AND_Gate
  // RiscV_Probe riscv_probe_1: pin names not known; wires that end beside it: IR
  ROM #(.addrWidth(10), .dataWidth(32), .Select("high")) rom_1 (.addr(PC[11:2]), .data(IR));
  D_Flip_Flop #(.trigger("rising"), .Pre_Clr_Positions("LEGACY"), .NegatePresetClear("false"), .enable("true"), .NewFFLayout("false")) u_IR1 (
    .clk(CLK), .D(and_7_out), .Q(IR1_q), .reset(RST));  // open: Qn, preset, en
  D_Flip_Flop #(.trigger("rising"), .Pre_Clr_Positions("LEGACY"), .NegatePresetClear("false"), .enable("true"), .NewFFLayout("false")) u_IR2 (
    .clk(CLK), .D(and_8_out), .Q(IR2_q), .reset(RST));  // open: Qn, preset, en
  D_Flip_Flop #(.trigger("rising"), .Pre_Clr_Positions("LEGACY"), .NegatePresetClear("false"), .enable("true"), .NewFFLayout("false")) u_IR3 (
    .clk(CLK), .D(and_9_out), .Q(IR3_q), .reset(RST));  // open: Qn, preset, en
  or or_9 (IR1_t, IR1, IRA);
  D_Flip_Flop #(.trigger("rising"), .Pre_Clr_Positions("LEGACY"), .NegatePresetClear("false"), .enable("true"), .NewFFLayout("false")) u_IE (
    .clk(CLK), .D(IE), .Qn(IE), .en(or_10_out), .reset(RST));  // open: Q, preset
  or or_10 (or_10_out, \中断请求 , uret);
  or or_11 (IR2_t, IR2, IRB);
  \单周期硬布线控制器  \u_单周期硬布线控制器_1  (
    .Funct({IR[30], IR[25], IR[14:12]}), .OP(IR[6:2]), .ALU_OP(\单周期硬布线控制器_1_alu_op ), .MemToReg(MemToReg),
    .MemWrite(MemWrite), .ALU_SRC(\单周期硬布线控制器_1_alu_src ), .RegWrite(RegWrite), .ecall(ecall),
    .S_type(S_type), .Jalr(JALR), .Beq(Beq), .JAL(JAL), .Bne(Bne), .in_3(IR[21]), .uret(uret), .Lui(Lui),
    .Sh(Sh), .Bltu(Bltu));  // open: rs1used, rs2used, csr
  Multiplexer #(.select(1), .width(12), .disabled("Z"), .enable("false")) multiplexer_3 (
    .in0(IR[31:20]), .in1({IR[31:25], IR[11:7]}), .out(multiplexer_3_out), .sel(S_type));
  assign bit_extender_1_out = {{20{IR[31]}}, {IR[31], IR[7], IR[30:25], IR[11:8]}};  // Bit_Extender bit_extender_1
  assign bit_extender_2_out = {{12{IR[31]}}, {IR[31], IR[19:12], IR[20], IR[30:21]}};  // Bit_Extender bit_extender_2
  assign bit_extender_3_out = {{12{IR[31]}}, IR[31:12]};  // Bit_Extender bit_extender_3
  Multiplexer #(.select(1), .width(5), .disabled("Z"), .enable("false")) multiplexer_4 (
    .in0(IR[19:15]), .in1(5'b10001), .out(multiplexer_4_out), .sel(ecall));
  Multiplexer #(.select(1), .width(5), .disabled("Z"), .enable("false")) multiplexer_5 (
    .in0(IR[24:20]), .in1(5'b01010), .out(multiplexer_5_out), .sel(ecall));
  assign bit_extender_4_out = {{20{multiplexer_3_out[11]}}, multiplexer_3_out};  // Bit_Extender bit_extender_4
  Shifter #(.width(32), .shift("ll")) shifter_1 (.in(bit_extender_1_out), .\dist (5'b00001), .out(shifter_1_out));
  Shifter #(.width(32), .shift("ll")) shifter_2 (.in(bit_extender_2_out), .\dist (5'b00001), .out(shifter_2_out));
  Shifter #(.width(32), .shift("ll")) shifter_3 (.in(bit_extender_3_out), .\dist (5'b01100), .out(imm_U__12));
  Priority_Encoder #(.select(2), .disabled("Z")) priority_encoder_2 (
    .in1(IR1_q), .in2(IR2_q), .in3(IR3_q), .out(\中断号 ), .gs(priority_encoder_2_gs), .en_in(1'b1));  // open: in0, en_out
  or or_12 (IR3_t, IR3, IRC);
  Regifile regifile_1 (
    .Din(RDin), .Clk(CLK), .R1(regifile_1_r1), .R2(regifile_1_r2), .WE(RegWrite), .W_num(IR[11:7]),
    .R1_num(multiplexer_4_out), .R2_num(multiplexer_5_out));
  Adder #(.width(32)) adder_2 (.a(shifter_1_out), .b(PC), .out(adder_2_out));  // open: cin, cout
  Adder #(.width(32)) adder_3 (.a(shifter_2_out), .b(PC), .out(adder_3_out));  // open: cin, cout
  Multiplexer #(.select(2), .width(32), .disabled("Z"), .enable("false")) multiplexer_6 (
    .in1(32'h30ac), .in2(32'h3150), .in3(32'h31f4), .out(\入口地址 ), .sel(\中断号 ));  // open: in0
  Multiplexer #(.select(1), .width(32), .disabled("Z"), .enable("false")) multiplexer_7 (
    .in0(regifile_1_r2), .in1(bit_extender_4_out), .out(multiplexer_7_out), .sel(\单周期硬布线控制器_1_alu_src ));
  and and_10 (\中断请求 , priority_encoder_2_gs, IE);
  Register #(.width(2), .trigger("rising"), .Select("low")) register_1 (
    .D(\中断号 ), .en(\中断请求 ), .Q(register_1_q), .clk(CLK), .clr(RST));
  Decoder #(.select(2), .tristate("false"), .disabled("Z"), .enable("false")) decoder_1 (
    .out1(clr1), .out2(clr2), .out3(clr3), .sel(register_1_q));  // open: out0
  ALU alu_1 (
    .X(regifile_1_r1), .Y(multiplexer_7_out), .AluOP(\单周期硬布线控制器_1_alu_op ), .Equal(equ), .Result(ALUResult),
    .out_6(less));  // open: Result_2, out_4
  assign and_11_out = 32'hffff & regifile_1_r2;  // AND_Gate and_11, 32 bits wide
  Shifter #(.width(32), .shift("ll")) shifter_4 (.in(regifile_1_r2), .\dist (5'b10000), .out(shifter_4_out));
  Multiplexer #(.select(1), .width(32), .disabled("Z"), .enable("false")) multiplexer_8 (
    .in0(regifile_1_r2), .in1(ShDin), .out(MDin), .sel(Sh));
  Multiplexer #(.select(1), .width(32), .disabled("Z"), .enable("false")) multiplexer_9 (
    .in0(32'hffff0000), .in1(32'hffff), .out(multiplexer_9_out), .sel(ALUResult[1]));
  Multiplexer #(.select(1), .width(32), .disabled("Z"), .enable("false")) multiplexer_10 (
    .in0(and_11_out), .in1(shifter_4_out), .out(multiplexer_10_out), .sel(ALUResult[1]));
  Comparator #(.width(32), .mode("twosComplement")) comparator_1 (
    .a(regifile_1_r1), .b(32'h22), .eq(comparator_1_eq));  // open: gt, lt
  not not_3 (not_3_out, comparator_1_eq);
  assign and_12_out = ram_1_data & multiplexer_9_out;  // AND_Gate and_12, 32 bits wide
  and and_13 (and_13_out, ecall, comparator_1_eq);
  and and_14 (halt, ecall, not_3_out);
  not not_4 (not_4_out, halt);
  or or_13 (or_13_out, not_4_out, Go);
  Counter #(.width(16), .max('hffff), .ongoal("wrap"), .trigger("rising"), .behavior("new")) counter_1 (
    .count(or_13_out), .Q(\总周期数 ), .clk(CLK), .clr(RST));  // open: load, D, carry, preset, down
  RAM #(.addrWidth(10), .dataWidth(32), .bus("separate"), .Select("high")) ram_1 (
    .addr(ALUResult[11:2]), .din(MDin), .data(ram_1_data), .str(MemWrite), .clk(CLK), .clr(RST));  // open: sel, ld
  Adder #(.width(32)) adder_4 (.a(and_12_out), .b(multiplexer_10_out), .out(ShDin));  // open: cin, cout
  Register #(.width(32), .trigger("rising"), .Select("low")) register_2 (
    .D(regifile_1_r2), .en(and_13_out), .Q(LedData), .clk(CLK), .clr(RST));
  D_Flip_Flop #(.trigger("high"), .Pre_Clr_Positions("LEGACY"), .NegatePresetClear("false"), .enable("true"), .NewFFLayout("false")) d_ff_4 (.Q(d_ff_4_q));  // open: clk, D, Qn, preset, en, reset
  // Probe on 13'hc
  Multiplexer #(.select(1), .width(32), .disabled("Z"), .enable("false")) multiplexer_11 (
    .in0(ALUResult), .in1(ram_1_data), .out(multiplexer_11_out), .sel(MemToReg));
  or or_14 (or_14_out, JAL, JALR);
  Multiplexer #(.select(1), .width(32), .disabled("Z"), .enable("false")) multiplexer_12 (
    .in0(multiplexer_11_out), .in1(PC_4), .out(multiplexer_12_out), .sel(or_14_out));
  Multiplexer #(.select(1), .width(32), .disabled("Z"), .enable("false")) multiplexer_13 (
    .in0(multiplexer_12_out), .in1(imm_U__12), .out(RDin), .sel(Lui));
  Comparator #(.width(13), .mode("twosComplement")) comparator_2 (
    .a(CNT_num), .b(13'hc), .eq(comparator_2_eq), .lt(comparator_2_lt));  // open: gt
  Clock #(.highDuration(1), .lowDuration(1)) clock_1 (.out(clock_1_out));
  Counter #(.width(13), .max('h1fff), .ongoal("stay"), .trigger("rising"), .behavior("old")) counter_2 (
    .count(comparator_2_lt), .Q(CNT_num), .clk(clock_1_out));  // open: load, D, carry, clr, preset
  Comparator #(.width(16), .mode("twosComplement")) comparator_3 (
    .a(16'h23b), .b(\总周期数 ), .eq(comparator_3_eq));  // open: gt, lt
  Comparator #(.width(16), .mode("twosComplement")) comparator_4 (
    .a(\总周期数 ), .b(16'h1), .eq(comparator_4_eq));  // open: gt, lt
  Comparator #(.width(16), .mode("twosComplement")) comparator_5 (
    .a(\总周期数 ), .b(16'h4), .eq(comparator_5_eq));  // open: gt, lt
  Comparator #(.width(16), .mode("twosComplement")) comparator_6 (
    .a(\总周期数 ), .b(16'h7), .eq(comparator_6_eq));  // open: gt, lt
  nand nand_1 (nand_1_out, d_ff_4_q, comparator_2_eq);
  or or_15 (or_15_out, comparator_3_eq, comparator_4_eq);
  assign controlled_inverter_1_out = or_15_out ? ~CLK : 1'bz;  // Controlled_Inverter controlled_inverter_1
  assign controlled_inverter_2_out = comparator_5_eq ? ~CLK : 1'bz;  // Controlled_Inverter controlled_inverter_2
  assign controlled_inverter_3_out = comparator_6_eq ? ~CLK : 1'bz;  // Controlled_Inverter controlled_inverter_3
  assign CLK = nand_1_out ? clock_1_out : 1'bz;  // Controlled_Buffer controlled_buffer_1
  Pull_Resistor #(.pull(1)) pull_resistor_1 (.node(CLK));
  Pull_Resistor #(.pull(0)) pull_resistor_2 (.node(controlled_inverter_1_out));
  Pull_Resistor #(.pull(0)) pull_resistor_3 (.node(controlled_inverter_2_out));
  Pull_Resistor #(.pull(0)) pull_resistor_4 (.node(controlled_inverter_3_out));

  // Notes on the sheet:
  //   中断源
  //   中断等待指示
  //   总复位信号应将除ROM以外所有存储组件全部清零
  //   三号中断源
  //   一号中断源
  //   一号中断等待指示
  //   二号中断源
  //   二号中断等待指示
  //   三号中断等待指示
  //   保存断点
  //   数码管输出
  //   数码管输出应该用寄存器锁存，否则显示数据只能一闪而过
  //   指令探针
  //   指令存储器
  //   Reset 
  //   Reset 
  //   Reset 
  //   指令字
  //   contents of rom_1 (hex, n*v repeats v):
  //   7d000113 100413 1f41993 41f9d993 433 c00913 800b13 140413 f47413 800293 100313 499993 89e9b3 1300533
  //   2200893 73 406282b3 fe0294e3 140413 f00f93 1f47433 1c41413 800293 100313 49d993 89e9b3 1300533
  //   2200893 73 406282b3 fe0294e3 1c45413 406b0b33 b0463 f95ff06f 2b3 fff2c293 1029293 fff2e293 500533
  //   2200893 73 f5dff06f 1112023 410113 a12023 410113 812023 410113 1312023 410113 1412023 410113 1512023
  //   410113 1612023 410113 100b13 300a13 100a93 1600433 441413 14469b3 1300533 2200893 73 fe0416e3
  //   415a0a33 fe0a10e3 ffc10113 12b03 ffc10113 12a83 ffc10113 12a03 ffc10113 12983 ffc10113 12403
  //   ffc10113 12503 ffc10113 12883 200073 1112023 410113 a12023 410113 812023 410113 1312023 410113
  //   1412023 410113 1512023 410113 1612023 410113 200b13 300a13 100a93 1600433 441413 14469b3 1300533
  //   2200893 73 fe0416e3 415a0a33 fe0a10e3 ffc10113 12b03 ffc10113 12a83 ffc10113 12a03 ffc10113 12983
  //   ffc10113 12403 ffc10113 12503 ffc10113 12883 200073 1112023 410113 a12023 410113 812023 410113
  //   1312023 410113 1412023 410113 1512023 410113 1612023 410113 300b13 300a13 100a93 1600433 441413
  //   14469b3 1300533 2200893 73 fe0416e3 415a0a33 fe0a10e3 ffc10113 12b03 ffc10113 12a83 ffc10113 12a03
  //   ffc10113 12983 ffc10113 12403 ffc10113 12503 ffc10113 12883 200073
  //   中断使能寄存器IE
  //   I
  //   S
  //   B
  //   跳转地址(beq/bne/bltu)
  //   J
  //   跳转地址(jal)
  //   U
  //   在中断响应周期和uret指令周期才可开/关中断
  //   Beq
  //   Bne
  //   MemToReg
  //   MemWrite
  //   AluOP
  //   AluSrcB
  //   RegWrite
  //   $a7编号
  //   $a0编号
  //   INTR
  //   SignImm
  //   选择需要清零的中断号
  //   WriteData
  //   ecall指令输出$a0到Led
  //   为方便自动评测，需要输出PC，IR，寄存器堆写如数据RDin
  //   跳转地址(jalr)
  //   存储器不支持半字访问，因此需要取出一个字的数据特殊处理
  //   RAM写使能MemWrite、RAM写入数据MDin等信号
  //   数据存储器
  //   ReadData
  //   控制位
  //   暂停节拍，不能为0
  //   保存到寄存器中的数据
  //   戳工具置1进入计数暂停模式，ctrl+k时钟自动运行到对应节拍暂停
  //   ctrl+k关闭时钟连续运行，将控制位置零，进入单步调试模式调试
  //   单级中断测试信号模拟器
  //   返回地址
  //   左移12位立即数
  //   可计数暂停的时钟源
endmodule

module \单周期_多级中断  (
  input  IR1,
  input  IR2,
  input  IR3,
  output RegWrite,
  output MemWrite,
  output [31:0] PC,
  output [31:0] IR,
  output [31:0] RDin,
  output [31:0] MDin,
  output [31:0] LedData
);

  wire _1_2_q, _2_2_q, _3_2_q, and_1_out, and_2_out, and_3_out, and_4_out, and_5_out, and_6_out, and_7_out,
       and_8_out, and_9_out, and_13_out, Beq, Bltu, Bne, CLK, clock_1_out, clr1, clr2, clr3, comparator_1_gt,
       comparator_2_eq, comparator_3_eq, comparator_3_lt, comparator_4_eq, comparator_5_eq, comparator_6_eq,
       comparator_7_eq, comparator_8_eq, csr, d_ff_1_q, d_ff_2_q, d_ff_3_q, d_ff_4_q, demultiplexer_1_out1,
       demultiplexer_1_out2, demultiplexer_1_out3, demultiplexer_2_out1, demultiplexer_2_out2,
       demultiplexer_2_out3, ecall, equ, Go, halt, IE, IR1_q, IR1_t, IR2_q, IR2_t, IR3_q, IR3_t, IRA, IRB,
       IRC, JAL, JALR, less, Lui, MemToReg, nand_1_out, not_1_out, not_2_out, not_3_out, not_4_out, or_1_out,
       or_2_out, or_6_out, or_7_out, or_8_out, or_11_out, or_13_out, or_14_out, or_15_out, or_16_out,
       or_17_out, priority_encoder_2_gs, pull_resistor_2_node, pull_resistor_3_node, pull_resistor_4_node,
       RST, S_type, Sh, uret, W1, W2, W3, \中断请求 , \单周期硬布线控制器_1_alu_src ;
  wire [1:0] multiplexer_11_out, priority_encoder_1_out, \running中断号 , \中断号 ;
  wire [3:0] \单周期硬布线控制器_1_alu_op ;
  wire [4:0] multiplexer_4_out, multiplexer_5_out;
  wire [11:0] multiplexer_3_out;
  wire [12:0] CNT_num;
  wire [15:0] \总周期数 ;
  wire [31:0] adder_2_out, adder_3_out, ALUResult, and_11_out, and_12_out, bit_extender_1_out,
       bit_extender_2_out, bit_extender_3_out, bit_extender_4_out, EPC, EPC1_q, EPC2_q, EPC3_q, imm_U__12,
       multiplexer_2_out, multiplexer_7_out, multiplexer_9_out, multiplexer_10_out, multiplexer_12_out,
       multiplexer_13_out, PC_4, ram_1_data, regifile_1_r1, regifile_1_r2, ShDin, shifter_1_out,
       shifter_2_out, shifter_4_out, \入口地址 , \断点 ;

  Button \u_继续运行  (.out(Go));
  Button _1 (.out(IRA));
  Button _2 (.out(IRB));
  Button _3 (.out(IRC));
  Button \u_总复位  (.out(RST));
  LED #(.active("true")) led_1 (.in(W1));
  LED #(.active("true")) led_2 (.in(W2));
  LED #(.active("true")) led_3 (.in(W3));
  and and_1 (and_1_out, Beq, equ);
  Hex_Digit_Display hex_digit_display_1 (.value(LedData[31:28]));  // open: dp
  not not_1 (not_1_out, equ);
  and and_2 (and_2_out, not_1_out, Bne);
  or or_1 (or_1_out, and_1_out, and_2_out, and_3_out);
  Priority_Encoder #(.select(2), .disabled("Z")) priority_encoder_1 (
    .in0(1'b1), .in1(or_1_out), .in2(JAL), .in3(JALR), .out(priority_encoder_1_out));  // open: gs, en_out, en_in
  Multiplexer #(.select(2), .width(32), .disabled("Z"), .enable("false")) multiplexer_1 (
    .in0(PC_4), .in1(adder_2_out), .in2(adder_3_out), .in3(ALUResult), .out(\断点 ),
    .sel(priority_encoder_1_out));
  Hex_Digit_Display hex_digit_display_2 (.value(LedData[23:20]));  // open: dp
  Hex_Digit_Display hex_digit_display_3 (.value(LedData[27:24]));  // open: dp
  and and_3 (and_3_out, less, Bltu);
  Hex_Digit_Display hex_digit_display_4 (.value(LedData[15:12]));  // open: dp
  Hex_Digit_Display hex_digit_display_5 (.value(LedData[19:16]));  // open: dp
  Multiplexer #(.select(2), .width(32), .disabled("Z"), .enable("false")) multiplexer_2 (
    .in0(\断点 ), .in1(\入口地址 ), .in2(EPC), .out(multiplexer_2_out), .sel({uret, \中断请求 }));  // open: in3
  not not_2 (not_2_out, halt);
  Hex_Digit_Display hex_digit_display_6 (.value(LedData[7:4]));  // open: dp
  Hex_Digit_Display hex_digit_display_7 (.value(LedData[11:8]));  // open: dp
  // Probe on \总周期数 
  Register #(.width(32), .trigger("rising"), .Select("low")) u_PC (
    .D(multiplexer_2_out), .en(or_2_out), .Q(PC), .clk(CLK), .clr(RST));
  or or_2 (or_2_out, not_2_out, Go);
  D_Flip_Flop #(.trigger("rising"), .Pre_Clr_Positions("LEGACY"), .NegatePresetClear("false"), .enable("true"), .NewFFLayout("false")) d_ff_1 (
    .clk(IRA), .D(1'b1), .Q(d_ff_1_q), .reset(IR1_q));  // open: Qn, preset, en
  or or_3 (W1, IR1_q, d_ff_1_q);
  D_Flip_Flop #(.trigger("rising"), .Pre_Clr_Positions("LEGACY"), .NegatePresetClear("false"), .enable("true"), .NewFFLayout("false")) d_ff_2 (
    .clk(IRB), .D(1'b1), .Q(d_ff_2_q), .reset(IR2_q));  // open: Qn, preset, en
  or or_4 (W2, IR2_q, d_ff_2_q);
  D_Flip_Flop #(.trigger("rising"), .Pre_Clr_Positions("LEGACY"), .NegatePresetClear("false"), .enable("true"), .NewFFLayout("false")) d_ff_3 (
    .clk(IRC), .D(1'b1), .Q(d_ff_3_q), .reset(IR3_q));  // open: Qn, preset, en
  or or_5 (W3, IR3_q, d_ff_3_q);
  Hex_Digit_Display hex_digit_display_8 (.value(LedData[3:0]));  // open: dp
  Adder #(.width(32)) adder_1 (.a(PC), .b(32'h4), .out(PC_4));  // open: cin, cout
  or or_6 (or_6_out, d_ff_1_q, IR1_q);
  or or_7 (or_7_out, d_ff_2_q, IR2_q);
  or or_8 (or_8_out, d_ff_3_q, IR3_q);
  and and_4 (and_4_out, or_6_out, ~and_5_out);  // AND_Gate
  and and_5 (and_5_out, clr1, uret);
  and and_6 (and_6_out, or_7_out, ~and_7_out);  // AND_Gate
  and and_7 (and_7_out, clr2, uret);
  and and_8 (and_8_out, or_8_out, ~and_9_out);  // AND_Gate
  and and_9 (and_9_out, clr3, uret);
  or or_9 (IR1_t, IR1, IRA);
  // RiscV_Probe riscv_probe_1: pin names not known; wires that end beside it: IR
  ROM #(.addrWidth(10), .dataWidth(32), .Select("high")) rom_1 (.addr(PC[11:2]), .data(IR));
  D_Flip_Flop #(.trigger("rising"), .Pre_Clr_Positions("LEGACY"), .NegatePresetClear("false"), .enable("true"), .NewFFLayout("false")) u_IR1 (
    .clk(CLK), .D(and_4_out), .Q(IR1_q), .reset(RST));  // open: Qn, preset, en
  D_Flip_Flop #(.trigger("rising"), .Pre_Clr_Positions("LEGACY"), .NegatePresetClear("false"), .enable("true"), .NewFFLayout("false")) u_IR2 (
    .clk(CLK), .D(and_6_out), .Q(IR2_q), .reset(RST));  // open: Qn, preset, en
  D_Flip_Flop #(.trigger("rising"), .Pre_Clr_Positions("LEGACY"), .NegatePresetClear("false"), .enable("true"), .NewFFLayout("false")) u_IR3 (
    .clk(CLK), .D(and_8_out), .Q(IR3_q), .reset(RST));  // open: Qn, preset, en
  or or_10 (IR2_t, IR2, IRB);
  D_Flip_Flop #(.trigger("rising"), .Pre_Clr_Positions("LEGACY"), .NegatePresetClear("false"), .enable("true"), .NewFFLayout("false")) u_IE (
    .clk(CLK), .D(IE), .Qn(IE), .en(or_11_out), .reset(RST));  // open: Q, preset
  or or_11 (or_11_out, \中断请求 , csr, uret);
  \单周期硬布线控制器  \u_单周期硬布线控制器_1  (
    .Funct({IR[30], IR[25], IR[14:12]}), .OP(IR[6:2]), .ALU_OP(\单周期硬布线控制器_1_alu_op ), .MemToReg(MemToReg),
    .MemWrite(MemWrite), .ALU_SRC(\单周期硬布线控制器_1_alu_src ), .RegWrite(RegWrite), .ecall(ecall),
    .S_type(S_type), .Jalr(JALR), .Beq(Beq), .JAL(JAL), .Bne(Bne), .in_3(IR[21]), .uret(uret), .Lui(Lui),
    .Sh(Sh), .Bltu(Bltu), .csr(csr));  // open: rs1used, rs2used
  Multiplexer #(.select(1), .width(12), .disabled("Z"), .enable("false")) multiplexer_3 (
    .in0(IR[31:20]), .in1({IR[31:25], IR[11:7]}), .out(multiplexer_3_out), .sel(S_type));
  assign bit_extender_1_out = {{20{IR[31]}}, {IR[31], IR[7], IR[30:25], IR[11:8]}};  // Bit_Extender bit_extender_1
  assign bit_extender_2_out = {{12{IR[31]}}, {IR[31], IR[19:12], IR[20], IR[30:21]}};  // Bit_Extender bit_extender_2
  assign bit_extender_3_out = {{12{IR[31]}}, IR[31:12]};  // Bit_Extender bit_extender_3
  or or_12 (IR3_t, IR3, IRC);
  Multiplexer #(.select(1), .width(5), .disabled("Z"), .enable("false")) multiplexer_4 (
    .in0(IR[19:15]), .in1(5'b10001), .out(multiplexer_4_out), .sel(ecall));
  Multiplexer #(.select(1), .width(5), .disabled("Z"), .enable("false")) multiplexer_5 (
    .in0(IR[24:20]), .in1(5'b01010), .out(multiplexer_5_out), .sel(ecall));
  assign bit_extender_4_out = {{20{multiplexer_3_out[11]}}, multiplexer_3_out};  // Bit_Extender bit_extender_4
  Shifter #(.width(32), .shift("ll")) shifter_1 (.in(bit_extender_1_out), .\dist (5'b00001), .out(shifter_1_out));
  Shifter #(.width(32), .shift("ll")) shifter_2 (.in(bit_extender_2_out), .\dist (5'b00001), .out(shifter_2_out));
  Shifter #(.width(32), .shift("ll")) shifter_3 (.in(bit_extender_3_out), .\dist (5'b01100), .out(imm_U__12));
  Priority_Encoder #(.select(2), .disabled("Z")) priority_encoder_2 (
    .in1(IR1_q), .in2(IR2_q), .in3(IR3_q), .out(\中断号 ), .gs(priority_encoder_2_gs), .en_in(1'b1));  // open: in0, en_out
  Regifile regifile_1 (
    .Din(RDin), .Clk(CLK), .R1(regifile_1_r1), .R2(regifile_1_r2), .WE(RegWrite), .W_num(IR[11:7]),
    .R1_num(multiplexer_4_out), .R2_num(multiplexer_5_out));
  Adder #(.width(32)) adder_2 (.a(shifter_1_out), .b(PC), .out(adder_2_out));  // open: cin, cout
  Adder #(.width(32)) adder_3 (.a(shifter_2_out), .b(PC), .out(adder_3_out));  // open: cin, cout
  Multiplexer #(.select(2), .width(32), .disabled("Z"), .enable("false")) multiplexer_6 (
    .in1(32'h30ac), .in2(32'h3158), .in3(32'h3204), .out(\入口地址 ), .sel(\中断号 ));  // open: in0
  and and_10 (\中断请求 , priority_encoder_2_gs, comparator_1_gt, IE);
  Comparator #(.width(2), .mode("unsigned")) comparator_1 (
    .a(\中断号 ), .b(\running中断号 ), .gt(comparator_1_gt));  // open: eq, lt
  Decoder #(.select(2), .tristate("false"), .disabled("Z"), .enable("false")) decoder_1 (
    .out1(clr1), .out2(clr2), .out3(clr3), .sel(\running中断号 ));  // open: out0
  Multiplexer #(.select(1), .width(32), .disabled("Z"), .enable("false")) multiplexer_7 (
    .in0(regifile_1_r2), .in1(bit_extender_4_out), .out(multiplexer_7_out), .sel(\单周期硬布线控制器_1_alu_src ));
  assign and_11_out = 32'hffff & regifile_1_r2;  // AND_Gate and_11, 32 bits wide
  Shifter #(.width(32), .shift("ll")) shifter_4 (.in(regifile_1_r2), .\dist (5'b10000), .out(shifter_4_out));
  ALU alu_1 (
    .X(regifile_1_r1), .Y(multiplexer_7_out), .AluOP(\单周期硬布线控制器_1_alu_op ), .Equal(equ), .Result(ALUResult),
    .out_6(less));  // open: Result_2, out_4
  Multiplexer #(.select(1), .width(32), .disabled("Z"), .enable("false")) multiplexer_8 (
    .in0(regifile_1_r2), .in1(ShDin), .out(MDin), .sel(Sh));
  Multiplexer #(.select(1), .width(32), .disabled("Z"), .enable("false")) multiplexer_9 (
    .in0(32'hffff0000), .in1(32'hffff), .out(multiplexer_9_out), .sel(ALUResult[1]));
  Multiplexer #(.select(1), .width(32), .disabled("Z"), .enable("false")) multiplexer_10 (
    .in0(and_11_out), .in1(shifter_4_out), .out(multiplexer_10_out), .sel(ALUResult[1]));
  Comparator #(.width(32), .mode("twosComplement")) comparator_2 (
    .a(regifile_1_r1), .b(32'h22), .eq(comparator_2_eq));  // open: gt, lt
  not not_3 (not_3_out, comparator_2_eq);
  assign and_12_out = ram_1_data & multiplexer_9_out;  // AND_Gate and_12, 32 bits wide
  and and_13 (and_13_out, ecall, comparator_2_eq);
  and and_14 (halt, ecall, not_3_out);
  not not_4 (not_4_out, halt);
  or or_13 (or_13_out, not_4_out, Go);
  Counter #(.width(16), .max('hffff), .ongoal("wrap"), .trigger("rising"), .behavior("new")) counter_1 (
    .count(or_13_out), .Q(\总周期数 ), .clk(CLK), .clr(RST));  // open: load, D, carry, preset, down
  RAM #(.addrWidth(10), .dataWidth(32), .bus("separate"), .Select("high")) ram_1 (
    .addr(ALUResult[11:2]), .din(MDin), .data(ram_1_data), .str(MemWrite), .clk(CLK), .clr(RST));  // open: sel, ld
  Adder #(.width(32)) adder_4 (.a(and_12_out), .b(multiplexer_10_out), .out(ShDin));  // open: cin, cout
  Register #(.width(32), .trigger("rising"), .Select("low")) register_1 (
    .D(regifile_1_r2), .en(and_13_out), .Q(LedData), .clk(CLK), .clr(RST));
  Demultiplexer #(.select(2), .width(1), .tristate("false"), .disabled("Z"), .enable("false")) demultiplexer_1 (
    .out1(demultiplexer_1_out1), .out2(demultiplexer_1_out2), .out3(demultiplexer_1_out3), .in(\中断请求 ),
    .sel(\中断号 ));  // open: out0
  Demultiplexer #(.select(2), .width(1), .tristate("false"), .disabled("Z"), .enable("false")) demultiplexer_2 (
    .out1(demultiplexer_2_out1), .out2(demultiplexer_2_out2), .out3(demultiplexer_2_out3), .in(or_14_out),
    .sel(multiplexer_11_out));  // open: out0
  or or_14 (or_14_out, \中断请求 , uret);
  Multiplexer #(.select(1), .width(2), .disabled("Z"), .enable("false")) multiplexer_11 (
    .in0(\中断号 ), .in1(\running中断号 ), .out(multiplexer_11_out), .sel(uret));
  D_Flip_Flop #(.trigger("high"), .Pre_Clr_Positions("LEGACY"), .NegatePresetClear("false"), .enable("true"), .NewFFLayout("false")) d_ff_4 (.Q(d_ff_4_q));  // open: clk, D, Qn, preset, en, reset
  // Probe on 13'hc
  Comparator #(.width(13), .mode("twosComplement")) comparator_3 (
    .a(CNT_num), .b(13'hc), .eq(comparator_3_eq), .lt(comparator_3_lt));  // open: gt
  Clock #(.highDuration(1), .lowDuration(1)) clock_1 (.out(clock_1_out));
  Multiplexer #(.select(1), .width(32), .disabled("Z"), .enable("false")) multiplexer_12 (
    .in0(ALUResult), .in1(ram_1_data), .out(multiplexer_12_out), .sel(MemToReg));
  or or_15 (or_15_out, JAL, JALR);
  Multiplexer #(.select(1), .width(32), .disabled("Z"), .enable("false")) multiplexer_13 (
    .in0(multiplexer_12_out), .in1(PC_4), .out(multiplexer_13_out), .sel(or_15_out));
  Counter #(.width(13), .max('h1fff), .ongoal("stay"), .trigger("rising"), .behavior("old")) counter_2 (
    .count(comparator_3_lt), .Q(CNT_num), .clk(clock_1_out));  // open: load, D, carry, clr, preset
  Comparator #(.width(16), .mode("twosComplement")) comparator_4 (
    .a(\总周期数 ), .b(16'h7), .eq(comparator_4_eq));  // open: gt, lt
  Comparator #(.width(16), .mode("twosComplement")) comparator_5 (
    .a(\总周期数 ), .b(16'h241), .eq(comparator_5_eq));  // open: gt, lt
  Multiplexer #(.select(1), .width(32), .disabled("Z"), .enable("false")) multiplexer_14 (
    .in0(multiplexer_13_out), .in1(imm_U__12), .out(RDin), .sel(Lui));
  Register #(.width(32), .trigger("rising"), .Select("low")) EPC1 (
    .D(\断点 ), .en(demultiplexer_1_out1), .Q(EPC1_q), .clk(CLK), .clr(RST));
  Register #(.width(32), .trigger("rising"), .Select("low")) EPC2 (
    .D(\断点 ), .en(demultiplexer_1_out2), .Q(EPC2_q), .clk(CLK), .clr(RST));
  Register #(.width(32), .trigger("rising"), .Select("low")) EPC3 (
    .D(\断点 ), .en(demultiplexer_1_out3), .Q(EPC3_q), .clk(CLK), .clr(RST));
  Register #(.width(1), .trigger("rising"), .Select("low")) _1_2 (
    .D(\中断请求 ), .en(demultiplexer_2_out1), .Q(_1_2_q), .clk(CLK), .clr(RST));
  Register #(.width(1), .trigger("rising"), .Select("low")) _2_2 (
    .D(\中断请求 ), .en(demultiplexer_2_out2), .Q(_2_2_q), .clk(CLK), .clr(RST));
  Register #(.width(1), .trigger("rising"), .Select("low")) _3_2 (
    .D(\中断请求 ), .en(demultiplexer_2_out3), .Q(_3_2_q), .clk(CLK), .clr(RST));
  nand nand_1 (nand_1_out, d_ff_4_q, comparator_3_eq);
  Comparator #(.width(16), .mode("twosComplement")) comparator_6 (
    .a(16'h258), .b(\总周期数 ), .eq(comparator_6_eq));  // open: gt, lt
  or or_16 (or_16_out, comparator_6_eq, comparator_7_eq);
  Comparator #(.width(16), .mode("twosComplement")) comparator_7 (
    .a(\总周期数 ), .b(16'h1), .eq(comparator_7_eq));  // open: gt, lt
  Comparator #(.width(16), .mode("twosComplement")) comparator_8 (
    .a(\总周期数 ), .b(16'h4), .eq(comparator_8_eq));  // open: gt, lt
  or or_17 (or_17_out, comparator_4_eq, comparator_5_eq);
  assign CLK = nand_1_out ? clock_1_out : 1'bz;  // Controlled_Buffer controlled_buffer_1
  Pull_Resistor #(.pull(1)) pull_resistor_1 (.node(CLK));
  Pull_Resistor #(.pull(0)) pull_resistor_2 (.node(pull_resistor_2_node));
  assign pull_resistor_2_node = or_16_out ? ~CLK : 1'bz;  // Controlled_Inverter controlled_inverter_1
  Pull_Resistor #(.pull(0)) pull_resistor_3 (.node(pull_resistor_3_node));
  assign pull_resistor_3_node = comparator_8_eq ? ~CLK : 1'bz;  // Controlled_Inverter controlled_inverter_2
  Pull_Resistor #(.pull(0)) pull_resistor_4 (.node(pull_resistor_4_node));
  assign pull_resistor_4_node = or_17_out ? ~CLK : 1'bz;  // Controlled_Inverter controlled_inverter_3
  Multiplexer #(.select(2), .width(32), .disabled("Z"), .enable("false")) multiplexer_15 (
    .in1(EPC1_q), .in2(EPC2_q), .in3(EPC3_q), .out(EPC), .sel(\running中断号 ));  // open: in0
  Priority_Encoder #(.select(2), .disabled("Z")) priority_encoder_3 (
    .in0(1'b1), .in1(_1_2_q), .in2(_2_2_q), .in3(_3_2_q), .out(\running中断号 ));  // open: gs, en_out, en_in

  // Notes on the sheet:
  //   中断源
  //   中断等待指示
  //   总复位信号应将除ROM以外所有存储组件全部清零
  //   数码管输出
  //   一号中断源
  //   一号中断等待指示
  //   二号中断源
  //   二号中断等待指示
  //   三号中断源
  //   三号中断等待指示
  //   数码管输出应该用寄存器锁存，否则显示数据只能一闪而过
  //   指令探针
  //   指令存储器
  //   指令字
  //   contents of rom_1 (hex, n*v repeats v):
  //   7d000113 100413 1f41993 41f9d993 433 c00913 800b13 140413 f47413 800293 100313 499993 89e9b3 1300533
  //   2200893 73 406282b3 fe0294e3 140413 f00f93 1f47433 1c41413 800293 100313 49d993 89e9b3 1300533
  //   2200893 73 406282b3 fe0294e3 1c45413 406b0b33 b0463 f95ff06f 2b3 fff2c293 1029293 fff2e293 500533
  //   2200893 73 f5dff06f 1112023 410113 a12023 410113 812023 410113 1312023 410113 1412023 410113 1512023
  //   410113 1612023 410113 40e073 100b13 300a13 100a93 1600433 441413 14469b3 1300533 2200893 73 fe0416e3
  //   415a0a33 fe0a10e3 40f073 ffc10113 12b03 ffc10113 12a83 ffc10113 12a03 ffc10113 12983 ffc10113 12403
  //   ffc10113 12503 ffc10113 12883 200073 1112023 410113 a12023 410113 812023 410113 1312023 410113
  //   1412023 410113 1512023 410113 1612023 410113 40e073 200b13 300a13 100a93 1600433 441413 14469b3
  //   1300533 2200893 73 fe0416e3 415a0a33 fe0a10e3 40f073 ffc10113 12b03 ffc10113 12a83 ffc10113 12a03
  //   ffc10113 12983 ffc10113 12403 ffc10113 12503 ffc10113 12883 200073 1112023 410113 a12023 410113
  //   812023 410113 1312023 410113 1412023 410113 1512023 410113 1612023 410113 40e073 300b13 300a13
  //   100a93 1600433 441413 14469b3 1300533 2200893 73 fe0416e3 415a0a33 fe0a10e3 40f073 ffc10113 12b03
  //   ffc10113 12a83 ffc10113 12a03 ffc10113 12983 ffc10113 12403 ffc10113 12503 ffc10113 12883 200073
  //   Reset 
  //   Reset 
  //   Reset 
  //   I
  //   S
  //   B
  //   J
  //   跳转地址(jal)
  //   U
  //   在中断响应周期和uret指令周期才可开/关中断
  //   中断使能寄存器IE
  //   Beq
  //   Bne
  //   MemToReg
  //   MemWrite
  //   AluOP
  //   AluSrcB
  //   RegWrite
  //   $a7编号
  //   $a0编号
  //   跳转地址(beq/bne/bltu)
  //   SignImm
  //   INTR
  //   防止中断服务程序在开中断后误产生中断请求
  //   选择需要清零的中断号
  //   为方便自动评测，需要输出PC，IR，寄存器堆写如数据RDin
  //   WriteData
  //   ecall指令输出$a0到Led
  //   RAM写使能MemWrite、RAM写入数据MDin等信号
  //   跳转地址(jalr)
  //   存储器不支持半字访问，因此需要取出一个字的数据特殊处理
  //   数据存储器
  //   ReadData
  //   中断响应周期保存断点
  //   控制位
  //   暂停节拍，不能为0
  //   戳工具置1进入计数暂停模式，ctrl+k时钟自动运行到对应节拍暂停
  //   ctrl+k关闭时钟连续运行，将控制位置零，进入单步调试模式调试
  //   保存到寄存器中的数据
  //   EPC寄存器堆
  //   如果该中断已经加入嵌套处理序列，则其中断号对应的寄存器状态为1
  //   中断请求为1则给新响应中断的寄存器置1；uret为1则给返回的中断寄存器置0
  //   多级中断测试信号模拟器
  //   返回地址
  //   左移12位立即数
  //   可计数暂停的时钟源
  //   中断返回周期送断点
  //   当前正在处理的中断的中断号
endmodule
module \流水线_单级中断  (
  output RegWrite,
  output MemWrite,
  output [31:0] IF_PC,
  output [31:0] ID_PC,
  output [31:0] EX_PC,
  output [31:0] M_PC,
  output [31:0] WB_PC,
  output [31:0] RDin,
  output [31:0] MDin,
  output [31:0] LedData
);

  wire and_1_out, and_2_out, and_3_out, and_5_out, and_6_out, and_7_out, and_8_out, and_9_out, and_10_out,
       and_12_out, and_13_out, and_14_out, and_15_out, Beq, Bltu, Bne, BranchTaken, CLK, clock_1_out, clr1,
       clr2, clr3, comparator_1_eq, comparator_2_eq, comparator_3_eq, comparator_3_lt, comparator_4_eq,
       Conditional, d_ff_1_q, d_ff_2_q, d_ff_3_q, d_ff_4_q, en, equ, EX_ecall, ex_mem_1_halt_2,
       ex_mem_1_jal_2, ex_mem_1_jalr_2, ex_mem_1_lui_2, ex_mem_1_memtoreg_2, ex_mem_1_regwrite_2,
       ex_mem_1_sh_2, EX_uret, Go, halt, ID_ecall, id_ex_1_alusrcb_2, id_ex_1_lui_2, id_ex_1_memtoreg_2,
       id_ex_1_memwrite_2, id_ex_1_regwrite_2, id_ex_1_sh_2, ID_uret, IE, IR1, IR1_q, IR2, IR2_q, IR3, IR3_q,
       JAL, JALR, less, mem_wb_1_jal_2, mem_wb_1_jalr_2, mem_wb_1_lui_2, mem_wb_1_memtoreg_2, nand_1_out,
       not_1_out, not_2_out, not_3_out, not_5_out, not_6_out, not_7_out, or_2_out, or_3_out, or_7_out,
       or_8_out, or_9_out, or_10_out, or_11_out, or_12_out, or_13_out, priority_encoder_2_gs, RST, S_type,
       Stall, W1, W2, W3, \中断请求 , \单周期硬布线控制器_1_alu_src , \单周期硬布线控制器_1_beq , \单周期硬布线控制器_1_bltu ,
       \单周期硬布线控制器_1_bne , \单周期硬布线控制器_1_jal , \单周期硬布线控制器_1_jalr , \单周期硬布线控制器_1_lui , \单周期硬布线控制器_1_memtoreg ,
       \单周期硬布线控制器_1_memwrite , \单周期硬布线控制器_1_regwrite , \单周期硬布线控制器_1_rs1used , \单周期硬布线控制器_1_rs2used ,
       \单周期硬布线控制器_1_sh , \相关处理逻辑_重定向_1_flush ;
  wire [1:0] id_ex_1_rs1fwd_2, id_ex_1_rs2fwd_2, priority_encoder_1_out, register_1_q, \中断号 ,
       \相关处理逻辑_重定向_1_rs1fwd , \相关处理逻辑_重定向_1_rs2fwd ;
  wire [3:0] id_ex_1_aluop_2, \单周期硬布线控制器_1_alu_op ;
  wire [4:0] ex_mem_1_rd_2, id_ex_1_rd_2, multiplexer_5_out, multiplexer_6_out, rd;
  wire [11:0] multiplexer_7_out;
  wire [12:0] CNT_num;
  wire [15:0] \LoadUse次数 , \总周期数 , \无条件分支数 , \条件分支成功数 ;
  wire [31:0] adder_1_out, adder_2_out, adder_3_out, adder_5_out, and_16_out, and_17_out, bit_extender_1_out,
       bit_extender_2_out, bit_extender_3_out, bit_extender_4_out, EPC, EX_ALUResult, EX_IR, ex_mem_1_rs2_2,
       id_ex_1_imm_b_2, id_ex_1_imm_is_2, id_ex_1_imm_j_2, id_ex_1_imm_u_2, id_ex_1_rs1_2, id_ex_1_rs2_2,
       ID_IR, IF_IR, imm_U, MEM_ALUResult, MEM_IR, mem_wb_1_aluresult_2, mem_wb_1_imm_u_2,
       mem_wb_1_readdata_2, multiplexer_2_out, multiplexer_3_out, multiplexer_4_out, multiplexer_8_out,
       multiplexer_9_out, multiplexer_11_out, multiplexer_13_out, multiplexer_14_out, multiplexer_15_out,
       multiplexer_16_out, ram_1_data, regifile_1_r1, regifile_1_r2, ShDin, shifter_1_out, shifter_2_out,
       shifter_3_out, shifter_4_out, WB_IR, \入口地址 , \断点 ;

  Button \u_总复位  (.out(RST));
  Button _1 (.out(IR1));
  Button _2 (.out(IR2));
  Button _3 (.out(IR3));
  // Probe on \总周期数 
  // Probe on \总周期数 
  Button \u_继续运行  (.out(Go));
  LED #(.active("true")) led_1 (.in(W1));
  LED #(.active("true")) led_2 (.in(W2));
  LED #(.active("true")) led_3 (.in(W3));
  not not_1 (not_1_out, equ);
  and and_1 (and_1_out, not_1_out, Bne);
  and and_2 (and_2_out, Beq, equ);
  or or_1 (Conditional, and_2_out, and_1_out, and_3_out);
  Priority_Encoder #(.select(2), .disabled("Z")) priority_encoder_1 (
    .in0(1'b1), .in1(Conditional), .in2(JAL), .in3(JALR), .out(priority_encoder_1_out));  // open: gs, en_out, en_in
  Hex_Digit_Display hex_digit_display_1 (.value(LedData[31:28]));  // open: dp
  // Probe on IF_PC[19:0]
  // RiscV_Probe riscv_probe_1: pin names not known; wires that end beside it: IF_IR
  and and_3 (and_3_out, less, Bltu);
  Multiplexer #(.select(2), .width(32), .disabled("Z"), .enable("false")) multiplexer_1 (
    .in0(adder_1_out), .in1(adder_2_out), .in2(adder_3_out), .in3(EX_ALUResult), .out(\断点 ),
    .sel(priority_encoder_1_out));
  Hex_Digit_Display hex_digit_display_2 (.value(LedData[27:24]));  // open: dp
  Hex_Digit_Display hex_digit_display_3 (.value(LedData[23:20]));  // open: dp
  // Probe on ID_PC[19:0]
  // RiscV_Probe riscv_probe_2: pin names not known; wires that end beside it: ID_IR
  \相关处理逻辑_重定向  \u_相关处理逻辑_重定向_1  (
    .rs1used(\单周期硬布线控制器_1_rs1used ), .rs2used(\单周期硬布线控制器_1_rs2used ), .BranchTaken(BranchTaken),
    .EX_RegWrite(id_ex_1_regwrite_2), .EX_WriteReg_num(id_ex_1_rd_2), .MEM_RegWrite(ex_mem_1_regwrite_2),
    .MEM_WriteReg_num(ex_mem_1_rd_2), .Instr(ID_IR), .Stall(Stall), .Flush(\相关处理逻辑_重定向_1_flush ),
    .ecall(ID_ecall), .EX_MemToReg(id_ex_1_memtoreg_2), .rs1Fwd(\相关处理逻辑_重定向_1_rs1fwd ),
    .EX_Lui(id_ex_1_lui_2), .rs2Fwd(\相关处理逻辑_重定向_1_rs2fwd ), .\中断请求 (\中断请求 ));
  not not_2 (not_2_out, halt);
  or or_2 (or_2_out, not_2_out, Go);
  Multiplexer #(.select(2), .width(32), .disabled("Z"), .enable("false")) multiplexer_2 (
    .in0(\断点 ), .in1(\入口地址 ), .in2(EPC), .out(multiplexer_2_out), .sel({EX_uret, \中断请求 }));  // open: in3
  Hex_Digit_Display hex_digit_display_4 (.value(LedData[19:16]));  // open: dp
  Hex_Digit_Display hex_digit_display_5 (.value(LedData[15:12]));  // open: dp
  not not_3 (not_3_out, Stall);
  and and_4 (en, not_3_out, or_2_out);
  not not_4 (BranchTaken, comparator_1_eq);
  Comparator #(.width(2), .mode("twosComplement")) comparator_1 (
    .a(2'b00), .b(priority_encoder_1_out), .eq(comparator_1_eq));  // open: gt, lt
  Register #(.width(32), .trigger("rising"), .Select("low")) PC (
    .D(multiplexer_2_out), .en(en), .Q(IF_PC), .clk(CLK), .clr(RST));
  Hex_Digit_Display hex_digit_display_6 (.value(LedData[11:8]));  // open: dp
  Hex_Digit_Display hex_digit_display_7 (.value(LedData[7:4]));  // open: dp
  // Probe on EX_PC[19:0]
  // RiscV_Probe riscv_probe_3: pin names not known; wires that end beside it: EX_IR
  Adder #(.width(32)) adder_1 (.a(IF_PC), .b(32'h4), .out(adder_1_out));  // open: cin, cout
  Hex_Digit_Display hex_digit_display_8 (.value(LedData[3:0]));  // open: dp
  ROM #(.addrWidth(10), .dataWidth(32), .Select("high")) rom_1 (.addr(IF_PC[11:2]), .data(IF_IR));
  // Probe on \总周期数 
  // Probe on M_PC[19:0]
  // RiscV_Probe riscv_probe_4: pin names not known; wires that end beside it: MEM_IR
  or or_3 (or_3_out, BranchTaken, \中断请求 , EX_uret);
  IF_ID if_id_1 (
    .IR(IF_IR), .PC(IF_PC), .IR_2(ID_IR), .PC_2(ID_PC), .en(en), .clk(CLK), .clr(or_3_out), .rst(RST));  // open: PredictJump, PredictJump_2
  // Probe on \总周期数 
  // Probe on \无条件分支数 
  // Probe on \条件分支成功数 
  // Probe on \LoadUse次数 
  // Probe on \LoadUse次数 
  // Probe on IF_PC[11:0]
  // Probe on WB_PC[19:0]
  // RiscV_Probe riscv_probe_5: pin names not known; wires that end beside it: WB_IR
  Comparator #(.width(32), .mode("twosComplement")) comparator_2 (
    .a(ID_IR), .b({32{1'b0}}), .eq(comparator_2_eq));  // open: gt, lt
  Multiplexer #(.select(1), .width(32), .disabled("Z"), .enable("false")) multiplexer_3 (
    .in0(ID_PC), .in1(IF_PC), .out(multiplexer_3_out), .sel(comparator_2_eq));
  // Probe on EX_PC[11:0]
  // Probe on ID_PC[11:0]
  \单周期硬布线控制器  \u_单周期硬布线控制器_1  (
    .Funct({ID_IR[30], ID_IR[25], ID_IR[14:12]}), .OP(ID_IR[6:2]), .ALU_OP(\单周期硬布线控制器_1_alu_op ),
    .MemToReg(\单周期硬布线控制器_1_memtoreg ), .MemWrite(\单周期硬布线控制器_1_memwrite ), .ALU_SRC(\单周期硬布线控制器_1_alu_src ),
    .RegWrite(\单周期硬布线控制器_1_regwrite ), .ecall(ID_ecall), .S_type(S_type), .Jalr(\单周期硬布线控制器_1_jalr ),
    .Beq(\单周期硬布线控制器_1_beq ), .JAL(\单周期硬布线控制器_1_jal ), .Bne(\单周期硬布线控制器_1_bne ), .in_3(ID_IR[21]),
    .uret(ID_uret), .Lui(\单周期硬布线控制器_1_lui ), .Sh(\单周期硬布线控制器_1_sh ), .Bltu(\单周期硬布线控制器_1_bltu ),
    .rs1used(\单周期硬布线控制器_1_rs1used ), .rs2used(\单周期硬布线控制器_1_rs2used ));  // open: csr
  D_Flip_Flop #(.trigger("rising"), .Pre_Clr_Positions("LEGACY"), .NegatePresetClear("false"), .enable("true"), .NewFFLayout("false")) d_ff_1 (
    .clk(IR1), .D(1'b1), .Q(d_ff_1_q), .reset(IR1_q));  // open: Qn, preset, en
  or or_4 (W1, IR1_q, d_ff_1_q);
  D_Flip_Flop #(.trigger("rising"), .Pre_Clr_Positions("LEGACY"), .NegatePresetClear("false"), .enable("true"), .NewFFLayout("false")) d_ff_2 (
    .clk(IR2), .D(1'b1), .Q(d_ff_2_q), .reset(IR2_q));  // open: Qn, preset, en
  or or_5 (W2, IR2_q, d_ff_2_q);
  D_Flip_Flop #(.trigger("rising"), .Pre_Clr_Positions("LEGACY"), .NegatePresetClear("false"), .enable("true"), .NewFFLayout("false")) d_ff_3 (
    .clk(IR3), .D(1'b1), .Q(d_ff_3_q), .reset(IR3_q));  // open: Qn, preset, en
  or or_6 (W3, IR3_q, d_ff_3_q);
  Multiplexer #(.select(1), .width(32), .disabled("Z"), .enable("false")) multiplexer_4 (
    .in0(multiplexer_3_out), .in1(\断点 ), .out(multiplexer_4_out), .sel(BranchTaken));
  // Probe on M_PC[11:0]
  D_Flip_Flop #(.trigger("high"), .Pre_Clr_Positions("LEGACY"), .NegatePresetClear("false"), .enable("true"), .NewFFLayout("false")) d_ff_4 (.Q(d_ff_4_q));  // open: clk, D, Qn, preset, en, reset
  // Probe on 13'he27
  Multiplexer #(.select(1), .width(5), .disabled("Z"), .enable("false")) multiplexer_5 (
    .in0(ID_IR[19:15]), .in1(5'b10001), .out(multiplexer_5_out), .sel(ID_ecall));
  Multiplexer #(.select(1), .width(5), .disabled("Z"), .enable("false")) multiplexer_6 (
    .in0(ID_IR[24:20]), .in1(5'b01010), .out(multiplexer_6_out), .sel(ID_ecall));
  assign bit_extender_1_out = {{20{multiplexer_7_out[11]}}, multiplexer_7_out};  // Bit_Extender bit_extender_1
  Multiplexer #(.select(1), .width(12), .disabled("Z"), .enable("false")) multiplexer_7 (
    .in0(ID_IR[31:20]), .in1({ID_IR[31:25], ID_IR[11:7]}), .out(multiplexer_7_out), .sel(S_type));
  assign bit_extender_2_out = {{20{ID_IR[31]}}, {ID_IR[31], ID_IR[7], ID_IR[30:25], ID_IR[11:8]}};  // Bit_Extender bit_extender_2
  assign bit_extender_3_out = {{12{ID_IR[31]}}, {ID_IR[31], ID_IR[19:12], ID_IR[20], ID_IR[30:21]}};  // Bit_Extender bit_extender_3
  assign bit_extender_4_out = {{12{ID_IR[31]}}, ID_IR[31:12]};  // Bit_Extender bit_extender_4
  Register #(.width(32), .trigger("rising"), .Select("low")) u_EPC (
    .D(multiplexer_4_out), .en(\中断请求 ), .Q(EPC), .clk(CLK), .clr(RST));
  // Probe on WB_PC[11:0]
  Comparator #(.width(13), .mode("twosComplement")) comparator_3 (
    .a(CNT_num), .b(13'he27), .eq(comparator_3_eq), .lt(comparator_3_lt));  // open: gt
  Clock #(.highDuration(1), .lowDuration(1)) clock_1 (.out(clock_1_out));
  or or_7 (or_7_out, d_ff_1_q, IR1_q);
  and and_5 (and_5_out, or_7_out, ~and_6_out);  // AND_Gate
  and and_6 (and_6_out, clr1, EX_uret);
  or or_8 (or_8_out, d_ff_2_q, IR2_q);
  and and_7 (and_7_out, or_8_out, ~and_8_out);  // AND_Gate
  and and_8 (and_8_out, clr2, EX_uret);
  or or_9 (or_9_out, d_ff_3_q, IR3_q);
  and and_9 (and_9_out, or_9_out, ~and_10_out);  // AND_Gate
  and and_10 (and_10_out, clr3, EX_uret);
  nand nand_1 (nand_1_out, d_ff_4_q, comparator_3_eq);
  Counter #(.width(13), .max('h1fff), .ongoal("stay"), .trigger("rising"), .behavior("old")) counter_1 (
    .count(comparator_3_lt), .Q(CNT_num), .clk(clock_1_out));  // open: load, D, carry, clr, preset
  Regifile regifile_1 (
    .Din(RDin), .Clk(CLK), .R1(regifile_1_r1), .R2(regifile_1_r2), .WE(RegWrite), .W_num(rd),
    .R1_num(multiplexer_5_out), .R2_num(multiplexer_6_out));
  D_Flip_Flop #(.trigger("rising"), .Pre_Clr_Positions("LEGACY"), .NegatePresetClear("false"), .enable("true"), .NewFFLayout("false")) u_IR1 (
    .clk(CLK), .D(and_5_out), .Q(IR1_q), .reset(RST));  // open: Qn, preset, en
  D_Flip_Flop #(.trigger("rising"), .Pre_Clr_Positions("LEGACY"), .NegatePresetClear("false"), .enable("true"), .NewFFLayout("false")) u_IR2 (
    .clk(CLK), .D(and_7_out), .Q(IR2_q), .reset(RST));  // open: Qn, preset, en
  D_Flip_Flop #(.trigger("rising"), .Pre_Clr_Positions("LEGACY"), .NegatePresetClear("false"), .enable("true"), .NewFFLayout("false")) u_IR3 (
    .clk(CLK), .D(and_9_out), .Q(IR3_q), .reset(RST));  // open: Qn, preset, en
  assign CLK = nand_1_out ? clock_1_out : 1'bz;  // Controlled_Buffer controlled_buffer_1
  or or_10 (or_10_out, \相关处理逻辑_重定向_1_flush , \中断请求 , EX_uret);
  ID_EX id_ex_1 (
    .Beq(\单周期硬布线控制器_1_beq ), .Bne(\单周期硬布线控制器_1_bne ), .MemToReg(\单周期硬布线控制器_1_memtoreg ),
    .MemWrite(\单周期硬布线控制器_1_memwrite ), .AluOP(\单周期硬布线控制器_1_alu_op ), .AluSrcB(\单周期硬布线控制器_1_alu_src ),
    .RegWrite(\单周期硬布线控制器_1_regwrite ), .Ecall(ID_ecall), .JAL(\单周期硬布线控制器_1_jal ), .JALR(\单周期硬布线控制器_1_jalr ),
    .Lui(\单周期硬布线控制器_1_lui ), .Sh(\单周期硬布线控制器_1_sh ), .Bltu(\单周期硬布线控制器_1_bltu ), .rs1(regifile_1_r1),
    .rs2(regifile_1_r2), .imm_IS(bit_extender_1_out), .imm_B(bit_extender_2_out), .imm_J(bit_extender_3_out),
    .imm_U(bit_extender_4_out), .rd(ID_IR[11:7]), .IR(ID_IR), .PC(ID_PC), .Beq_2(Beq), .Bne_2(Bne),
    .MemToReg_2(id_ex_1_memtoreg_2), .MemWrite_2(id_ex_1_memwrite_2), .AluOP_2(id_ex_1_aluop_2),
    .AluSrcB_2(id_ex_1_alusrcb_2), .RegWrite_2(id_ex_1_regwrite_2), .Ecall_2(EX_ecall), .JAL_2(JAL),
    .JALR_2(JALR), .Lui_2(id_ex_1_lui_2), .Sh_2(id_ex_1_sh_2), .Bltu_2(Bltu), .rs1_2(id_ex_1_rs1_2),
    .rs2_2(id_ex_1_rs2_2), .imm_IS_2(id_ex_1_imm_is_2), .imm_B_2(id_ex_1_imm_b_2), .imm_J_2(id_ex_1_imm_j_2),
    .imm_U_2(id_ex_1_imm_u_2), .rd_2(id_ex_1_rd_2), .IR_2(EX_IR), .PC_2(EX_PC), .en(or_2_out), .clk(CLK),
    .clr(or_10_out), .rs1Fwd(\相关处理逻辑_重定向_1_rs1fwd ), .rs2Fwd(\相关处理逻辑_重定向_1_rs2fwd ),
    .rs1Fwd_2(id_ex_1_rs1fwd_2), .rs2Fwd_2(id_ex_1_rs2fwd_2), .uret(ID_uret), .uret_2(EX_uret), .rst(RST));  // open: PredictJump, PredictJump_2
  D_Flip_Flop #(.trigger("rising"), .Pre_Clr_Positions("LEGACY"), .NegatePresetClear("false"), .enable("true"), .NewFFLayout("false")) u_IE (
    .clk(CLK), .D(IE), .Qn(IE), .en(or_11_out), .reset(RST));  // open: Q, preset
  or or_11 (or_11_out, \中断请求 , EX_uret);
  Pull_Resistor #(.pull(1)) pull_resistor_1 (.node(CLK));
  Shifter #(.width(32), .shift("ll")) shifter_1 (.in(id_ex_1_imm_b_2), .\dist (5'b00001), .out(shifter_1_out));
  Shifter #(.width(32), .shift("ll")) shifter_2 (.in(id_ex_1_imm_j_2), .\dist (5'b00001), .out(shifter_2_out));
  Shifter #(.width(32), .shift("ll")) shifter_3 (.in(id_ex_1_imm_u_2), .\dist (5'b01100), .out(shifter_3_out));
  Priority_Encoder #(.select(2), .disabled("Z")) priority_encoder_2 (
    .in1(IR1_q), .in2(IR2_q), .in3(IR3_q), .out(\中断号 ), .gs(priority_encoder_2_gs), .en_in(1'b1));  // open: in0, en_out
  not not_5 (not_5_out, halt);
  Multiplexer #(.select(2), .width(32), .disabled("Z"), .enable("false")) multiplexer_8 (
    .in0(id_ex_1_rs1_2), .in1(RDin), .in2(MEM_ALUResult), .in3(imm_U), .out(multiplexer_8_out),
    .sel(id_ex_1_rs1fwd_2));
  Multiplexer #(.select(2), .width(32), .disabled("Z"), .enable("false")) multiplexer_9 (
    .in0(id_ex_1_rs2_2), .in1(RDin), .in2(MEM_ALUResult), .in3(imm_U), .out(multiplexer_9_out),
    .sel(id_ex_1_rs2fwd_2));
  Adder #(.width(32)) adder_2 (.a(shifter_1_out), .b(EX_PC), .out(adder_2_out));  // open: cin, cout
  Adder #(.width(32)) adder_3 (.a(shifter_2_out), .b(EX_PC), .out(adder_3_out));  // open: cin, cout
  Multiplexer #(.select(2), .width(32), .disabled("Z"), .enable("false")) multiplexer_10 (
    .in1(32'h30ac), .in2(32'h3150), .in3(32'h31f4), .out(\入口地址 ), .sel(\中断号 ));  // open: in0
  or or_12 (or_12_out, not_5_out, Go);
  Counter #(.width(16), .max('hffff), .ongoal("wrap"), .trigger("rising"), .behavior("new")) counter_2 (
    .count(or_12_out), .Q(\总周期数 ), .clk(CLK), .clr(RST));  // open: load, D, carry, preset, down
  Multiplexer #(.select(1), .width(32), .disabled("Z"), .enable("false")) multiplexer_11 (
    .in0(multiplexer_9_out), .in1(id_ex_1_imm_is_2), .out(multiplexer_11_out), .sel(id_ex_1_alusrcb_2));
  and and_11 (\中断请求 , priority_encoder_2_gs, IE);
  Register #(.width(2), .trigger("rising"), .Select("low")) register_1 (
    .D(\中断号 ), .en(\中断请求 ), .Q(register_1_q), .clk(CLK), .clr(RST));
  Decoder #(.select(2), .tristate("false"), .disabled("Z"), .enable("false")) decoder_1 (
    .out1(clr1), .out2(clr2), .out3(clr3), .sel(register_1_q));  // open: out0
  ALU alu_1 (
    .X(multiplexer_8_out), .Y(multiplexer_11_out), .AluOP(id_ex_1_aluop_2), .Equal(equ),
    .Result(EX_ALUResult), .out_6(less));  // open: Result_2, out_4
  Comparator #(.width(32), .mode("twosComplement")) comparator_4 (
    .a(multiplexer_8_out), .b(32'h22), .eq(comparator_4_eq));  // open: gt, lt
  not not_6 (not_6_out, comparator_4_eq);
  Counter #(.width(16), .max('hffff), .ongoal("wrap"), .trigger("rising"), .behavior("new")) counter_3 (
    .count(Stall), .Q(\LoadUse次数 ), .clk(CLK), .clr(RST));  // open: load, D, carry, preset, down
  Register #(.width(32), .trigger("rising"), .Select("low")) register_2 (
    .D(multiplexer_9_out), .en(and_12_out), .Q(LedData), .clk(CLK), .clr(RST));
  and and_12 (and_12_out, EX_ecall, comparator_4_eq);
  and and_13 (and_13_out, EX_ecall, not_6_out);
  not not_7 (not_7_out, Conditional);
  and and_14 (and_14_out, BranchTaken, not_7_out);
  Counter #(.width(16), .max('hffff), .ongoal("wrap"), .trigger("rising"), .behavior("new")) counter_4 (
    .count(and_14_out), .Q(\无条件分支数 ), .clk(CLK), .clr(RST));  // open: load, D, carry, preset, down
  EX_MEM ex_mem_1 (
    .MemToReg(id_ex_1_memtoreg_2), .MemWrite(id_ex_1_memwrite_2), .RegWrite(id_ex_1_regwrite_2), .JAL(JAL),
    .JALR(JALR), .Lui(id_ex_1_lui_2), .Sh(id_ex_1_sh_2), .ALUResult(EX_ALUResult), .rs2(multiplexer_9_out),
    .imm_U(shifter_3_out), .halt(and_13_out), .rd(id_ex_1_rd_2), .IR(EX_IR), .PC(EX_PC),
    .MemToReg_2(ex_mem_1_memtoreg_2), .MemWrite_2(MemWrite), .RegWrite_2(ex_mem_1_regwrite_2),
    .JAL_2(ex_mem_1_jal_2), .JALR_2(ex_mem_1_jalr_2), .Lui_2(ex_mem_1_lui_2), .Sh_2(ex_mem_1_sh_2),
    .ALUResult_2(MEM_ALUResult), .rs2_2(ex_mem_1_rs2_2), .imm_U_2(imm_U), .halt_2(ex_mem_1_halt_2),
    .rd_2(ex_mem_1_rd_2), .IR_2(MEM_IR), .PC_2(M_PC), .en(or_2_out), .clk(CLK), .rst(RST));
  Multiplexer #(.select(1), .width(32), .disabled("Z"), .enable("false")) multiplexer_12 (
    .in0(ex_mem_1_rs2_2), .in1(ShDin), .out(MDin), .sel(ex_mem_1_sh_2));
  Shifter #(.width(32), .shift("ll")) shifter_4 (.in(ex_mem_1_rs2_2), .\dist (5'b10000), .out(shifter_4_out));
  and and_15 (and_15_out, BranchTaken, Conditional);
  Counter #(.width(16), .max('hffff), .ongoal("wrap"), .trigger("rising"), .behavior("new")) counter_5 (
    .count(and_15_out), .Q(\条件分支成功数 ), .clk(CLK), .clr(RST));  // open: load, D, carry, preset, down
  Multiplexer #(.select(1), .width(32), .disabled("Z"), .enable("false")) multiplexer_13 (
    .in0(32'hffff0000), .in1(32'hffff), .out(multiplexer_13_out), .sel(MEM_ALUResult[1]));
  assign and_16_out = 32'hffff & ex_mem_1_rs2_2;  // AND_Gate and_16, 32 bits wide
  Multiplexer #(.select(1), .width(32), .disabled("Z"), .enable("false")) multiplexer_14 (
    .in0(and_16_out), .in1(shifter_4_out), .out(multiplexer_14_out), .sel(MEM_ALUResult[1]));
  assign and_17_out = ram_1_data & multiplexer_13_out;  // AND_Gate and_17, 32 bits wide
  RAM #(.addrWidth(10), .dataWidth(32), .bus("separate"), .Select("high")) ram_1 (
    .addr(MEM_ALUResult[11:2]), .din(MDin), .data(ram_1_data), .str(MemWrite), .clk(CLK), .clr(RST));  // open: sel, ld
  Adder #(.width(32)) adder_4 (.a(and_17_out), .b(multiplexer_14_out), .out(ShDin));  // open: cin, cout
  MEM_WB mem_wb_1 (
    .MemToReg(ex_mem_1_memtoreg_2), .RegWrite(ex_mem_1_regwrite_2), .JAL(ex_mem_1_jal_2),
    .JALR(ex_mem_1_jalr_2), .Lui(ex_mem_1_lui_2), .ALUResult(MEM_ALUResult), .ReadData(ram_1_data),
    .imm_U(imm_U), .halt(ex_mem_1_halt_2), .rd(ex_mem_1_rd_2), .IR(MEM_IR), .PC(M_PC),
    .MemToReg_2(mem_wb_1_memtoreg_2), .RegWrite_2(RegWrite), .JAL_2(mem_wb_1_jal_2),
    .JALR_2(mem_wb_1_jalr_2), .Lui_2(mem_wb_1_lui_2), .ALUResult_2(mem_wb_1_aluresult_2),
    .ReadData_2(mem_wb_1_readdata_2), .imm_U_2(mem_wb_1_imm_u_2), .halt_2(halt), .rd_2(rd), .IR_2(WB_IR),
    .PC_2(WB_PC), .en(or_2_out), .clk(CLK), .rst(RST));
  Multiplexer #(.select(1), .width(32), .disabled("Z"), .enable("false")) multiplexer_15 (
    .in0(mem_wb_1_aluresult_2), .in1(mem_wb_1_readdata_2), .out(multiplexer_15_out), .sel(mem_wb_1_memtoreg_2));
  Adder #(.width(32)) adder_5 (.a(32'h4), .b(WB_PC), .out(adder_5_out));  // open: cin, cout
  or or_13 (or_13_out, mem_wb_1_jalr_2, mem_wb_1_jal_2);
  Multiplexer #(.select(1), .width(32), .disabled("Z"), .enable("false")) multiplexer_16 (
    .in0(multiplexer_15_out), .in1(adder_5_out), .out(multiplexer_16_out), .sel(or_13_out));
  Multiplexer #(.select(1), .width(32), .disabled("Z"), .enable("false")) multiplexer_17 (
    .in0(multiplexer_16_out), .in1(mem_wb_1_imm_u_2), .out(RDin), .sel(mem_wb_1_lui_2));

  // Other names for the same wires on the sheet: MEM_PC[31:0] = M_PC; 插入气泡数[15:0] = \LoadUse次数 

  // Notes on the sheet:
  //   中断源
  //   时空图监测，可删除
  //   中断等待指示
  //   Stall
  //   数码管输出
  //   BranchTaken
  //   BranchTaken
  //   取指(IF)
  //   指令存储器
  //   contents of rom_1 (hex, n*v repeats v):
  //   7d000113 100413 1f41993 41f9d993 433 c00913 800b13 140413 f47413 800293 100313 499993 89e9b3 1300533
  //   2200893 73 406282b3 fe0294e3 140413 f00f93 1f47433 1c41413 800293 100313 49d993 89e9b3 1300533
  //   2200893 73 406282b3 fe0294e3 1c45413 406b0b33 b0463 f95ff06f 2b3 fff2c293 1029293 fff2e293 500533
  //   2200893 73 f5dff06f 1112023 410113 a12023 410113 812023 410113 1312023 410113 1412023 410113 1512023
  //   410113 1612023 410113 100b13 300a13 100a93 1600433 441413 14469b3 1300533 2200893 73 fe0416e3
  //   415a0a33 fe0a10e3 ffc10113 12b03 ffc10113 12a83 ffc10113 12a03 ffc10113 12983 ffc10113 12403
  //   ffc10113 12503 ffc10113 12883 200073 1112023 410113 a12023 410113 812023 410113 1312023 410113
  //   1412023 410113 1512023 410113 1612023 410113 200b13 300a13 100a93 1600433 441413 14469b3 1300533
  //   2200893 73 fe0416e3 415a0a33 fe0a10e3 ffc10113 12b03 ffc10113 12a83 ffc10113 12a03 ffc10113 12983
  //   ffc10113 12403 ffc10113 12503 ffc10113 12883 200073 1112023 410113 a12023 410113 812023 410113
  //   1312023 410113 1412023 410113 1512023 410113 1612023 410113 300b13 300a13 100a93 1600433 441413
  //   14469b3 1300533 2200893 73 fe0416e3 415a0a33 fe0a10e3 ffc10113 12b03 ffc10113 12a83 ffc10113 12a03
  //   ffc10113 12983 ffc10113 12403 ffc10113 12503 ffc10113 12883 200073
  //   uret指令后面跟气泡
  //   不能把气泡作为断点
  //   Lui
  //   Sh
  //   Bltu
  //   I
  //   S
  //   B
  //   J
  //   U
  //   一号中断源
  //   一号中断等待指示
  //   二号中断源
  //   二号中断等待指示
  //   三号中断源
  //   三号中断等待指示
  //   保存断点
  //   控制位
  //   Instr
  //   rs1used
  //   JAL
  //   JALR
  //   $a7编号
  //   $a0编号
  //   流水调试日志用
  //   暂停节拍，不能为0
  //   rs2used
  //   Beq
  //   Bne
  //   MemToReg
  //   MemWrite
  //   AluOP
  //   AluSrcB
  //   RegWrite
  //   译码取数(ID)
  //   戳工具置1进入计数暂停模式，ctrl+k时钟自动运行到对应节拍暂停
  //   ctrl+k关闭时钟连续运行，将控制位置零，进入单步调试模式调试
  //   SignImm
  //   rs1Fwd
  //   rs2Fwd
  //   Reset 
  //   Reset 
  //   Reset 
  //   可计数暂停的时钟源
  //   Flush
  //   在中断响应周期和uret指令周期才可开/关中断
  //   中断使能寄存器IE
  //   跳转地址(beq/bne/bltu)
  //   跳转地址(jal)
  //   INTR
  //   为方便自动评测，需要输出流水线各段保存的PC值，注意是PC不是PC+4，另外ID段寄存器写入信息，Mem段内存写入信息也要输出
  //   指令执行(EX)
  //   选择需要清零的中断号
  //   EX.Lui
  //   ecall指令输出$a0到Led
  //   跳转地址(jalr)
  //   WriteData
  //   存储器不支持半字访问，因此需要取出一个字的数据特殊处理
  //   数据存储器
  //   访存(MEM)
  //   ReadData
  //   返回地址
  //   左移12位立即数
  //   写回(WB)
  //   保存到寄存器中的数据
endmodule

module \双位预测状态机  (
  input  \跳转 ,
  input  S1,
  input  S0,
  output N1,
  output N0
);

  wire and_1_out, and_2_out, and_3_out, and_4_out, not_1_out, not_2_out, not_3_out, not_4_out, not_5_out;

  not not_1 (not_1_out, S0);
  not not_2 (not_2_out, \跳转 );
  not not_3 (not_3_out, S0);
  not not_4 (not_4_out, S1);
  not not_5 (not_5_out, S0);
  and and_1 (and_1_out, S1, not_1_out);
  and and_2 (and_2_out, \跳转 , S0);
  and and_3 (and_3_out, not_2_out, S1, not_3_out);
  and and_4 (and_4_out, \跳转 , not_4_out, not_5_out);
  or or_1 (N1, and_1_out, and_2_out);
  or or_2 (N0, and_3_out, and_4_out);
endmodule

// Max2
module \Max2_归并比较  (
  input  [31:0] X,
  input  [31:0] Y,
  input  [2:0] Y_num,
  input  [2:0] X_num,
  output [31:0] MAX,
  output [2:0] MAX_num
);

  wire comparator_1_eq, comparator_1_gt, or_1_out;

  Comparator #(.width(32), .mode("unsigned")) comparator_1 (
    .a(X), .b(Y), .gt(comparator_1_gt), .eq(comparator_1_eq));  // open: lt
  or or_1 (or_1_out, comparator_1_gt, comparator_1_eq);
  Multiplexer #(.select(1), .width(32), .disabled("Z"), .enable("false")) multiplexer_1 (
    .in0(Y), .in1(X), .out(MAX), .sel(or_1_out));
  Multiplexer #(.select(1), .width(3), .disabled("Z"), .enable("false")) multiplexer_2 (
    .in0(Y_num), .in1(X_num), .out(MAX_num), .sel(or_1_out));

  // Notes on the sheet:
  //   输出两个输入中的较大值，并输出较大值的3位编号
endmodule

// BTB
module \分支预测缓冲器  (
  input  [31:0] IF_PC,
  input  EX_Branch,
  input  [31:0] EX_PC,
  input  CLK,
  input  EX_BranchTaken,
  input  [31:0] EX_BranchAddr,
  input  rst,
  output PredictJump,
  output [31:0] JumpAddr
);

  wire and_1_out, and_2_out, and_3_out, and_4_out, and_5_out, and_6_out, and_7_out, and_8_out, and_17_out,
       and_18_out, and_19_out, and_20_out, and_21_out, and_22_out, and_23_out, and_24_out, comparator_1_eq,
       comparator_2_eq, comparator_3_eq, comparator_4_eq, comparator_5_eq, comparator_6_eq, comparator_7_eq,
       comparator_8_eq, comparator_9_eq, comparator_10_eq, comparator_11_eq, comparator_12_eq,
       comparator_13_eq, comparator_14_eq, comparator_15_eq, comparator_16_eq, Full, H0, H1, H2, H3, H4, H5,
       H6, H7, Hit, L0, L1, L2, L3, L4, L5, L6, L7, not_1_out, not_2_out, not_3_out, not_4_out, not_5_out,
       not_6_out, not_7_out, not_8_out, not_9_out, or_1_out, or_2_out, or_3_out, or_4_out, or_5_out,
       or_6_out, or_7_out, or_8_out, v0, v1, v2, v3, v4, v5, v6, v7, WE0, WE1, WE2, WE3, WE4, WE5, WE6, WE7;
  wire [0:0] controlled_buffer_9_out;
  wire [1:0] multiplexer_1_out, multiplexer_2_out, multiplexer_3_out, multiplexer_4_out, multiplexer_5_out,
       multiplexer_6_out, multiplexer_7_out, multiplexer_8_out, State0, State1, State2, State3, State4,
       State5, State6, State7, \双位预测状态机_1_n0 , \双位预测状态机_2_n0 , \双位预测状态机_3_n0 , \双位预测状态机_4_n0 ,
       \双位预测状态机_5_n0 , \双位预测状态机_6_n0 , \双位预测状态机_7_n0 , \双位预测状态机_8_n0 ;
  wire [2:0] \max2_归并比较_1_max_num , \max2_归并比较_2_max_num , \max2_归并比较_3_max_num , \max2_归并比较_4_max_num ,
       \max2_归并比较_5_max_num , \max2_归并比较_6_max_num , multiplexer_9_out, RowFull, RowNotFull;
  wire [31:0] BDAddr0, BDAddr1, BDAddr2, BDAddr3, BDAddr4, BDAddr5, BDAddr6, BDAddr7, BSAddr0, BSAddr1,
       BSAddr2, BSAddr3, BSAddr4, BSAddr5, BSAddr6, BSAddr7, Cnt0, Cnt1, Cnt2, Cnt3, Cnt4, Cnt5, Cnt6, Cnt7,
       \max2_归并比较_1_max , \max2_归并比较_2_max , \max2_归并比较_3_max , \max2_归并比较_4_max , \max2_归并比较_5_max ,
       \max2_归并比较_6_max ;

  and and_1 (and_1_out, EX_Branch, WE0);
  and and_2 (and_2_out, EX_Branch, WE1);
  and and_3 (and_3_out, EX_Branch, WE2);
  and and_4 (and_4_out, EX_Branch, WE3);
  and and_5 (and_5_out, EX_Branch, WE4);
  and and_6 (and_6_out, EX_Branch, WE5);
  and and_7 (and_7_out, EX_Branch, WE6);
  and and_8 (and_8_out, EX_Branch, WE7);
  Register #(.width(1), .trigger("rising"), .Select("low")) register_1 (
    .D(1'b1), .en(and_1_out), .Q(v0), .clk(CLK), .clr(rst));
  Register #(.width(1), .trigger("rising"), .Select("low")) register_2 (
    .D(1'b1), .en(and_2_out), .Q(v1), .clk(CLK), .clr(rst));
  Register #(.width(1), .trigger("rising"), .Select("low")) register_3 (
    .D(1'b1), .en(and_3_out), .Q(v2), .clk(CLK), .clr(rst));
  Register #(.width(1), .trigger("rising"), .Select("low")) register_4 (
    .D(1'b1), .en(and_4_out), .Q(v3), .clk(CLK), .clr(rst));
  Register #(.width(1), .trigger("rising"), .Select("low")) register_5 (
    .D(1'b1), .en(and_5_out), .Q(v4), .clk(CLK), .clr(rst));
  Register #(.width(1), .trigger("rising"), .Select("low")) register_6 (
    .D(1'b1), .en(and_6_out), .Q(v5), .clk(CLK), .clr(rst));
  Register #(.width(1), .trigger("rising"), .Select("low")) register_7 (
    .D(1'b1), .en(and_7_out), .Q(v6), .clk(CLK), .clr(rst));
  Register #(.width(1), .trigger("rising"), .Select("low")) register_8 (
    .D(1'b1), .en(and_8_out), .Q(v7), .clk(CLK), .clr(rst));
  Comparator #(.width(32), .mode("unsigned")) comparator_1 (
    .a(BSAddr0), .b(IF_PC), .eq(comparator_1_eq));  // open: gt, lt
  Comparator #(.width(32), .mode("unsigned")) comparator_2 (
    .a(BSAddr1), .b(IF_PC), .eq(comparator_2_eq));  // open: gt, lt
  Comparator #(.width(32), .mode("unsigned")) comparator_3 (
    .a(BSAddr2), .b(IF_PC), .eq(comparator_3_eq));  // open: gt, lt
  Comparator #(.width(32), .mode("unsigned")) comparator_4 (
    .a(BSAddr3), .b(IF_PC), .eq(comparator_4_eq));  // open: gt, lt
  Comparator #(.width(32), .mode("unsigned")) comparator_5 (
    .a(BSAddr4), .b(IF_PC), .eq(comparator_5_eq));  // open: gt, lt
  Comparator #(.width(32), .mode("unsigned")) comparator_6 (
    .a(BSAddr5), .b(IF_PC), .eq(comparator_6_eq));  // open: gt, lt
  Comparator #(.width(32), .mode("unsigned")) comparator_7 (
    .a(BSAddr6), .b(IF_PC), .eq(comparator_7_eq));  // open: gt, lt
  Comparator #(.width(32), .mode("unsigned")) comparator_8 (
    .a(BSAddr7), .b(IF_PC), .eq(comparator_8_eq));  // open: gt, lt
  and and_9 (L0, comparator_1_eq, v0);
  and and_10 (L1, comparator_2_eq, v1);
  and and_11 (L2, comparator_3_eq, v2);
  and and_12 (L3, comparator_4_eq, v3);
  and and_13 (L4, comparator_5_eq, v4);
  and and_14 (L5, comparator_6_eq, v5);
  and and_15 (L6, comparator_7_eq, v6);
  and and_16 (L7, comparator_8_eq, v7);
  Register #(.width(32), .trigger("rising"), .Select("low")) register_9 (
    .D(EX_PC), .en(and_1_out), .Q(BSAddr0), .clk(CLK), .clr(rst));
  Register #(.width(32), .trigger("rising"), .Select("low")) register_10 (
    .D(EX_PC), .en(and_2_out), .Q(BSAddr1), .clk(CLK), .clr(rst));
  Register #(.width(32), .trigger("rising"), .Select("low")) register_11 (
    .D(EX_PC), .en(and_3_out), .Q(BSAddr2), .clk(CLK), .clr(rst));
  Register #(.width(32), .trigger("rising"), .Select("low")) register_12 (
    .D(EX_PC), .en(and_4_out), .Q(BSAddr3), .clk(CLK), .clr(rst));
  Register #(.width(32), .trigger("rising"), .Select("low")) register_13 (
    .D(EX_PC), .en(and_5_out), .Q(BSAddr4), .clk(CLK), .clr(rst));
  Register #(.width(32), .trigger("rising"), .Select("low")) register_14 (
    .D(EX_PC), .en(and_6_out), .Q(BSAddr5), .clk(CLK), .clr(rst));
  Register #(.width(32), .trigger("rising"), .Select("low")) register_15 (
    .D(EX_PC), .en(and_7_out), .Q(BSAddr6), .clk(CLK), .clr(rst));
  Register #(.width(32), .trigger("rising"), .Select("low")) register_16 (
    .D(EX_PC), .en(and_8_out), .Q(BSAddr7), .clk(CLK), .clr(rst));
  assign JumpAddr = L0 ? BDAddr0 : 32'bz;  // Controlled_Buffer controlled_buffer_1
  assign JumpAddr = L1 ? BDAddr1 : 32'bz;  // Controlled_Buffer controlled_buffer_2
  assign JumpAddr = L2 ? BDAddr2 : 32'bz;  // Controlled_Buffer controlled_buffer_3
  assign JumpAddr = L3 ? BDAddr3 : 32'bz;  // Controlled_Buffer controlled_buffer_4
  assign JumpAddr = L4 ? BDAddr4 : 32'bz;  // Controlled_Buffer controlled_buffer_5
  assign JumpAddr = L5 ? BDAddr5 : 32'bz;  // Controlled_Buffer controlled_buffer_6
  assign JumpAddr = L6 ? BDAddr6 : 32'bz;  // Controlled_Buffer controlled_buffer_7
  assign JumpAddr = L7 ? BDAddr7 : 32'bz;  // Controlled_Buffer controlled_buffer_8
  Register #(.width(32), .trigger("rising"), .Select("low")) register_17 (
    .D(EX_BranchAddr), .en(and_1_out), .Q(BDAddr0), .clk(CLK), .clr(rst));
  Register #(.width(32), .trigger("rising"), .Select("low")) register_18 (
    .D(EX_BranchAddr), .en(and_2_out), .Q(BDAddr1), .clk(CLK), .clr(rst));
  Register #(.width(32), .trigger("rising"), .Select("low")) register_19 (
    .D(EX_BranchAddr), .en(and_3_out), .Q(BDAddr2), .clk(CLK), .clr(rst));
  Register #(.width(32), .trigger("rising"), .Select("low")) register_20 (
    .D(EX_BranchAddr), .en(and_4_out), .Q(BDAddr3), .clk(CLK), .clr(rst));
  Register #(.width(32), .trigger("rising"), .Select("low")) register_21 (
    .D(EX_BranchAddr), .en(and_5_out), .Q(BDAddr4), .clk(CLK), .clr(rst));
  Register #(.width(32), .trigger("rising"), .Select("low")) register_22 (
    .D(EX_BranchAddr), .en(and_6_out), .Q(BDAddr5), .clk(CLK), .clr(rst));
  Register #(.width(32), .trigger("rising"), .Select("low")) register_23 (
    .D(EX_BranchAddr), .en(and_7_out), .Q(BDAddr6), .clk(CLK), .clr(rst));
  Register #(.width(32), .trigger("rising"), .Select("low")) register_24 (
    .D(EX_BranchAddr), .en(and_8_out), .Q(BDAddr7), .clk(CLK), .clr(rst));
  \双位预测状态机  \u_双位预测状态机_1  (
    .\跳转 (EX_BranchTaken), .S1(State0[1]), .S0(State0[0]), .N1(\双位预测状态机_1_n0 [1]), .N0(\双位预测状态机_1_n0 [0]));
  \双位预测状态机  \u_双位预测状态机_2  (
    .\跳转 (EX_BranchTaken), .S1(State1[1]), .S0(State1[0]), .N1(\双位预测状态机_2_n0 [1]), .N0(\双位预测状态机_2_n0 [0]));
  \双位预测状态机  \u_双位预测状态机_3  (
    .\跳转 (EX_BranchTaken), .S1(State2[1]), .S0(State2[0]), .N1(\双位预测状态机_3_n0 [1]), .N0(\双位预测状态机_3_n0 [0]));
  \双位预测状态机  \u_双位预测状态机_4  (
    .\跳转 (EX_BranchTaken), .S1(State3[1]), .S0(State3[0]), .N1(\双位预测状态机_4_n0 [1]), .N0(\双位预测状态机_4_n0 [0]));
  \双位预测状态机  \u_双位预测状态机_5  (
    .\跳转 (EX_BranchTaken), .S1(State4[1]), .S0(State4[0]), .N1(\双位预测状态机_5_n0 [1]), .N0(\双位预测状态机_5_n0 [0]));
  \双位预测状态机  \u_双位预测状态机_6  (
    .\跳转 (EX_BranchTaken), .S1(State5[1]), .S0(State5[0]), .N1(\双位预测状态机_6_n0 [1]), .N0(\双位预测状态机_6_n0 [0]));
  \双位预测状态机  \u_双位预测状态机_7  (
    .\跳转 (EX_BranchTaken), .S1(State6[1]), .S0(State6[0]), .N1(\双位预测状态机_7_n0 [1]), .N0(\双位预测状态机_7_n0 [0]));
  \双位预测状态机  \u_双位预测状态机_8  (
    .\跳转 (EX_BranchTaken), .S1(State7[1]), .S0(State7[0]), .N1(\双位预测状态机_8_n0 [1]), .N0(\双位预测状态机_8_n0 [0]));
  assign {PredictJump, controlled_buffer_9_out[0]} = L0 ? State0 : 2'bz;  // Controlled_Buffer controlled_buffer_9
  assign {PredictJump, controlled_buffer_9_out[0]} = L1 ? State1 : 2'bz;  // Controlled_Buffer controlled_buffer_10
  assign {PredictJump, controlled_buffer_9_out[0]} = L2 ? State2 : 2'bz;  // Controlled_Buffer controlled_buffer_11
  assign {PredictJump, controlled_buffer_9_out[0]} = L3 ? State3 : 2'bz;  // Controlled_Buffer controlled_buffer_12
  assign {PredictJump, controlled_buffer_9_out[0]} = L4 ? State4 : 2'bz;  // Controlled_Buffer controlled_buffer_13
  assign {PredictJump, controlled_buffer_9_out[0]} = L5 ? State5 : 2'bz;  // Controlled_Buffer controlled_buffer_14
  assign {PredictJump, controlled_buffer_9_out[0]} = L6 ? State6 : 2'bz;  // Controlled_Buffer controlled_buffer_15
  assign {PredictJump, controlled_buffer_9_out[0]} = L7 ? State7 : 2'bz;  // Controlled_Buffer controlled_buffer_16
  Multiplexer #(.select(1), .width(2), .disabled("Z"), .enable("false")) multiplexer_1 (
    .in0(2'b11), .in1(\双位预测状态机_1_n0 ), .out(multiplexer_1_out), .sel(H0));
  Multiplexer #(.select(1), .width(2), .disabled("Z"), .enable("false")) multiplexer_2 (
    .in0(2'b11), .in1(\双位预测状态机_2_n0 ), .out(multiplexer_2_out), .sel(H1));
  Multiplexer #(.select(1), .width(2), .disabled("Z"), .enable("false")) multiplexer_3 (
    .in0(2'b11), .in1(\双位预测状态机_3_n0 ), .out(multiplexer_3_out), .sel(H2));
  Multiplexer #(.select(1), .width(2), .disabled("Z"), .enable("false")) multiplexer_4 (
    .in0(2'b11), .in1(\双位预测状态机_4_n0 ), .out(multiplexer_4_out), .sel(H3));
  Multiplexer #(.select(1), .width(2), .disabled("Z"), .enable("false")) multiplexer_5 (
    .in0(2'b11), .in1(\双位预测状态机_5_n0 ), .out(multiplexer_5_out), .sel(H4));
  Multiplexer #(.select(1), .width(2), .disabled("Z"), .enable("false")) multiplexer_6 (
    .in0(2'b11), .in1(\双位预测状态机_6_n0 ), .out(multiplexer_6_out), .sel(H5));
  Multiplexer #(.select(1), .width(2), .disabled("Z"), .enable("false")) multiplexer_7 (
    .in0(2'b11), .in1(\双位预测状态机_7_n0 ), .out(multiplexer_7_out), .sel(H6));
  Multiplexer #(.select(1), .width(2), .disabled("Z"), .enable("false")) multiplexer_8 (
    .in0(2'b11), .in1(\双位预测状态机_8_n0 ), .out(multiplexer_8_out), .sel(H7));
  Pull_Resistor #(.pull(0)) pull_resistor_1 (.node(PredictJump));
  Register #(.width(2), .trigger("rising"), .Select("low")) register_25 (
    .D(multiplexer_1_out), .en(or_1_out), .Q(State0), .clk(CLK), .clr(rst));
  or or_1 (or_1_out, and_1_out, H0);
  Register #(.width(2), .trigger("rising"), .Select("low")) register_26 (
    .D(multiplexer_2_out), .en(or_2_out), .Q(State1), .clk(CLK), .clr(rst));
  or or_2 (or_2_out, and_2_out, H1);
  Register #(.width(2), .trigger("rising"), .Select("low")) register_27 (
    .D(multiplexer_3_out), .en(or_3_out), .Q(State2), .clk(CLK), .clr(rst));
  or or_3 (or_3_out, and_3_out, H2);
  Register #(.width(2), .trigger("rising"), .Select("low")) register_28 (
    .D(multiplexer_4_out), .en(or_4_out), .Q(State3), .clk(CLK), .clr(rst));
  or or_4 (or_4_out, and_4_out, H3);
  Register #(.width(2), .trigger("rising"), .Select("low")) register_29 (
    .D(multiplexer_5_out), .en(or_5_out), .Q(State4), .clk(CLK), .clr(rst));
  or or_5 (or_5_out, and_5_out, H4);
  Register #(.width(2), .trigger("rising"), .Select("low")) register_30 (
    .D(multiplexer_6_out), .en(or_6_out), .Q(State5), .clk(CLK), .clr(rst));
  or or_6 (or_6_out, and_6_out, H5);
  Register #(.width(2), .trigger("rising"), .Select("low")) register_31 (
    .D(multiplexer_7_out), .en(or_7_out), .Q(State6), .clk(CLK), .clr(rst));
  or or_7 (or_7_out, and_7_out, H6);
  Register #(.width(2), .trigger("rising"), .Select("low")) register_32 (
    .D(multiplexer_8_out), .en(or_8_out), .Q(State7), .clk(CLK), .clr(rst));
  or or_8 (or_8_out, and_8_out, H7);
  and and_17 (and_17_out, v0, EX_Branch);
  Counter #(.width(32), .max('hffffffff), .ongoal("wrap"), .trigger("rising"), .behavior("new")) counter_1 (
    .load(or_1_out), .D({32{1'b0}}), .count(and_17_out), .Q(Cnt0), .clk(CLK), .clr(rst));  // open: carry, preset, down
  // Probe on Cnt0
  and and_18 (and_18_out, v1, EX_Branch);
  Counter #(.width(32), .max('hffffffff), .ongoal("wrap"), .trigger("rising"), .behavior("new")) counter_2 (
    .load(or_2_out), .D({32{1'b0}}), .count(and_18_out), .Q(Cnt1), .clk(CLK), .clr(rst));  // open: carry, preset, down
  // Probe on Cnt1
  and and_19 (and_19_out, v2, EX_Branch);
  Counter #(.width(32), .max('hffffffff), .ongoal("wrap"), .trigger("rising"), .behavior("new")) counter_3 (
    .load(or_3_out), .D({32{1'b0}}), .count(and_19_out), .Q(Cnt2), .clk(CLK), .clr(rst));  // open: carry, preset, down
  // Probe on Cnt2
  and and_20 (and_20_out, v3, EX_Branch);
  Counter #(.width(32), .max('hffffffff), .ongoal("wrap"), .trigger("rising"), .behavior("new")) counter_4 (
    .load(or_4_out), .D({32{1'b0}}), .count(and_20_out), .Q(Cnt3), .clk(CLK), .clr(rst));  // open: carry, preset, down
  // Probe on Cnt3
  and and_21 (and_21_out, v4, EX_Branch);
  Counter #(.width(32), .max('hffffffff), .ongoal("wrap"), .trigger("rising"), .behavior("new")) counter_5 (
    .load(or_5_out), .D({32{1'b0}}), .count(and_21_out), .Q(Cnt4), .clk(CLK), .clr(rst));  // open: carry, preset, down
  // Probe on Cnt4
  and and_22 (and_22_out, v5, EX_Branch);
  Counter #(.width(32), .max('hffffffff), .ongoal("wrap"), .trigger("rising"), .behavior("new")) counter_6 (
    .load(or_6_out), .D({32{1'b0}}), .count(and_22_out), .Q(Cnt5), .clk(CLK), .clr(rst));  // open: carry, preset, down
  // Probe on Cnt5
  and and_23 (and_23_out, v6, EX_Branch);
  Counter #(.width(32), .max('hffffffff), .ongoal("wrap"), .trigger("rising"), .behavior("new")) counter_7 (
    .load(or_7_out), .D({32{1'b0}}), .count(and_23_out), .Q(Cnt6), .clk(CLK), .clr(rst));  // open: carry, preset, down
  // Probe on Cnt6
  and and_24 (and_24_out, v7, EX_Branch);
  Counter #(.width(32), .max('hffffffff), .ongoal("wrap"), .trigger("rising"), .behavior("new")) counter_8 (
    .load(or_8_out), .D({32{1'b0}}), .count(and_24_out), .Q(Cnt7), .clk(CLK), .clr(rst));  // open: carry, preset, down
  // Probe on Cnt7
  Comparator #(.width(32), .mode("unsigned")) comparator_9 (
    .a(BSAddr0), .b(EX_PC), .eq(comparator_9_eq));  // open: gt, lt
  Comparator #(.width(32), .mode("unsigned")) comparator_10 (
    .a(BSAddr1), .b(EX_PC), .eq(comparator_10_eq));  // open: gt, lt
  Comparator #(.width(32), .mode("unsigned")) comparator_11 (
    .a(BSAddr2), .b(EX_PC), .eq(comparator_11_eq));  // open: gt, lt
  Comparator #(.width(32), .mode("unsigned")) comparator_12 (
    .a(BSAddr3), .b(EX_PC), .eq(comparator_12_eq));  // open: gt, lt
  Comparator #(.width(32), .mode("unsigned")) comparator_13 (
    .a(BSAddr4), .b(EX_PC), .eq(comparator_13_eq));  // open: gt, lt
  Comparator #(.width(32), .mode("unsigned")) comparator_14 (
    .a(BSAddr5), .b(EX_PC), .eq(comparator_14_eq));  // open: gt, lt
  Comparator #(.width(32), .mode("unsigned")) comparator_15 (
    .a(BSAddr6), .b(EX_PC), .eq(comparator_15_eq));  // open: gt, lt
  Comparator #(.width(32), .mode("unsigned")) comparator_16 (
    .a(BSAddr7), .b(EX_PC), .eq(comparator_16_eq));  // open: gt, lt
  not not_1 (not_1_out, v0);
  not not_2 (not_2_out, v1);
  not not_3 (not_3_out, v2);
  not not_4 (not_4_out, v3);
  not not_5 (not_5_out, v4);
  not not_6 (not_6_out, v5);
  not not_7 (not_7_out, v6);
  not not_8 (not_8_out, v7);
  not not_9 (not_9_out, Hit);
  and and_25 (H0, comparator_9_eq, v0);
  and and_26 (H1, comparator_10_eq, v1);
  and and_27 (H2, comparator_11_eq, v2);
  and and_28 (H3, comparator_12_eq, v3);
  and and_29 (H4, comparator_13_eq, v4);
  and and_30 (H5, comparator_14_eq, v5);
  and and_31 (H6, comparator_15_eq, v6);
  and and_32 (H7, comparator_16_eq, v7);
  \Max2_归并比较  \max2_归并比较_1  (
    .X(Cnt0), .Y(Cnt1), .Y_num(3'b001), .X_num(3'b000), .MAX(\max2_归并比较_1_max ),
    .MAX_num(\max2_归并比较_1_max_num ));
  \Max2_归并比较  \max2_归并比较_2  (
    .X(Cnt2), .Y(Cnt3), .Y_num(3'b011), .X_num(3'b010), .MAX(\max2_归并比较_2_max ),
    .MAX_num(\max2_归并比较_2_max_num ));
  \Max2_归并比较  \max2_归并比较_3  (
    .X(Cnt4), .Y(Cnt5), .Y_num(3'b101), .X_num(3'b100), .MAX(\max2_归并比较_3_max ),
    .MAX_num(\max2_归并比较_3_max_num ));
  \Max2_归并比较  \max2_归并比较_4  (
    .X(Cnt6), .Y(Cnt7), .Y_num(3'b111), .X_num(3'b110), .MAX(\max2_归并比较_4_max ),
    .MAX_num(\max2_归并比较_4_max_num ));
  Demultiplexer #(.select(3), .width(1), .tristate("false"), .disabled("Z"), .enable("false")) demultiplexer_1 (
    .out0(WE0), .out1(WE1), .out2(WE2), .out3(WE3), .out4(WE4), .out5(WE5), .out6(WE6), .out7(WE7),
    .in(not_9_out), .sel(multiplexer_9_out));
  Multiplexer #(.select(1), .width(3), .disabled("Z"), .enable("false")) multiplexer_9 (
    .in0(RowNotFull), .in1(RowFull), .out(multiplexer_9_out), .sel(Full));
  or or_9 (Hit, H0, H1, H2, H3, H4, H5, H6, H7);
  Priority_Encoder #(.select(3), .disabled("Z")) priority_encoder_1 (
    .in0(not_1_out), .in1(not_2_out), .in2(not_3_out), .in3(not_4_out), .in4(not_5_out), .in5(not_6_out),
    .in6(not_7_out), .in7(not_8_out), .out(RowNotFull), .en_out(Full), .en_in(1'b1));  // open: gs
  \Max2_归并比较  \max2_归并比较_5  (
    .X(\max2_归并比较_1_max ), .Y(\max2_归并比较_2_max ), .Y_num(\max2_归并比较_2_max_num ),
    .X_num(\max2_归并比较_1_max_num ), .MAX(\max2_归并比较_5_max ), .MAX_num(\max2_归并比较_5_max_num ));
  \Max2_归并比较  \max2_归并比较_6  (
    .X(\max2_归并比较_3_max ), .Y(\max2_归并比较_4_max ), .Y_num(\max2_归并比较_4_max_num ),
    .X_num(\max2_归并比较_3_max_num ), .MAX(\max2_归并比较_6_max ), .MAX_num(\max2_归并比较_6_max_num ));
  \Max2_归并比较  \max2_归并比较_7  (
    .X(\max2_归并比较_5_max ), .Y(\max2_归并比较_6_max ), .Y_num(\max2_归并比较_6_max_num ),
    .X_num(\max2_归并比较_5_max_num ), .MAX_num(RowFull));  // open: MAX

  // Notes on the sheet:
  //   输入引脚区
  //   输出引脚区
  //   预测位初始值
  //   cache没满则选这一行写入
  //   cache满则选这一行写入
endmodule

module \动态分支预测  (
  output RegWrite,
  output MemWrite,
  output [31:0] IF_PC,
  output [31:0] ID_PC,
  output [31:0] EX_PC,
  output [31:0] M_PC,
  output [31:0] WB_PC,
  output [31:0] RDin,
  output [31:0] MDin,
  output [31:0] LedData
);

  wire and_1_out, and_2_out, and_3_out, and_5_out, and_6_out, and_7_out, and_8_out, Beq, Bltu, Bne,
       BranchTaken, CLK, clock_1_out, comparator_1_eq, comparator_2_eq, comparator_2_lt, comparator_3_eq,
       Conditional, d_ff_1_q, en, equ, EX_Branch, EX_ecall, ex_mem_1_halt_2, ex_mem_1_jal_2, ex_mem_1_jalr_2,
       ex_mem_1_lui_2, ex_mem_1_memtoreg_2, ex_mem_1_regwrite_2, ex_mem_1_sh_2, Go, halt, ID_ecall,
       id_ex_1_alusrcb_2, id_ex_1_lui_2, id_ex_1_memtoreg_2, id_ex_1_memwrite_2, id_ex_1_predictjump_2,
       id_ex_1_regwrite_2, id_ex_1_sh_2, if_id_1_predictjump_2, IR1, IR2, IR3, JAL, JALR, less,
       mem_wb_1_jal_2, mem_wb_1_jalr_2, mem_wb_1_lui_2, mem_wb_1_memtoreg_2, nand_1_out, not_1_out,
       not_2_out, not_3_out, not_5_out, not_6_out, not_7_out, or_2_out, or_3_out, or_5_out, or_6_out,
       PredictErr, PredictJump, RST, S_type, Stall, W1, W2, W3, \单周期硬布线控制器_1_alu_src , \单周期硬布线控制器_1_beq ,
       \单周期硬布线控制器_1_bltu , \单周期硬布线控制器_1_bne , \单周期硬布线控制器_1_jal , \单周期硬布线控制器_1_jalr , \单周期硬布线控制器_1_lui ,
       \单周期硬布线控制器_1_memtoreg , \单周期硬布线控制器_1_memwrite , \单周期硬布线控制器_1_regwrite , \单周期硬布线控制器_1_rs1used ,
       \单周期硬布线控制器_1_rs2used , \单周期硬布线控制器_1_sh , \相关处理逻辑_重定向_1_flush ;
  wire [1:0] id_ex_1_rs1fwd_2, id_ex_1_rs2fwd_2, priority_encoder_1_out, \相关处理逻辑_重定向_1_rs1fwd ,
       \相关处理逻辑_重定向_1_rs2fwd ;
  wire [3:0] id_ex_1_aluop_2, \单周期硬布线控制器_1_alu_op ;
  wire [4:0] ex_mem_1_rd_2, id_ex_1_rd_2, multiplexer_4_out, multiplexer_5_out, rd;
  wire [11:0] multiplexer_6_out;
  wire [12:0] CNT_num;
  wire [15:0] \LoadUse次数 , \分支指令数目 , \总周期数 , \无条件分支数 , \条件分支成功数 , \预测失败次数 ;
  wire [31:0] adder_1_out, adder_2_out, adder_3_out, adder_4_out, adder_6_out, and_9_out, and_10_out,
       bit_extender_1_out, bit_extender_2_out, bit_extender_3_out, bit_extender_4_out, EX_ALUResult,
       EX_BranchAddr, EX_IR, ex_mem_1_rs2_2, id_ex_1_imm_b_2, id_ex_1_imm_is_2, id_ex_1_imm_j_2,
       id_ex_1_imm_u_2, id_ex_1_rs1_2, id_ex_1_rs2_2, ID_IR, IF_IR, imm_U, MEM_ALUResult, MEM_IR,
       mem_wb_1_aluresult_2, mem_wb_1_imm_u_2, mem_wb_1_readdata_2, multiplexer_1_out, multiplexer_2_out,
       multiplexer_3_out, multiplexer_7_out, multiplexer_8_out, multiplexer_9_out, multiplexer_11_out,
       multiplexer_12_out, multiplexer_13_out, multiplexer_14_out, ram_1_data, regifile_1_r1, regifile_1_r2,
       ShDin, shifter_1_out, shifter_2_out, shifter_3_out, shifter_4_out, WB_IR, \分支预测缓冲器_1_jumpaddr ;

  Button \u_总复位  (.out(RST));
  Button _1 (.out(IR1));
  Button _2 (.out(IR2));
  Button _3 (.out(IR3));
  // Probe on \总周期数 
  // Probe on \总周期数 
  Button \u_继续运行  (.out(Go));
  LED #(.active("true")) led_1 (.in(W1));
  LED #(.active("true")) led_2 (.in(W2));
  LED #(.active("true")) led_3 (.in(W3));
  not not_1 (not_1_out, equ);
  and and_1 (and_1_out, Beq, equ);
  Adder #(.width(32)) adder_1 (.a(EX_PC), .b(32'h4), .out(adder_1_out));  // open: cin, cout
  Hex_Digit_Display hex_digit_display_1 (.value(LedData[31:28]));  // open: dp
  // Probe on IF_PC[19:0]
  // RiscV_Probe riscv_probe_1: pin names not known; wires that end beside it: IF_IR
  and and_2 (and_2_out, not_1_out, Bne);
  and and_3 (and_3_out, less, Bltu);
  or or_1 (Conditional, and_1_out, and_2_out, and_3_out);
  Priority_Encoder #(.select(2), .disabled("Z")) priority_encoder_1 (
    .in0(1'b1), .in1(Conditional), .in2(JAL), .in3(JALR), .out(priority_encoder_1_out));  // open: gs, en_out, en_in
  Multiplexer #(.select(2), .width(32), .disabled("Z"), .enable("false")) multiplexer_1 (
    .in0(adder_1_out), .in1(adder_3_out), .in2(adder_4_out), .in3(EX_ALUResult), .out(multiplexer_1_out),
    .sel(priority_encoder_1_out));
  Multiplexer #(.select(1), .width(32), .disabled("Z"), .enable("false")) multiplexer_2 (
    .in0(adder_2_out), .in1(\分支预测缓冲器_1_jumpaddr ), .out(multiplexer_2_out), .sel(PredictJump));
  or or_2 (or_2_out, Beq, Bne, Bltu);
  assign EX_BranchAddr = or_2_out ? adder_3_out : 32'bz;  // Controlled_Buffer controlled_buffer_1
  assign EX_BranchAddr = JAL ? adder_4_out : 32'bz;  // Controlled_Buffer controlled_buffer_2
  assign EX_BranchAddr = JALR ? EX_ALUResult : 32'bz;  // Controlled_Buffer controlled_buffer_3
  Hex_Digit_Display hex_digit_display_2 (.value(LedData[23:20]));  // open: dp
  Hex_Digit_Display hex_digit_display_3 (.value(LedData[27:24]));  // open: dp
  // Probe on ID_PC[19:0]
  // RiscV_Probe riscv_probe_2: pin names not known; wires that end beside it: ID_IR
  \相关处理逻辑_重定向  \u_相关处理逻辑_重定向_1  (
    .rs1used(\单周期硬布线控制器_1_rs1used ), .rs2used(\单周期硬布线控制器_1_rs2used ), .BranchTaken(PredictErr),
    .EX_RegWrite(id_ex_1_regwrite_2), .EX_WriteReg_num(id_ex_1_rd_2), .MEM_RegWrite(ex_mem_1_regwrite_2),
    .MEM_WriteReg_num(ex_mem_1_rd_2), .Instr(ID_IR), .Stall(Stall), .Flush(\相关处理逻辑_重定向_1_flush ),
    .ecall(ID_ecall), .EX_MemToReg(id_ex_1_memtoreg_2), .rs1Fwd(\相关处理逻辑_重定向_1_rs1fwd ),
    .EX_Lui(id_ex_1_lui_2), .rs2Fwd(\相关处理逻辑_重定向_1_rs2fwd ), .\中断请求 (1'b0));
  not not_2 (not_2_out, halt);
  or or_3 (or_3_out, not_2_out, Go);
  Multiplexer #(.select(1), .width(32), .disabled("Z"), .enable("false")) multiplexer_3 (
    .in0(multiplexer_2_out), .in1(multiplexer_1_out), .out(multiplexer_3_out), .sel(PredictErr));
  \分支预测缓冲器  \u_分支预测缓冲器_1  (
    .IF_PC(IF_PC), .EX_Branch(EX_Branch), .EX_PC(EX_PC), .CLK(CLK), .EX_BranchTaken(BranchTaken),
    .EX_BranchAddr(EX_BranchAddr), .PredictJump(PredictJump), .JumpAddr(\分支预测缓冲器_1_jumpaddr ), .rst(RST));
  Hex_Digit_Display hex_digit_display_4 (.value(LedData[19:16]));  // open: dp
  Hex_Digit_Display hex_digit_display_5 (.value(LedData[15:12]));  // open: dp
  not not_3 (not_3_out, Stall);
  and and_4 (en, not_3_out, or_3_out);
  not not_4 (BranchTaken, comparator_1_eq);
  Comparator #(.width(2), .mode("twosComplement")) comparator_1 (
    .a(2'b00), .b(priority_encoder_1_out), .eq(comparator_1_eq));  // open: gt, lt
  Register #(.width(32), .trigger("rising"), .Select("low")) PC (
    .D(multiplexer_3_out), .en(en), .Q(IF_PC), .clk(CLK), .clr(RST));
  Hex_Digit_Display hex_digit_display_6 (.value(LedData[11:8]));  // open: dp
  Hex_Digit_Display hex_digit_display_7 (.value(LedData[7:4]));  // open: dp
  // Probe on EX_PC[19:0]
  // RiscV_Probe riscv_probe_3: pin names not known; wires that end beside it: EX_IR
  or or_4 (EX_Branch, Beq, Bne, Bltu, JAL, JALR);
  Hex_Digit_Display hex_digit_display_8 (.value(LedData[3:0]));  // open: dp
  ROM #(.addrWidth(10), .dataWidth(32), .Select("high")) rom_1 (.addr(IF_PC[11:2]), .data(IF_IR));
  Adder #(.width(32)) adder_2 (.a(IF_PC), .b(32'h4), .out(adder_2_out));  // open: cin, cout
  // Probe on \总周期数 
  // Probe on M_PC[19:0]
  // RiscV_Probe riscv_probe_4: pin names not known; wires that end beside it: MEM_IR
  IF_ID if_id_1 (
    .IR(IF_IR), .PC(IF_PC), .IR_2(ID_IR), .PC_2(ID_PC), .en(en), .clk(CLK), .clr(PredictErr),
    .PredictJump(PredictJump), .PredictJump_2(if_id_1_predictjump_2), .rst(RST));
  // Probe on \总周期数 
  // Probe on \无条件分支数 
  // Probe on \条件分支成功数 
  // Probe on \LoadUse次数 
  // Probe on \LoadUse次数 
  // Probe on IF_PC[11:0]
  // Probe on WB_PC[19:0]
  // RiscV_Probe riscv_probe_5: pin names not known; wires that end beside it: WB_IR
  // Probe on ID_PC[11:0]
  // Probe on EX_PC[11:0]
  \单周期硬布线控制器  \u_单周期硬布线控制器_1  (
    .Funct({ID_IR[30], ID_IR[25], ID_IR[14:12]}), .OP(ID_IR[6:2]), .ALU_OP(\单周期硬布线控制器_1_alu_op ),
    .MemToReg(\单周期硬布线控制器_1_memtoreg ), .MemWrite(\单周期硬布线控制器_1_memwrite ), .ALU_SRC(\单周期硬布线控制器_1_alu_src ),
    .RegWrite(\单周期硬布线控制器_1_regwrite ), .ecall(ID_ecall), .S_type(S_type), .Jalr(\单周期硬布线控制器_1_jalr ),
    .Beq(\单周期硬布线控制器_1_beq ), .JAL(\单周期硬布线控制器_1_jal ), .Bne(\单周期硬布线控制器_1_bne ), .in_3(ID_IR[21]),
    .Lui(\单周期硬布线控制器_1_lui ), .Sh(\单周期硬布线控制器_1_sh ), .Bltu(\单周期硬布线控制器_1_bltu ),
    .rs1used(\单周期硬布线控制器_1_rs1used ), .rs2used(\单周期硬布线控制器_1_rs2used ));  // open: uret, csr
  // Probe on M_PC[11:0]
  D_Flip_Flop #(.trigger("high"), .Pre_Clr_Positions("LEGACY"), .NegatePresetClear("false"), .enable("true"), .NewFFLayout("false")) d_ff_1 (.Q(d_ff_1_q));  // open: clk, D, Qn, preset, en, reset
  // Probe on 13'he27
  Multiplexer #(.select(1), .width(5), .disabled("Z"), .enable("false")) multiplexer_4 (
    .in0(ID_IR[19:15]), .in1(5'b10001), .out(multiplexer_4_out), .sel(ID_ecall));
  Multiplexer #(.select(1), .width(5), .disabled("Z"), .enable("false")) multiplexer_5 (
    .in0(ID_IR[24:20]), .in1(5'b01010), .out(multiplexer_5_out), .sel(ID_ecall));
  Multiplexer #(.select(1), .width(12), .disabled("Z"), .enable("false")) multiplexer_6 (
    .in0(ID_IR[31:20]), .in1({ID_IR[31:25], ID_IR[11:7]}), .out(multiplexer_6_out), .sel(S_type));
  assign bit_extender_1_out = {{20{multiplexer_6_out[11]}}, multiplexer_6_out};  // Bit_Extender bit_extender_1
  assign bit_extender_2_out = {{20{ID_IR[31]}}, {ID_IR[31], ID_IR[7], ID_IR[30:25], ID_IR[11:8]}};  // Bit_Extender bit_extender_2
  assign bit_extender_3_out = {{12{ID_IR[31]}}, {ID_IR[31], ID_IR[19:12], ID_IR[20], ID_IR[30:21]}};  // Bit_Extender bit_extender_3
  assign bit_extender_4_out = {{12{ID_IR[31]}}, ID_IR[31:12]};  // Bit_Extender bit_extender_4
  // Probe on WB_PC[11:0]
  Comparator #(.width(13), .mode("twosComplement")) comparator_2 (
    .a(CNT_num), .b(13'he27), .eq(comparator_2_eq), .lt(comparator_2_lt));  // open: gt
  Clock #(.highDuration(1), .lowDuration(1)) clock_1 (.out(clock_1_out));
  nand nand_1 (nand_1_out, d_ff_1_q, comparator_2_eq);
  Counter #(.width(13), .max('h1fff), .ongoal("stay"), .trigger("rising"), .behavior("old")) counter_1 (
    .count(comparator_2_lt), .Q(CNT_num), .clk(clock_1_out));  // open: load, D, carry, clr, preset
  Regifile regifile_1 (
    .Din(RDin), .Clk(CLK), .R1(regifile_1_r1), .R2(regifile_1_r2), .WE(RegWrite), .W_num(rd),
    .R1_num(multiplexer_4_out), .R2_num(multiplexer_5_out));
  assign CLK = nand_1_out ? clock_1_out : 1'bz;  // Controlled_Buffer controlled_buffer_4
  ID_EX id_ex_1 (
    .Beq(\单周期硬布线控制器_1_beq ), .Bne(\单周期硬布线控制器_1_bne ), .MemToReg(\单周期硬布线控制器_1_memtoreg ),
    .MemWrite(\单周期硬布线控制器_1_memwrite ), .AluOP(\单周期硬布线控制器_1_alu_op ), .AluSrcB(\单周期硬布线控制器_1_alu_src ),
    .RegWrite(\单周期硬布线控制器_1_regwrite ), .Ecall(ID_ecall), .JAL(\单周期硬布线控制器_1_jal ), .JALR(\单周期硬布线控制器_1_jalr ),
    .Lui(\单周期硬布线控制器_1_lui ), .Sh(\单周期硬布线控制器_1_sh ), .Bltu(\单周期硬布线控制器_1_bltu ), .rs1(regifile_1_r1),
    .rs2(regifile_1_r2), .imm_IS(bit_extender_1_out), .imm_B(bit_extender_2_out), .imm_J(bit_extender_3_out),
    .imm_U(bit_extender_4_out), .rd(ID_IR[11:7]), .IR(ID_IR), .PC(ID_PC), .Beq_2(Beq), .Bne_2(Bne),
    .MemToReg_2(id_ex_1_memtoreg_2), .MemWrite_2(id_ex_1_memwrite_2), .AluOP_2(id_ex_1_aluop_2),
    .AluSrcB_2(id_ex_1_alusrcb_2), .RegWrite_2(id_ex_1_regwrite_2), .Ecall_2(EX_ecall), .JAL_2(JAL),
    .JALR_2(JALR), .Lui_2(id_ex_1_lui_2), .Sh_2(id_ex_1_sh_2), .Bltu_2(Bltu), .rs1_2(id_ex_1_rs1_2),
    .rs2_2(id_ex_1_rs2_2), .imm_IS_2(id_ex_1_imm_is_2), .imm_B_2(id_ex_1_imm_b_2), .imm_J_2(id_ex_1_imm_j_2),
    .imm_U_2(id_ex_1_imm_u_2), .rd_2(id_ex_1_rd_2), .IR_2(EX_IR), .PC_2(EX_PC), .en(or_3_out), .clk(CLK),
    .clr(\相关处理逻辑_重定向_1_flush ), .rs1Fwd(\相关处理逻辑_重定向_1_rs1fwd ), .rs2Fwd(\相关处理逻辑_重定向_1_rs2fwd ),
    .rs1Fwd_2(id_ex_1_rs1fwd_2), .rs2Fwd_2(id_ex_1_rs2fwd_2), .PredictJump(if_id_1_predictjump_2),
    .PredictJump_2(id_ex_1_predictjump_2), .rst(RST));  // open: uret, uret_2
  Pull_Resistor #(.pull(1)) pull_resistor_1 (.node(CLK));
  Shifter #(.width(32), .shift("ll")) shifter_1 (.in(id_ex_1_imm_b_2), .\dist (5'b00001), .out(shifter_1_out));
  Shifter #(.width(32), .shift("ll")) shifter_2 (.in(id_ex_1_imm_j_2), .\dist (5'b00001), .out(shifter_2_out));
  Shifter #(.width(32), .shift("ll")) shifter_3 (.in(id_ex_1_imm_u_2), .\dist (5'b01100), .out(shifter_3_out));
  xor xor_1 (PredictErr, id_ex_1_predictjump_2, BranchTaken);
  not not_5 (not_5_out, halt);
  Multiplexer #(.select(2), .width(32), .disabled("Z"), .enable("false")) multiplexer_7 (
    .in0(id_ex_1_rs1_2), .in1(RDin), .in2(MEM_ALUResult), .in3(imm_U), .out(multiplexer_7_out),
    .sel(id_ex_1_rs1fwd_2));
  Multiplexer #(.select(2), .width(32), .disabled("Z"), .enable("false")) multiplexer_8 (
    .in0(id_ex_1_rs2_2), .in1(RDin), .in2(MEM_ALUResult), .in3(imm_U), .out(multiplexer_8_out),
    .sel(id_ex_1_rs2fwd_2));
  Adder #(.width(32)) adder_3 (.a(shifter_1_out), .b(EX_PC), .out(adder_3_out));  // open: cin, cout
  Adder #(.width(32)) adder_4 (.a(shifter_2_out), .b(EX_PC), .out(adder_4_out));  // open: cin, cout
  or or_5 (or_5_out, not_5_out, Go);
  Counter #(.width(16), .max('hffff), .ongoal("wrap"), .trigger("rising"), .behavior("new")) counter_2 (
    .count(or_5_out), .Q(\总周期数 ), .clk(CLK), .clr(RST));  // open: load, D, carry, preset, down
  Multiplexer #(.select(1), .width(32), .disabled("Z"), .enable("false")) multiplexer_9 (
    .in0(multiplexer_8_out), .in1(id_ex_1_imm_is_2), .out(multiplexer_9_out), .sel(id_ex_1_alusrcb_2));
  ALU alu_1 (
    .X(multiplexer_7_out), .Y(multiplexer_9_out), .AluOP(id_ex_1_aluop_2), .Equal(equ),
    .Result(EX_ALUResult), .out_6(less));  // open: Result_2, out_4
  Comparator #(.width(32), .mode("twosComplement")) comparator_3 (
    .a(multiplexer_7_out), .b(32'h22), .eq(comparator_3_eq));  // open: gt, lt
  not not_6 (not_6_out, comparator_3_eq);
  Counter #(.width(16), .max('hffff), .ongoal("wrap"), .trigger("rising"), .behavior("new")) counter_3 (
    .count(Stall), .Q(\LoadUse次数 ), .clk(CLK), .clr(RST));  // open: load, D, carry, preset, down
  Register #(.width(32), .trigger("rising"), .Select("low")) register_1 (
    .D(multiplexer_8_out), .en(and_5_out), .Q(LedData), .clk(CLK), .clr(RST));
  and and_5 (and_5_out, EX_ecall, comparator_3_eq);
  and and_6 (and_6_out, EX_ecall, not_6_out);
  not not_7 (not_7_out, Conditional);
  and and_7 (and_7_out, BranchTaken, not_7_out);
  Counter #(.width(16), .max('hffff), .ongoal("wrap"), .trigger("rising"), .behavior("new")) counter_4 (
    .count(and_7_out), .Q(\无条件分支数 ), .clk(CLK), .clr(RST));  // open: load, D, carry, preset, down
  EX_MEM ex_mem_1 (
    .MemToReg(id_ex_1_memtoreg_2), .MemWrite(id_ex_1_memwrite_2), .RegWrite(id_ex_1_regwrite_2), .JAL(JAL),
    .JALR(JALR), .Lui(id_ex_1_lui_2), .Sh(id_ex_1_sh_2), .ALUResult(EX_ALUResult), .rs2(multiplexer_8_out),
    .imm_U(shifter_3_out), .halt(and_6_out), .rd(id_ex_1_rd_2), .IR(EX_IR), .PC(EX_PC),
    .MemToReg_2(ex_mem_1_memtoreg_2), .MemWrite_2(MemWrite), .RegWrite_2(ex_mem_1_regwrite_2),
    .JAL_2(ex_mem_1_jal_2), .JALR_2(ex_mem_1_jalr_2), .Lui_2(ex_mem_1_lui_2), .Sh_2(ex_mem_1_sh_2),
    .ALUResult_2(MEM_ALUResult), .rs2_2(ex_mem_1_rs2_2), .imm_U_2(imm_U), .halt_2(ex_mem_1_halt_2),
    .rd_2(ex_mem_1_rd_2), .IR_2(MEM_IR), .PC_2(M_PC), .en(or_3_out), .clk(CLK), .rst(RST));
  Multiplexer #(.select(1), .width(32), .disabled("Z"), .enable("false")) multiplexer_10 (
    .in0(ex_mem_1_rs2_2), .in1(ShDin), .out(MDin), .sel(ex_mem_1_sh_2));
  Shifter #(.width(32), .shift("ll")) shifter_4 (.in(ex_mem_1_rs2_2), .\dist (5'b10000), .out(shifter_4_out));
  and and_8 (and_8_out, BranchTaken, Conditional);
  Counter #(.width(16), .max('hffff), .ongoal("wrap"), .trigger("rising"), .behavior("new")) counter_5 (
    .count(and_8_out), .Q(\条件分支成功数 ), .clk(CLK), .clr(RST));  // open: load, D, carry, preset, down
  Multiplexer #(.select(1), .width(32), .disabled("Z"), .enable("false")) multiplexer_11 (
    .in0(32'hffff0000), .in1(32'hffff), .out(multiplexer_11_out), .sel(MEM_ALUResult[1]));
  assign and_9_out = 32'hffff & ex_mem_1_rs2_2;  // AND_Gate and_9, 32 bits wide
  Multiplexer #(.select(1), .width(32), .disabled("Z"), .enable("false")) multiplexer_12 (
    .in0(and_9_out), .in1(shifter_4_out), .out(multiplexer_12_out), .sel(MEM_ALUResult[1]));
  assign and_10_out = ram_1_data & multiplexer_11_out;  // AND_Gate and_10, 32 bits wide
  Counter #(.width(16), .max('hffff), .ongoal("wrap"), .trigger("rising"), .behavior("new")) counter_6 (
    .count(EX_Branch), .Q(\分支指令数目 ), .clk(CLK), .clr(RST));  // open: load, D, carry, preset, down
  // Probe on \分支指令数目 
  RAM #(.addrWidth(10), .dataWidth(32), .bus("separate"), .Select("high")) ram_1 (
    .addr(MEM_ALUResult[11:2]), .din(MDin), .data(ram_1_data), .str(MemWrite), .clk(CLK), .clr(RST));  // open: sel, ld
  Adder #(.width(32)) adder_5 (.a(and_10_out), .b(multiplexer_12_out), .out(ShDin));  // open: cin, cout
  Counter #(.width(16), .max('hffff), .ongoal("wrap"), .trigger("rising"), .behavior("new")) counter_7 (
    .count(PredictErr), .Q(\预测失败次数 ), .clk(CLK), .clr(RST));  // open: load, D, carry, preset, down
  // Probe on \预测失败次数 
  MEM_WB mem_wb_1 (
    .MemToReg(ex_mem_1_memtoreg_2), .RegWrite(ex_mem_1_regwrite_2), .JAL(ex_mem_1_jal_2),
    .JALR(ex_mem_1_jalr_2), .Lui(ex_mem_1_lui_2), .ALUResult(MEM_ALUResult), .ReadData(ram_1_data),
    .imm_U(imm_U), .halt(ex_mem_1_halt_2), .rd(ex_mem_1_rd_2), .IR(MEM_IR), .PC(M_PC),
    .MemToReg_2(mem_wb_1_memtoreg_2), .RegWrite_2(RegWrite), .JAL_2(mem_wb_1_jal_2),
    .JALR_2(mem_wb_1_jalr_2), .Lui_2(mem_wb_1_lui_2), .ALUResult_2(mem_wb_1_aluresult_2),
    .ReadData_2(mem_wb_1_readdata_2), .imm_U_2(mem_wb_1_imm_u_2), .halt_2(halt), .rd_2(rd), .IR_2(WB_IR),
    .PC_2(WB_PC), .en(or_3_out), .clk(CLK), .rst(RST));
  Multiplexer #(.select(1), .width(32), .disabled("Z"), .enable("false")) multiplexer_13 (
    .in0(mem_wb_1_aluresult_2), .in1(mem_wb_1_readdata_2), .out(multiplexer_13_out), .sel(mem_wb_1_memtoreg_2));
  Adder #(.width(32)) adder_6 (.a(32'h4), .b(WB_PC), .out(adder_6_out));  // open: cin, cout
  or or_6 (or_6_out, mem_wb_1_jalr_2, mem_wb_1_jal_2);
  Multiplexer #(.select(1), .width(32), .disabled("Z"), .enable("false")) multiplexer_14 (
    .in0(multiplexer_13_out), .in1(adder_6_out), .out(multiplexer_14_out), .sel(or_6_out));
  Multiplexer #(.select(1), .width(32), .disabled("Z"), .enable("false")) multiplexer_15 (
    .in0(multiplexer_14_out), .in1(mem_wb_1_imm_u_2), .out(RDin), .sel(mem_wb_1_lui_2));

  // Other names for the same wires on the sheet: MEM_PC[31:0] = M_PC; 插入气泡数[15:0] = \LoadUse次数 

  // Notes on the sheet:
  //   中断源
  //   时空图监测，可删除
  //   中断等待指示
  //   修订地址
  //   预测跳转
  //   预测地址
  //   Stall
  //   分支地址
  //   数码管输出
  //   BranchTaken
  //   PredictErr
  //   顺序地址
  //   取指(IF)
  //   指令存储器
  //   contents of rom_1 (hex, n*v repeats v):
  //   100493 100006f 100493 200913 300993 100006f 100493 200913 300993 100006f 100493 200913 300993
  //   100006f 100493 200913 300993 3c0000ef 100413 100493 1f49493 900533 2200893 73 24d493 48463 fedff06f
  //   900533 2200893 73 100493 249493 900533 2200893 73 48463 fedff06f 100493 1f49493 900533 2200893 73
  //   4034d493 900533 2200893 73 4044d493 900533 2200893 73 4044d493 900533 2200893 73 4044d493 900533
  //   2200893 73 4044d493 900533 2200893 73 4044d493 900533 2200893 73 4044d493 900533 2200893 73 4044d493
  //   900533 2200893 73 100413 1f41993 41f9d993 433 c00913 300b13 140413 f47413 800293 100313 499993
  //   89e9b3 1300533 2200893 73 406282b3 fe0294e3 140413 f00f93 1f47433 1c41413 800293 100313 49d993
  //   89e9b3 1300533 2200893 73 406282b3 fe0294e3 1c45413 406b0b33 b0463 f95ff06f 2b3 fff2c293 829293
  //   ff2e293 500533 2200893 73 fff00413 493 84a023 140413 448493 84a023 140413 448493 84a023 140413
  //   448493 84a023 140413 448493 84a023 140413 448493 84a023 140413 448493 84a023 140413 448493 84a023
  //   140413 448493 84a023 140413 448493 84a023 140413 448493 84a023 140413 448493 84a023 140413 448493
  //   84a023 140413 448493 84a023 140413 448493 84a023 140413 448493 84a023 140413 448493 140413 433
  //   3c00493 42983 4aa03 149a2b3 28663 134a023 1442023 ffc48493 fe9412e3 800533 2200893 73 440413 3c00493
  //   fc9416e3 a00893 73 100293 300313 800493 849493 7648493 900533 2200893 73 800e13 5494b3 6494b3 900533
  //   2200893 73 fffe0e13 fe0e14e3 a00893 73 800e13 fedc04b7 fff00413 1045413 84e4b3 900533 2200893 73
  //   ba984b7 900533 73 76544b7 900533 73 32104b7 900533 73 fffe0e13 fa0e1ee3 a00893 73 313 2000e13 100493
  //   100913 931023 900533 2200893 73 12484b3 230313 fffe0e13 fe0e12e3 1000e13 313 32483 900533 2200893 73
  //   430313 fffe0e13 fe0e14e3 a00893 73 ff100493 900533 2200893 73 148493 fe9068e3 900533 2200893 73
  //   a00893 73 413 140413 800533 2200893 73 240413 800533 2200893 73 340413 800533 2200893 73 440413
  //   800533 2200893 73 540413 800533 2200893 73 640413 800533 2200893 73 740413 800533 2200893 73 840413
  //   800533 2200893 2200893 73 8067
  //   Lui
  //   Sh
  //   Bltu
  //   I
  //   S
  //   B
  //   J
  //   U
  //   控制位
  //   Instr
  //   rs1used
  //   JAL
  //   JALR
  //   $a7编号
  //   $a0编号
  //   流水调试日志用
  //   暂停节拍，不能为0
  //   rs2used
  //   Beq
  //   Bne
  //   MemToReg
  //   MemWrite
  //   AluOP
  //   AluSrcB
  //   RegWrite
  //   译码取数(ID)
  //   戳工具置1进入计数暂停模式，ctrl+k时钟自动运行到对应节拍暂停
  //   ctrl+k关闭时钟连续运行，将控制位置零，进入单步调试模式调试
  //   SignImm
  //   rs1Fwd
  //   rs2Fwd
  //   可计数暂停的时钟源
  //   Flush
  //   跳转地址(beq/bne/bltu)
  //   跳转地址(jal)
  //   为方便自动评测，需要输出流水线各段保存的PC值，注意是PC不是PC+4，另外ID段寄存器写入信息，Mem段内存写入信息也要输出
  //   指令执行(EX)
  //   EX.Lui
  //   ecall指令输出$a0到Led
  //   跳转地址(jalr)
  //   WriteData
  //   存储器不支持半字访问，因此需要取出一个字的数据特殊处理
  //   数据存储器
  //   访存(MEM)
  //   ReadData
  //   返回地址
  //   左移12位立即数
  //   写回(WB)
  //   保存到寄存器中的数据
endmodule

module \封装正确性测试  (
);

  wire IR1, IR2, IR3, MemW, RegW;
  wire [31:0] EX_PC, ID_PC, IF_PC, IR, LED, MDin, MDinr, MEM_PC, PC, RDin, RDinr, WB_PC;

  \单周期RISC_V  \u_单周期risc_v_1  (
    .IR1(IR1), .IR2(IR2), .IR3(IR3), .RegWrite(RegW), .MemWrite(MemW), .PC(PC), .IR(IR), .RDin(RDin),
    .MDin(MDin), .LedData(LED));
  \气泡流水线  \u_气泡流水线_1  (
    .RegWrite(RegW), .MemWrite(MemW), .IF_PC(IF_PC), .ID_PC(ID_PC), .EX_PC(EX_PC), .M_PC(MEM_PC),
    .WB_PC(WB_PC), .RDin(RDinr), .MDin(MDinr), .LedData(LED));
  \单周期_单级中断  \u_单周期_单级中断_1  (
    .IR1(IR1), .IR2(IR2), .IR3(IR3), .RegWrite(RegW), .MemWrite(MemW), .PC(PC), .IR(IR), .RDin(RDin),
    .MDin(MDin), .LedData(LED));
  \理想流水线  \u_理想流水线_1  (
    .RegWrite(RegW), .MemWrite(MemW), .IF_PC(IF_PC), .ID_PC(ID_PC), .EX_PC(EX_PC), .M_PC(MEM_PC),
    .WB_PC(WB_PC), .RDin(RDinr), .MDin(MDinr), .LedData(LED));
  \重定向流水线  \u_重定向流水线_1  (
    .RegWrite(RegW), .MemWrite(MemW), .IF_PC(IF_PC), .ID_PC(ID_PC), .EX_PC(EX_PC), .M_PC(MEM_PC),
    .WB_PC(WB_PC), .RDin(RDinr), .MDin(MDinr), .LedData(LED));
  \单周期_多级中断  \u_单周期_多级中断_1  (
    .IR1(IR1), .IR2(IR2), .IR3(IR3), .RegWrite(RegW), .MemWrite(MemW), .PC(PC), .IR(IR), .RDin(RDin),
    .MDin(MDin), .LedData(LED));

  // Notes on the sheet:
  //   单周期封装测试
  //   气泡流水封装测试
  //   单周期+单级中断封装测试
  //   请检查上面封装有无位宽不匹配，引脚标签是否和连接的标签相对应，否则无法在educoder平台上正确测试
  //   理想流水封装测试
  //   重定向流水封装测试
  //   单周期+多级中断封装测试
endmodule
